// Digital circuit !testing2.dig as structural Verilog
module testing2 (
  input  clk,
  input  EN_EN,
  input  EN,
  input  [7:0] LOC,
  input  EN_2,
  input  in_9,
  input  in_10,
  input  [7:0] in_11,
  output [7:0] out_4,
  output out_5,
  output [15:0] out_8
);

  wire and_1_out, and_2_out, delay_1_out, delay_2_out, delay_3_out, delay_4_out, driver_1_out, driver_3_out,
       keyboard_1_av;
  wire [7:0] add_1_s, delay_5_out, driverinvsel_2_out, driverinvsel_3_out;
  wire [15:0] eeprom_1_d, keyboard_1_d;

  assign driver_1_out = EN_EN ? EN : 1'bz;  // Driver driver_1
  assign driver_1_out = ~EN_EN ? clk : 1'bz;  // DriverInvSel driverinvsel_1
  Delay #(.delayTime(10)) delay_1 (.in(driver_1_out), .out(delay_1_out));
  Keyboard keyboard_1 (.C(delay_1_out), .en(driver_1_out), .D(keyboard_1_d), .av(keyboard_1_av));
  Add #(.Bits(8)) add_1 (.a(out_4), .b(8'h1), .c_i(1'b0), .s(add_1_s), .c_o(out_5));
  and and_1 (and_1_out, keyboard_1_av, driver_1_out);
  assign driverinvsel_2_out = ~EN_2 ? add_1_s : 8'bz;  // DriverInvSel driverinvsel_2
  assign driverinvsel_2_out = EN_2 ? LOC : 8'bz;  // Driver driver_2
  and and_2 (and_2_out, keyboard_1_av, ~clk);  // And
  Delay #(.delayTime(10)) delay_2 (.in(and_2_out), .out(delay_2_out));
  assign driver_3_out = delay_2_out ? delay_2_out : 1'bz;  // Driver driver_3
  Delay #(.delayTime(10)) delay_3 (.in(driver_3_out), .out(delay_3_out));
  assign driver_3_out = EN_2 ? EN_2 : 1'bz;  // Driver driver_4
  Register #(.Bits(16)) register_1 (.D(keyboard_1_d), .C(and_1_out), .en(keyboard_1_av), .Q(out_8));
  Register #(.Bits(8)) register_2 (.D(driverinvsel_2_out), .C(delay_3_out), .en(driver_3_out), .Q(out_4));
  PullDown pulldown_1 (.out(driver_3_out));
  Delay #(.delayTime(10)) delay_4 (.in(driver_3_out), .out(delay_4_out));
  assign driverinvsel_3_out = ~in_10 ? out_4 : 8'bz;  // DriverInvSel driverinvsel_3
  assign driverinvsel_3_out = in_10 ? in_11 : 8'bz;  // Driver driver_5
  Delay #(.Bits(8), .delayTime(20)) delay_5 (.in(driverinvsel_3_out), .out(delay_5_out));
  EEPROM #(.AddrBits(8), .Bits(16)) eeprom_1 (.A(delay_5_out), .CS(1'b1), .WE(delay_4_out), .OE(in_9), .D(eeprom_1_d));
  assign eeprom_1_d = delay_4_out ? out_8 : 16'bz;  // Driver driver_6

  // Notes on the sheet:
  //   clk: Hz: 10
  //   NEED TO TYPE SLOW. FIX?
  //   CORRECT CURCUIT FOR MAIN PAS14
  //   contents of eeprom_1 (hex, n*v repeats v):
  //   73,6f,20,77,6f,75,6c,64,20,74,68,69,73,20,61,6c,73,6f,20,77,6f
  //   ,72,6c,3f,a
endmodule
