// Digital circuit vgadisplay.dig as structural Verilog
module vgadisplay (
  input  clock,
  input  [15:0] CD,
  input  [6:0] MAN,
  output [3:0] R,
  output [3:0] G,
  output [3:0] B,
  output hs,
  output vs,
  output de,
  output [10:0] CA
);

  wire vgacharpos_1_p3, vgacharpos_1_p4, vgasync_1_h, vgasync_1_pic, vgasync_1_v;
  wire [6:0] vgastring_1_c_o, vgastring_2_c_o;
  wire [7:0] vgacharpos_1_p5, vgacharpos_1_p6, vgastring_1_cx_o, vgastring_1_cy_o;
  wire [11:0] vgastring_1_bg_o, vgastring_1_fg_o, vgastring_2_bg_o, vgastring_2_fg_o;
  wire [15:0] vgasync_1_x, vgasync_1_y;

  vgasync vgasync_1 (
    .clock(clock), .H(vgasync_1_h), .V(vgasync_1_v), .pic(vgasync_1_pic), .X(vgasync_1_x), .Y(vgasync_1_y));
  // vgacharpos vgacharpos_1: pin names not known; wires that end beside it: vgasync_1_x, vgasync_1_y, vgacharpos_1_p3, vgacharpos_1_p4, vgacharpos_1_p5, vgacharpos_1_p6
  vgastring vgastring_1 (
    .CX_i(vgacharpos_1_p5), .CY_i(vgacharpos_1_p6), .C_i({7{1'b0}}), .FG_i({12{1'b0}}), .BG_i({12{1'b0}}),
    .FG_c(12'he07), .BG_c({12{1'b0}}), .CX_c({6{1'b0}}), .CY_c({8{1'b0}}), .C_0(MAN), .C_1(7'b1000010),
    .C_2(7'b1000011), .C_3(7'b1000100), .EN(1'b1), .CX_o(vgastring_1_cx_o), .CY_o(vgastring_1_cy_o),
    .C_o(vgastring_1_c_o), .FG_o(vgastring_1_fg_o), .BG_o(vgastring_1_bg_o));
  vgastring vgastring_2 (
    .CX_i(vgastring_1_cx_o), .CY_i(vgastring_1_cy_o), .C_i(vgastring_1_c_o), .FG_i(vgastring_1_fg_o),
    .BG_i(vgastring_1_bg_o), .FG_c(12'he07), .BG_c(12'h222), .CX_c(6'b000001), .CY_c(8'h1), .C_0(7'b1000001),
    .C_1(7'b1000010), .C_2(7'b1000011), .C_3(7'b1000100), .EN(1'b1), .C_o(vgastring_2_c_o),
    .FG_o(vgastring_2_fg_o), .BG_o(vgastring_2_bg_o));  // open: CX_o, CY_o
  // vgatext vgatext_1: pin names not known; wires that end beside it: vgasync_1_h, vgasync_1_v, vgasync_1_pic, vgacharpos_1_p3, vgacharpos_1_p4, CD, clock, vgastring_2_c_o, vgastring_2_fg_o, vgastring_2_bg_o, R, G, B, hs, vs, de, CA

  // Other names for the same wires on the sheet: C = clock

  // Notes on the sheet:
  //   clock: Hz: 2147483647
  //   MAN: default 65
endmodule
