// Digital circuit vgastring.dig as structural Verilog
module vgastring (
  input  [7:0] CX_i,
  input  [7:0] CY_i,
  input  [6:0] C_i,
  input  [11:0] FG_i,
  input  [11:0] BG_i,
  input  [11:0] FG_c,
  input  [11:0] BG_c,
  input  [5:0] CX_c,
  input  [7:0] CY_c,
  input  [6:0] C_0,
  input  [6:0] C_1,
  input  [6:0] C_2,
  input  [6:0] C_3,
  input  EN,
  output [7:0] CX_o,
  output [7:0] CY_o,
  output [6:0] C_o,
  output [11:0] FG_o,
  output [11:0] BG_o
);

  wire and_1_out, comparator_1_eq, comparator_2_eq;
  wire [6:0] multiplexer_1_out;

  Comparator #(.Bits(6)) comparator_1 (.a(CX_i[7:2]), .b(CX_c), .eq(comparator_1_eq));  // open: gt, lt
  Comparator #(.Bits(8)) comparator_2 (.a(CY_i), .b(CY_c), .eq(comparator_2_eq));  // open: gt, lt
  Multiplexer #(.Selector_Bits(2), .Bits(7)) multiplexer_1 (
    .sel(CX_i[1:0]), .in_0(C_0), .in_1(C_1), .in_2(C_2), .in_3(C_3), .out(multiplexer_1_out));
  Multiplexer #(.Bits(12)) multiplexer_2 (.sel(and_1_out), .in_0(FG_i), .in_1(FG_c), .out(FG_o));
  Multiplexer #(.Bits(12)) multiplexer_3 (.sel(and_1_out), .in_0(BG_i), .in_1(BG_c), .out(BG_o));
  Multiplexer #(.Bits(7)) multiplexer_4 (.sel(and_1_out), .in_0(C_i), .in_1(multiplexer_1_out), .out(C_o));
  and and_1 (and_1_out, comparator_1_eq, EN, comparator_2_eq);

  assign CX_o = CX_i;
  assign CY_o = CY_i;
endmodule
