// Digital circuit vgatest2.dig as structural Verilog
module vgatest2 (
  input  clock,
  input  [6:0] D,
  input  [7:0] A,
  input  clk,
  output [3:0] R,
  output [3:0] G,
  output [3:0] B,
  output hs,
  output vs,
  output de,
  output [10:0] CA,
  output [7:0] out_12,
  output [6:0] out_13
);

  wire add_1_c_o, comparator_1_eq, comparator_2_eq, comparator_3_eq, comparator_4_eq, comparator_5_eq,
       comparator_6_eq, comparator_7_eq, comparator_8_eq, comparator_9_eq, comparator_10_eq,
       comparator_11_eq, comparator_12_eq, comparator_13_eq, comparator_14_eq, comparator_15_eq,
       comparator_16_eq, comparator_17_eq, comparator_18_eq, comparator_19_eq, comparator_20_eq,
       comparator_21_eq, comparator_22_eq, comparator_23_eq, comparator_24_eq, comparator_25_eq,
       comparator_26_eq, comparator_27_eq, comparator_28_eq, comparator_29_eq, comparator_30_eq,
       comparator_31_eq, comparator_32_eq, comparator_33_eq, comparator_34_eq, comparator_35_eq,
       comparator_36_eq, comparator_37_eq, comparator_38_eq, comparator_39_eq, comparator_40_eq,
       comparator_41_eq, comparator_42_eq, comparator_43_eq, comparator_44_eq, comparator_45_eq,
       comparator_46_eq, comparator_47_eq, comparator_48_eq, comparator_49_eq, comparator_50_eq,
       comparator_51_eq, comparator_52_eq, comparator_53_eq, comparator_54_eq, comparator_55_eq,
       comparator_56_eq, comparator_57_eq, comparator_58_eq, comparator_59_eq, comparator_60_eq,
       comparator_61_eq, comparator_62_eq, comparator_63_eq, comparator_64_eq, comparator_65_eq,
       comparator_66_eq, comparator_67_eq, comparator_68_eq, comparator_69_eq, comparator_70_eq,
       comparator_71_eq, comparator_72_eq, comparator_73_eq, comparator_74_eq, comparator_75_eq,
       comparator_76_eq, comparator_77_eq, comparator_78_eq, comparator_79_eq, comparator_80_eq,
       comparator_81_eq, comparator_82_eq, comparator_83_eq, comparator_84_eq, comparator_85_eq,
       comparator_86_eq, comparator_87_eq, comparator_88_eq, comparator_89_eq, comparator_90_eq,
       comparator_91_eq, comparator_92_eq, comparator_93_eq, comparator_94_eq, comparator_95_eq,
       comparator_96_eq, comparator_97_eq, comparator_98_eq, comparator_99_eq, comparator_100_eq,
       comparator_101_eq, comparator_102_eq, comparator_103_eq, comparator_104_eq, comparator_105_eq,
       comparator_106_eq, comparator_107_eq, comparator_108_eq, comparator_109_eq, comparator_110_eq,
       comparator_111_eq, comparator_112_eq, comparator_113_eq, comparator_114_eq, comparator_115_eq,
       comparator_116_eq, comparator_117_eq, comparator_118_eq, comparator_119_eq, comparator_120_eq,
       comparator_121_eq, comparator_122_eq, comparator_123_eq, comparator_124_eq, comparator_125_eq,
       comparator_126_eq, comparator_127_eq, comparator_128_eq, comparator_129_eq, comparator_130_eq,
       comparator_131_eq, comparator_132_eq, comparator_133_eq, comparator_134_eq, comparator_135_eq,
       comparator_136_eq, comparator_137_eq, comparator_138_eq, comparator_139_eq, comparator_140_eq,
       comparator_141_eq, comparator_142_eq, comparator_143_eq, comparator_144_eq, comparator_145_eq,
       comparator_146_eq, comparator_147_eq, comparator_148_eq, comparator_149_eq, comparator_150_eq,
       comparator_151_eq, comparator_152_eq, comparator_153_eq, comparator_154_eq, comparator_155_eq,
       comparator_156_eq, comparator_157_eq, comparator_158_eq, comparator_159_eq, comparator_160_eq,
       delay_1_out, delay_2_out, delay_3_out, delay_4_out, delay_5_out, delay_6_out, delay_7_out,
       delay_8_out, delay_9_out, delay_10_out, delay_11_out, delay_12_out, delay_13_out, delay_14_out,
       delay_15_out, delay_16_out, delay_17_out, delay_18_out, delay_19_out, delay_20_out, delay_21_out,
       delay_22_out, delay_23_out, delay_24_out, delay_25_out, delay_26_out, delay_27_out, delay_28_out,
       delay_29_out, delay_30_out, delay_31_out, delay_32_out, delay_33_out, delay_34_out, delay_35_out,
       delay_36_out, delay_37_out, delay_38_out, delay_39_out, delay_40_out, delay_41_out, delay_42_out,
       delay_43_out, delay_44_out, delay_45_out, delay_46_out, delay_47_out, delay_48_out, delay_49_out,
       delay_50_out, delay_51_out, delay_52_out, delay_53_out, delay_54_out, delay_55_out, delay_56_out,
       delay_57_out, delay_58_out, delay_59_out, delay_60_out, delay_61_out, delay_62_out, delay_63_out,
       delay_64_out, delay_65_out, delay_66_out, delay_67_out, delay_68_out, delay_69_out, delay_70_out,
       delay_71_out, delay_72_out, delay_73_out, delay_74_out, delay_75_out, delay_76_out, delay_77_out,
       delay_78_out, delay_79_out, delay_80_out, delay_81_out, delay_82_out, delay_83_out, delay_84_out,
       delay_85_out, delay_86_out, delay_87_out, delay_88_out, delay_89_out, delay_90_out, delay_91_out,
       delay_92_out, delay_93_out, delay_94_out, delay_95_out, delay_96_out, delay_97_out, delay_98_out,
       delay_99_out, delay_100_out, delay_101_out, delay_102_out, delay_103_out, delay_104_out,
       delay_105_out, delay_106_out, delay_107_out, delay_108_out, delay_109_out, delay_110_out,
       delay_111_out, delay_112_out, delay_113_out, delay_114_out, delay_115_out, delay_116_out,
       delay_117_out, delay_118_out, delay_119_out, delay_120_out, delay_121_out, delay_122_out,
       delay_123_out, delay_124_out, delay_125_out, delay_126_out, delay_127_out, delay_128_out,
       delay_129_out, delay_130_out, delay_131_out, delay_132_out, delay_133_out, delay_134_out,
       delay_135_out, delay_136_out, delay_137_out, delay_138_out, delay_139_out, delay_140_out,
       delay_141_out, delay_142_out, delay_143_out, delay_144_out, delay_145_out, delay_146_out,
       delay_147_out, delay_148_out, delay_149_out, delay_150_out, delay_151_out, delay_152_out,
       delay_153_out, delay_154_out, delay_155_out, delay_156_out, delay_157_out, delay_158_out,
       delay_159_out, delay_160_out, delay_161_out, delay_162_out, not_1_out, vgacharpos_1_p3,
       vgacharpos_1_p4, vgasync_1_h, vgasync_1_pic, vgasync_1_v, WR_out;
  wire [6:0] driver_2_out, register_2_q, register_3_q, register_4_q, register_5_q, register_6_q,
       register_7_q, register_8_q, register_9_q, register_10_q, register_11_q, register_12_q, register_13_q,
       register_14_q, register_15_q, register_16_q, register_17_q, register_18_q, register_19_q,
       register_20_q, register_21_q, register_22_q, register_23_q, register_24_q, register_25_q,
       register_26_q, register_27_q, register_28_q, register_29_q, register_30_q, register_31_q,
       register_32_q, register_33_q, register_34_q, register_35_q, register_36_q, register_37_q,
       register_38_q, register_39_q, register_40_q, register_41_q, register_42_q, register_43_q,
       register_44_q, register_45_q, register_46_q, register_47_q, register_48_q, register_49_q,
       register_50_q, register_51_q, register_52_q, register_53_q, register_54_q, register_55_q,
       register_56_q, register_57_q, register_58_q, register_59_q, register_60_q, register_61_q,
       register_62_q, register_63_q, register_64_q, register_65_q, register_66_q, register_67_q,
       register_68_q, register_69_q, register_70_q, register_71_q, register_72_q, register_73_q,
       register_74_q, register_75_q, register_76_q, register_77_q, register_78_q, register_79_q,
       register_80_q, register_81_q, register_82_q, register_83_q, register_84_q, register_85_q,
       register_86_q, register_87_q, register_88_q, register_89_q, register_90_q, register_91_q,
       register_92_q, register_93_q, register_94_q, register_95_q, register_96_q, register_97_q,
       register_98_q, register_99_q, register_100_q, register_101_q, register_102_q, register_103_q,
       register_104_q, register_105_q, register_106_q, register_107_q, register_108_q, register_109_q,
       register_110_q, register_111_q, register_112_q, register_113_q, register_114_q, register_115_q,
       register_116_q, register_117_q, register_118_q, register_119_q, register_120_q, register_121_q,
       register_122_q, register_123_q, register_124_q, register_125_q, register_126_q, register_127_q,
       register_128_q, register_129_q, register_130_q, register_131_q, register_132_q, register_133_q,
       register_134_q, register_135_q, register_136_q, register_137_q, register_138_q, register_139_q,
       register_140_q, register_141_q, register_142_q, register_143_q, register_144_q, register_145_q,
       register_146_q, register_147_q, register_148_q, register_149_q, register_150_q, register_151_q,
       register_152_q, register_153_q, register_154_q, register_155_q, register_156_q, register_157_q,
       register_158_q, register_159_q, register_160_q, register_161_q, vgastring_1_c_o, vgastring_2_c_o,
       vgastring_3_c_o, vgastring_4_c_o, vgastring_5_c_o, vgastring_6_c_o, vgastring_7_c_o, vgastring_8_c_o,
       vgastring_9_c_o, vgastring_10_c_o, vgastring_11_c_o, vgastring_12_c_o, vgastring_13_c_o,
       vgastring_14_c_o, vgastring_15_c_o, vgastring_16_c_o, vgastring_17_c_o, vgastring_18_c_o,
       vgastring_19_c_o, vgastring_20_c_o, vgastring_21_c_o, vgastring_22_c_o, vgastring_23_c_o,
       vgastring_24_c_o, vgastring_25_c_o, vgastring_26_c_o, vgastring_27_c_o, vgastring_28_c_o,
       vgastring_29_c_o, vgastring_30_c_o, vgastring_31_c_o, vgastring_32_c_o, vgastring_33_c_o,
       vgastring_34_c_o, vgastring_35_c_o, vgastring_36_c_o, vgastring_37_c_o, vgastring_38_c_o,
       vgastring_39_c_o, vgastring_40_c_o;
  wire [7:0] add_1_s, driverinvsel_1_out, vgacharpos_1_p5, vgacharpos_1_p6, vgastring_1_cx_o,
       vgastring_1_cy_o, vgastring_2_cx_o, vgastring_2_cy_o, vgastring_3_cx_o, vgastring_3_cy_o,
       vgastring_4_cx_o, vgastring_4_cy_o, vgastring_5_cx_o, vgastring_5_cy_o, vgastring_6_cx_o,
       vgastring_6_cy_o, vgastring_7_cx_o, vgastring_7_cy_o, vgastring_8_cx_o, vgastring_8_cy_o,
       vgastring_9_cx_o, vgastring_9_cy_o, vgastring_10_cx_o, vgastring_10_cy_o, vgastring_11_cx_o,
       vgastring_11_cy_o, vgastring_12_cx_o, vgastring_12_cy_o, vgastring_13_cx_o, vgastring_13_cy_o,
       vgastring_14_cx_o, vgastring_14_cy_o, vgastring_15_cx_o, vgastring_15_cy_o, vgastring_16_cx_o,
       vgastring_16_cy_o, vgastring_17_cx_o, vgastring_17_cy_o, vgastring_18_cx_o, vgastring_18_cy_o,
       vgastring_19_cx_o, vgastring_19_cy_o, vgastring_20_cx_o, vgastring_20_cy_o, vgastring_21_cx_o,
       vgastring_21_cy_o, vgastring_22_cx_o, vgastring_22_cy_o, vgastring_23_cx_o, vgastring_23_cy_o,
       vgastring_24_cx_o, vgastring_24_cy_o, vgastring_25_cx_o, vgastring_25_cy_o, vgastring_26_cx_o,
       vgastring_26_cy_o, vgastring_27_cx_o, vgastring_27_cy_o, vgastring_28_cx_o, vgastring_28_cy_o,
       vgastring_29_cx_o, vgastring_29_cy_o, vgastring_30_cx_o, vgastring_30_cy_o, vgastring_31_cx_o,
       vgastring_31_cy_o, vgastring_32_cx_o, vgastring_32_cy_o, vgastring_33_cx_o, vgastring_33_cy_o,
       vgastring_34_cx_o, vgastring_34_cy_o, vgastring_35_cx_o, vgastring_35_cy_o, vgastring_36_cx_o,
       vgastring_36_cy_o, vgastring_37_cx_o, vgastring_37_cy_o, vgastring_38_cx_o, vgastring_38_cy_o,
       vgastring_39_cx_o, vgastring_39_cy_o, vgastring_40_cx_o, vgastring_40_cy_o;
  wire [11:0] vgastring_1_bg_o, vgastring_1_fg_o, vgastring_2_bg_o, vgastring_2_fg_o, vgastring_3_bg_o,
       vgastring_3_fg_o, vgastring_4_bg_o, vgastring_4_fg_o, vgastring_5_bg_o, vgastring_5_fg_o,
       vgastring_6_bg_o, vgastring_6_fg_o, vgastring_7_bg_o, vgastring_7_fg_o, vgastring_8_bg_o,
       vgastring_8_fg_o, vgastring_9_bg_o, vgastring_9_fg_o, vgastring_10_bg_o, vgastring_10_fg_o,
       vgastring_11_bg_o, vgastring_11_fg_o, vgastring_12_bg_o, vgastring_12_fg_o, vgastring_13_bg_o,
       vgastring_13_fg_o, vgastring_14_bg_o, vgastring_14_fg_o, vgastring_15_bg_o, vgastring_15_fg_o,
       vgastring_16_bg_o, vgastring_16_fg_o, vgastring_17_bg_o, vgastring_17_fg_o, vgastring_18_bg_o,
       vgastring_18_fg_o, vgastring_19_bg_o, vgastring_19_fg_o, vgastring_20_bg_o, vgastring_20_fg_o,
       vgastring_21_bg_o, vgastring_21_fg_o, vgastring_22_bg_o, vgastring_22_fg_o, vgastring_23_bg_o,
       vgastring_23_fg_o, vgastring_24_bg_o, vgastring_24_fg_o, vgastring_25_bg_o, vgastring_25_fg_o,
       vgastring_26_bg_o, vgastring_26_fg_o, vgastring_27_bg_o, vgastring_27_fg_o, vgastring_28_bg_o,
       vgastring_28_fg_o, vgastring_29_bg_o, vgastring_29_fg_o, vgastring_30_bg_o, vgastring_30_fg_o,
       vgastring_31_bg_o, vgastring_31_fg_o, vgastring_32_bg_o, vgastring_32_fg_o, vgastring_33_bg_o,
       vgastring_33_fg_o, vgastring_34_bg_o, vgastring_34_fg_o, vgastring_35_bg_o, vgastring_35_fg_o,
       vgastring_36_bg_o, vgastring_36_fg_o, vgastring_37_bg_o, vgastring_37_fg_o, vgastring_38_bg_o,
       vgastring_38_fg_o, vgastring_39_bg_o, vgastring_39_fg_o, vgastring_40_bg_o, vgastring_40_fg_o;
  wire [15:0] Char_ROM_d, vgasync_1_x, vgasync_1_y, vgatext_1_p6;

  Add #(.Bits(8)) add_1 (.a(out_12), .b(8'h1), .c_i(1'b0), .s(add_1_s), .c_o(add_1_c_o));
  Delay #(.delayTime(10)) delay_1 (.in(clk), .out(delay_1_out));
  Register #(.Bits(8)) register_1 (.D(add_1_s), .C(delay_1_out), .en(clk), .Q(out_12));
  Button WR (.out(WR_out));
  assign driverinvsel_1_out = ~WR_out ? out_12 : 8'bz;  // DriverInvSel driverinvsel_1
  assign driverinvsel_1_out = WR_out ? A : 8'bz;  // Driver driver_1
  Delay #(.delayTime(10)) delay_2 (.in(WR_out), .out(delay_2_out));
  not not_1 (not_1_out, WR_out);
  EEPROM #(.AddrBits(8), .Bits(7)) eeprom_1 (
    .A(driverinvsel_1_out), .CS(1'b1), .WE(delay_2_out), .OE(not_1_out), .D(out_13));
  assign driver_2_out = not_1_out ? out_13 : 7'bz;  // Driver driver_2
  assign out_13 = delay_2_out ? D : 7'bz;  // Driver driver_3
  vgasync vgasync_1 (
    .clock(clock), .H(vgasync_1_h), .V(vgasync_1_v), .pic(vgasync_1_pic), .X(vgasync_1_x), .Y(vgasync_1_y));
  Comparator #(.Bits(8)) comparator_1 (.a(out_12), .b({8{1'b0}}), .eq(comparator_1_eq));  // open: gt, lt
  Comparator #(.Bits(8)) comparator_2 (.a(out_12), .b(8'h1), .eq(comparator_2_eq));  // open: gt, lt
  Comparator #(.Bits(8)) comparator_3 (.a(out_12), .b(8'h2), .eq(comparator_3_eq));  // open: gt, lt
  Comparator #(.Bits(8)) comparator_4 (.a(out_12), .b(8'h3), .eq(comparator_4_eq));  // open: gt, lt
  Comparator #(.Bits(8)) comparator_5 (.a(out_12), .b(8'h28), .eq(comparator_5_eq));  // open: gt, lt
  Comparator #(.Bits(8)) comparator_6 (.a(out_12), .b(8'h29), .eq(comparator_6_eq));  // open: gt, lt
  Comparator #(.Bits(8)) comparator_7 (.a(out_12), .b(8'h2a), .eq(comparator_7_eq));  // open: gt, lt
  Comparator #(.Bits(8)) comparator_8 (.a(out_12), .b(8'h2b), .eq(comparator_8_eq));  // open: gt, lt
  Comparator #(.Bits(8)) comparator_9 (.a(out_12), .b(8'h50), .eq(comparator_9_eq));  // open: gt, lt
  Comparator #(.Bits(8)) comparator_10 (.a(out_12), .b(8'h51), .eq(comparator_10_eq));  // open: gt, lt
  Comparator #(.Bits(8)) comparator_11 (.a(out_12), .b(8'h52), .eq(comparator_11_eq));  // open: gt, lt
  Comparator #(.Bits(8)) comparator_12 (.a(out_12), .b(8'h53), .eq(comparator_12_eq));  // open: gt, lt
  Comparator #(.Bits(8)) comparator_13 (.a(out_12), .b(8'h78), .eq(comparator_13_eq));  // open: gt, lt
  Comparator #(.Bits(8)) comparator_14 (.a(out_12), .b(8'h79), .eq(comparator_14_eq));  // open: gt, lt
  Comparator #(.Bits(8)) comparator_15 (.a(out_12), .b(8'h7a), .eq(comparator_15_eq));  // open: gt, lt
  Comparator #(.Bits(8)) comparator_16 (.a(out_12), .b(8'h7b), .eq(comparator_16_eq));  // open: gt, lt
  Delay #(.delayTime(10)) delay_3 (.in(comparator_1_eq), .out(delay_3_out));
  Delay #(.delayTime(10)) delay_4 (.in(comparator_2_eq), .out(delay_4_out));
  Delay #(.delayTime(10)) delay_5 (.in(comparator_3_eq), .out(delay_5_out));
  Delay #(.delayTime(10)) delay_6 (.in(comparator_4_eq), .out(delay_6_out));
  Delay #(.delayTime(10)) delay_7 (.in(comparator_5_eq), .out(delay_7_out));
  Delay #(.delayTime(10)) delay_8 (.in(comparator_6_eq), .out(delay_8_out));
  Delay #(.delayTime(10)) delay_9 (.in(comparator_7_eq), .out(delay_9_out));
  Delay #(.delayTime(10)) delay_10 (.in(comparator_8_eq), .out(delay_10_out));
  Delay #(.delayTime(10)) delay_11 (.in(comparator_9_eq), .out(delay_11_out));
  Delay #(.delayTime(10)) delay_12 (.in(comparator_10_eq), .out(delay_12_out));
  Delay #(.delayTime(10)) delay_13 (.in(comparator_11_eq), .out(delay_13_out));
  Delay #(.delayTime(10)) delay_14 (.in(comparator_12_eq), .out(delay_14_out));
  Delay #(.delayTime(10)) delay_15 (.in(comparator_13_eq), .out(delay_15_out));
  Delay #(.delayTime(10)) delay_16 (.in(comparator_14_eq), .out(delay_16_out));
  Delay #(.delayTime(10)) delay_17 (.in(comparator_15_eq), .out(delay_17_out));
  Delay #(.delayTime(10)) delay_18 (.in(comparator_16_eq), .out(delay_18_out));
  // vgacharpos vgacharpos_1: pin names not known; wires that end beside it: vgasync_1_x, vgasync_1_y, vgacharpos_1_p3, vgacharpos_1_p4, vgacharpos_1_p5, vgacharpos_1_p6
  Register #(.Bits(7)) register_2 (.D(driver_2_out), .C(delay_3_out), .en(comparator_1_eq), .Q(register_2_q));
  Register #(.Bits(7)) register_3 (.D(driver_2_out), .C(delay_4_out), .en(comparator_2_eq), .Q(register_3_q));
  Register #(.Bits(7)) register_4 (.D(driver_2_out), .C(delay_5_out), .en(comparator_3_eq), .Q(register_4_q));
  Register #(.Bits(7)) register_5 (.D(driver_2_out), .C(delay_6_out), .en(comparator_4_eq), .Q(register_5_q));
  Register #(.Bits(7)) register_6 (.D(driver_2_out), .C(delay_7_out), .en(comparator_5_eq), .Q(register_6_q));
  Register #(.Bits(7)) register_7 (.D(driver_2_out), .C(delay_8_out), .en(comparator_6_eq), .Q(register_7_q));
  Register #(.Bits(7)) register_8 (.D(driver_2_out), .C(delay_9_out), .en(comparator_7_eq), .Q(register_8_q));
  Register #(.Bits(7)) register_9 (.D(driver_2_out), .C(delay_10_out), .en(comparator_8_eq), .Q(register_9_q));
  Register #(.Bits(7)) register_10 (.D(driver_2_out), .C(delay_11_out), .en(comparator_9_eq), .Q(register_10_q));
  Register #(.Bits(7)) register_11 (.D(driver_2_out), .C(delay_12_out), .en(comparator_10_eq), .Q(register_11_q));
  Register #(.Bits(7)) register_12 (.D(driver_2_out), .C(delay_13_out), .en(comparator_11_eq), .Q(register_12_q));
  Register #(.Bits(7)) register_13 (.D(driver_2_out), .C(delay_14_out), .en(comparator_12_eq), .Q(register_13_q));
  Register #(.Bits(7)) register_14 (.D(driver_2_out), .C(delay_15_out), .en(comparator_13_eq), .Q(register_14_q));
  Register #(.Bits(7)) register_15 (.D(driver_2_out), .C(delay_16_out), .en(comparator_14_eq), .Q(register_15_q));
  Register #(.Bits(7)) register_16 (.D(driver_2_out), .C(delay_17_out), .en(comparator_15_eq), .Q(register_16_q));
  Register #(.Bits(7)) register_17 (.D(driver_2_out), .C(delay_18_out), .en(comparator_16_eq), .Q(register_17_q));
  vgastring vgastring_1 (
    .CX_i(vgacharpos_1_p5), .CY_i(vgacharpos_1_p6), .C_i({7{1'b0}}), .FG_i({12{1'b0}}), .BG_i({12{1'b0}}),
    .FG_c(12'he07), .BG_c({12{1'b0}}), .CX_c({6{1'b0}}), .CY_c({8{1'b0}}), .C_0(register_2_q),
    .C_1(register_3_q), .C_2(register_4_q), .C_3(register_5_q), .EN(1'b1), .CX_o(vgastring_1_cx_o),
    .CY_o(vgastring_1_cy_o), .C_o(vgastring_1_c_o), .FG_o(vgastring_1_fg_o), .BG_o(vgastring_1_bg_o));
  vgastring vgastring_2 (
    .CX_i(vgastring_37_cx_o), .CY_i(vgastring_37_cy_o), .C_i(vgastring_37_c_o), .FG_i(vgastring_37_fg_o),
    .BG_i(vgastring_37_bg_o), .FG_c(12'he07), .BG_c({12{1'b0}}), .CX_c({6{1'b0}}), .CY_c(8'h1),
    .C_0(register_6_q), .C_1(register_7_q), .C_2(register_8_q), .C_3(register_9_q), .EN(1'b1),
    .CX_o(vgastring_2_cx_o), .CY_o(vgastring_2_cy_o), .C_o(vgastring_2_c_o), .FG_o(vgastring_2_fg_o),
    .BG_o(vgastring_2_bg_o));
  vgastring vgastring_3 (
    .CX_i(vgastring_38_cx_o), .CY_i(vgastring_38_cy_o), .C_i(vgastring_38_c_o), .FG_i(vgastring_38_fg_o),
    .BG_i(vgastring_38_bg_o), .FG_c(12'he07), .BG_c({12{1'b0}}), .CX_c({6{1'b0}}), .CY_c(8'h2),
    .C_0(register_10_q), .C_1(register_11_q), .C_2(register_12_q), .C_3(register_13_q), .EN(1'b1),
    .CX_o(vgastring_3_cx_o), .CY_o(vgastring_3_cy_o), .C_o(vgastring_3_c_o), .FG_o(vgastring_3_fg_o),
    .BG_o(vgastring_3_bg_o));
  vgastring vgastring_4 (
    .CX_i(vgastring_39_cx_o), .CY_i(vgastring_39_cy_o), .C_i(vgastring_39_c_o), .FG_i(vgastring_39_fg_o),
    .BG_i(vgastring_39_bg_o), .FG_c(12'he07), .BG_c({12{1'b0}}), .CX_c({6{1'b0}}), .CY_c(8'h3),
    .C_0(register_14_q), .C_1(register_15_q), .C_2(register_16_q), .C_3(register_17_q), .EN(1'b1),
    .CX_o(vgastring_4_cx_o), .CY_o(vgastring_4_cy_o), .C_o(vgastring_4_c_o), .FG_o(vgastring_4_fg_o),
    .BG_o(vgastring_4_bg_o));
  Comparator #(.Bits(8)) comparator_17 (.a(out_12), .b(8'h4), .eq(comparator_17_eq));  // open: gt, lt
  Comparator #(.Bits(8)) comparator_18 (.a(out_12), .b(8'h5), .eq(comparator_18_eq));  // open: gt, lt
  Comparator #(.Bits(8)) comparator_19 (.a(out_12), .b(8'h6), .eq(comparator_19_eq));  // open: gt, lt
  Comparator #(.Bits(8)) comparator_20 (.a(out_12), .b(8'h7), .eq(comparator_20_eq));  // open: gt, lt
  Comparator #(.Bits(8)) comparator_21 (.a(out_12), .b(8'h2c), .eq(comparator_21_eq));  // open: gt, lt
  Comparator #(.Bits(8)) comparator_22 (.a(out_12), .b(8'h2d), .eq(comparator_22_eq));  // open: gt, lt
  Comparator #(.Bits(8)) comparator_23 (.a(out_12), .b(8'h2e), .eq(comparator_23_eq));  // open: gt, lt
  Comparator #(.Bits(8)) comparator_24 (.a(out_12), .b(8'h2f), .eq(comparator_24_eq));  // open: gt, lt
  Comparator #(.Bits(8)) comparator_25 (.a(out_12), .b(8'h54), .eq(comparator_25_eq));  // open: gt, lt
  Comparator #(.Bits(8)) comparator_26 (.a(out_12), .b(8'h55), .eq(comparator_26_eq));  // open: gt, lt
  Comparator #(.Bits(8)) comparator_27 (.a(out_12), .b(8'h56), .eq(comparator_27_eq));  // open: gt, lt
  Comparator #(.Bits(8)) comparator_28 (.a(out_12), .b(8'h57), .eq(comparator_28_eq));  // open: gt, lt
  Comparator #(.Bits(8)) comparator_29 (.a(out_12), .b(8'h7c), .eq(comparator_29_eq));  // open: gt, lt
  Comparator #(.Bits(8)) comparator_30 (.a(out_12), .b(8'h7d), .eq(comparator_30_eq));  // open: gt, lt
  Comparator #(.Bits(8)) comparator_31 (.a(out_12), .b(8'h7e), .eq(comparator_31_eq));  // open: gt, lt
  Comparator #(.Bits(8)) comparator_32 (.a(out_12), .b(8'h7f), .eq(comparator_32_eq));  // open: gt, lt
  Delay #(.delayTime(10)) delay_19 (.in(comparator_17_eq), .out(delay_19_out));
  Delay #(.delayTime(10)) delay_20 (.in(comparator_18_eq), .out(delay_20_out));
  Delay #(.delayTime(10)) delay_21 (.in(comparator_19_eq), .out(delay_21_out));
  Delay #(.delayTime(10)) delay_22 (.in(comparator_20_eq), .out(delay_22_out));
  Delay #(.delayTime(10)) delay_23 (.in(comparator_21_eq), .out(delay_23_out));
  Delay #(.delayTime(10)) delay_24 (.in(comparator_22_eq), .out(delay_24_out));
  Delay #(.delayTime(10)) delay_25 (.in(comparator_23_eq), .out(delay_25_out));
  Delay #(.delayTime(10)) delay_26 (.in(comparator_24_eq), .out(delay_26_out));
  Delay #(.delayTime(10)) delay_27 (.in(comparator_25_eq), .out(delay_27_out));
  Delay #(.delayTime(10)) delay_28 (.in(comparator_26_eq), .out(delay_28_out));
  Delay #(.delayTime(10)) delay_29 (.in(comparator_27_eq), .out(delay_29_out));
  Delay #(.delayTime(10)) delay_30 (.in(comparator_28_eq), .out(delay_30_out));
  Delay #(.delayTime(10)) delay_31 (.in(comparator_29_eq), .out(delay_31_out));
  Delay #(.delayTime(10)) delay_32 (.in(comparator_30_eq), .out(delay_32_out));
  Delay #(.delayTime(10)) delay_33 (.in(comparator_31_eq), .out(delay_33_out));
  Delay #(.delayTime(10)) delay_34 (.in(comparator_32_eq), .out(delay_34_out));
  Register #(.Bits(7)) register_18 (.D(driver_2_out), .C(delay_19_out), .en(comparator_17_eq), .Q(register_18_q));
  Register #(.Bits(7)) register_19 (.D(driver_2_out), .C(delay_20_out), .en(comparator_18_eq), .Q(register_19_q));
  Register #(.Bits(7)) register_20 (.D(driver_2_out), .C(delay_21_out), .en(comparator_19_eq), .Q(register_20_q));
  Register #(.Bits(7)) register_21 (.D(driver_2_out), .C(delay_22_out), .en(comparator_20_eq), .Q(register_21_q));
  Register #(.Bits(7)) register_22 (.D(driver_2_out), .C(delay_23_out), .en(comparator_21_eq), .Q(register_22_q));
  Register #(.Bits(7)) register_23 (.D(driver_2_out), .C(delay_24_out), .en(comparator_22_eq), .Q(register_23_q));
  Register #(.Bits(7)) register_24 (.D(driver_2_out), .C(delay_25_out), .en(comparator_23_eq), .Q(register_24_q));
  Register #(.Bits(7)) register_25 (.D(driver_2_out), .C(delay_26_out), .en(comparator_24_eq), .Q(register_25_q));
  Register #(.Bits(7)) register_26 (.D(driver_2_out), .C(delay_27_out), .en(comparator_25_eq), .Q(register_26_q));
  Register #(.Bits(7)) register_27 (.D(driver_2_out), .C(delay_28_out), .en(comparator_26_eq), .Q(register_27_q));
  Register #(.Bits(7)) register_28 (.D(driver_2_out), .C(delay_29_out), .en(comparator_27_eq), .Q(register_28_q));
  Register #(.Bits(7)) register_29 (.D(driver_2_out), .C(delay_30_out), .en(comparator_28_eq), .Q(register_29_q));
  Register #(.Bits(7)) register_30 (.D(driver_2_out), .C(delay_31_out), .en(comparator_29_eq), .Q(register_30_q));
  Register #(.Bits(7)) register_31 (.D(driver_2_out), .C(delay_32_out), .en(comparator_30_eq), .Q(register_31_q));
  Register #(.Bits(7)) register_32 (.D(driver_2_out), .C(delay_33_out), .en(comparator_31_eq), .Q(register_32_q));
  Register #(.Bits(7)) register_33 (.D(driver_2_out), .C(delay_34_out), .en(comparator_32_eq), .Q(register_33_q));
  vgastring vgastring_5 (
    .CX_i(vgastring_1_cx_o), .CY_i(vgastring_1_cy_o), .C_i(vgastring_1_c_o), .FG_i(vgastring_1_fg_o),
    .BG_i(vgastring_1_bg_o), .FG_c(12'he09), .BG_c({12{1'b0}}), .CX_c(6'b000001), .CY_c({8{1'b0}}),
    .C_0(register_18_q), .C_1(register_19_q), .C_2(register_20_q), .C_3(register_21_q), .EN(1'b1),
    .CX_o(vgastring_5_cx_o), .CY_o(vgastring_5_cy_o), .C_o(vgastring_5_c_o), .FG_o(vgastring_5_fg_o),
    .BG_o(vgastring_5_bg_o));
  vgastring vgastring_6 (
    .CX_i(vgastring_2_cx_o), .CY_i(vgastring_2_cy_o), .C_i(vgastring_2_c_o), .FG_i(vgastring_2_fg_o),
    .BG_i(vgastring_2_bg_o), .FG_c(12'he09), .BG_c({12{1'b0}}), .CX_c(6'b000001), .CY_c(8'h1),
    .C_0(register_22_q), .C_1(register_23_q), .C_2(register_24_q), .C_3(register_25_q), .EN(1'b1),
    .CX_o(vgastring_6_cx_o), .CY_o(vgastring_6_cy_o), .C_o(vgastring_6_c_o), .FG_o(vgastring_6_fg_o),
    .BG_o(vgastring_6_bg_o));
  vgastring vgastring_7 (
    .CX_i(vgastring_3_cx_o), .CY_i(vgastring_3_cy_o), .C_i(vgastring_3_c_o), .FG_i(vgastring_3_fg_o),
    .BG_i(vgastring_3_bg_o), .FG_c(12'he09), .BG_c({12{1'b0}}), .CX_c(6'b000001), .CY_c(8'h2),
    .C_0(register_26_q), .C_1(register_27_q), .C_2(register_28_q), .C_3(register_29_q), .EN(1'b1),
    .CX_o(vgastring_7_cx_o), .CY_o(vgastring_7_cy_o), .C_o(vgastring_7_c_o), .FG_o(vgastring_7_fg_o),
    .BG_o(vgastring_7_bg_o));
  vgastring vgastring_8 (
    .CX_i(vgastring_4_cx_o), .CY_i(vgastring_4_cy_o), .C_i(vgastring_4_c_o), .FG_i(vgastring_4_fg_o),
    .BG_i(vgastring_4_bg_o), .FG_c(12'he09), .BG_c({12{1'b0}}), .CX_c(6'b000001), .CY_c(8'h3),
    .C_0(register_30_q), .C_1(register_31_q), .C_2(register_32_q), .C_3(register_33_q), .EN(1'b1),
    .CX_o(vgastring_8_cx_o), .CY_o(vgastring_8_cy_o), .C_o(vgastring_8_c_o), .FG_o(vgastring_8_fg_o),
    .BG_o(vgastring_8_bg_o));
  Comparator #(.Bits(8)) comparator_33 (.a(out_12), .b(8'h8), .eq(comparator_33_eq));  // open: gt, lt
  Comparator #(.Bits(8)) comparator_34 (.a(out_12), .b(8'h9), .eq(comparator_34_eq));  // open: gt, lt
  Comparator #(.Bits(8)) comparator_35 (.a(out_12), .b(8'ha), .eq(comparator_35_eq));  // open: gt, lt
  Comparator #(.Bits(8)) comparator_36 (.a(out_12), .b(8'hb), .eq(comparator_36_eq));  // open: gt, lt
  Comparator #(.Bits(8)) comparator_37 (.a(out_12), .b(8'h30), .eq(comparator_37_eq));  // open: gt, lt
  Comparator #(.Bits(8)) comparator_38 (.a(out_12), .b(8'h31), .eq(comparator_38_eq));  // open: gt, lt
  Comparator #(.Bits(8)) comparator_39 (.a(out_12), .b(8'h32), .eq(comparator_39_eq));  // open: gt, lt
  Comparator #(.Bits(8)) comparator_40 (.a(out_12), .b(8'h33), .eq(comparator_40_eq));  // open: gt, lt
  Comparator #(.Bits(8)) comparator_41 (.a(out_12), .b(8'h58), .eq(comparator_41_eq));  // open: gt, lt
  Comparator #(.Bits(8)) comparator_42 (.a(out_12), .b(8'h59), .eq(comparator_42_eq));  // open: gt, lt
  Comparator #(.Bits(8)) comparator_43 (.a(out_12), .b(8'h5a), .eq(comparator_43_eq));  // open: gt, lt
  Comparator #(.Bits(8)) comparator_44 (.a(out_12), .b(8'h5b), .eq(comparator_44_eq));  // open: gt, lt
  Comparator #(.Bits(8)) comparator_45 (.a(out_12), .b(8'h80), .eq(comparator_45_eq));  // open: gt, lt
  Comparator #(.Bits(8)) comparator_46 (.a(out_12), .b(8'h81), .eq(comparator_46_eq));  // open: gt, lt
  Comparator #(.Bits(8)) comparator_47 (.a(out_12), .b(8'h82), .eq(comparator_47_eq));  // open: gt, lt
  Comparator #(.Bits(8)) comparator_48 (.a(out_12), .b(8'h83), .eq(comparator_48_eq));  // open: gt, lt
  Delay #(.delayTime(10)) delay_35 (.in(comparator_33_eq), .out(delay_35_out));
  Delay #(.delayTime(10)) delay_36 (.in(comparator_34_eq), .out(delay_36_out));
  Delay #(.delayTime(10)) delay_37 (.in(comparator_35_eq), .out(delay_37_out));
  Delay #(.delayTime(10)) delay_38 (.in(comparator_36_eq), .out(delay_38_out));
  Delay #(.delayTime(10)) delay_39 (.in(comparator_37_eq), .out(delay_39_out));
  Delay #(.delayTime(10)) delay_40 (.in(comparator_38_eq), .out(delay_40_out));
  Delay #(.delayTime(10)) delay_41 (.in(comparator_39_eq), .out(delay_41_out));
  Delay #(.delayTime(10)) delay_42 (.in(comparator_40_eq), .out(delay_42_out));
  Delay #(.delayTime(10)) delay_43 (.in(comparator_41_eq), .out(delay_43_out));
  Delay #(.delayTime(10)) delay_44 (.in(comparator_42_eq), .out(delay_44_out));
  Delay #(.delayTime(10)) delay_45 (.in(comparator_43_eq), .out(delay_45_out));
  Delay #(.delayTime(10)) delay_46 (.in(comparator_44_eq), .out(delay_46_out));
  Delay #(.delayTime(10)) delay_47 (.in(comparator_45_eq), .out(delay_47_out));
  Delay #(.delayTime(10)) delay_48 (.in(comparator_46_eq), .out(delay_48_out));
  Delay #(.delayTime(10)) delay_49 (.in(comparator_47_eq), .out(delay_49_out));
  Delay #(.delayTime(10)) delay_50 (.in(comparator_48_eq), .out(delay_50_out));
  Register #(.Bits(7)) register_34 (.D(driver_2_out), .C(delay_35_out), .en(comparator_33_eq), .Q(register_34_q));
  Register #(.Bits(7)) register_35 (.D(driver_2_out), .C(delay_36_out), .en(comparator_34_eq), .Q(register_35_q));
  Register #(.Bits(7)) register_36 (.D(driver_2_out), .C(delay_37_out), .en(comparator_35_eq), .Q(register_36_q));
  Register #(.Bits(7)) register_37 (.D(driver_2_out), .C(delay_38_out), .en(comparator_36_eq), .Q(register_37_q));
  Register #(.Bits(7)) register_38 (.D(driver_2_out), .C(delay_39_out), .en(comparator_37_eq), .Q(register_38_q));
  Register #(.Bits(7)) register_39 (.D(driver_2_out), .C(delay_40_out), .en(comparator_38_eq), .Q(register_39_q));
  Register #(.Bits(7)) register_40 (.D(driver_2_out), .C(delay_41_out), .en(comparator_39_eq), .Q(register_40_q));
  Register #(.Bits(7)) register_41 (.D(driver_2_out), .C(delay_42_out), .en(comparator_40_eq), .Q(register_41_q));
  Register #(.Bits(7)) register_42 (.D(driver_2_out), .C(delay_43_out), .en(comparator_41_eq), .Q(register_42_q));
  Register #(.Bits(7)) register_43 (.D(driver_2_out), .C(delay_44_out), .en(comparator_42_eq), .Q(register_43_q));
  Register #(.Bits(7)) register_44 (.D(driver_2_out), .C(delay_45_out), .en(comparator_43_eq), .Q(register_44_q));
  Register #(.Bits(7)) register_45 (.D(driver_2_out), .C(delay_46_out), .en(comparator_44_eq), .Q(register_45_q));
  Register #(.Bits(7)) register_46 (.D(driver_2_out), .C(delay_47_out), .en(comparator_45_eq), .Q(register_46_q));
  Register #(.Bits(7)) register_47 (.D(driver_2_out), .C(delay_48_out), .en(comparator_46_eq), .Q(register_47_q));
  Register #(.Bits(7)) register_48 (.D(driver_2_out), .C(delay_49_out), .en(comparator_47_eq), .Q(register_48_q));
  Register #(.Bits(7)) register_49 (.D(driver_2_out), .C(delay_50_out), .en(comparator_48_eq), .Q(register_49_q));
  vgastring vgastring_9 (
    .CX_i(vgastring_5_cx_o), .CY_i(vgastring_5_cy_o), .C_i(vgastring_5_c_o), .FG_i(vgastring_5_fg_o),
    .BG_i(vgastring_5_bg_o), .FG_c(12'he09), .BG_c({12{1'b0}}), .CX_c(6'b000010), .CY_c({8{1'b0}}),
    .C_0(register_34_q), .C_1(register_35_q), .C_2(register_36_q), .C_3(register_37_q), .EN(1'b1),
    .CX_o(vgastring_9_cx_o), .CY_o(vgastring_9_cy_o), .C_o(vgastring_9_c_o), .FG_o(vgastring_9_fg_o),
    .BG_o(vgastring_9_bg_o));
  vgastring vgastring_10 (
    .CX_i(vgastring_6_cx_o), .CY_i(vgastring_6_cy_o), .C_i(vgastring_6_c_o), .FG_i(vgastring_6_fg_o),
    .BG_i(vgastring_6_bg_o), .FG_c(12'he09), .BG_c({12{1'b0}}), .CX_c(6'b000010), .CY_c(8'h1),
    .C_0(register_38_q), .C_1(register_39_q), .C_2(register_40_q), .C_3(register_41_q), .EN(1'b1),
    .CX_o(vgastring_10_cx_o), .CY_o(vgastring_10_cy_o), .C_o(vgastring_10_c_o), .FG_o(vgastring_10_fg_o),
    .BG_o(vgastring_10_bg_o));
  vgastring vgastring_11 (
    .CX_i(vgastring_7_cx_o), .CY_i(vgastring_7_cy_o), .C_i(vgastring_7_c_o), .FG_i(vgastring_7_fg_o),
    .BG_i(vgastring_7_bg_o), .FG_c(12'he09), .BG_c({12{1'b0}}), .CX_c(6'b000010), .CY_c(8'h2),
    .C_0(register_42_q), .C_1(register_43_q), .C_2(register_44_q), .C_3(register_45_q), .EN(1'b1),
    .CX_o(vgastring_11_cx_o), .CY_o(vgastring_11_cy_o), .C_o(vgastring_11_c_o), .FG_o(vgastring_11_fg_o),
    .BG_o(vgastring_11_bg_o));
  vgastring vgastring_12 (
    .CX_i(vgastring_8_cx_o), .CY_i(vgastring_8_cy_o), .C_i(vgastring_8_c_o), .FG_i(vgastring_8_fg_o),
    .BG_i(vgastring_8_bg_o), .FG_c(12'he09), .BG_c({12{1'b0}}), .CX_c(6'b000010), .CY_c(8'h3),
    .C_0(register_46_q), .C_1(register_47_q), .C_2(register_48_q), .C_3(register_49_q), .EN(1'b1),
    .CX_o(vgastring_12_cx_o), .CY_o(vgastring_12_cy_o), .C_o(vgastring_12_c_o), .FG_o(vgastring_12_fg_o),
    .BG_o(vgastring_12_bg_o));
  Comparator #(.Bits(8)) comparator_49 (.a(out_12), .b(8'hc), .eq(comparator_49_eq));  // open: gt, lt
  Comparator #(.Bits(8)) comparator_50 (.a(out_12), .b(8'hd), .eq(comparator_50_eq));  // open: gt, lt
  Comparator #(.Bits(8)) comparator_51 (.a(out_12), .b(8'he), .eq(comparator_51_eq));  // open: gt, lt
  Comparator #(.Bits(8)) comparator_52 (.a(out_12), .b(8'hf), .eq(comparator_52_eq));  // open: gt, lt
  Comparator #(.Bits(8)) comparator_53 (.a(out_12), .b(8'h34), .eq(comparator_53_eq));  // open: gt, lt
  Comparator #(.Bits(8)) comparator_54 (.a(out_12), .b(8'h35), .eq(comparator_54_eq));  // open: gt, lt
  Comparator #(.Bits(8)) comparator_55 (.a(out_12), .b(8'h36), .eq(comparator_55_eq));  // open: gt, lt
  Comparator #(.Bits(8)) comparator_56 (.a(out_12), .b(8'h37), .eq(comparator_56_eq));  // open: gt, lt
  Comparator #(.Bits(8)) comparator_57 (.a(out_12), .b(8'h5c), .eq(comparator_57_eq));  // open: gt, lt
  Comparator #(.Bits(8)) comparator_58 (.a(out_12), .b(8'h5d), .eq(comparator_58_eq));  // open: gt, lt
  Comparator #(.Bits(8)) comparator_59 (.a(out_12), .b(8'h5e), .eq(comparator_59_eq));  // open: gt, lt
  Comparator #(.Bits(8)) comparator_60 (.a(out_12), .b(8'h5f), .eq(comparator_60_eq));  // open: gt, lt
  Comparator #(.Bits(8)) comparator_61 (.a(out_12), .b(8'h84), .eq(comparator_61_eq));  // open: gt, lt
  Comparator #(.Bits(8)) comparator_62 (.a(out_12), .b(8'h85), .eq(comparator_62_eq));  // open: gt, lt
  Comparator #(.Bits(8)) comparator_63 (.a(out_12), .b(8'h86), .eq(comparator_63_eq));  // open: gt, lt
  Comparator #(.Bits(8)) comparator_64 (.a(out_12), .b(8'h87), .eq(comparator_64_eq));  // open: gt, lt
  Delay #(.delayTime(10)) delay_51 (.in(comparator_49_eq), .out(delay_51_out));
  Delay #(.delayTime(10)) delay_52 (.in(comparator_50_eq), .out(delay_52_out));
  Delay #(.delayTime(10)) delay_53 (.in(comparator_51_eq), .out(delay_53_out));
  Delay #(.delayTime(10)) delay_54 (.in(comparator_52_eq), .out(delay_54_out));
  Delay #(.delayTime(10)) delay_55 (.in(comparator_53_eq), .out(delay_55_out));
  Delay #(.delayTime(10)) delay_56 (.in(comparator_54_eq), .out(delay_56_out));
  Delay #(.delayTime(10)) delay_57 (.in(comparator_55_eq), .out(delay_57_out));
  Delay #(.delayTime(10)) delay_58 (.in(comparator_56_eq), .out(delay_58_out));
  Delay #(.delayTime(10)) delay_59 (.in(comparator_57_eq), .out(delay_59_out));
  Delay #(.delayTime(10)) delay_60 (.in(comparator_58_eq), .out(delay_60_out));
  Delay #(.delayTime(10)) delay_61 (.in(comparator_59_eq), .out(delay_61_out));
  Delay #(.delayTime(10)) delay_62 (.in(comparator_60_eq), .out(delay_62_out));
  Delay #(.delayTime(10)) delay_63 (.in(comparator_61_eq), .out(delay_63_out));
  Delay #(.delayTime(10)) delay_64 (.in(comparator_62_eq), .out(delay_64_out));
  Delay #(.delayTime(10)) delay_65 (.in(comparator_63_eq), .out(delay_65_out));
  Delay #(.delayTime(10)) delay_66 (.in(comparator_64_eq), .out(delay_66_out));
  Register #(.Bits(7)) register_50 (.D(driver_2_out), .C(delay_51_out), .en(comparator_49_eq), .Q(register_50_q));
  Register #(.Bits(7)) register_51 (.D(driver_2_out), .C(delay_52_out), .en(comparator_50_eq), .Q(register_51_q));
  Register #(.Bits(7)) register_52 (.D(driver_2_out), .C(delay_53_out), .en(comparator_51_eq), .Q(register_52_q));
  Register #(.Bits(7)) register_53 (.D(driver_2_out), .C(delay_54_out), .en(comparator_52_eq), .Q(register_53_q));
  Register #(.Bits(7)) register_54 (.D(driver_2_out), .C(delay_55_out), .en(comparator_53_eq), .Q(register_54_q));
  Register #(.Bits(7)) register_55 (.D(driver_2_out), .C(delay_56_out), .en(comparator_54_eq), .Q(register_55_q));
  Register #(.Bits(7)) register_56 (.D(driver_2_out), .C(delay_57_out), .en(comparator_55_eq), .Q(register_56_q));
  Register #(.Bits(7)) register_57 (.D(driver_2_out), .C(delay_58_out), .en(comparator_56_eq), .Q(register_57_q));
  Register #(.Bits(7)) register_58 (.D(driver_2_out), .C(delay_59_out), .en(comparator_57_eq), .Q(register_58_q));
  Register #(.Bits(7)) register_59 (.D(driver_2_out), .C(delay_60_out), .en(comparator_58_eq), .Q(register_59_q));
  Register #(.Bits(7)) register_60 (.D(driver_2_out), .C(delay_61_out), .en(comparator_59_eq), .Q(register_60_q));
  Register #(.Bits(7)) register_61 (.D(driver_2_out), .C(delay_62_out), .en(comparator_60_eq), .Q(register_61_q));
  Register #(.Bits(7)) register_62 (.D(driver_2_out), .C(delay_63_out), .en(comparator_61_eq), .Q(register_62_q));
  Register #(.Bits(7)) register_63 (.D(driver_2_out), .C(delay_64_out), .en(comparator_62_eq), .Q(register_63_q));
  Register #(.Bits(7)) register_64 (.D(driver_2_out), .C(delay_65_out), .en(comparator_63_eq), .Q(register_64_q));
  Register #(.Bits(7)) register_65 (.D(driver_2_out), .C(delay_66_out), .en(comparator_64_eq), .Q(register_65_q));
  vgastring vgastring_13 (
    .CX_i(vgastring_9_cx_o), .CY_i(vgastring_9_cy_o), .C_i(vgastring_9_c_o), .FG_i(vgastring_9_fg_o),
    .BG_i(vgastring_9_bg_o), .FG_c(12'he09), .BG_c({12{1'b0}}), .CX_c(6'b000011), .CY_c({8{1'b0}}),
    .C_0(register_50_q), .C_1(register_51_q), .C_2(register_52_q), .C_3(register_53_q), .EN(1'b1),
    .CX_o(vgastring_13_cx_o), .CY_o(vgastring_13_cy_o), .C_o(vgastring_13_c_o), .FG_o(vgastring_13_fg_o),
    .BG_o(vgastring_13_bg_o));
  vgastring vgastring_14 (
    .CX_i(vgastring_10_cx_o), .CY_i(vgastring_10_cy_o), .C_i(vgastring_10_c_o), .FG_i(vgastring_10_fg_o),
    .BG_i(vgastring_10_bg_o), .FG_c(12'he09), .BG_c({12{1'b0}}), .CX_c(6'b000011), .CY_c(8'h1),
    .C_0(register_54_q), .C_1(register_55_q), .C_2(register_56_q), .C_3(register_57_q), .EN(1'b1),
    .CX_o(vgastring_14_cx_o), .CY_o(vgastring_14_cy_o), .C_o(vgastring_14_c_o), .FG_o(vgastring_14_fg_o),
    .BG_o(vgastring_14_bg_o));
  vgastring vgastring_15 (
    .CX_i(vgastring_11_cx_o), .CY_i(vgastring_11_cy_o), .C_i(vgastring_11_c_o), .FG_i(vgastring_11_fg_o),
    .BG_i(vgastring_11_bg_o), .FG_c(12'he09), .BG_c({12{1'b0}}), .CX_c(6'b000011), .CY_c(8'h2),
    .C_0(register_58_q), .C_1(register_59_q), .C_2(register_60_q), .C_3(register_61_q), .EN(1'b1),
    .CX_o(vgastring_15_cx_o), .CY_o(vgastring_15_cy_o), .C_o(vgastring_15_c_o), .FG_o(vgastring_15_fg_o),
    .BG_o(vgastring_15_bg_o));
  vgastring vgastring_16 (
    .CX_i(vgastring_12_cx_o), .CY_i(vgastring_12_cy_o), .C_i(vgastring_12_c_o), .FG_i(vgastring_12_fg_o),
    .BG_i(vgastring_12_bg_o), .FG_c(12'he09), .BG_c({12{1'b0}}), .CX_c(6'b000011), .CY_c(8'h3),
    .C_0(register_62_q), .C_1(register_63_q), .C_2(register_64_q), .C_3(register_65_q), .EN(1'b1),
    .CX_o(vgastring_16_cx_o), .CY_o(vgastring_16_cy_o), .C_o(vgastring_16_c_o), .FG_o(vgastring_16_fg_o),
    .BG_o(vgastring_16_bg_o));
  Comparator #(.Bits(8)) comparator_65 (.a(out_12), .b(8'h10), .eq(comparator_65_eq));  // open: gt, lt
  Comparator #(.Bits(8)) comparator_66 (.a(out_12), .b(8'h11), .eq(comparator_66_eq));  // open: gt, lt
  Comparator #(.Bits(8)) comparator_67 (.a(out_12), .b(8'h12), .eq(comparator_67_eq));  // open: gt, lt
  Comparator #(.Bits(8)) comparator_68 (.a(out_12), .b(8'h13), .eq(comparator_68_eq));  // open: gt, lt
  Comparator #(.Bits(8)) comparator_69 (.a(out_12), .b(8'h38), .eq(comparator_69_eq));  // open: gt, lt
  Comparator #(.Bits(8)) comparator_70 (.a(out_12), .b(8'h39), .eq(comparator_70_eq));  // open: gt, lt
  Comparator #(.Bits(8)) comparator_71 (.a(out_12), .b(8'h3a), .eq(comparator_71_eq));  // open: gt, lt
  Comparator #(.Bits(8)) comparator_72 (.a(out_12), .b(8'h3b), .eq(comparator_72_eq));  // open: gt, lt
  Comparator #(.Bits(8)) comparator_73 (.a(out_12), .b(8'h60), .eq(comparator_73_eq));  // open: gt, lt
  Comparator #(.Bits(8)) comparator_74 (.a(out_12), .b(8'h61), .eq(comparator_74_eq));  // open: gt, lt
  Comparator #(.Bits(8)) comparator_75 (.a(out_12), .b(8'h62), .eq(comparator_75_eq));  // open: gt, lt
  Comparator #(.Bits(8)) comparator_76 (.a(out_12), .b(8'h63), .eq(comparator_76_eq));  // open: gt, lt
  Comparator #(.Bits(8)) comparator_77 (.a(out_12), .b(8'h88), .eq(comparator_77_eq));  // open: gt, lt
  Comparator #(.Bits(8)) comparator_78 (.a(out_12), .b(8'h89), .eq(comparator_78_eq));  // open: gt, lt
  Comparator #(.Bits(8)) comparator_79 (.a(out_12), .b(8'h8a), .eq(comparator_79_eq));  // open: gt, lt
  Comparator #(.Bits(8)) comparator_80 (.a(out_12), .b(8'h8b), .eq(comparator_80_eq));  // open: gt, lt
  Delay #(.delayTime(10)) delay_67 (.in(comparator_65_eq), .out(delay_67_out));
  Delay #(.delayTime(10)) delay_68 (.in(comparator_66_eq), .out(delay_68_out));
  Delay #(.delayTime(10)) delay_69 (.in(comparator_67_eq), .out(delay_69_out));
  Delay #(.delayTime(10)) delay_70 (.in(comparator_68_eq), .out(delay_70_out));
  Delay #(.delayTime(10)) delay_71 (.in(comparator_69_eq), .out(delay_71_out));
  Delay #(.delayTime(10)) delay_72 (.in(comparator_70_eq), .out(delay_72_out));
  Delay #(.delayTime(10)) delay_73 (.in(comparator_71_eq), .out(delay_73_out));
  Delay #(.delayTime(10)) delay_74 (.in(comparator_72_eq), .out(delay_74_out));
  Delay #(.delayTime(10)) delay_75 (.in(comparator_73_eq), .out(delay_75_out));
  Delay #(.delayTime(10)) delay_76 (.in(comparator_74_eq), .out(delay_76_out));
  Delay #(.delayTime(10)) delay_77 (.in(comparator_75_eq), .out(delay_77_out));
  Delay #(.delayTime(10)) delay_78 (.in(comparator_76_eq), .out(delay_78_out));
  Delay #(.delayTime(10)) delay_79 (.in(comparator_77_eq), .out(delay_79_out));
  Delay #(.delayTime(10)) delay_80 (.in(comparator_78_eq), .out(delay_80_out));
  Delay #(.delayTime(10)) delay_81 (.in(comparator_79_eq), .out(delay_81_out));
  Delay #(.delayTime(10)) delay_82 (.in(comparator_80_eq), .out(delay_82_out));
  Register #(.Bits(7)) register_66 (.D(driver_2_out), .C(delay_67_out), .en(comparator_65_eq), .Q(register_66_q));
  Register #(.Bits(7)) register_67 (.D(driver_2_out), .C(delay_68_out), .en(comparator_66_eq), .Q(register_67_q));
  Register #(.Bits(7)) register_68 (.D(driver_2_out), .C(delay_69_out), .en(comparator_67_eq), .Q(register_68_q));
  Register #(.Bits(7)) register_69 (.D(driver_2_out), .C(delay_70_out), .en(comparator_68_eq), .Q(register_69_q));
  Register #(.Bits(7)) register_70 (.D(driver_2_out), .C(delay_71_out), .en(comparator_69_eq), .Q(register_70_q));
  Register #(.Bits(7)) register_71 (.D(driver_2_out), .C(delay_72_out), .en(comparator_70_eq), .Q(register_71_q));
  Register #(.Bits(7)) register_72 (.D(driver_2_out), .C(delay_73_out), .en(comparator_71_eq), .Q(register_72_q));
  Register #(.Bits(7)) register_73 (.D(driver_2_out), .C(delay_74_out), .en(comparator_72_eq), .Q(register_73_q));
  Register #(.Bits(7)) register_74 (.D(driver_2_out), .C(delay_75_out), .en(comparator_73_eq), .Q(register_74_q));
  Register #(.Bits(7)) register_75 (.D(driver_2_out), .C(delay_76_out), .en(comparator_74_eq), .Q(register_75_q));
  Register #(.Bits(7)) register_76 (.D(driver_2_out), .C(delay_77_out), .en(comparator_75_eq), .Q(register_76_q));
  Register #(.Bits(7)) register_77 (.D(driver_2_out), .C(delay_78_out), .en(comparator_76_eq), .Q(register_77_q));
  Register #(.Bits(7)) register_78 (.D(driver_2_out), .C(delay_79_out), .en(comparator_77_eq), .Q(register_78_q));
  Register #(.Bits(7)) register_79 (.D(driver_2_out), .C(delay_80_out), .en(comparator_78_eq), .Q(register_79_q));
  Register #(.Bits(7)) register_80 (.D(driver_2_out), .C(delay_81_out), .en(comparator_79_eq), .Q(register_80_q));
  Register #(.Bits(7)) register_81 (.D(driver_2_out), .C(delay_82_out), .en(comparator_80_eq), .Q(register_81_q));
  vgastring vgastring_17 (
    .CX_i(vgastring_13_cx_o), .CY_i(vgastring_13_cy_o), .C_i(vgastring_13_c_o), .FG_i(vgastring_13_fg_o),
    .BG_i(vgastring_13_bg_o), .FG_c(12'he07), .BG_c({12{1'b0}}), .CX_c(6'b000100), .CY_c({8{1'b0}}),
    .C_0(register_66_q), .C_1(register_67_q), .C_2(register_68_q), .C_3(register_69_q), .EN(1'b1),
    .CX_o(vgastring_17_cx_o), .CY_o(vgastring_17_cy_o), .C_o(vgastring_17_c_o), .FG_o(vgastring_17_fg_o),
    .BG_o(vgastring_17_bg_o));
  vgastring vgastring_18 (
    .CX_i(vgastring_14_cx_o), .CY_i(vgastring_14_cy_o), .C_i(vgastring_14_c_o), .FG_i(vgastring_14_fg_o),
    .BG_i(vgastring_14_bg_o), .FG_c(12'he07), .BG_c({12{1'b0}}), .CX_c(6'b000100), .CY_c(8'h1),
    .C_0(register_70_q), .C_1(register_71_q), .C_2(register_72_q), .C_3(register_73_q), .EN(1'b1),
    .CX_o(vgastring_18_cx_o), .CY_o(vgastring_18_cy_o), .C_o(vgastring_18_c_o), .FG_o(vgastring_18_fg_o),
    .BG_o(vgastring_18_bg_o));
  vgastring vgastring_19 (
    .CX_i(vgastring_15_cx_o), .CY_i(vgastring_15_cy_o), .C_i(vgastring_15_c_o), .FG_i(vgastring_15_fg_o),
    .BG_i(vgastring_15_bg_o), .FG_c(12'he07), .BG_c({12{1'b0}}), .CX_c(6'b000100), .CY_c(8'h2),
    .C_0(register_74_q), .C_1(register_75_q), .C_2(register_76_q), .C_3(register_77_q), .EN(1'b1),
    .CX_o(vgastring_19_cx_o), .CY_o(vgastring_19_cy_o), .C_o(vgastring_19_c_o), .FG_o(vgastring_19_fg_o),
    .BG_o(vgastring_19_bg_o));
  vgastring vgastring_20 (
    .CX_i(vgastring_16_cx_o), .CY_i(vgastring_16_cy_o), .C_i(vgastring_16_c_o), .FG_i(vgastring_16_fg_o),
    .BG_i(vgastring_16_bg_o), .FG_c(12'he07), .BG_c({12{1'b0}}), .CX_c(6'b000100), .CY_c(8'h3),
    .C_0(register_78_q), .C_1(register_79_q), .C_2(register_80_q), .C_3(register_81_q), .EN(1'b1),
    .CX_o(vgastring_20_cx_o), .CY_o(vgastring_20_cy_o), .C_o(vgastring_20_c_o), .FG_o(vgastring_20_fg_o),
    .BG_o(vgastring_20_bg_o));
  Comparator #(.Bits(8)) comparator_81 (.a(out_12), .b(8'h14), .eq(comparator_81_eq));  // open: gt, lt
  Comparator #(.Bits(8)) comparator_82 (.a(out_12), .b(8'h15), .eq(comparator_82_eq));  // open: gt, lt
  Comparator #(.Bits(8)) comparator_83 (.a(out_12), .b(8'h16), .eq(comparator_83_eq));  // open: gt, lt
  Comparator #(.Bits(8)) comparator_84 (.a(out_12), .b(8'h17), .eq(comparator_84_eq));  // open: gt, lt
  Comparator #(.Bits(8)) comparator_85 (.a(out_12), .b(8'h3c), .eq(comparator_85_eq));  // open: gt, lt
  Comparator #(.Bits(8)) comparator_86 (.a(out_12), .b(8'h3d), .eq(comparator_86_eq));  // open: gt, lt
  Comparator #(.Bits(8)) comparator_87 (.a(out_12), .b(8'h3e), .eq(comparator_87_eq));  // open: gt, lt
  Comparator #(.Bits(8)) comparator_88 (.a(out_12), .b(8'h3f), .eq(comparator_88_eq));  // open: gt, lt
  Comparator #(.Bits(8)) comparator_89 (.a(out_12), .b(8'h64), .eq(comparator_89_eq));  // open: gt, lt
  Comparator #(.Bits(8)) comparator_90 (.a(out_12), .b(8'h65), .eq(comparator_90_eq));  // open: gt, lt
  Comparator #(.Bits(8)) comparator_91 (.a(out_12), .b(8'h66), .eq(comparator_91_eq));  // open: gt, lt
  Comparator #(.Bits(8)) comparator_92 (.a(out_12), .b(8'h67), .eq(comparator_92_eq));  // open: gt, lt
  Comparator #(.Bits(8)) comparator_93 (.a(out_12), .b(8'h8c), .eq(comparator_93_eq));  // open: gt, lt
  Comparator #(.Bits(8)) comparator_94 (.a(out_12), .b(8'h8d), .eq(comparator_94_eq));  // open: gt, lt
  Comparator #(.Bits(8)) comparator_95 (.a(out_12), .b(8'h8e), .eq(comparator_95_eq));  // open: gt, lt
  Comparator #(.Bits(8)) comparator_96 (.a(out_12), .b(8'h8f), .eq(comparator_96_eq));  // open: gt, lt
  Delay #(.delayTime(10)) delay_83 (.in(comparator_81_eq), .out(delay_83_out));
  Delay #(.delayTime(10)) delay_84 (.in(comparator_82_eq), .out(delay_84_out));
  Delay #(.delayTime(10)) delay_85 (.in(comparator_83_eq), .out(delay_85_out));
  Delay #(.delayTime(10)) delay_86 (.in(comparator_84_eq), .out(delay_86_out));
  Delay #(.delayTime(10)) delay_87 (.in(comparator_85_eq), .out(delay_87_out));
  Delay #(.delayTime(10)) delay_88 (.in(comparator_86_eq), .out(delay_88_out));
  Delay #(.delayTime(10)) delay_89 (.in(comparator_87_eq), .out(delay_89_out));
  Delay #(.delayTime(10)) delay_90 (.in(comparator_88_eq), .out(delay_90_out));
  Delay #(.delayTime(10)) delay_91 (.in(comparator_89_eq), .out(delay_91_out));
  Delay #(.delayTime(10)) delay_92 (.in(comparator_90_eq), .out(delay_92_out));
  Delay #(.delayTime(10)) delay_93 (.in(comparator_91_eq), .out(delay_93_out));
  Delay #(.delayTime(10)) delay_94 (.in(comparator_92_eq), .out(delay_94_out));
  Delay #(.delayTime(10)) delay_95 (.in(comparator_93_eq), .out(delay_95_out));
  Delay #(.delayTime(10)) delay_96 (.in(comparator_94_eq), .out(delay_96_out));
  Delay #(.delayTime(10)) delay_97 (.in(comparator_95_eq), .out(delay_97_out));
  Delay #(.delayTime(10)) delay_98 (.in(comparator_96_eq), .out(delay_98_out));
  Register #(.Bits(7)) register_82 (.D(driver_2_out), .C(delay_83_out), .en(comparator_81_eq), .Q(register_82_q));
  Register #(.Bits(7)) register_83 (.D(driver_2_out), .C(delay_84_out), .en(comparator_82_eq), .Q(register_83_q));
  Register #(.Bits(7)) register_84 (.D(driver_2_out), .C(delay_85_out), .en(comparator_83_eq), .Q(register_84_q));
  Register #(.Bits(7)) register_85 (.D(driver_2_out), .C(delay_86_out), .en(comparator_84_eq), .Q(register_85_q));
  Register #(.Bits(7)) register_86 (.D(driver_2_out), .C(delay_87_out), .en(comparator_85_eq), .Q(register_86_q));
  Register #(.Bits(7)) register_87 (.D(driver_2_out), .C(delay_88_out), .en(comparator_86_eq), .Q(register_87_q));
  Register #(.Bits(7)) register_88 (.D(driver_2_out), .C(delay_89_out), .en(comparator_87_eq), .Q(register_88_q));
  Register #(.Bits(7)) register_89 (.D(driver_2_out), .C(delay_90_out), .en(comparator_88_eq), .Q(register_89_q));
  Register #(.Bits(7)) register_90 (.D(driver_2_out), .C(delay_91_out), .en(comparator_89_eq), .Q(register_90_q));
  Register #(.Bits(7)) register_91 (.D(driver_2_out), .C(delay_92_out), .en(comparator_90_eq), .Q(register_91_q));
  Register #(.Bits(7)) register_92 (.D(driver_2_out), .C(delay_93_out), .en(comparator_91_eq), .Q(register_92_q));
  Register #(.Bits(7)) register_93 (.D(driver_2_out), .C(delay_94_out), .en(comparator_92_eq), .Q(register_93_q));
  Register #(.Bits(7)) register_94 (.D(driver_2_out), .C(delay_95_out), .en(comparator_93_eq), .Q(register_94_q));
  Register #(.Bits(7)) register_95 (.D(driver_2_out), .C(delay_96_out), .en(comparator_94_eq), .Q(register_95_q));
  Register #(.Bits(7)) register_96 (.D(driver_2_out), .C(delay_97_out), .en(comparator_95_eq), .Q(register_96_q));
  Register #(.Bits(7)) register_97 (.D(driver_2_out), .C(delay_98_out), .en(comparator_96_eq), .Q(register_97_q));
  vgastring vgastring_21 (
    .CX_i(vgastring_17_cx_o), .CY_i(vgastring_17_cy_o), .C_i(vgastring_17_c_o), .FG_i(vgastring_17_fg_o),
    .BG_i(vgastring_17_bg_o), .FG_c(12'he09), .BG_c({12{1'b0}}), .CX_c(6'b000101), .CY_c({8{1'b0}}),
    .C_0(register_82_q), .C_1(register_83_q), .C_2(register_84_q), .C_3(register_85_q), .EN(1'b1),
    .CX_o(vgastring_21_cx_o), .CY_o(vgastring_21_cy_o), .C_o(vgastring_21_c_o), .FG_o(vgastring_21_fg_o),
    .BG_o(vgastring_21_bg_o));
  vgastring vgastring_22 (
    .CX_i(vgastring_18_cx_o), .CY_i(vgastring_18_cy_o), .C_i(vgastring_18_c_o), .FG_i(vgastring_18_fg_o),
    .BG_i(vgastring_18_bg_o), .FG_c(12'he09), .BG_c({12{1'b0}}), .CX_c(6'b000101), .CY_c(8'h1),
    .C_0(register_86_q), .C_1(register_87_q), .C_2(register_88_q), .C_3(register_89_q), .EN(1'b1),
    .CX_o(vgastring_22_cx_o), .CY_o(vgastring_22_cy_o), .C_o(vgastring_22_c_o), .FG_o(vgastring_22_fg_o),
    .BG_o(vgastring_22_bg_o));
  vgastring vgastring_23 (
    .CX_i(vgastring_19_cx_o), .CY_i(vgastring_19_cy_o), .C_i(vgastring_19_c_o), .FG_i(vgastring_19_fg_o),
    .BG_i(vgastring_19_bg_o), .FG_c(12'he09), .BG_c({12{1'b0}}), .CX_c(6'b000101), .CY_c(8'h2),
    .C_0(register_90_q), .C_1(register_91_q), .C_2(register_92_q), .C_3(register_93_q), .EN(1'b1),
    .CX_o(vgastring_23_cx_o), .CY_o(vgastring_23_cy_o), .C_o(vgastring_23_c_o), .FG_o(vgastring_23_fg_o),
    .BG_o(vgastring_23_bg_o));
  vgastring vgastring_24 (
    .CX_i(vgastring_20_cx_o), .CY_i(vgastring_20_cy_o), .C_i(vgastring_20_c_o), .FG_i(vgastring_20_fg_o),
    .BG_i(vgastring_20_bg_o), .FG_c(12'he09), .BG_c({12{1'b0}}), .CX_c(6'b000101), .CY_c(8'h3),
    .C_0(register_94_q), .C_1(register_95_q), .C_2(register_96_q), .C_3(register_97_q), .EN(1'b1),
    .CX_o(vgastring_24_cx_o), .CY_o(vgastring_24_cy_o), .C_o(vgastring_24_c_o), .FG_o(vgastring_24_fg_o),
    .BG_o(vgastring_24_bg_o));
  Comparator #(.Bits(8)) comparator_97 (.a(out_12), .b(8'h18), .eq(comparator_97_eq));  // open: gt, lt
  Comparator #(.Bits(8)) comparator_98 (.a(out_12), .b(8'h19), .eq(comparator_98_eq));  // open: gt, lt
  Comparator #(.Bits(8)) comparator_99 (.a(out_12), .b(8'h1a), .eq(comparator_99_eq));  // open: gt, lt
  Comparator #(.Bits(8)) comparator_100 (.a(out_12), .b(8'h1b), .eq(comparator_100_eq));  // open: gt, lt
  Comparator #(.Bits(8)) comparator_101 (.a(out_12), .b(8'h40), .eq(comparator_101_eq));  // open: gt, lt
  Comparator #(.Bits(8)) comparator_102 (.a(out_12), .b(8'h41), .eq(comparator_102_eq));  // open: gt, lt
  Comparator #(.Bits(8)) comparator_103 (.a(out_12), .b(8'h42), .eq(comparator_103_eq));  // open: gt, lt
  Comparator #(.Bits(8)) comparator_104 (.a(out_12), .b(8'h43), .eq(comparator_104_eq));  // open: gt, lt
  Comparator #(.Bits(8)) comparator_105 (.a(out_12), .b(8'h68), .eq(comparator_105_eq));  // open: gt, lt
  Comparator #(.Bits(8)) comparator_106 (.a(out_12), .b(8'h69), .eq(comparator_106_eq));  // open: gt, lt
  Comparator #(.Bits(8)) comparator_107 (.a(out_12), .b(8'h6a), .eq(comparator_107_eq));  // open: gt, lt
  Comparator #(.Bits(8)) comparator_108 (.a(out_12), .b(8'h6b), .eq(comparator_108_eq));  // open: gt, lt
  Comparator #(.Bits(8)) comparator_109 (.a(out_12), .b(8'h90), .eq(comparator_109_eq));  // open: gt, lt
  Comparator #(.Bits(8)) comparator_110 (.a(out_12), .b(8'h91), .eq(comparator_110_eq));  // open: gt, lt
  Comparator #(.Bits(8)) comparator_111 (.a(out_12), .b(8'h92), .eq(comparator_111_eq));  // open: gt, lt
  Comparator #(.Bits(8)) comparator_112 (.a(out_12), .b(8'h93), .eq(comparator_112_eq));  // open: gt, lt
  Delay #(.delayTime(10)) delay_99 (.in(comparator_97_eq), .out(delay_99_out));
  Delay #(.delayTime(10)) delay_100 (.in(comparator_98_eq), .out(delay_100_out));
  Delay #(.delayTime(10)) delay_101 (.in(comparator_99_eq), .out(delay_101_out));
  Delay #(.delayTime(10)) delay_102 (.in(comparator_100_eq), .out(delay_102_out));
  Delay #(.delayTime(10)) delay_103 (.in(comparator_101_eq), .out(delay_103_out));
  Delay #(.delayTime(10)) delay_104 (.in(comparator_102_eq), .out(delay_104_out));
  Delay #(.delayTime(10)) delay_105 (.in(comparator_103_eq), .out(delay_105_out));
  Delay #(.delayTime(10)) delay_106 (.in(comparator_104_eq), .out(delay_106_out));
  Delay #(.delayTime(10)) delay_107 (.in(comparator_105_eq), .out(delay_107_out));
  Delay #(.delayTime(10)) delay_108 (.in(comparator_106_eq), .out(delay_108_out));
  Delay #(.delayTime(10)) delay_109 (.in(comparator_107_eq), .out(delay_109_out));
  Delay #(.delayTime(10)) delay_110 (.in(comparator_108_eq), .out(delay_110_out));
  Delay #(.delayTime(10)) delay_111 (.in(comparator_109_eq), .out(delay_111_out));
  Delay #(.delayTime(10)) delay_112 (.in(comparator_110_eq), .out(delay_112_out));
  Delay #(.delayTime(10)) delay_113 (.in(comparator_111_eq), .out(delay_113_out));
  Delay #(.delayTime(10)) delay_114 (.in(comparator_112_eq), .out(delay_114_out));
  Register #(.Bits(7)) register_98 (.D(driver_2_out), .C(delay_99_out), .en(comparator_97_eq), .Q(register_98_q));
  Register #(.Bits(7)) register_99 (.D(driver_2_out), .C(delay_100_out), .en(comparator_98_eq), .Q(register_99_q));
  Register #(.Bits(7)) register_100 (.D(driver_2_out), .C(delay_101_out), .en(comparator_99_eq), .Q(register_100_q));
  Register #(.Bits(7)) register_101 (.D(driver_2_out), .C(delay_102_out), .en(comparator_100_eq), .Q(register_101_q));
  Register #(.Bits(7)) register_102 (.D(driver_2_out), .C(delay_103_out), .en(comparator_101_eq), .Q(register_102_q));
  Register #(.Bits(7)) register_103 (.D(driver_2_out), .C(delay_104_out), .en(comparator_102_eq), .Q(register_103_q));
  Register #(.Bits(7)) register_104 (.D(driver_2_out), .C(delay_105_out), .en(comparator_103_eq), .Q(register_104_q));
  Register #(.Bits(7)) register_105 (.D(driver_2_out), .C(delay_106_out), .en(comparator_104_eq), .Q(register_105_q));
  Register #(.Bits(7)) register_106 (.D(driver_2_out), .C(delay_107_out), .en(comparator_105_eq), .Q(register_106_q));
  Register #(.Bits(7)) register_107 (.D(driver_2_out), .C(delay_108_out), .en(comparator_106_eq), .Q(register_107_q));
  Register #(.Bits(7)) register_108 (.D(driver_2_out), .C(delay_109_out), .en(comparator_107_eq), .Q(register_108_q));
  Register #(.Bits(7)) register_109 (.D(driver_2_out), .C(delay_110_out), .en(comparator_108_eq), .Q(register_109_q));
  Register #(.Bits(7)) register_110 (.D(driver_2_out), .C(delay_111_out), .en(comparator_109_eq), .Q(register_110_q));
  Register #(.Bits(7)) register_111 (.D(driver_2_out), .C(delay_112_out), .en(comparator_110_eq), .Q(register_111_q));
  Register #(.Bits(7)) register_112 (.D(driver_2_out), .C(delay_113_out), .en(comparator_111_eq), .Q(register_112_q));
  Register #(.Bits(7)) register_113 (.D(driver_2_out), .C(delay_114_out), .en(comparator_112_eq), .Q(register_113_q));
  vgastring vgastring_25 (
    .CX_i(vgastring_21_cx_o), .CY_i(vgastring_21_cy_o), .C_i(vgastring_21_c_o), .FG_i(vgastring_21_fg_o),
    .BG_i(vgastring_21_bg_o), .FG_c(12'he09), .BG_c({12{1'b0}}), .CX_c(6'b000110), .CY_c({8{1'b0}}),
    .C_0(register_98_q), .C_1(register_99_q), .C_2(register_100_q), .C_3(register_101_q), .EN(1'b1),
    .CX_o(vgastring_25_cx_o), .CY_o(vgastring_25_cy_o), .C_o(vgastring_25_c_o), .FG_o(vgastring_25_fg_o),
    .BG_o(vgastring_25_bg_o));
  vgastring vgastring_26 (
    .CX_i(vgastring_22_cx_o), .CY_i(vgastring_22_cy_o), .C_i(vgastring_22_c_o), .FG_i(vgastring_22_fg_o),
    .BG_i(vgastring_22_bg_o), .FG_c(12'he09), .BG_c({12{1'b0}}), .CX_c(6'b000110), .CY_c(8'h1),
    .C_0(register_102_q), .C_1(register_103_q), .C_2(register_104_q), .C_3(register_105_q), .EN(1'b1),
    .CX_o(vgastring_26_cx_o), .CY_o(vgastring_26_cy_o), .C_o(vgastring_26_c_o), .FG_o(vgastring_26_fg_o),
    .BG_o(vgastring_26_bg_o));
  vgastring vgastring_27 (
    .CX_i(vgastring_23_cx_o), .CY_i(vgastring_23_cy_o), .C_i(vgastring_23_c_o), .FG_i(vgastring_23_fg_o),
    .BG_i(vgastring_23_bg_o), .FG_c(12'he09), .BG_c({12{1'b0}}), .CX_c(6'b000110), .CY_c(8'h2),
    .C_0(register_106_q), .C_1(register_107_q), .C_2(register_108_q), .C_3(register_109_q), .EN(1'b1),
    .CX_o(vgastring_27_cx_o), .CY_o(vgastring_27_cy_o), .C_o(vgastring_27_c_o), .FG_o(vgastring_27_fg_o),
    .BG_o(vgastring_27_bg_o));
  vgastring vgastring_28 (
    .CX_i(vgastring_24_cx_o), .CY_i(vgastring_24_cy_o), .C_i(vgastring_24_c_o), .FG_i(vgastring_24_fg_o),
    .BG_i(vgastring_24_bg_o), .FG_c(12'he09), .BG_c({12{1'b0}}), .CX_c(6'b000110), .CY_c(8'h3),
    .C_0(register_110_q), .C_1(register_111_q), .C_2(register_112_q), .C_3(register_113_q), .EN(1'b1),
    .CX_o(vgastring_28_cx_o), .CY_o(vgastring_28_cy_o), .C_o(vgastring_28_c_o), .FG_o(vgastring_28_fg_o),
    .BG_o(vgastring_28_bg_o));
  Comparator #(.Bits(8)) comparator_113 (.a(out_12), .b(8'h1c), .eq(comparator_113_eq));  // open: gt, lt
  Comparator #(.Bits(8)) comparator_114 (.a(out_12), .b(8'h1d), .eq(comparator_114_eq));  // open: gt, lt
  Comparator #(.Bits(8)) comparator_115 (.a(out_12), .b(8'h1e), .eq(comparator_115_eq));  // open: gt, lt
  Comparator #(.Bits(8)) comparator_116 (.a(out_12), .b(8'h1f), .eq(comparator_116_eq));  // open: gt, lt
  Comparator #(.Bits(8)) comparator_117 (.a(out_12), .b(8'h44), .eq(comparator_117_eq));  // open: gt, lt
  Comparator #(.Bits(8)) comparator_118 (.a(out_12), .b(8'h45), .eq(comparator_118_eq));  // open: gt, lt
  Comparator #(.Bits(8)) comparator_119 (.a(out_12), .b(8'h46), .eq(comparator_119_eq));  // open: gt, lt
  Comparator #(.Bits(8)) comparator_120 (.a(out_12), .b(8'h47), .eq(comparator_120_eq));  // open: gt, lt
  Comparator #(.Bits(8)) comparator_121 (.a(out_12), .b(8'h6c), .eq(comparator_121_eq));  // open: gt, lt
  Comparator #(.Bits(8)) comparator_122 (.a(out_12), .b(8'h6d), .eq(comparator_122_eq));  // open: gt, lt
  Comparator #(.Bits(8)) comparator_123 (.a(out_12), .b(8'h6e), .eq(comparator_123_eq));  // open: gt, lt
  Comparator #(.Bits(8)) comparator_124 (.a(out_12), .b(8'h6f), .eq(comparator_124_eq));  // open: gt, lt
  Comparator #(.Bits(8)) comparator_125 (.a(out_12), .b(8'h94), .eq(comparator_125_eq));  // open: gt, lt
  Comparator #(.Bits(8)) comparator_126 (.a(out_12), .b(8'h95), .eq(comparator_126_eq));  // open: gt, lt
  Comparator #(.Bits(8)) comparator_127 (.a(out_12), .b(8'h96), .eq(comparator_127_eq));  // open: gt, lt
  Comparator #(.Bits(8)) comparator_128 (.a(out_12), .b(8'h97), .eq(comparator_128_eq));  // open: gt, lt
  Delay #(.delayTime(10)) delay_115 (.in(comparator_113_eq), .out(delay_115_out));
  Delay #(.delayTime(10)) delay_116 (.in(comparator_114_eq), .out(delay_116_out));
  Delay #(.delayTime(10)) delay_117 (.in(comparator_115_eq), .out(delay_117_out));
  Delay #(.delayTime(10)) delay_118 (.in(comparator_116_eq), .out(delay_118_out));
  Delay #(.delayTime(10)) delay_119 (.in(comparator_117_eq), .out(delay_119_out));
  Delay #(.delayTime(10)) delay_120 (.in(comparator_118_eq), .out(delay_120_out));
  Delay #(.delayTime(10)) delay_121 (.in(comparator_119_eq), .out(delay_121_out));
  Delay #(.delayTime(10)) delay_122 (.in(comparator_120_eq), .out(delay_122_out));
  Delay #(.delayTime(10)) delay_123 (.in(comparator_121_eq), .out(delay_123_out));
  Delay #(.delayTime(10)) delay_124 (.in(comparator_122_eq), .out(delay_124_out));
  Delay #(.delayTime(10)) delay_125 (.in(comparator_123_eq), .out(delay_125_out));
  Delay #(.delayTime(10)) delay_126 (.in(comparator_124_eq), .out(delay_126_out));
  Delay #(.delayTime(10)) delay_127 (.in(comparator_125_eq), .out(delay_127_out));
  Delay #(.delayTime(10)) delay_128 (.in(comparator_126_eq), .out(delay_128_out));
  Delay #(.delayTime(10)) delay_129 (.in(comparator_127_eq), .out(delay_129_out));
  Delay #(.delayTime(10)) delay_130 (.in(comparator_128_eq), .out(delay_130_out));
  Register #(.Bits(7)) register_114 (.D(driver_2_out), .C(delay_115_out), .en(comparator_113_eq), .Q(register_114_q));
  Register #(.Bits(7)) register_115 (.D(driver_2_out), .C(delay_116_out), .en(comparator_114_eq), .Q(register_115_q));
  Register #(.Bits(7)) register_116 (.D(driver_2_out), .C(delay_117_out), .en(comparator_115_eq), .Q(register_116_q));
  Register #(.Bits(7)) register_117 (.D(driver_2_out), .C(delay_118_out), .en(comparator_116_eq), .Q(register_117_q));
  Register #(.Bits(7)) register_118 (.D(driver_2_out), .C(delay_119_out), .en(comparator_117_eq), .Q(register_118_q));
  Register #(.Bits(7)) register_119 (.D(driver_2_out), .C(delay_120_out), .en(comparator_118_eq), .Q(register_119_q));
  Register #(.Bits(7)) register_120 (.D(driver_2_out), .C(delay_121_out), .en(comparator_119_eq), .Q(register_120_q));
  Register #(.Bits(7)) register_121 (.D(driver_2_out), .C(delay_122_out), .en(comparator_120_eq), .Q(register_121_q));
  Register #(.Bits(7)) register_122 (.D(driver_2_out), .C(delay_123_out), .en(comparator_121_eq), .Q(register_122_q));
  Register #(.Bits(7)) register_123 (.D(driver_2_out), .C(delay_124_out), .en(comparator_122_eq), .Q(register_123_q));
  Register #(.Bits(7)) register_124 (.D(driver_2_out), .C(delay_125_out), .en(comparator_123_eq), .Q(register_124_q));
  Register #(.Bits(7)) register_125 (.D(driver_2_out), .C(delay_126_out), .en(comparator_124_eq), .Q(register_125_q));
  Register #(.Bits(7)) register_126 (.D(driver_2_out), .C(delay_127_out), .en(comparator_125_eq), .Q(register_126_q));
  Register #(.Bits(7)) register_127 (.D(driver_2_out), .C(delay_128_out), .en(comparator_126_eq), .Q(register_127_q));
  Register #(.Bits(7)) register_128 (.D(driver_2_out), .C(delay_129_out), .en(comparator_127_eq), .Q(register_128_q));
  Register #(.Bits(7)) register_129 (.D(driver_2_out), .C(delay_130_out), .en(comparator_128_eq), .Q(register_129_q));
  vgastring vgastring_29 (
    .CX_i(vgastring_25_cx_o), .CY_i(vgastring_25_cy_o), .C_i(vgastring_25_c_o), .FG_i(vgastring_25_fg_o),
    .BG_i(vgastring_25_bg_o), .FG_c(12'he09), .BG_c({12{1'b0}}), .CX_c(6'b000111), .CY_c({8{1'b0}}),
    .C_0(register_114_q), .C_1(register_115_q), .C_2(register_116_q), .C_3(register_117_q), .EN(1'b1),
    .CX_o(vgastring_29_cx_o), .CY_o(vgastring_29_cy_o), .C_o(vgastring_29_c_o), .FG_o(vgastring_29_fg_o),
    .BG_o(vgastring_29_bg_o));
  vgastring vgastring_30 (
    .CX_i(vgastring_26_cx_o), .CY_i(vgastring_26_cy_o), .C_i(vgastring_26_c_o), .FG_i(vgastring_26_fg_o),
    .BG_i(vgastring_26_bg_o), .FG_c(12'he09), .BG_c({12{1'b0}}), .CX_c(6'b000111), .CY_c(8'h1),
    .C_0(register_118_q), .C_1(register_119_q), .C_2(register_120_q), .C_3(register_121_q), .EN(1'b1),
    .CX_o(vgastring_30_cx_o), .CY_o(vgastring_30_cy_o), .C_o(vgastring_30_c_o), .FG_o(vgastring_30_fg_o),
    .BG_o(vgastring_30_bg_o));
  vgastring vgastring_31 (
    .CX_i(vgastring_27_cx_o), .CY_i(vgastring_27_cy_o), .C_i(vgastring_27_c_o), .FG_i(vgastring_27_fg_o),
    .BG_i(vgastring_27_bg_o), .FG_c(12'he09), .BG_c({12{1'b0}}), .CX_c(6'b000111), .CY_c(8'h2),
    .C_0(register_122_q), .C_1(register_123_q), .C_2(register_124_q), .C_3(register_125_q), .EN(1'b1),
    .CX_o(vgastring_31_cx_o), .CY_o(vgastring_31_cy_o), .C_o(vgastring_31_c_o), .FG_o(vgastring_31_fg_o),
    .BG_o(vgastring_31_bg_o));
  vgastring vgastring_32 (
    .CX_i(vgastring_28_cx_o), .CY_i(vgastring_28_cy_o), .C_i(vgastring_28_c_o), .FG_i(vgastring_28_fg_o),
    .BG_i(vgastring_28_bg_o), .FG_c(12'he09), .BG_c({12{1'b0}}), .CX_c(6'b000111), .CY_c(8'h3),
    .C_0(register_126_q), .C_1(register_127_q), .C_2(register_128_q), .C_3(register_129_q), .EN(1'b1),
    .CX_o(vgastring_32_cx_o), .CY_o(vgastring_32_cy_o), .C_o(vgastring_32_c_o), .FG_o(vgastring_32_fg_o),
    .BG_o(vgastring_32_bg_o));
  Comparator #(.Bits(8)) comparator_129 (.a(out_12), .b(8'h20), .eq(comparator_129_eq));  // open: gt, lt
  Comparator #(.Bits(8)) comparator_130 (.a(out_12), .b(8'h21), .eq(comparator_130_eq));  // open: gt, lt
  Comparator #(.Bits(8)) comparator_131 (.a(out_12), .b(8'h22), .eq(comparator_131_eq));  // open: gt, lt
  Comparator #(.Bits(8)) comparator_132 (.a(out_12), .b(8'h23), .eq(comparator_132_eq));  // open: gt, lt
  Comparator #(.Bits(8)) comparator_133 (.a(out_12), .b(8'h48), .eq(comparator_133_eq));  // open: gt, lt
  Comparator #(.Bits(8)) comparator_134 (.a(out_12), .b(8'h49), .eq(comparator_134_eq));  // open: gt, lt
  Comparator #(.Bits(8)) comparator_135 (.a(out_12), .b(8'h4a), .eq(comparator_135_eq));  // open: gt, lt
  Comparator #(.Bits(8)) comparator_136 (.a(out_12), .b(8'h4b), .eq(comparator_136_eq));  // open: gt, lt
  Comparator #(.Bits(8)) comparator_137 (.a(out_12), .b(8'h70), .eq(comparator_137_eq));  // open: gt, lt
  Comparator #(.Bits(8)) comparator_138 (.a(out_12), .b(8'h71), .eq(comparator_138_eq));  // open: gt, lt
  Comparator #(.Bits(8)) comparator_139 (.a(out_12), .b(8'h72), .eq(comparator_139_eq));  // open: gt, lt
  Comparator #(.Bits(8)) comparator_140 (.a(out_12), .b(8'h73), .eq(comparator_140_eq));  // open: gt, lt
  Comparator #(.Bits(8)) comparator_141 (.a(out_12), .b(8'h98), .eq(comparator_141_eq));  // open: gt, lt
  Comparator #(.Bits(8)) comparator_142 (.a(out_12), .b(8'h99), .eq(comparator_142_eq));  // open: gt, lt
  Comparator #(.Bits(8)) comparator_143 (.a(out_12), .b(8'h9a), .eq(comparator_143_eq));  // open: gt, lt
  Comparator #(.Bits(8)) comparator_144 (.a(out_12), .b(8'h9b), .eq(comparator_144_eq));  // open: gt, lt
  Delay #(.delayTime(10)) delay_131 (.in(comparator_129_eq), .out(delay_131_out));
  Delay #(.delayTime(10)) delay_132 (.in(comparator_130_eq), .out(delay_132_out));
  Delay #(.delayTime(10)) delay_133 (.in(comparator_131_eq), .out(delay_133_out));
  Delay #(.delayTime(10)) delay_134 (.in(comparator_132_eq), .out(delay_134_out));
  Delay #(.delayTime(10)) delay_135 (.in(comparator_133_eq), .out(delay_135_out));
  Delay #(.delayTime(10)) delay_136 (.in(comparator_134_eq), .out(delay_136_out));
  Delay #(.delayTime(10)) delay_137 (.in(comparator_135_eq), .out(delay_137_out));
  Delay #(.delayTime(10)) delay_138 (.in(comparator_136_eq), .out(delay_138_out));
  Delay #(.delayTime(10)) delay_139 (.in(comparator_137_eq), .out(delay_139_out));
  Delay #(.delayTime(10)) delay_140 (.in(comparator_138_eq), .out(delay_140_out));
  Delay #(.delayTime(10)) delay_141 (.in(comparator_139_eq), .out(delay_141_out));
  Delay #(.delayTime(10)) delay_142 (.in(comparator_140_eq), .out(delay_142_out));
  Delay #(.delayTime(10)) delay_143 (.in(comparator_141_eq), .out(delay_143_out));
  Delay #(.delayTime(10)) delay_144 (.in(comparator_142_eq), .out(delay_144_out));
  Delay #(.delayTime(10)) delay_145 (.in(comparator_143_eq), .out(delay_145_out));
  Delay #(.delayTime(10)) delay_146 (.in(comparator_144_eq), .out(delay_146_out));
  Register #(.Bits(7)) register_130 (.D(driver_2_out), .C(delay_131_out), .en(comparator_129_eq), .Q(register_130_q));
  Register #(.Bits(7)) register_131 (.D(driver_2_out), .C(delay_132_out), .en(comparator_130_eq), .Q(register_131_q));
  Register #(.Bits(7)) register_132 (.D(driver_2_out), .C(delay_133_out), .en(comparator_131_eq), .Q(register_132_q));
  Register #(.Bits(7)) register_133 (.D(driver_2_out), .C(delay_134_out), .en(comparator_132_eq), .Q(register_133_q));
  Register #(.Bits(7)) register_134 (.D(driver_2_out), .C(delay_135_out), .en(comparator_133_eq), .Q(register_134_q));
  Register #(.Bits(7)) register_135 (.D(driver_2_out), .C(delay_136_out), .en(comparator_134_eq), .Q(register_135_q));
  Register #(.Bits(7)) register_136 (.D(driver_2_out), .C(delay_137_out), .en(comparator_135_eq), .Q(register_136_q));
  Register #(.Bits(7)) register_137 (.D(driver_2_out), .C(delay_138_out), .en(comparator_136_eq), .Q(register_137_q));
  Register #(.Bits(7)) register_138 (.D(driver_2_out), .C(delay_139_out), .en(comparator_137_eq), .Q(register_138_q));
  Register #(.Bits(7)) register_139 (.D(driver_2_out), .C(delay_140_out), .en(comparator_138_eq), .Q(register_139_q));
  Register #(.Bits(7)) register_140 (.D(driver_2_out), .C(delay_141_out), .en(comparator_139_eq), .Q(register_140_q));
  Register #(.Bits(7)) register_141 (.D(driver_2_out), .C(delay_142_out), .en(comparator_140_eq), .Q(register_141_q));
  Register #(.Bits(7)) register_142 (.D(driver_2_out), .C(delay_143_out), .en(comparator_141_eq), .Q(register_142_q));
  Register #(.Bits(7)) register_143 (.D(driver_2_out), .C(delay_144_out), .en(comparator_142_eq), .Q(register_143_q));
  Register #(.Bits(7)) register_144 (.D(driver_2_out), .C(delay_145_out), .en(comparator_143_eq), .Q(register_144_q));
  Register #(.Bits(7)) register_145 (.D(driver_2_out), .C(delay_146_out), .en(comparator_144_eq), .Q(register_145_q));
  vgastring vgastring_33 (
    .CX_i(vgastring_29_cx_o), .CY_i(vgastring_29_cy_o), .C_i(vgastring_29_c_o), .FG_i(vgastring_29_fg_o),
    .BG_i(vgastring_29_bg_o), .FG_c(12'he09), .BG_c({12{1'b0}}), .CX_c(6'b001000), .CY_c({8{1'b0}}),
    .C_0(register_130_q), .C_1(register_131_q), .C_2(register_132_q), .C_3(register_133_q), .EN(1'b1),
    .CX_o(vgastring_33_cx_o), .CY_o(vgastring_33_cy_o), .C_o(vgastring_33_c_o), .FG_o(vgastring_33_fg_o),
    .BG_o(vgastring_33_bg_o));
  vgastring vgastring_34 (
    .CX_i(vgastring_30_cx_o), .CY_i(vgastring_30_cy_o), .C_i(vgastring_30_c_o), .FG_i(vgastring_30_fg_o),
    .BG_i(vgastring_30_bg_o), .FG_c(12'he09), .BG_c({12{1'b0}}), .CX_c(6'b001000), .CY_c(8'h1),
    .C_0(register_134_q), .C_1(register_135_q), .C_2(register_136_q), .C_3(register_137_q), .EN(1'b1),
    .CX_o(vgastring_34_cx_o), .CY_o(vgastring_34_cy_o), .C_o(vgastring_34_c_o), .FG_o(vgastring_34_fg_o),
    .BG_o(vgastring_34_bg_o));
  vgastring vgastring_35 (
    .CX_i(vgastring_31_cx_o), .CY_i(vgastring_31_cy_o), .C_i(vgastring_31_c_o), .FG_i(vgastring_31_fg_o),
    .BG_i(vgastring_31_bg_o), .FG_c(12'he09), .BG_c({12{1'b0}}), .CX_c(6'b001000), .CY_c(8'h2),
    .C_0(register_138_q), .C_1(register_139_q), .C_2(register_140_q), .C_3(register_141_q), .EN(1'b1),
    .CX_o(vgastring_35_cx_o), .CY_o(vgastring_35_cy_o), .C_o(vgastring_35_c_o), .FG_o(vgastring_35_fg_o),
    .BG_o(vgastring_35_bg_o));
  vgastring vgastring_36 (
    .CX_i(vgastring_32_cx_o), .CY_i(vgastring_32_cy_o), .C_i(vgastring_32_c_o), .FG_i(vgastring_32_fg_o),
    .BG_i(vgastring_32_bg_o), .FG_c(12'he09), .BG_c({12{1'b0}}), .CX_c(6'b001000), .CY_c(8'h3),
    .C_0(register_142_q), .C_1(register_143_q), .C_2(register_144_q), .C_3(register_145_q), .EN(1'b1),
    .CX_o(vgastring_36_cx_o), .CY_o(vgastring_36_cy_o), .C_o(vgastring_36_c_o), .FG_o(vgastring_36_fg_o),
    .BG_o(vgastring_36_bg_o));
  Comparator #(.Bits(8)) comparator_145 (.a(out_12), .b(8'h24), .eq(comparator_145_eq));  // open: gt, lt
  Comparator #(.Bits(8)) comparator_146 (.a(out_12), .b(8'h25), .eq(comparator_146_eq));  // open: gt, lt
  Comparator #(.Bits(8)) comparator_147 (.a(out_12), .b(8'h26), .eq(comparator_147_eq));  // open: gt, lt
  Comparator #(.Bits(8)) comparator_148 (.a(out_12), .b(8'h27), .eq(comparator_148_eq));  // open: gt, lt
  Comparator #(.Bits(8)) comparator_149 (.a(out_12), .b(8'h4c), .eq(comparator_149_eq));  // open: gt, lt
  Comparator #(.Bits(8)) comparator_150 (.a(out_12), .b(8'h4d), .eq(comparator_150_eq));  // open: gt, lt
  Comparator #(.Bits(8)) comparator_151 (.a(out_12), .b(8'h4e), .eq(comparator_151_eq));  // open: gt, lt
  Comparator #(.Bits(8)) comparator_152 (.a(out_12), .b(8'h4f), .eq(comparator_152_eq));  // open: gt, lt
  Comparator #(.Bits(8)) comparator_153 (.a(out_12), .b(8'h74), .eq(comparator_153_eq));  // open: gt, lt
  Comparator #(.Bits(8)) comparator_154 (.a(out_12), .b(8'h75), .eq(comparator_154_eq));  // open: gt, lt
  Comparator #(.Bits(8)) comparator_155 (.a(out_12), .b(8'h76), .eq(comparator_155_eq));  // open: gt, lt
  Comparator #(.Bits(8)) comparator_156 (.a(out_12), .b(8'h77), .eq(comparator_156_eq));  // open: gt, lt
  Comparator #(.Bits(8)) comparator_157 (.a(out_12), .b(8'h9c), .eq(comparator_157_eq));  // open: gt, lt
  Comparator #(.Bits(8)) comparator_158 (.a(out_12), .b(8'h9d), .eq(comparator_158_eq));  // open: gt, lt
  Comparator #(.Bits(8)) comparator_159 (.a(out_12), .b(8'h9e), .eq(comparator_159_eq));  // open: gt, lt
  Comparator #(.Bits(8)) comparator_160 (.a(out_12), .b(8'h9f), .eq(comparator_160_eq));  // open: gt, lt
  Delay #(.delayTime(10)) delay_147 (.in(comparator_145_eq), .out(delay_147_out));
  Delay #(.delayTime(10)) delay_148 (.in(comparator_146_eq), .out(delay_148_out));
  Delay #(.delayTime(10)) delay_149 (.in(comparator_147_eq), .out(delay_149_out));
  Delay #(.delayTime(10)) delay_150 (.in(comparator_148_eq), .out(delay_150_out));
  Delay #(.delayTime(10)) delay_151 (.in(comparator_149_eq), .out(delay_151_out));
  Delay #(.delayTime(10)) delay_152 (.in(comparator_150_eq), .out(delay_152_out));
  Delay #(.delayTime(10)) delay_153 (.in(comparator_151_eq), .out(delay_153_out));
  Delay #(.delayTime(10)) delay_154 (.in(comparator_152_eq), .out(delay_154_out));
  Delay #(.delayTime(10)) delay_155 (.in(comparator_153_eq), .out(delay_155_out));
  Delay #(.delayTime(10)) delay_156 (.in(comparator_154_eq), .out(delay_156_out));
  Delay #(.delayTime(10)) delay_157 (.in(comparator_155_eq), .out(delay_157_out));
  Delay #(.delayTime(10)) delay_158 (.in(comparator_156_eq), .out(delay_158_out));
  Delay #(.delayTime(10)) delay_159 (.in(comparator_157_eq), .out(delay_159_out));
  Delay #(.delayTime(10)) delay_160 (.in(comparator_158_eq), .out(delay_160_out));
  Delay #(.delayTime(10)) delay_161 (.in(comparator_159_eq), .out(delay_161_out));
  Delay #(.delayTime(10)) delay_162 (.in(comparator_160_eq), .out(delay_162_out));
  Register #(.Bits(7)) register_146 (.D(driver_2_out), .C(delay_147_out), .en(comparator_145_eq), .Q(register_146_q));
  Register #(.Bits(7)) register_147 (.D(driver_2_out), .C(delay_148_out), .en(comparator_146_eq), .Q(register_147_q));
  Register #(.Bits(7)) register_148 (.D(driver_2_out), .C(delay_149_out), .en(comparator_147_eq), .Q(register_148_q));
  Register #(.Bits(7)) register_149 (.D(driver_2_out), .C(delay_150_out), .en(comparator_148_eq), .Q(register_149_q));
  Register #(.Bits(7)) register_150 (.D(driver_2_out), .C(delay_151_out), .en(comparator_149_eq), .Q(register_150_q));
  Register #(.Bits(7)) register_151 (.D(driver_2_out), .C(delay_152_out), .en(comparator_150_eq), .Q(register_151_q));
  Register #(.Bits(7)) register_152 (.D(driver_2_out), .C(delay_153_out), .en(comparator_151_eq), .Q(register_152_q));
  Register #(.Bits(7)) register_153 (.D(driver_2_out), .C(delay_154_out), .en(comparator_152_eq), .Q(register_153_q));
  Register #(.Bits(7)) register_154 (.D(driver_2_out), .C(delay_155_out), .en(comparator_153_eq), .Q(register_154_q));
  Register #(.Bits(7)) register_155 (.D(driver_2_out), .C(delay_156_out), .en(comparator_154_eq), .Q(register_155_q));
  Register #(.Bits(7)) register_156 (.D(driver_2_out), .C(delay_157_out), .en(comparator_155_eq), .Q(register_156_q));
  Register #(.Bits(7)) register_157 (.D(driver_2_out), .C(delay_158_out), .en(comparator_156_eq), .Q(register_157_q));
  Register #(.Bits(7)) register_158 (.D(driver_2_out), .C(delay_159_out), .en(comparator_157_eq), .Q(register_158_q));
  Register #(.Bits(7)) register_159 (.D(driver_2_out), .C(delay_160_out), .en(comparator_158_eq), .Q(register_159_q));
  Register #(.Bits(7)) register_160 (.D(driver_2_out), .C(delay_161_out), .en(comparator_159_eq), .Q(register_160_q));
  Register #(.Bits(7)) register_161 (.D(driver_2_out), .C(delay_162_out), .en(comparator_160_eq), .Q(register_161_q));
  vgastring vgastring_37 (
    .CX_i(vgastring_33_cx_o), .CY_i(vgastring_33_cy_o), .C_i(vgastring_33_c_o), .FG_i(vgastring_33_fg_o),
    .BG_i(vgastring_33_bg_o), .FG_c(12'he09), .BG_c({12{1'b0}}), .CX_c(6'b001001), .CY_c({8{1'b0}}),
    .C_0(register_146_q), .C_1(register_147_q), .C_2(register_148_q), .C_3(register_149_q), .EN(1'b1),
    .CX_o(vgastring_37_cx_o), .CY_o(vgastring_37_cy_o), .C_o(vgastring_37_c_o), .FG_o(vgastring_37_fg_o),
    .BG_o(vgastring_37_bg_o));
  vgastring vgastring_38 (
    .CX_i(vgastring_34_cx_o), .CY_i(vgastring_34_cy_o), .C_i(vgastring_34_c_o), .FG_i(vgastring_34_fg_o),
    .BG_i(vgastring_34_bg_o), .FG_c(12'he09), .BG_c({12{1'b0}}), .CX_c(6'b001001), .CY_c(8'h1),
    .C_0(register_150_q), .C_1(register_151_q), .C_2(register_152_q), .C_3(register_153_q), .EN(1'b1),
    .CX_o(vgastring_38_cx_o), .CY_o(vgastring_38_cy_o), .C_o(vgastring_38_c_o), .FG_o(vgastring_38_fg_o),
    .BG_o(vgastring_38_bg_o));
  vgastring vgastring_39 (
    .CX_i(vgastring_35_cx_o), .CY_i(vgastring_35_cy_o), .C_i(vgastring_35_c_o), .FG_i(vgastring_35_fg_o),
    .BG_i(vgastring_35_bg_o), .FG_c(12'he09), .BG_c({12{1'b0}}), .CX_c(6'b001001), .CY_c(8'h2),
    .C_0(register_154_q), .C_1(register_155_q), .C_2(register_156_q), .C_3(register_157_q), .EN(1'b1),
    .CX_o(vgastring_39_cx_o), .CY_o(vgastring_39_cy_o), .C_o(vgastring_39_c_o), .FG_o(vgastring_39_fg_o),
    .BG_o(vgastring_39_bg_o));
  vgastring vgastring_40 (
    .CX_i(vgastring_36_cx_o), .CY_i(vgastring_36_cy_o), .C_i(vgastring_36_c_o), .FG_i(vgastring_36_fg_o),
    .BG_i(vgastring_36_bg_o), .FG_c(12'he09), .BG_c({12{1'b0}}), .CX_c(6'b001001), .CY_c(8'h3),
    .C_0(register_158_q), .C_1(register_159_q), .C_2(register_160_q), .C_3(register_161_q), .EN(1'b1),
    .CX_o(vgastring_40_cx_o), .CY_o(vgastring_40_cy_o), .C_o(vgastring_40_c_o), .FG_o(vgastring_40_fg_o),
    .BG_o(vgastring_40_bg_o));
  // vgatext vgatext_1: pin names not known; wires that end beside it: vgasync_1_h, vgasync_1_v, vgasync_1_pic, vgacharpos_1_p3, vgacharpos_1_p4, vgatext_1_p6, clock, vgastring_40_c_o, vgastring_40_fg_o, vgastring_40_bg_o, R, G, B, hs, vs, de, CA
  ROM #(.AddrBits(11), .Bits(16)) Char_ROM (.A(CA), .sel(1'b1), .D(Char_ROM_d));
  VGA vga_1 (.R(R), .G(G), .B(B), .H(hs), .V(vs), .C(clock));
  D_FF #(.Bits(16)) d_ff_1 (.D(Char_ROM_d), .C(clock), .Q(vgatext_1_p6));  // open: nQ

  // Other names for the same wires on the sheet: C = clock

  // Notes on the sheet:
  //   clock: Hz: 2147483647
  //   clk: Hz: 50
  //   contents of eeprom_1 (hex, n*v repeats v):
  //   7*41,43,41,41,49,41,41,41,45,41,0,45,37*0,44,536*0,43
  //   contents of Char_ROM (hex, n*v repeats v):
  //   35*0,8*180,0,0,8*180,12*0,3e7c,1e78,30*0,3e7c,3ffc,4182,6*6186
  //   ,4182,3e7c,3e7c,4182,6*6186,4182,3ffc,3e7c,10*0,3e7c,3ff8,4180
  //   ,6*6180,4180,3e7c,3e7c,182,6*186,182,1ffc,3e7c,10*0,3e00,3f00
  //   ,4188,6188,6198,61b0,61b0,61e0,61e0,4180,3e7c,3e7c,182,786,786
  //   ,d86,d86,1986,1186,1182,fc,7c,10*0,3e00,3f00,4180,6*6180,4180
  //   ,3f00,3e00,4000,6060,6060,6030,6030,6018,6008,4000,3e78,3e7c,12*0
  //   ,8,8,18,30,30,60,60,23*0,7c,78,200,600,600,c00,800,1800,1000,4*0
  //   ,1000,1800,800,c00,600,600,200,78,7c,10*0,3e00,1e00,40,60,60,30
  //   ,10,18,8,4*0,8,18,10,30,60,60,40,1e00,3e00,12*0,1188,1188,1998
  //   ,db0,db0,7e0,7e0,180,3e7c,3e7c,180,7e0,7e0,db0,db0,1998,1188,1188
  //   ,14*0,8*180,3e7c,3e7c,8*180,25*0,600,600,c00,c00,1800,1000,1000
  //   ,22*0,3e7c,3e7c,40*0,180,180,12*0,8,8,18,30,30,60,60,4*0,600,600
  //   ,c00,c00,1800,1000,1000,12*0,3e7c,3e7c,4006,600e,601a,6032,6036
  //   ,6066,6066,6006,0,0,6006,6606,6606,6c06,4c06,5806,7006,6002,3e7c,3e7c
  //   ,10*0,3e00,1f00,8*180,0,0,8*180,1ff8,3e7c,10*0,3e7c,1e7c,2,6*6
  //   ,2,3e7c,3e7c,4000,6*6000,4000,3e78,3e7c,10*0,3e7c,1e7c,2,6*6,2
  //   ,3e7c,3e7c,2,6*6,2,1e7c,3e7c,11*0,4002,7*6006,4002,3e7c,3e7c,2
  //   ,7*6,2,11*0,3e7c,3e78,4000,6*6000,4000,3e7c,3e7c,2,6*6,2,1e7c
  //   ,3e7c,10*0,3e7c,3e78,4000,6*6000,4000,3e7c,3e7c,4002,6*6006,4002
  //   ,3e7c,3e7c,10*0,3e7c,1e7c,2,7*6,0,0,8*6,2,11*0,3e7c,3e7c,4002
  //   ,6*6006,4002,3e7c,3e7c,4002,6*6006,4002,3e7c,3e7c,10*0,3e7c,3e7c
  //   ,4002,6*6006,4002,3e7c,3e7c,2,6*6,2,1e7c,3e7c,15*0,180,180,8*0
  //   ,180,180,17*0,8*180,0,0,0,600,600,c00,c00,1800,1000,1000,14*0
  //   ,40,c0,c0,180,180,300,300,4*0,300,300,180,180,c0,c0,40,17*0,3e7c,3e7c
  //   ,8*0,1e78,3e7c,17*0,200,300,300,180,180,c0,c0,4*0,c0,c0,180,180
  //   ,300,300,200,12*0,3e7c,1e7c,2,6*6,2,7c,fc,8*180,12*0,3e7c,3ffc
  //   ,4182,6*6186,6182,fc,7c,7*6000,4000,3e78,3e7c,10*0,3e7c,3e7c,4002
  //   ,6*6006,4002,3e7c,3e7c,4002,7*6006,4002,11*0,3e7c,1ffc,182,6*186
  //   ,182,3e7c,3e7c,182,6*186,182,1ffc,3e7c,10*0,3e7c,3e78,4000,7*6000
  //   ,0,0,7*6000,4000,3e78,3e7c,10*0,3e7c,1ffc,182,7*186,0,0,7*186
  //   ,182,1ffc,3e7c,10*0,3e7c,3e78,4000,6*6000,4000,3e7c,3e7c,4000
  //   ,6*6000,4000,3e78,3e7c,10*0,3e7c,3e78,4000,6*6000,4000,3e7c,3e7c
  //   ,4000,7*6000,4000,11*0,3e7c,3e78,4000,7*6000,7c,7c,6002,6*6006
  //   ,4002,3e7c,3e7c,11*0,4002,7*6006,4002,3e7c,3e7c,4002,7*6006,4002
  //   ,11*0,3e7c,1ff8,8*180,0,0,8*180,1ff8,3e7c,10*0,7c,7c,2,7*6,0,0
  //   ,7*6006,4002,3e7c,3e7c,11*0,4000,6008,6008,6018,6030,6030,6060,6060
  //   ,4000,3e00,3e00,4000,6060,6060,6030,6030,6018,6008,6008,4000,12*0
  //   ,4000,8*6000,0,0,7*6000,4000,3e78,3e7c,11*0,4002,6006,700e,581a
  //   ,4c32,6c36,6666,6666,6006,0,0,8*6186,4002,12*0,4002,6006,7006
  //   ,5806,4c06,6c06,6606,6606,6006,0,0,6006,6066,6066,6036,6032,601a
  //   ,600e,6006,4002,11*0,3e7c,3e7c,4002,7*6006,0,0,7*6006,4002,3e7c,3e7c
  //   ,10*0,3e7c,3e7c,4002,6*6006,4002,3e7c,3e7c,4000,7*6000,4000,11*0
  //   ,3e7c,3e7c,4002,7*6006,0,0,6006,6066,6066,6036,6032,601a,600e
  //   ,4006,3e7c,3e7c,10*0,3e7c,3e7c,4002,6*6006,4006,3e00,3e00,4000
  //   ,6060,6060,6030,6030,6018,6008,6008,4000,11*0,3e7c,3e78,4000,6*6000
  //   ,4000,3e7c,3e7c,2,6*6,2,1e7c,3e7c,10*0,3e7c,1ff8,8*180,0,0,8*180
  //   ,13*0,4002,8*6006,0,0,7*6006,4002,3e7c,3e7c,11*0,4000,6008,6008
  //   ,6018,6030,6030,6060,6060,6000,0,0,6000,6600,6600,6c00,4c00,5800
  //   ,7000,6000,4000,12*0,4002,8*6006,0,0,7*6186,4182,3ffc,3e7c,12*0
  //   ,1008,1008,1818,c30,c30,660,660,4*0,660,660,c30,c30,1818,1008,1008
  //   ,14*0,1008,1008,1818,c30,c30,660,660,0,0,0,8*180,12*0,3e7c,1e78
  //   ,0,8,18,30,30,60,60,4*0,600,600,c00,c00,1800,1000,0,1e78,3e7c
  //   ,10*0,3e00,3e00,4000,7*6000,0,0,7*6000,4000,3e00,3e00,12*0,1000,1000
  //   ,1800,c00,c00,600,600,4*0,60,60,30,30,18,8,8,12*0,7c,7c,2,7*6
  //   ,0,0,7*6,2,7c,7c,12*0,240,660,660,c30,810,1818,1008,43*0,1e78,3e7c
endmodule
