// Digital circuit !testing.dig as structural Verilog
module testing (
  input  in_1,
  input  in_2,
  input  in_3,
  input  in_4,
  input  in_5,
  input  in_6,
  input  in_7,
  input  in_8,
  input  in_10,
  input  in_11,
  input  in_12,
  input  in_13,
  input  in_14,
  input  in_15,
  input  in_16,
  input  in_17,
  input  in_81,
  input  in_82,
  input  in_83,
  input  in_84,
  input  in_85,
  input  in_86,
  input  CLK,
  input  EN_EN,
  input  EN,
  input  [7:0] LOC,
  input  EN_2,
  input  EN_3,
  input  in_96,
  input  [7:0] in_97,
  input  in_98,
  input  in_99,
  input  ON,
  input  OFF,
  output [7:0] Y,
  output [7:0] X,
  output [15:0] Z,
  output out_20,
  output out_21,
  output out_22,
  output out_23,
  output out_24,
  output out_25,
  output out_26,
  output out_27,
  output out_28,
  output out_29,
  output out_30,
  output out_31,
  output out_32,
  output out_33,
  output out_34,
  output out_35,
  output out_36,
  output out_37,
  output out_38,
  output out_39,
  output out_40,
  output out_41,
  output out_42,
  output out_43,
  output out_44,
  output out_45,
  output out_46,
  output out_47,
  output out_48,
  output out_49,
  output out_50,
  output out_51,
  output out_52,
  output out_53,
  output out_54,
  output out_55,
  output out_56,
  output out_57,
  output out_58,
  output out_59,
  output out_60,
  output out_61,
  output out_62,
  output out_63,
  output out_64,
  output out_65,
  output out_66,
  output out_67,
  output out_68,
  output out_69,
  output out_70,
  output out_71,
  output out_72,
  output out_73,
  output out_74,
  output out_75,
  output out_76,
  output out_77,
  output out_78,
  output out_79,
  output [13:0] O,
  output [5:0] out_87,
  output [15:0] out_88,
  output [7:0] out_92
);

  wire add_1_c_o, and_1_out, and_2_out, and_3_out, and_4_out, and_5_out, and_6_out, and_7_out, button_1_out,
       delay_1_out, delay_2_out, delay_3_out, delay_4_out, delay_5_out, delay_6_out, delay_7_out,
       driver_1_out, driver_2_out, driver_4_out, driver_9_out, driverinvsel_4_out, keyboard_1_av, not_1_out,
       not_2_out, not_3_out, not_4_out, not_5_out, OFF_out, ON_out, or_1_out, register_2_q, t_ff_1_nq,
       t_ff_1_q;
  wire [7:0] add_1_s, driver_7_out, driverinvsel_2_out;
  wire [15:0] eeprom_1_d;

  Delay #(.delayTime(10)) delay_1 (.in(EN_3), .out(delay_1_out));
  and and_1 (and_1_out, EN_3, not_1_out);
  not not_1 (not_1_out, delay_1_out);
  assign driver_1_out = and_1_out ? and_1_out : 1'bz;  // Driver driver_1
  and and_2 (and_2_out, t_ff_1_q, CLK);
  assign driver_2_out = EN_EN ? EN : 1'bz;  // Driver driver_2
  assign driver_2_out = ~EN_EN ? keyboard_1_av : 1'bz;  // DriverInvSel driverinvsel_1
  PullDown pulldown_1 (.out(driver_1_out));
  Keyboard keyboard_1 (.C(and_2_out), .en(driver_2_out), .D(out_88), .av(keyboard_1_av));
  assign driver_1_out = and_5_out ? and_5_out : 1'bz;  // Driver driver_3
  T_FF t_ff_1 (.T(driver_1_out), .C(delay_2_out), .Q(t_ff_1_q), .nQ(t_ff_1_nq));
  Delay #(.delayTime(2)) delay_2 (.in(driver_1_out), .out(delay_2_out));
  not not_2 (not_2_out, keyboard_1_av);
  not not_3 (not_3_out, delay_3_out);
  Delay #(.delayTime(10)) delay_3 (.in(not_2_out), .out(delay_3_out));
  and and_3 (and_3_out, and_2_out, keyboard_1_av);
  and and_4 (and_4_out, not_2_out, not_3_out);
  and and_5 (and_5_out, t_ff_1_q, and_4_out);
  Add #(.Bits(8)) add_1 (.a(out_92), .b(8'h1), .c_i(1'b0), .s(add_1_s), .c_o(add_1_c_o));
  assign driver_4_out = and_3_out ? and_3_out : 1'bz;  // Driver driver_4
  assign driverinvsel_2_out = ~EN_2 ? add_1_s : 8'bz;  // DriverInvSel driverinvsel_2
  assign driverinvsel_2_out = EN_2 ? LOC : 8'bz;  // Driver driver_5
  PullDown pulldown_2 (.out(driver_4_out));
  Delay #(.delayTime(10)) delay_4 (.in(driver_4_out), .out(delay_4_out));
  assign driver_4_out = EN_2 ? EN_2 : 1'bz;  // Driver driver_6
  Register #(.Bits(8)) register_1 (.D(driverinvsel_2_out), .C(delay_4_out), .en(driver_4_out), .Q(out_92));
  assign driver_7_out = in_96 ? in_97 : 8'bz;  // Driver driver_7
  assign driver_7_out = ~in_96 ? out_92 : 8'bz;  // DriverInvSel driverinvsel_3
  EEPROM #(.AddrBits(8), .Bits(16)) eeprom_1 (.A(driver_7_out), .CS(1'b1), .WE(and_2_out), .OE(in_98), .D(eeprom_1_d));
  assign eeprom_1_d = and_2_out ? out_88 : 16'bz;  // Driver driver_8
  Delay #(.delayTime(10)) delay_5 (.in(ON_out), .out(delay_5_out));
  Button u_ON (.out(ON_out));
  Delay #(.delayTime(10)) delay_6 (.in(OFF_out), .out(delay_6_out));
  Button u_OFF (.out(OFF_out));
  not not_4 (not_4_out, delay_5_out);
  not not_5 (not_5_out, delay_6_out);
  and and_6 (and_6_out, not_4_out, ON_out);
  and and_7 (and_7_out, not_5_out, OFF_out);
  Button button_1 (.out(button_1_out));
  or or_1 (or_1_out, and_6_out, and_7_out);
  assign driver_9_out = and_6_out ? and_6_out : 1'bz;  // Driver driver_9
  assign driverinvsel_4_out = ~or_1_out ? in_99 : 1'bz;  // DriverInvSel driverinvsel_4
  assign driver_9_out = ~or_1_out ? button_1_out : 1'bz;  // DriverInvSel driverinvsel_5
  assign driverinvsel_4_out = and_6_out ? ON : 1'bz;  // Driver driver_10
  assign driver_9_out = and_7_out ? and_7_out : 1'bz;  // Driver driver_11
  assign driverinvsel_4_out = and_7_out ? OFF : 1'bz;  // Driver driver_12
  Delay #(.delayTime(10)) delay_7 (.in(driver_9_out), .out(delay_7_out));
  Register register_2 (.D(driverinvsel_4_out), .C(delay_7_out), .en(driver_9_out), .Q(register_2_q));

  assign O = {in_1, in_2, in_3, in_4, in_5, in_6, in_7, in_8, in_12, in_13, in_14, in_15, in_16, in_17};
  assign out_20 = in_1;
  assign out_21 = in_2;
  assign out_22 = in_3;
  assign out_23 = in_4;
  assign out_24 = in_5;
  assign out_25 = in_6;
  assign out_26 = in_7;
  assign out_27 = in_8;
  assign out_28 = in_10;
  assign out_29 = in_11;
  assign out_30 = in_12;
  assign out_31 = in_13;
  assign out_32 = in_14;
  assign out_33 = in_15;
  assign out_34 = in_16;
  assign out_35 = in_17;
  assign out_36 = in_10;
  assign out_37 = in_11;
  assign out_38 = in_7;
  assign out_39 = in_8;
  assign out_40 = in_5;
  assign out_41 = in_6;
  assign out_42 = in_3;
  assign out_43 = in_4;
  assign out_44 = in_16;
  assign out_45 = in_17;
  assign out_46 = in_14;
  assign out_47 = in_15;
  assign out_48 = in_12;
  assign out_49 = in_13;
  assign out_50 = in_1;
  assign out_51 = in_2;
  assign out_52 = in_1;
  assign out_53 = in_2;
  assign out_54 = in_3;
  assign out_55 = in_4;
  assign out_56 = in_5;
  assign out_57 = in_6;
  assign out_58 = in_7;
  assign out_59 = in_8;
  assign out_60 = in_12;
  assign out_61 = in_13;
  assign out_62 = in_14;
  assign out_63 = in_15;
  assign out_64 = in_16;
  assign out_65 = in_17;
  assign out_66 = in_16;
  assign out_67 = in_17;
  assign out_68 = in_14;
  assign out_69 = in_15;
  assign out_70 = in_12;
  assign out_71 = in_13;
  assign out_72 = in_7;
  assign out_73 = in_8;
  assign out_74 = in_5;
  assign out_75 = in_6;
  assign out_76 = in_3;
  assign out_77 = in_4;
  assign out_78 = in_1;
  assign out_79 = in_2;
  assign out_87 = {in_86, in_85, in_84, in_83, in_82, in_81};
  assign X = {in_10, in_11, in_12, in_13, in_14, in_15, in_16, in_17};
  assign Y = {in_1, in_2, in_3, in_4, in_5, in_6, in_7, in_8};
  assign Z = {in_1, in_2, in_3, in_4, in_5, in_6, in_7, in_8, in_10, in_11, in_12, in_13, in_14, in_15, in_16, in_17};

  // Notes on the sheet:
  //   CLK: Hz: 100
  //   ON: default 1
  //   X
  //   Y
  //   MUST START TEXT WITH ANY CHAR (WILL BE IGNORED)
  //   WHEN AV IS ON, TOGGLE DELAY? MUST JUMP TO A PART 
  //   THAT TOGGLES EN ON KEYBOARD...
  //   CPU WILL ADD RANDOM CHAR AT END OF STRING
  //   contents of eeprom_1 (hex, n*v repeats v):
  //   6c70,73,20,69,73,20,61,74,65,74,73,88e3
endmodule
