// Digital circuit !testing3.dig as structural Verilog
module testing3 (
  input  [15:0] IN,
  output [15:0] IN_OUT,
  output [6:0] OUT,
  output [8:0] IN_REST
);

  wire comparator_1_eq, comparator_1_gt, comparator_1_lt, comparator_2_eq, comparator_2_gt, comparator_2_lt,
       comparator_3_eq, comparator_3_gt, comparator_3_lt, comparator_4_eq, comparator_4_gt, comparator_4_lt,
       comparator_5_eq, comparator_5_gt, comparator_5_lt, comparator_6_eq, comparator_6_gt, comparator_6_lt,
       comparator_7_eq, comparator_7_gt, comparator_7_lt, comparator_8_eq, comparator_8_gt, comparator_8_lt,
       comparator_9_eq, comparator_9_gt, comparator_9_lt, comparator_10_eq, comparator_10_gt,
       comparator_10_lt, comparator_11_eq, comparator_11_gt, comparator_11_lt, comparator_12_eq,
       comparator_12_gt, comparator_12_lt, comparator_13_eq, comparator_13_gt, comparator_13_lt,
       comparator_14_eq, comparator_14_gt, comparator_14_lt, comparator_15_eq, comparator_15_gt,
       comparator_15_lt, comparator_16_eq, comparator_16_gt, comparator_16_lt, comparator_17_eq,
       comparator_17_gt, comparator_17_lt, comparator_18_eq, comparator_18_gt, comparator_18_lt,
       comparator_19_eq, comparator_19_gt, comparator_19_lt, comparator_20_eq, comparator_20_gt,
       comparator_20_lt, comparator_21_eq, comparator_21_gt, comparator_21_lt, comparator_22_eq,
       comparator_22_gt, comparator_22_lt, comparator_23_eq, comparator_23_gt, comparator_23_lt,
       comparator_24_eq, comparator_24_gt, comparator_24_lt, comparator_25_eq, comparator_25_gt,
       comparator_25_lt, comparator_26_eq, comparator_26_gt, comparator_26_lt, driver_1_out;

  Comparator #(.Bits(7)) comparator_1 (
    .a(7'b1100001), .b(IN[6:0]), .gt(comparator_1_gt), .eq(comparator_1_eq), .lt(comparator_1_lt));
  Comparator #(.Bits(7)) comparator_2 (
    .a(7'b1100010), .b(IN[6:0]), .gt(comparator_2_gt), .eq(comparator_2_eq), .lt(comparator_2_lt));
  Comparator #(.Bits(7)) comparator_3 (
    .a(7'b1100011), .b(IN[6:0]), .gt(comparator_3_gt), .eq(comparator_3_eq), .lt(comparator_3_lt));
  Comparator #(.Bits(7)) comparator_4 (
    .a(7'b1100100), .b(IN[6:0]), .gt(comparator_4_gt), .eq(comparator_4_eq), .lt(comparator_4_lt));
  Comparator #(.Bits(7)) comparator_5 (
    .a(7'b1100101), .b(IN[6:0]), .gt(comparator_5_gt), .eq(comparator_5_eq), .lt(comparator_5_lt));
  Comparator #(.Bits(7)) comparator_6 (
    .a(7'b1100110), .b(IN[6:0]), .gt(comparator_6_gt), .eq(comparator_6_eq), .lt(comparator_6_lt));
  Comparator #(.Bits(7)) comparator_7 (
    .a(7'b1100111), .b(IN[6:0]), .gt(comparator_7_gt), .eq(comparator_7_eq), .lt(comparator_7_lt));
  Comparator #(.Bits(7)) comparator_8 (
    .a(7'b1101000), .b(IN[6:0]), .gt(comparator_8_gt), .eq(comparator_8_eq), .lt(comparator_8_lt));
  Comparator #(.Bits(7)) comparator_9 (
    .a(7'b1101001), .b(IN[6:0]), .gt(comparator_9_gt), .eq(comparator_9_eq), .lt(comparator_9_lt));
  Comparator #(.Bits(7)) comparator_10 (
    .a(7'b1101010), .b(IN[6:0]), .gt(comparator_10_gt), .eq(comparator_10_eq), .lt(comparator_10_lt));
  Comparator #(.Bits(7)) comparator_11 (
    .a(7'b1101011), .b(IN[6:0]), .gt(comparator_11_gt), .eq(comparator_11_eq), .lt(comparator_11_lt));
  Comparator #(.Bits(7)) comparator_12 (
    .a(7'b1101100), .b(IN[6:0]), .gt(comparator_12_gt), .eq(comparator_12_eq), .lt(comparator_12_lt));
  Comparator #(.Bits(7)) comparator_13 (
    .a(7'b1101101), .b(IN[6:0]), .gt(comparator_13_gt), .eq(comparator_13_eq), .lt(comparator_13_lt));
  Comparator #(.Bits(7)) comparator_14 (
    .a(7'b1101110), .b(IN[6:0]), .gt(comparator_14_gt), .eq(comparator_14_eq), .lt(comparator_14_lt));
  Comparator #(.Bits(7)) comparator_15 (
    .a(7'b1101111), .b(IN[6:0]), .gt(comparator_15_gt), .eq(comparator_15_eq), .lt(comparator_15_lt));
  Comparator #(.Bits(7)) comparator_16 (
    .a(7'b1110000), .b(IN[6:0]), .gt(comparator_16_gt), .eq(comparator_16_eq), .lt(comparator_16_lt));
  Comparator #(.Bits(7)) comparator_17 (
    .a(7'b1110001), .b(IN[6:0]), .gt(comparator_17_gt), .eq(comparator_17_eq), .lt(comparator_17_lt));
  Comparator #(.Bits(7)) comparator_18 (
    .a(7'b1110010), .b(IN[6:0]), .gt(comparator_18_gt), .eq(comparator_18_eq), .lt(comparator_18_lt));
  Comparator #(.Bits(7)) comparator_19 (
    .a(7'b1110011), .b(IN[6:0]), .gt(comparator_19_gt), .eq(comparator_19_eq), .lt(comparator_19_lt));
  Comparator #(.Bits(7)) comparator_20 (
    .a(7'b1110100), .b(IN[6:0]), .gt(comparator_20_gt), .eq(comparator_20_eq), .lt(comparator_20_lt));
  Comparator #(.Bits(7)) comparator_21 (
    .a(7'b1110101), .b(IN[6:0]), .gt(comparator_21_gt), .eq(comparator_21_eq), .lt(comparator_21_lt));
  Comparator #(.Bits(7)) comparator_22 (
    .a(7'b1110110), .b(IN[6:0]), .gt(comparator_22_gt), .eq(comparator_22_eq), .lt(comparator_22_lt));
  Comparator #(.Bits(7)) comparator_23 (
    .a(7'b1110111), .b(IN[6:0]), .gt(comparator_23_gt), .eq(comparator_23_eq), .lt(comparator_23_lt));
  Comparator #(.Bits(7)) comparator_24 (
    .a(7'b1111000), .b(IN[6:0]), .gt(comparator_24_gt), .eq(comparator_24_eq), .lt(comparator_24_lt));
  Comparator #(.Bits(7)) comparator_25 (
    .a(7'b1111001), .b(IN[6:0]), .gt(comparator_25_gt), .eq(comparator_25_eq), .lt(comparator_25_lt));
  Comparator #(.Bits(7)) comparator_26 (
    .a(7'b1111010), .b(IN[6:0]), .gt(comparator_26_gt), .eq(comparator_26_eq), .lt(comparator_26_lt));
  assign OUT = ~driver_1_out ? IN[6:0] : 7'bz;  // DriverInvSel driverinvsel_1
  assign driver_1_out = comparator_1_eq ? comparator_1_eq : 1'bz;  // Driver driver_1
  assign driver_1_out = comparator_2_eq ? comparator_2_eq : 1'bz;  // Driver driver_2
  assign driver_1_out = comparator_3_eq ? comparator_3_eq : 1'bz;  // Driver driver_3
  assign driver_1_out = comparator_4_eq ? comparator_4_eq : 1'bz;  // Driver driver_4
  assign driver_1_out = comparator_5_eq ? comparator_5_eq : 1'bz;  // Driver driver_5
  assign driver_1_out = comparator_6_eq ? comparator_6_eq : 1'bz;  // Driver driver_6
  assign driver_1_out = comparator_7_eq ? comparator_7_eq : 1'bz;  // Driver driver_7
  assign driver_1_out = comparator_8_eq ? comparator_8_eq : 1'bz;  // Driver driver_8
  assign driver_1_out = comparator_9_eq ? comparator_9_eq : 1'bz;  // Driver driver_9
  assign driver_1_out = comparator_10_eq ? comparator_10_eq : 1'bz;  // Driver driver_10
  assign driver_1_out = comparator_11_eq ? comparator_11_eq : 1'bz;  // Driver driver_11
  assign driver_1_out = comparator_12_eq ? comparator_12_eq : 1'bz;  // Driver driver_12
  assign driver_1_out = comparator_13_eq ? comparator_13_eq : 1'bz;  // Driver driver_13
  assign driver_1_out = comparator_14_eq ? comparator_14_eq : 1'bz;  // Driver driver_14
  assign driver_1_out = comparator_15_eq ? comparator_15_eq : 1'bz;  // Driver driver_15
  assign driver_1_out = comparator_16_eq ? comparator_16_eq : 1'bz;  // Driver driver_16
  assign driver_1_out = comparator_17_eq ? comparator_17_eq : 1'bz;  // Driver driver_17
  assign driver_1_out = comparator_18_eq ? comparator_18_eq : 1'bz;  // Driver driver_18
  assign driver_1_out = comparator_19_eq ? comparator_19_eq : 1'bz;  // Driver driver_19
  assign driver_1_out = comparator_20_eq ? comparator_20_eq : 1'bz;  // Driver driver_20
  assign driver_1_out = comparator_21_eq ? comparator_21_eq : 1'bz;  // Driver driver_21
  assign driver_1_out = comparator_22_eq ? comparator_22_eq : 1'bz;  // Driver driver_22
  assign driver_1_out = comparator_23_eq ? comparator_23_eq : 1'bz;  // Driver driver_23
  assign driver_1_out = comparator_24_eq ? comparator_24_eq : 1'bz;  // Driver driver_24
  assign driver_1_out = comparator_25_eq ? comparator_25_eq : 1'bz;  // Driver driver_25
  assign driver_1_out = comparator_26_eq ? comparator_26_eq : 1'bz;  // Driver driver_26
  assign OUT = comparator_1_eq ? 7'b1000001 : 7'bz;  // Driver driver_27
  assign OUT = comparator_2_eq ? 7'b1000010 : 7'bz;  // Driver driver_28
  assign OUT = comparator_3_eq ? 7'b1000011 : 7'bz;  // Driver driver_29
  assign OUT = comparator_4_eq ? 7'b1000100 : 7'bz;  // Driver driver_30
  assign OUT = comparator_5_eq ? 7'b1000101 : 7'bz;  // Driver driver_31
  assign OUT = comparator_6_eq ? 7'b1000110 : 7'bz;  // Driver driver_32
  assign OUT = comparator_7_eq ? 7'b1000111 : 7'bz;  // Driver driver_33
  assign OUT = comparator_8_eq ? 7'b1001000 : 7'bz;  // Driver driver_34
  assign OUT = comparator_9_eq ? 7'b1001001 : 7'bz;  // Driver driver_35
  assign OUT = comparator_10_eq ? 7'b1001010 : 7'bz;  // Driver driver_36
  assign OUT = comparator_11_eq ? 7'b1001011 : 7'bz;  // Driver driver_37
  assign OUT = comparator_12_eq ? 7'b1001100 : 7'bz;  // Driver driver_38
  assign OUT = comparator_13_eq ? 7'b1001101 : 7'bz;  // Driver driver_39
  assign OUT = comparator_14_eq ? 7'b1001110 : 7'bz;  // Driver driver_40
  assign OUT = comparator_15_eq ? 7'b1001111 : 7'bz;  // Driver driver_41
  assign OUT = comparator_16_eq ? 7'b1010000 : 7'bz;  // Driver driver_42
  assign OUT = comparator_17_eq ? 7'b1010001 : 7'bz;  // Driver driver_43
  assign OUT = comparator_18_eq ? 7'b1010010 : 7'bz;  // Driver driver_44
  assign OUT = comparator_19_eq ? 7'b1010011 : 7'bz;  // Driver driver_45
  assign OUT = comparator_20_eq ? 7'b1010100 : 7'bz;  // Driver driver_46
  assign OUT = comparator_21_eq ? 7'b1010101 : 7'bz;  // Driver driver_47
  assign OUT = comparator_22_eq ? 7'b1010110 : 7'bz;  // Driver driver_48
  assign OUT = comparator_23_eq ? 7'b1010111 : 7'bz;  // Driver driver_49
  assign OUT = comparator_24_eq ? 7'b1011000 : 7'bz;  // Driver driver_50
  assign OUT = comparator_25_eq ? 7'b1011001 : 7'bz;  // Driver driver_51
  assign OUT = comparator_26_eq ? 7'b1011010 : 7'bz;  // Driver driver_52
  PullDown pulldown_1 (.out(driver_1_out));

  assign IN_OUT = IN;
  assign IN_REST = IN[15:7];

  // Notes on the sheet:
  //   IN: default 65
endmodule
