// Digital circuit CPR.dig as structural Verilog
module CPR (
  input  clock,
  input  clock_manual,
  input  manual,
  input  clear,
  output ovfl,
  output [1:0] count,
  output \null ,
  output next,
  output copy,
  output run
);

  wire driver_1_out, driverinvsel_2_out, not_1_out, not_2_out, not_3_out, not_4_out;

  assign driver_1_out = clock_manual ? manual : 1'bz;  // Driver driver_1
  PullDown pulldown_1 (.out(driver_1_out));
  assign driver_1_out = ~clock_manual ? clock : 1'bz;  // DriverInvSel driverinvsel_1
  assign driverinvsel_2_out = ~clear ? driver_1_out : 1'bz;  // DriverInvSel driverinvsel_2
  Counter #(.Bits(2)) counter_1 (.en(driverinvsel_2_out), .C(driverinvsel_2_out), .clr(clear), .out(count), .ovf(ovfl));
  assign driverinvsel_2_out = clear ? clear : 1'bz;  // Driver driver_2
  not not_1 (not_1_out, count[0]);
  not not_2 (not_2_out, count[1]);
  not not_3 (not_3_out, count[1]);
  not not_4 (not_4_out, count[0]);
  and and_1 (\null , not_1_out, not_2_out);
  and and_2 (copy, count[0], not_3_out);
  and and_3 (run, not_4_out, count[1]);
  and and_4 (next, count[0], count[1]);

  // Notes on the sheet:
  //   PAS11-v5 CPR
endmodule
