// Digital circuit clkdecode.dig as structural Verilog
module clkdecode (
  input  [2:0] i,
  output o1,
  output o2,
  output o3,
  output o4,
  output o5,
  output o6,
  output o7,
  output o8
);

  wire not_1_out, not_2_out, not_3_out, not_4_out, not_5_out, not_6_out, not_7_out, not_8_out, not_9_out,
       not_10_out, not_11_out, not_12_out;

  not not_1 (not_1_out, i[0]);
  not not_2 (not_2_out, i[1]);
  not not_3 (not_3_out, i[2]);
  not not_4 (not_4_out, i[1]);
  not not_5 (not_5_out, i[2]);
  not not_6 (not_6_out, i[0]);
  not not_7 (not_7_out, i[2]);
  not not_8 (not_8_out, i[2]);
  not not_9 (not_9_out, i[0]);
  not not_10 (not_10_out, i[1]);
  not not_11 (not_11_out, i[1]);
  not not_12 (not_12_out, i[0]);
  and and_1 (o1, not_1_out, not_2_out, not_3_out);
  and and_2 (o2, i[0], not_4_out, not_5_out);
  and and_3 (o3, not_6_out, i[1], not_7_out);
  and and_4 (o4, i[0], i[1], not_8_out);
  and and_5 (o5, not_9_out, not_10_out, i[2]);
  and and_6 (o6, i[0], not_11_out, i[2]);
  and and_7 (o7, not_12_out, i[1], i[2]);
  and and_8 (o8, i[0], i[1], i[2]);
endmodule
