// Digital circuit CORE.dig as structural Verilog
module CORE (
  input  [7:0] M_LD8___D,
  input  [15:0] M_LD___A,
  input  M_LD8___EN,
  input  M_LD___EN,
  input  [15:0] M_ST___A,
  input  [7:0] M_ST___D,
  input  M_ST___EN,
  input  [15:0] M_ST___A_2,
  input  M_ST___EN_2,
  input  [15:0] M_LD16___D,
  input  M_LD16___EN,
  input  CLK1,
  input  in_28,
  input  in_29,
  input  in_30,
  input  [15:0] BRKADDR,
  input  [24:0] VAL,
  input  [7:0] ADDR,
  input  [7:0] BRMADDR,
  input  _1,
  input  [3:0] in_52,
  input  _100,
  input  MAN,
  input  in_58,
  input  in_59,
  input  in_60,
  input  in_61,
  input  in_62,
  input  in_63,
  input  in_64,
  input  in_65,
  input  in_66,
  input  in_67,
  input  in_68,
  input  in_69,
  input  in_70,
  input  in_71,
  input  in_72,
  input  in_73,
  input  in_74,
  input  in_75,
  input  in_76,
  input  in_77,
  input  in_78,
  input  in_79,
  input  in_80,
  input  in_81,
  input  in_82,
  input  [7:0] M_Y,
  input  in_89,
  input  in_90,
  input  in_91,
  input  in_92,
  input  [1:0] M_GHGMD_D,
  input  MAN_OP_EN,
  input  [7:0] MAN_OP_DATA,
  input  clk,
  input  in_97,
  input  in_99,
  input  VGA_clock,
  input  [7:0] D,
  input  [7:0] A,
  input  clk_2,
  input  [7:0] D_x,
  input  [7:0] A_2,
  input  clk_3,
  input  [7:0] D_y,
  input  [7:0] X,
  input  [7:0] Y,
  input  [24:0] in_155,
  input  clk_4,
  input  EN_EN,
  input  EN,
  input  [7:0] LOC,
  input  [6:0] in_164,
  input  [6:0] in_166,
  input  clk_5,
  input  [7:0] X_3,
  input  [7:0] Y_3,
  input  in_176,
  input  in_177,
  input  in_178,
  input  in_179,
  input  in_180,
  input  in_181,
  input  in_182,
  input  in_183,
  input  in_185,
  input  in_186,
  input  in_187,
  input  in_188,
  input  in_189,
  input  in_190,
  input  in_191,
  input  in_192,
  input  in_194,
  input  in_195,
  input  in_196,
  input  in_197,
  input  in_198,
  input  in_199,
  input  in_200,
  input  in_201,
  input  [15:0] in_219,
  input  [7:0] in_225,
  input  [1:0] in_227,
  input  in_228,
  input  in_229,
  input  in_230,
  input  in_231,
  input  [7:0] in_232,
  input  [7:0] in_235,
  input  [7:0] A_3,
  input  [5:0] in_241,
  input  [7:0] in_242,
  input  [7:0] M_IN,
  input  M_C,
  input  M_WR,
  input  M_RD,
  input  clk_6,
  input  in_330,
  input  [7:0] EXT_A,
  input  EXT_L_MAN,
  output f1_16384,
  output _8192,
  output f2_2_4092,
  output _2048,
  output f4_2_1024,
  output f4_2_512,
  output _256,
  output f6_2_128,
  output f7_2_64,
  output f8_2_1,
  output _32,
  output _16,
  output _8,
  output _4,
  output _2,
  output [2:0] out_31,
  output HEARTBEAT,
  output out_33,
  output [1:0] out_34,
  output out_35,
  output out_37,
  output [15:0] PC,
  output [15:0] out_39,
  output out_43,
  output [7:0] out_44,
  output [7:0] out_45,
  output [24:0] out_46,
  output out_47,
  output [15:0] out_48,
  output [7:0] out_49,
  output [1:0] out_50,
  output [1:0] out_53,
  output [3:0] out_56,
  output [3:0] out_57,
  output [24:0] out_83,
  output out_84,
  output out_85,
  output out_86,
  output [7:0] W_MUL,
  output [2:0] out_98,
  output [7:0] out_100,
  output [15:0] out_101,
  output [7:0] out_102,
  output [3:0] R,
  output [3:0] G,
  output [3:0] B,
  output hs,
  output vs,
  output de,
  output [10:0] CA,
  output [7:0] out_114,
  output [6:0] out_115,
  output [5:0] out_119,
  output [13:0] out_120,
  output out_121,
  output [7:0] out_122,
  output [1:0] out_126,
  output [5:0] out_127,
  output [7:0] out_128,
  output [13:0] out_129,
  output out_130,
  output out_131,
  output out_132,
  output out_133,
  output out_134,
  output out_135,
  output out_136,
  output out_137,
  output out_138,
  output out_139,
  output out_140,
  output out_141,
  output out_142,
  output out_143,
  output out_144,
  output out_145,
  output out_146,
  output out_147,
  output out_148,
  output out_149,
  output out_150,
  output out_151,
  output out_152,
  output out_153,
  output out_154,
  output [7:0] out_159,
  output out_160,
  output [15:0] out_162,
  output [8:0] out_163,
  output [8:0] out_165,
  output [8:0] out_167,
  output [6:0] out_169,
  output [6:0] out_170,
  output [7:0] Y_2,
  output [5:0] X_2,
  output [13:0] Z,
  output [15:0] out_184,
  output [7:0] out_193,
  output [7:0] out_202,
  output out_203,
  output out_204,
  output out_205,
  output out_206,
  output out_207,
  output out_208,
  output out_209,
  output out_210,
  output out_211,
  output out_212,
  output out_213,
  output out_214,
  output out_215,
  output out_216,
  output out_217,
  output out_218,
  output [7:0] out_220,
  output [7:0] out_221,
  output [7:0] out_222,
  output [7:0] out_223,
  output [7:0] out_224,
  output out_226,
  output [7:0] out_233,
  output [6:0] out_234,
  output [6:0] out_236,
  output [2:0] out_237,
  output [2:0] out_238,
  output [6:0] out_240,
  output [13:0] out_243,
  output [6:0] out_244,
  output [6:0] out_245,
  output [6:0] out_246,
  output [6:0] out_247,
  output [6:0] out_248,
  output [6:0] out_249,
  output [6:0] out_250,
  output [6:0] out_251,
  output [6:0] out_252,
  output [6:0] out_253,
  output [6:0] out_254,
  output [6:0] out_255,
  output [6:0] out_256,
  output [6:0] out_257,
  output [6:0] out_258,
  output [6:0] out_259,
  output [6:0] out_260,
  output [6:0] out_261,
  output [6:0] out_262,
  output [6:0] out_263,
  output [6:0] out_264,
  output [6:0] out_265,
  output [6:0] out_266,
  output [6:0] out_267,
  output [6:0] out_268,
  output [6:0] out_269,
  output [6:0] out_270,
  output [6:0] out_271,
  output [6:0] out_272,
  output [6:0] out_273,
  output [6:0] out_274,
  output [6:0] out_275,
  output [6:0] out_276,
  output [6:0] out_277,
  output [6:0] out_278,
  output [6:0] out_279,
  output [6:0] out_280,
  output [6:0] out_281,
  output [6:0] out_282,
  output [6:0] out_283,
  output [6:0] out_284,
  output [6:0] out_285,
  output [6:0] out_286,
  output [6:0] out_287,
  output [6:0] out_288,
  output [6:0] out_289,
  output [6:0] out_290,
  output [6:0] out_291,
  output [6:0] out_292,
  output [6:0] out_293,
  output [6:0] out_294,
  output [6:0] out_295,
  output [6:0] out_296,
  output [6:0] out_297,
  output [6:0] out_298,
  output [6:0] out_299,
  output [6:0] out_300,
  output [6:0] out_301,
  output [6:0] out_302,
  output [6:0] out_303,
  output [6:0] out_304,
  output [6:0] out_305,
  output [6:0] out_306,
  output [6:0] out_307,
  output [6:0] out_308,
  output [6:0] out_309,
  output [6:0] out_310,
  output [6:0] out_311,
  output [6:0] out_312,
  output [6:0] out_313,
  output [6:0] out_314,
  output [6:0] out_315,
  output [6:0] out_316,
  output [6:0] out_317,
  output [6:0] out_318,
  output [6:0] out_319,
  output [6:0] out_320,
  output [7:0] out_325,
  output out_326,
  output [6:0] out_327,
  output [3:0] out_328,
  output [7:0] out_331,
  output [24:0] out_333
);

  wire A_EN, ADC, ADD, add_7_c_o, add_9_c_o, add_10_c_o, AND, and_1_out, and_2_out, and_3_out, and_4_out,
       and_6_out, and_7_out, and_8_out, and_9_out, and_10_out, and_11_out, and_12_out, and_13_out,
       and_14_out, and_15_out, and_16_out, and_17_out, and_18_out, and_19_out, and_20_out, and_27_out,
       and_28_out, and_29_out, and_30_out, and_31_out, and_32_out, and_33_out, and_38_out, and_39_out,
       and_40_out, and_41_out, and_42_out, and_43_out, and_53_out, and_54_out, and_55_out, and_56_out,
       and_57_out, and_58_out, and_59_out, and_60_out, and_61_out, and_62_out, and_63_out, and_64_out,
       and_65_out, and_66_out, and_67_out, and_68_out, and_69_out, and_70_out, and_71_out, and_72_out,
       and_73_out, and_74_out, and_75_out, and_76_out, and_77_out, and_78_out, and_79_out, and_80_out,
       and_81_out, and_82_out, and_83_out, and_84_out, and_85_out, and_86_out, and_87_out, and_88_out,
       and_89_out, and_90_out, and_91_out, and_92_out, and_93_out, and_94_out, and_95_out, and_96_out,
       and_97_out, and_98_out, and_103_out, and_104_out, and_105_out, and_106_out, and_107_out, and_108_out,
       and_109_out, and_110_out, and_111_out, and_112_out, and_113_out, and_114_out, and_115_out,
       and_116_out, and_117_out, and_120_out, and_121_out, and_122_out, ASL, ASR, B_EN, BBE, BCA, BCC, BCS,
       BEQ, BMI, BNC, BNE, BNG, BNN, BNO, BNZ, BOV, BPL, BR, BRK, BRK_out, BRM, BRM_out, BSE, button_1_out,
       BZE, C_EN, CBR, CHGMD, CLB, CLC, CLE, clkdecode_1_o1, clkdecode_1_o2, clkdecode_1_o3, clkdecode_1_o4,
       clkdecode_1_o5, clkdecode_1_o6, clkdecode_1_o7, clkdecode_1_o8, CLN, CLS, CLV, CLZ, CMP, CNT,
       comparator_1_eq, comparator_1_gt, comparator_1_lt, comparator_3_eq, comparator_3_gt, comparator_3_lt,
       comparator_4_eq, comparator_4_gt, comparator_4_lt, comparator_5_eq, comparator_6_eq, comparator_7_eq,
       comparator_8_eq, comparator_9_eq, comparator_10_eq, comparator_11_eq, comparator_12_eq,
       comparator_13_eq, comparator_14_eq, comparator_15_eq, comparator_16_eq, comparator_17_eq,
       comparator_18_eq, comparator_19_eq, comparator_20_eq, comparator_21_eq, comparator_21_gt,
       comparator_21_lt, comparator_22_eq, comparator_22_gt, comparator_22_lt, comparator_23_eq,
       comparator_23_gt, comparator_23_lt, comparator_24_eq, comparator_24_gt, comparator_24_lt,
       comparator_25_eq, comparator_26_eq, comparator_27_eq, comparator_28_eq, comparator_29_eq,
       comparator_30_eq, comparator_31_eq, comparator_32_eq, comparator_33_eq, comparator_34_eq,
       comparator_35_eq, comparator_36_eq, comparator_37_eq, comparator_38_eq, comparator_39_eq,
       comparator_40_eq, comparator_41_eq, comparator_41_gt, comparator_41_lt, comparator_42_eq,
       comparator_42_gt, comparator_42_lt, comparator_43_eq, comparator_43_gt, comparator_43_lt,
       comparator_44_eq, comparator_44_gt, comparator_44_lt, comparator_45_eq, comparator_46_eq,
       comparator_47_eq, comparator_48_eq, comparator_49_eq, comparator_50_eq, comparator_51_eq,
       comparator_52_eq, comparator_53_eq, comparator_54_eq, comparator_55_eq, comparator_56_eq,
       comparator_57_eq, comparator_58_eq, comparator_59_eq, comparator_60_eq, comparator_61_eq,
       comparator_61_gt, comparator_61_lt, comparator_62_eq, comparator_62_gt, comparator_62_lt,
       comparator_63_eq, comparator_63_gt, comparator_63_lt, comparator_64_eq, comparator_64_gt,
       comparator_64_lt, comparator_65_eq, comparator_66_eq, comparator_67_eq, comparator_68_eq,
       comparator_69_eq, comparator_70_eq, comparator_71_eq, comparator_72_eq, comparator_73_eq,
       comparator_74_eq, comparator_75_eq, comparator_76_eq, comparator_77_eq, comparator_78_eq,
       comparator_79_eq, comparator_80_eq, comparator_81_eq, comparator_81_gt, comparator_81_lt,
       comparator_82_eq, comparator_82_gt, comparator_82_lt, comparator_83_eq, comparator_83_gt,
       comparator_83_lt, comparator_84_eq, comparator_84_gt, comparator_84_lt, comparator_85_eq,
       comparator_86_eq, comparator_87_eq, comparator_88_eq, comparator_89_eq, comparator_90_eq,
       comparator_91_eq, comparator_92_eq, comparator_93_eq, comparator_94_eq, comparator_95_eq,
       comparator_96_eq, comparator_97_eq, comparator_98_eq, comparator_99_eq, comparator_100_eq,
       comparator_101_eq, comparator_101_gt, comparator_101_lt, comparator_102_eq, comparator_102_gt,
       comparator_102_lt, comparator_103_eq, comparator_103_gt, comparator_103_lt, comparator_104_eq,
       comparator_104_gt, comparator_104_lt, comparator_105_eq, comparator_106_eq, comparator_107_eq,
       comparator_108_eq, comparator_109_eq, comparator_110_eq, comparator_111_eq, comparator_112_eq,
       comparator_113_eq, comparator_114_eq, comparator_115_eq, comparator_116_eq, comparator_117_eq,
       comparator_118_eq, comparator_119_eq, comparator_120_eq, comparator_121_eq, comparator_121_gt,
       comparator_121_lt, comparator_122_eq, comparator_122_gt, comparator_122_lt, comparator_123_eq,
       comparator_123_gt, comparator_123_lt, comparator_124_eq, comparator_124_gt, comparator_124_lt,
       comparator_125_eq, comparator_126_eq, comparator_127_eq, comparator_128_eq, comparator_129_eq,
       comparator_130_eq, comparator_131_eq, comparator_132_eq, comparator_133_eq, comparator_134_eq,
       comparator_135_eq, comparator_136_eq, comparator_137_eq, comparator_138_eq, comparator_139_eq,
       comparator_140_eq, comparator_141_eq, comparator_141_gt, comparator_141_lt, comparator_142_eq,
       comparator_142_gt, comparator_142_lt, comparator_143_eq, comparator_143_gt, comparator_143_lt,
       comparator_144_eq, comparator_144_gt, comparator_144_lt, comparator_145_eq, comparator_146_eq,
       comparator_147_eq, comparator_148_eq, comparator_149_eq, comparator_150_eq, comparator_151_eq,
       comparator_152_eq, comparator_153_eq, comparator_154_eq, comparator_155_eq, comparator_156_eq,
       comparator_157_eq, comparator_158_eq, comparator_159_eq, comparator_160_eq, comparator_161_eq,
       comparator_161_gt, comparator_161_lt, comparator_162_eq, comparator_162_gt, comparator_162_lt,
       comparator_163_eq, comparator_163_gt, comparator_163_lt, comparator_164_eq, comparator_164_gt,
       comparator_164_lt, comparator_165_eq, comparator_166_eq, comparator_167_eq, comparator_168_eq,
       comparator_169_eq, comparator_170_eq, comparator_171_eq, comparator_172_eq, comparator_173_eq,
       comparator_174_eq, comparator_175_eq, comparator_176_eq, comparator_177_eq, comparator_178_eq,
       comparator_179_eq, comparator_180_eq, comparator_181_eq, comparator_181_gt, comparator_181_lt,
       comparator_182_eq, comparator_182_gt, comparator_182_lt, comparator_183_eq, comparator_183_gt,
       comparator_183_lt, comparator_184_eq, comparator_184_gt, comparator_184_lt, comparator_185_eq,
       comparator_186_eq, comparator_187_eq, comparator_188_eq, comparator_189_eq, comparator_190_eq,
       comparator_191_eq, comparator_192_eq, comparator_193_eq, comparator_194_eq, comparator_195_eq,
       comparator_196_eq, comparator_197_eq, comparator_198_eq, comparator_199_eq, comparator_200_eq,
       comparator_201_eq, comparator_201_gt, comparator_201_lt, comparator_202_eq, comparator_202_gt,
       comparator_202_lt, comparator_203_eq, comparator_203_gt, comparator_203_lt, comparator_204_eq,
       comparator_204_gt, comparator_204_lt, COPY, counter_1_ovf, counter_2_ovf, counter_3_ovf,
       counter_4_ovf, CPR_CLEAR_out, CPR_CLK_MAN_out, CPR_MANUAL_out, CPR_START_STOP_out, d_ff_1_nq,
       d_ff_2_nq, d_ff_3_nq, d_ff_4_nq, d_ff_5_nq, d_ff_6_nq, d_ff_7_nq, d_ff_8_nq, d_ff_9_nq, d_ff_10_nq,
       d_ff_11_nq, d_ff_12_nq, d_ff_13_nq, d_ff_14_nq, delay_1_out, delay_2_out, delay_3_out, delay_4_out,
       delay_5_out, delay_6_out, delay_7_out, delay_8_out, delay_9_out, delay_10_out, delay_11_out,
       delay_12_out, delay_13_out, delay_14_out, delay_15_out, delay_16_out, delay_17_out, delay_18_out,
       delay_19_out, delay_20_out, delay_21_out, delay_22_out, delay_23_out, delay_24_out, delay_25_out,
       delay_26_out, delay_27_out, delay_28_out, delay_29_out, delay_30_out, delay_31_out, delay_32_out,
       delay_33_out, delay_34_out, delay_35_out, delay_36_out, delay_37_out, delay_38_out, delay_39_out,
       delay_40_out, delay_41_out, delay_42_out, delay_43_out, delay_44_out, delay_45_out, delay_46_out,
       delay_47_out, delay_48_out, delay_49_out, delay_50_out, delay_51_out, delay_52_out, delay_53_out,
       delay_54_out, delay_55_out, delay_57_out, delay_58_out, delay_59_out, delay_60_out, delay_61_out,
       delay_62_out, delay_63_out, delay_64_out, delay_65_out, delay_66_out, delay_67_out, delay_68_out,
       delay_69_out, delay_70_out, delay_71_out, delay_72_out, delay_73_out, delay_74_out, delay_75_out,
       delay_76_out, delay_77_out, delay_78_out, delay_79_out, delay_80_out, delay_81_out, delay_83_out,
       delay_84_out, delay_85_out, delay_86_out, delay_87_out, delay_88_out, delay_89_out, delay_90_out,
       delay_91_out, delay_92_out, delay_93_out, delay_94_out, delay_95_out, delay_96_out, delay_97_out,
       delay_98_out, delay_99_out, delay_100_out, delay_101_out, delay_102_out, delay_103_out, delay_104_out,
       delay_105_out, delay_106_out, delay_107_out, delay_108_out, delay_109_out, delay_110_out,
       delay_112_out, delay_113_out, delay_114_out, delay_115_out, delay_116_out, delay_117_out,
       delay_118_out, delay_120_out, delay_121_out, delay_122_out, delay_123_out, delay_124_out,
       delay_125_out, delay_126_out, delay_127_out, delay_128_out, delay_129_out, delay_130_out,
       delay_131_out, delay_132_out, delay_133_out, delay_134_out, delay_135_out, delay_136_out,
       delay_137_out, delay_138_out, delay_139_out, delay_140_out, delay_141_out, delay_142_out,
       delay_143_out, delay_144_out, delay_145_out, delay_146_out, delay_147_out, delay_148_out,
       delay_149_out, delay_150_out, delay_151_out, delay_152_out, delay_153_out, delay_154_out,
       delay_155_out, delay_156_out, delay_157_out, delay_158_out, delay_159_out, delay_160_out,
       delay_161_out, delay_162_out, delay_163_out, delay_164_out, delay_165_out, delay_166_out,
       delay_167_out, delay_168_out, delay_169_out, delay_170_out, delay_171_out, delay_172_out,
       delay_173_out, delay_174_out, delay_175_out, delay_176_out, delay_177_out, delay_178_out,
       delay_179_out, delay_180_out, delay_181_out, delay_182_out, delay_183_out, delay_184_out,
       delay_185_out, delay_186_out, delay_187_out, delay_188_out, delay_189_out, delay_190_out,
       delay_191_out, delay_192_out, delay_193_out, delay_194_out, delay_195_out, delay_196_out,
       delay_197_out, delay_198_out, delay_199_out, delay_200_out, delay_201_out, delay_202_out,
       delay_203_out, delay_204_out, delay_205_out, delay_206_out, delay_207_out, delay_208_out,
       delay_209_out, delay_210_out, delay_211_out, delay_212_out, delay_213_out, delay_214_out,
       delay_215_out, delay_216_out, delay_217_out, delay_218_out, delay_219_out, delay_220_out,
       delay_221_out, delay_222_out, delay_223_out, delay_224_out, delay_225_out, delay_226_out,
       delay_227_out, delay_228_out, delay_229_out, delay_230_out, delay_231_out, delay_232_out,
       delay_233_out, delay_234_out, delay_235_out, delay_236_out, delay_237_out, delay_238_out,
       delay_239_out, delay_240_out, delay_241_out, delay_242_out, delay_243_out, delay_244_out,
       delay_245_out, delay_246_out, delay_247_out, delay_248_out, delay_249_out, delay_250_out,
       delay_251_out, delay_252_out, delay_253_out, delay_254_out, delay_255_out, delay_256_out,
       delay_257_out, delay_258_out, delay_259_out, delay_260_out, delay_261_out, delay_262_out,
       delay_263_out, delay_264_out, delay_265_out, delay_266_out, delay_267_out, delay_268_out,
       delay_269_out, delay_270_out, delay_271_out, delay_272_out, delay_273_out, delay_274_out,
       delay_275_out, delay_276_out, delay_277_out, delay_278_out, delay_279_out, delay_280_out,
       delay_281_out, delay_282_out, delay_283_out, delay_284_out, delay_285_out, delay_286_out,
       delay_287_out, delay_288_out, delay_289_out, delay_290_out, delay_291_out, delay_292_out,
       delay_293_out, delay_294_out, delay_295_out, delay_296_out, delay_297_out, delay_298_out,
       delay_299_out, delay_300_out, delay_301_out, delay_302_out, delay_303_out, delay_304_out,
       delay_305_out, delay_306_out, delay_307_out, delay_308_out, delay_309_out, delay_310_out,
       delay_311_out, delay_312_out, delay_313_out, delay_314_out, delay_315_out, delay_316_out,
       delay_317_out, delay_318_out, delay_319_out, delay_320_out, delay_321_out, delay_322_out,
       delay_323_out, delay_324_out, delay_325_out, delay_326_out, delay_327_out, delay_328_out,
       delay_329_out, delay_330_out, delay_331_out, delay_332_out, delay_333_out, delay_334_out,
       delay_335_out, delay_336_out, delay_337_out, delay_338_out, delay_339_out, delay_340_out,
       delay_341_out, delay_342_out, delay_343_out, delay_344_out, delay_345_out, delay_346_out,
       delay_347_out, delay_348_out, delay_349_out, delay_350_out, delay_351_out, delay_352_out,
       delay_353_out, delay_354_out, delay_355_out, delay_356_out, delay_357_out, delay_358_out,
       delay_359_out, delay_360_out, delay_361_out, delay_362_out, delay_363_out, delay_364_out,
       delay_365_out, delay_366_out, delay_367_out, delay_368_out, delay_369_out, delay_370_out,
       delay_371_out, delay_372_out, dipswitch_1_out, DISP_C1, DISP_C2, DISP_C3, DISP_C4, DISP_C5, DISP_C6,
       DISP_C7, DISP_C8, DIV, driver_1_out, driver_5_out, driver_29_out, driver_30_out, driver_155_out,
       driver_156_out, driver_157_out, driver_158_out, driver_159_out, driver_160_out, driver_161_out,
       driver_162_out, driver_164_out, driver_165_out, driver_166_out, driver_167_out, driver_190_out,
       driver_207_out, driver_226_out, driver_249_out, driver_250_out, driver_251_out, driver_252_out,
       driver_287_out, driver_288_out, driver_341_out, driver_344_out, driver_352_out, driver_356_out,
       driver_360_out, driver_362_out, driver_384_out, driver_395_out, driver_403_out, driver_460_out,
       driver_471_out, driver_472_out, driver_473_out, driver_474_out, driver_475_out, driver_476_out,
       driver_477_out, driver_478_out, driver_479_out, driver_480_out, driver_481_out, driver_503_out,
       driver_513_out, driver_551_out, driver_573_out, driver_600_out, driver_634_out, driver_660_out,
       driver_661_out, driver_662_out, driver_663_out, driver_664_out, driver_667_out, driver_669_out,
       driver_670_out, driver_671_out, driver_684_out, driver_692_out, driverinvsel_1_out,
       driverinvsel_14_out, driverinvsel_15_out, driverinvsel_17_out, driverinvsel_24_out,
       driverinvsel_25_out, driverinvsel_26_out, eeprom_1_d, EN_NEG, EN_out, EN_ZERO, EXT_L, EXT_L_out, INT,
       INT_DEL, INT_FULL, INT_TEST, INTERUPT, INTST, INV, K_M, K_OFF, K_ON, keyboard_1_av, KMSWP, LDA, LDA_t,
       LDB, LDB_t, LDC, LDX, LDX_t, LDY, LDY_t, LDZ, LEDD_SET, leddisplay_1_ledd_0, leddisplay_1_ledd_1,
       leddisplay_1_ledd_2, leddisplay_1_ledd_3, leddisplay_1_ledd_4, leddisplay_1_ledd_5,
       leddisplay_1_ledd_6, leddisplay_1_ledd_7, LSL, LSR, M_ADC, M_ADD, M_AND, M_ASL, M_ASR, M_CHGMD, M_CLB,
       M_CLC, M_CLE, M_CLN, M_CLS, M_CLV, M_CLZ, M_CMP, M_CNT, M_DIV, M_INV, M_LD___EN_t, M_LDA, M_LDA_2_out,
       M_LDA_out, M_LDA_t, M_LDB, M_LDB_2_out, M_LDB_out, M_LDB_t, M_LDC, M_LDC_out, M_LDX, M_LDX_2_out,
       M_LDX_out, M_LDX_t, M_LDY, M_LDY_2_out, M_LDY_out, M_LDY_t, M_LDZ, M_LDZ_out, M_LSL, M_LSR, M_MLC,
       M_MUL, M_NAND, M_NOR, M_NOT, M_OR, M_PHA, M_PHP, M_PLA, M_PLP, M_ROL, M_ROR, M_SBC, M_SEB, M_SEC,
       M_SEE, M_SEN, M_SES, M_SEV, M_SEZ, M_SMM, M_SPP, M_SSP, M_ST___EN_t, M_ST_out, M_STA, M_STA_out,
       M_STB, M_STB_out, M_STX, M_STX_out, M_STY, M_STY_out, M_SUB, M_TAB, M_TAX, M_TAY, M_TBA, M_TBX, M_TBY,
       M_TGLDEC, M_TGLINTDIS, M_TGLZADDR, M_TSX, M_TXA, M_TXB, M_TXS, M_TXY, M_TYA, M_TYB, M_TYX, M_XNOR,
       M_XOR, MAN_COPY_out, MAN_DELAY_out, MAN_INT_DELAY_out, MAN_INT_FULL_2_out, MAN_INT_FULL_out,
       MAN_K_NEXT_out, MAN_K_READ_out, MAN_M_NEXT_out, MAN_M_READ_out, MAN_NEXT_out, MAN_OP_SEND_out,
       MAN_RUN_out, MAN_SET_DELAY_out, MAN_TGL_K_or_M_out, MLC, MUL, NAND, NEXT, NOR, NOT, not_1_out,
       not_2_out, not_3_out, not_4_out, not_5_out, not_6_out, not_7_out, not_8_out, not_9_out, not_10_out,
       not_11_out, not_13_out, not_14_out, not_15_out, not_16_out, not_17_out, not_18_out, not_19_out,
       not_20_out, not_21_out, not_22_out, not_23_out, not_24_out, not_26_out, not_27_out, not_28_out,
       not_29_out, not_30_out, not_31_out, not_32_out, not_33_out, not_34_out, not_35_out, not_36_out,
       not_37_out, not_38_out, not_39_out, not_40_out, not_41_out, not_42_out, not_43_out, not_44_out,
       not_45_out, not_46_out, not_47_out, not_48_out, not_49_out, not_50_out, not_51_out, not_52_out,
       not_53_out, not_54_out, not_55_out, not_56_out, not_57_out, not_58_out, not_59_out, not_61_out,
       not_62_out, not_63_out, not_64_out, not_65_out, not_66_out, not_67_out, not_68_out, not_69_out,
       not_70_out, not_71_out, not_72_out, not_73_out, not_74_out, not_75_out, not_76_out, not_77_out,
       not_78_out, not_79_out, not_80_out, not_81_out, not_82_out, not_83_out, not_84_out, not_85_out,
       not_86_out, not_87_out, not_88_out, not_89_out, NULL, O__eq, O__gt, O__lt, O_CARRY, O_DEC, O_INT_BRK,
       O_INTDIS, O_MD8, O_MD16, O_MD32, O_MD64, O_NEG, O_OVFL, O_ZADDR, O_ZERO, op_sel_1__98, op_sel_1__99,
       op_sel_1__100, op_sel_1__101, op_sel_1__102, op_sel_1__103, op_sel_1__104, op_sel_1__105,
       op_sel_1__106, op_sel_1__109, op_sel_1__110, op_sel_1__111, op_sel_1__112, op_sel_1__113,
       op_sel_1__114, op_sel_1__115, op_sel_1__116, op_sel_1__117, OR, or_1_out, or_4_out, or_5_out,
       or_6_out, or_7_out, or_8_out, or_9_out, or_11_out, or_12_out, or_13_out, PHA, PHP, PLA, PLP,
       pulldown_6_out, pulldown_8_out, pulldown_14_out, pulldown_17_out, pulldown_19_out, pulldown_20_out,
       pulldown_21_out, pulldown_22_out, pulldown_23_out, pulldown_24_out, pulldown_25_out, pulldown_26_out,
       pulldown_37_out, pulldown_39_out, pulldown_41_out, pulldown_42_out, pulldown_43_out, pulldown_45_out,
       pulldown_47_out, pulldown_49_out, pulldown_50_out, pulldown_51_out, pulldown_81_out, pulldown_84_out,
       pulldown_85_out, pulldown_86_out, pulldown_89_out, pulldown_90_out, pulldown_100_out,
       pulldown_101_out, pulldown_102_out, pulldown_109_out, pulldown_111_out, pulldown_127_out,
       pulldown_132_out, pulldown_133_out, pulldown_138_out, pulldown_139_out, pulldown_140_out,
       pulldown_141_out, pulldown_150_out, pulldown_156_out, pulldown_158_out, pulldown_160_out,
       pulldown_162_out, pulldown_164_out, pulldown_166_out, pulldown_168_out, pulldown_174_out,
       pulldown_181_out, pulldown_183_out, pulldown_184_out, pulldown_186_out, pulldown_187_out,
       pulldown_188_out, pulldown_189_out, pulldown_191_out, RE_out, ROL, ROR, rs_ff_as_1_q, rs_ff_as_2_q,
       rs_ff_as_3_q, RUN, SBC, SBRK, SBRK_out, SBRM, SBRM_out, SCLK1_out, SEB, SEC, SEE, SEN, SES, SEV, SEZ,
       SIDEL, SMM, SPP, SSP, STA, STB, STC, STX, STY, STZ, SUB, t_ff_1_q, t_ff_2_q, t_ff_3_q, t_ff_5_nq,
       t_ff_5_q, t_ff_6_q, t_ff_7_q, t_ff_8_nq, t_ff_8_q, t_ff_12_q, TAB, TAX, TAY, TBA, TBX, TBY, TGLDEC,
       TGLINTDIS, TGLZADDR, TSX, tunnel, TXA, TXB, TXS, TXY, TYA, TYB, TYX, VGA_C, vgacharpos_1_p3,
       vgacharpos_1_p4, vgasync_1_h, vgasync_1_pic, vgasync_1_v, W__eq, W__gt, W__lt, W_C_ADC, W_C_ADD,
       W_C_SBC, W_C_SUB, W_MUL_OVFL, W_NEG, W_ZERO, WR2_MRAM, WR2M_out, WR_2_out, WR_out, X_EN, XNOR, XOR,
       Y_EN, Z_EN;
  wire [0:0] A_t;
  wire [1:0] O_MODE, pulldown_151_out;
  wire [3:0] add_1_s, driverinvsel_5_out, pulldown_18_out, register_2_q, W_CNT;
  wire [5:0] add_10_s, CX_c0, CX_c1, CX_c2, CX_c3, CX_c4, CX_c5, CX_c6, CX_c7, CX_c8, CX_c9, CX_c10, CX_c11,
       CX_c12, CX_c13, CX_c14, CX_c15, CX_c16, CX_c17, CX_c18, CX_c19, CX_c20, CX_c21, CX_c22, CX_c23,
       CX_c24, CX_c25, CX_c26, CX_c27, CX_c28, CX_c29, CX_c30, CX_c31, CX_c32, CX_c33, CX_c34, CX_c35,
       CX_c36, CX_c37, CX_c38, CX_c39, driverinvsel_27_out;
  wire [6:0] _16_bascii_to_7_bascii_1_out, driver_688_out, driver_700_out, pulldown_203_out, register_33_q,
       register_34_q, register_37_q, register_38_q, register_41_q, register_42_q, register_45_q,
       register_46_q, register_57_q, register_58_q, register_61_q, register_62_q, register_65_q,
       register_66_q, register_69_q, register_70_q, register_81_q, register_82_q, register_85_q,
       register_86_q, register_89_q, register_90_q, register_93_q, register_94_q, register_105_q,
       register_106_q, register_109_q, register_110_q, register_113_q, register_114_q, register_117_q,
       register_118_q, register_129_q, register_130_q, register_133_q, register_134_q, register_137_q,
       register_138_q, register_141_q, register_142_q, register_153_q, register_154_q, register_157_q,
       register_158_q, register_161_q, register_162_q, register_165_q, register_166_q, register_177_q,
       register_178_q, register_181_q, register_182_q, register_185_q, register_186_q, register_188_q,
       register_189_q, register_190_q, register_191_q, register_201_q, register_202_q, register_205_q,
       register_206_q, register_209_q, register_210_q, register_213_q, register_214_q, register_225_q,
       register_226_q, register_229_q, register_230_q, register_233_q, register_234_q, register_237_q,
       register_238_q, register_249_q, register_250_q, register_253_q, register_254_q, register_257_q,
       register_258_q, register_261_q, register_262_q, vgastring_1_c_o, vgastring_2_c_o, vgastring_3_c_o,
       vgastring_4_c_o, vgastring_5_c_o, vgastring_6_c_o, vgastring_7_c_o, vgastring_8_c_o, vgastring_9_c_o,
       vgastring_10_c_o, vgastring_11_c_o, vgastring_12_c_o, vgastring_13_c_o, vgastring_14_c_o,
       vgastring_15_c_o, vgastring_16_c_o, vgastring_17_c_o, vgastring_18_c_o, vgastring_19_c_o,
       vgastring_20_c_o, vgastring_21_c_o, vgastring_22_c_o, vgastring_23_c_o, vgastring_24_c_o,
       vgastring_25_c_o, vgastring_26_c_o, vgastring_27_c_o, vgastring_28_c_o, vgastring_29_c_o,
       vgastring_30_c_o, vgastring_31_c_o, vgastring_32_c_o, vgastring_33_c_o, vgastring_34_c_o,
       vgastring_35_c_o, vgastring_36_c_o, vgastring_37_c_o, vgastring_38_c_o, vgastring_39_c_o,
       vgastring_40_c_o;
  wire [7:0] add_4_s, add_7_s, add_8_s, add_9_s, B_t, CY_c0, CY_c1, CY_c2, CY_c3, CY_c4, CY_c5, CY_c6, CY_c7,
       CY_c8, CY_c9, CY_c10, CY_c11, CY_c12, CY_c13, CY_c14, CY_c15, CY_c16, CY_c17, CY_c18, CY_c19, CY_c20,
       CY_c21, CY_c22, CY_c23, CY_c24, CY_c25, CY_c26, CY_c27, CY_c28, CY_c29, CY_c30, CY_c31, CY_c32,
       CY_c33, CY_c34, CY_c35, CY_c36, CY_c37, CY_c38, CY_c39, delay_119_out, DISP_OUT, driver_2_out,
       driver_4_out, driver_154_out, driver_191_out, driver_340_out, driver_521_out, driver_668_out,
       driver_685_out, driver_691_out, driver_695_out, driverinvsel_13_out, driverinvsel_16_out,
       driverinvsel_21_out, driverinvsel_23_out, eeprom_3_d, LDA___D, LDB___D, LDX___D, LDY___D,
       leddisplay_1_ledd_d, M_ADDER_s, M_LD8___D_t, M_LD___D, M_ST___D_t, OP, PS, pulldown_5_out,
       pulldown_7_out, pulldown_9_out, pulldown_11_out, pulldown_36_out, pulldown_38_out, pulldown_40_out,
       pulldown_87_out, pulldown_88_out, pulldown_108_out, pulldown_110_out, pulldown_177_out, register_9_q,
       register_10_q, register_11_q, register_12_q, register_13_q, register_14_q, register_15_q, SP, sub_1_s,
       vgacharpos_1_p5, vgacharpos_1_p6, vgastring_1_cx_o, vgastring_1_cy_o, vgastring_2_cx_o,
       vgastring_2_cy_o, vgastring_3_cx_o, vgastring_3_cy_o, vgastring_4_cx_o, vgastring_4_cy_o,
       vgastring_5_cx_o, vgastring_5_cy_o, vgastring_6_cx_o, vgastring_6_cy_o, vgastring_7_cx_o,
       vgastring_7_cy_o, vgastring_8_cx_o, vgastring_8_cy_o, vgastring_9_cx_o, vgastring_9_cy_o,
       vgastring_10_cx_o, vgastring_10_cy_o, vgastring_11_cx_o, vgastring_11_cy_o, vgastring_12_cx_o,
       vgastring_12_cy_o, vgastring_13_cx_o, vgastring_13_cy_o, vgastring_14_cx_o, vgastring_14_cy_o,
       vgastring_15_cx_o, vgastring_15_cy_o, vgastring_16_cx_o, vgastring_16_cy_o, vgastring_17_cx_o,
       vgastring_17_cy_o, vgastring_18_cx_o, vgastring_18_cy_o, vgastring_19_cx_o, vgastring_19_cy_o,
       vgastring_20_cx_o, vgastring_20_cy_o, vgastring_21_cx_o, vgastring_21_cy_o, vgastring_22_cx_o,
       vgastring_22_cy_o, vgastring_23_cx_o, vgastring_23_cy_o, vgastring_24_cx_o, vgastring_24_cy_o,
       vgastring_25_cx_o, vgastring_25_cy_o, vgastring_26_cx_o, vgastring_26_cy_o, vgastring_27_cx_o,
       vgastring_27_cy_o, vgastring_28_cx_o, vgastring_28_cy_o, vgastring_29_cx_o, vgastring_29_cy_o,
       vgastring_30_cx_o, vgastring_30_cy_o, vgastring_31_cx_o, vgastring_31_cy_o, vgastring_32_cx_o,
       vgastring_32_cy_o, vgastring_33_cx_o, vgastring_33_cy_o, vgastring_34_cx_o, vgastring_34_cy_o,
       vgastring_35_cx_o, vgastring_35_cy_o, vgastring_36_cx_o, vgastring_36_cy_o, vgastring_37_cx_o,
       vgastring_37_cy_o, vgastring_38_cx_o, vgastring_38_cy_o, vgastring_39_cx_o, vgastring_39_cy_o,
       vgastring_40_cx_o, vgastring_40_cy_o, W_A, W_ADC, W_ADD, W_AND, W_ASL, W_ASR, W_DIVQ, W_DIVR, W_INV,
       W_LSL, W_LSR, W_NAND, W_NOR, W_NOT, W_OR, W_PS, W_ROL, W_ROR, W_SBC, W_SUB, W_XNOR, W_XOR, Z1, Z2;
  wire [7:6] X_t;
  wire [11:0] BG_c0, FG_c0, vgastring_1_bg_o, vgastring_1_fg_o, vgastring_2_bg_o, vgastring_2_fg_o,
       vgastring_3_bg_o, vgastring_3_fg_o, vgastring_4_bg_o, vgastring_4_fg_o, vgastring_5_bg_o,
       vgastring_5_fg_o, vgastring_6_bg_o, vgastring_6_fg_o, vgastring_7_bg_o, vgastring_7_fg_o,
       vgastring_8_bg_o, vgastring_8_fg_o, vgastring_9_bg_o, vgastring_9_fg_o, vgastring_10_bg_o,
       vgastring_10_fg_o, vgastring_11_bg_o, vgastring_11_fg_o, vgastring_12_bg_o, vgastring_12_fg_o,
       vgastring_13_bg_o, vgastring_13_fg_o, vgastring_14_bg_o, vgastring_14_fg_o, vgastring_15_bg_o,
       vgastring_15_fg_o, vgastring_16_bg_o, vgastring_16_fg_o, vgastring_17_bg_o, vgastring_17_fg_o,
       vgastring_18_bg_o, vgastring_18_fg_o, vgastring_19_bg_o, vgastring_19_fg_o, vgastring_20_bg_o,
       vgastring_20_fg_o, vgastring_21_bg_o, vgastring_21_fg_o, vgastring_22_bg_o, vgastring_22_fg_o,
       vgastring_23_bg_o, vgastring_23_fg_o, vgastring_24_bg_o, vgastring_24_fg_o, vgastring_25_bg_o,
       vgastring_25_fg_o, vgastring_26_bg_o, vgastring_26_fg_o, vgastring_27_bg_o, vgastring_27_fg_o,
       vgastring_28_bg_o, vgastring_28_fg_o, vgastring_29_bg_o, vgastring_29_fg_o, vgastring_30_bg_o,
       vgastring_30_fg_o, vgastring_31_bg_o, vgastring_31_fg_o, vgastring_32_bg_o, vgastring_32_fg_o,
       vgastring_33_bg_o, vgastring_33_fg_o, vgastring_34_bg_o, vgastring_34_fg_o, vgastring_35_bg_o,
       vgastring_35_fg_o, vgastring_36_bg_o, vgastring_36_fg_o, vgastring_37_bg_o, vgastring_37_fg_o,
       vgastring_38_bg_o, vgastring_38_fg_o, vgastring_39_bg_o, vgastring_39_fg_o, vgastring_40_bg_o,
       vgastring_40_fg_o;
  wire [13:0] pulldown_202_out;
  wire [15:0] _8_16decoder_1__8_16_out, C, Char_ROM_d, driver_163_out, driver_433_out, K_ADDER_s,
       keyboard_1_d, M_LD16___D_t, M_LD___A_t, M_ST___A_t, M_ST___A_t_t, O_MUL, pulldown_13_out,
       pulldown_15_out, pulldown_44_out, pulldown_46_out, pulldown_48_out, pulldown_99_out, pulldown_172_out,
       pulldown_179_out, SP_DECODED, vgasync_1_x, vgasync_1_y, vgatext_1_p6;
  wire [24:0] driver_199_out, driver_303_out, eeprom_2_d, K_ROM_d;

  Button button_1 (.out(button_1_out));
  assign driver_1_out = in_228 ? in_228 : 1'bz;  // Driver driver_1
  assign driverinvsel_1_out = ~in_228 ? in_228 : 1'bz;  // DriverInvSel driverinvsel_1
  assign driver_2_out = in_231 ? in_225 : 8'bz;  // Driver driver_2
  Delay #(.delayTime(10)) delay_1 (.in(button_1_out), .out(delay_1_out));
  PullDown pulldown_1 (.out(driver_1_out));
  Delay #(.delayTime(10)) delay_2 (.in(driver_1_out), .out(delay_2_out));
  PullDown pulldown_2 (.out(driverinvsel_1_out));
  Register #(.Bits(8)) register_1 (.D(driver_2_out), .C(delay_1_out), .en(button_1_out), .Q(out_224));
  EEPROM eeprom_1 (.A(in_227), .CS(in_229), .WE(delay_2_out), .OE(driverinvsel_1_out), .D(eeprom_1_d));
  assign out_226 = ~in_228 ? eeprom_1_d : 1'bz;  // DriverInvSel driverinvsel_2
  PullDown pulldown_3 (.out(eeprom_1_d));
  assign eeprom_1_d = in_228 ? in_230 : 1'bz;  // Driver driver_3
  PullDown pulldown_4 (.out(out_226));
  Button u_EXT_L (.out(EXT_L_out));
  assign driver_4_out = EXT_L_MAN ? EXT_A : 8'bz;  // Driver driver_4
  assign driver_4_out = ~EXT_L_MAN ? {X_t, X_2} : 8'bz;  // DriverInvSel driverinvsel_3
  ROM #(.AddrBits(8), .Bits(25)) rom_1 (.A(driver_4_out), .sel(1'b1), .D(out_333));
  assign driver_5_out = EXT_L_MAN ? EXT_L_out : 1'bz;  // Driver driver_5
  assign driver_5_out = ~EXT_L_MAN ? EXT_L : 1'bz;  // DriverInvSel driverinvsel_4
  PullDown #(.Bits(8)) pulldown_5 (.out(pulldown_5_out));
  PullDown pulldown_6 (.out(pulldown_6_out));
  PullDown #(.Bits(8)) pulldown_7 (.out(pulldown_7_out));
  PullDown pulldown_8 (.out(pulldown_8_out));
  PullDown #(.Bits(8)) pulldown_9 (.out(pulldown_9_out));
  PullDown pulldown_10 (.out(X_EN));
  PullDown #(.Bits(8)) pulldown_11 (.out(pulldown_11_out));
  PullDown pulldown_12 (.out(Y_EN));
  PullDown #(.Bits(16)) pulldown_13 (.out(pulldown_13_out));
  PullDown pulldown_14 (.out(pulldown_14_out));
  PullDown #(.Bits(16)) pulldown_15 (.out(pulldown_15_out));
  PullDown pulldown_16 (.out(Z_EN));
  assign pulldown_6_out = driver_5_out ? driver_5_out : 1'bz;  // Driver driver_6
  assign pulldown_8_out = driver_5_out ? driver_5_out : 1'bz;  // Driver driver_7
  assign pulldown_14_out = driver_5_out ? driver_5_out : 1'bz;  // Driver driver_8
  assign pulldown_5_out = driver_5_out ? {{7{1'b0}}, out_333[24]} : 8'bz;  // Driver driver_9
  assign pulldown_7_out = driver_5_out ? out_333[7:0] : 8'bz;  // Driver driver_10
  assign pulldown_13_out = driver_5_out ? out_333[23:8] : 16'bz;  // Driver driver_11
  assign pulldown_6_out = PLA ? PLA : 1'bz;  // Driver driver_12
  assign pulldown_5_out = PLA ? W_A : 8'bz;  // Driver driver_13
  assign pulldown_6_out = M_PLA ? M_PLA : 1'bz;  // Driver driver_14
  assign pulldown_5_out = M_PLA ? W_A : 8'bz;  // Driver driver_15
  assign pulldown_6_out = TYA ? TYA : 1'bz;  // Driver driver_16
  Button MAN_SET_DELAY (.out(MAN_SET_DELAY_out));
  Button MAN_DELAY (.out(MAN_DELAY_out));
  PullDown pulldown_17 (.out(pulldown_17_out));
  PullDown #(.Bits(4)) pulldown_18 (.out(pulldown_18_out));
  Button MAN_INT_DELAY (.out(MAN_INT_DELAY_out));
  PullDown pulldown_19 (.out(pulldown_19_out));
  PullDown pulldown_20 (.out(pulldown_20_out));
  PullDown pulldown_21 (.out(pulldown_21_out));
  PullDown pulldown_22 (.out(pulldown_22_out));
  assign pulldown_6_out = M_TYA ? M_TYA : 1'bz;  // Driver driver_17
  assign pulldown_5_out = TYA ? Y_2 : 8'bz;  // Driver driver_18
  Delay #(.delayTime(20)) delay_3 (.in(delay_4_out), .out(delay_3_out));
  Delay #(.delayTime(20)) delay_4 (.in(INT_DEL), .out(delay_4_out));
  assign pulldown_5_out = M_TYA ? Y_2 : 8'bz;  // Driver driver_19
  Delay #(.delayTime(20)) delay_5 (.in(delay_3_out), .out(delay_5_out));
  assign pulldown_6_out = TXA ? TXA : 1'bz;  // Driver driver_20
  Delay #(.delayTime(20)) delay_6 (.in(delay_7_out), .out(delay_6_out));
  Delay #(.delayTime(20)) delay_7 (.in(INT_DEL), .out(delay_7_out));
  and and_1 (and_1_out, INT_DEL, ~delay_5_out);  // And
  assign pulldown_5_out = TXA ? {X_t, X_2} : 8'bz;  // Driver driver_21
  Delay #(.delayTime(20)) delay_8 (.in(delay_6_out), .out(delay_8_out));
  assign pulldown_6_out = M_TXA ? M_TXA : 1'bz;  // Driver driver_22
  Button MAN_INT_FULL (.out(MAN_INT_FULL_out));
  PullDown pulldown_23 (.out(pulldown_23_out));
  PullDown pulldown_24 (.out(pulldown_24_out));
  PullDown pulldown_25 (.out(pulldown_25_out));
  PullDown pulldown_26 (.out(pulldown_26_out));
  and and_2 (and_2_out, INT_DEL, ~delay_8_out);  // And
  assign INTST = and_1_out ? and_1_out : 1'bz;  // Driver driver_23
  PullDown pulldown_27 (.out(INTST));
  assign pulldown_5_out = M_TXA ? {X_t, X_2} : 8'bz;  // Driver driver_24
  Delay #(.delayTime(10)) delay_9 (.in(INT_FULL), .out(delay_9_out));
  assign pulldown_24_out = delay_9_out ? delay_9_out : 1'bz;  // Driver driver_25
  assign pulldown_24_out = MAN_INT_FULL_out ? MAN_INT_FULL_out : 1'bz;  // Driver driver_26
  Delay #(.delayTime(10)) delay_10 (.in(pulldown_24_out), .out(delay_10_out));
  assign pulldown_24_out = and_12_out ? and_12_out : 1'bz;  // Driver driver_27
  assign driverinvsel_5_out = ~MAN ? X_2[3:0] : 4'bz;  // DriverInvSel driverinvsel_5
  assign driverinvsel_5_out = MAN ? in_52 : 4'bz;  // Driver driver_28
  assign driver_29_out = MAN_SET_DELAY_out ? MAN_SET_DELAY_out : 1'bz;  // Driver driver_29
  assign driver_30_out = and_2_out ? and_2_out : 1'bz;  // Driver driver_30
  assign driver_30_out = MAN_DELAY_out ? MAN_DELAY_out : 1'bz;  // Driver driver_31
  assign driver_30_out = and_7_out ? and_7_out : 1'bz;  // Driver driver_32
  assign pulldown_20_out = and_8_out ? and_8_out : 1'bz;  // Driver driver_33
  assign pulldown_20_out = MAN_INT_DELAY_out ? MAN_INT_DELAY_out : 1'bz;  // Driver driver_34
  Delay #(.delayTime(10)) delay_11 (.in(pulldown_20_out), .out(delay_11_out));
  assign pulldown_20_out = and_16_out ? and_16_out : 1'bz;  // Driver driver_35
  assign pulldown_6_out = TBA ? TBA : 1'bz;  // Driver driver_36
  T_FF t_ff_1 (.T(pulldown_24_out), .C(delay_10_out), .Q(t_ff_1_q));  // open: nQ
  assign driver_29_out = SIDEL ? SIDEL : 1'bz;  // Driver driver_37
  PullDown pulldown_28 (.out(driver_29_out));
  PullDown pulldown_29 (.out(driver_30_out));
  Delay #(.delayTime(10)) delay_12 (.in(driver_30_out), .out(delay_12_out));
  T_FF t_ff_2 (.T(pulldown_20_out), .C(delay_11_out), .Q(t_ff_2_q));  // open: nQ
  assign pulldown_6_out = M_TBA ? M_TBA : 1'bz;  // Driver driver_38
  assign pulldown_5_out = TBA ? B_t : 8'bz;  // Driver driver_39
  assign pulldown_8_out = op_sel_1__104 ? op_sel_1__104 : 1'bz;  // Driver driver_40
  and and_3 (and_3_out, t_ff_1_q, HEARTBEAT);
  T_FF t_ff_3 (.T(driver_30_out), .C(delay_12_out), .Q(t_ff_3_q));  // open: nQ
  and and_4 (and_4_out, t_ff_2_q, _100);
  assign pulldown_5_out = M_TBA ? B_t : 8'bz;  // Driver driver_41
  assign pulldown_7_out = op_sel_1__104 ? out_159 : 8'bz;  // Driver driver_42
  and and_5 (pulldown_17_out, t_ff_3_q, _1);
  assign pulldown_6_out = DIV ? DIV : 1'bz;  // Driver driver_43
  assign pulldown_8_out = TYB ? TYB : 1'bz;  // Driver driver_44
  assign pulldown_23_out = ~and_12_out ? and_3_out : 1'bz;  // DriverInvSel driverinvsel_6
  assign pulldown_25_out = pulldown_23_out ? pulldown_23_out : 1'bz;  // Driver driver_45
  assign pulldown_25_out = delay_15_out ? delay_15_out : 1'bz;  // Driver driver_46
  Delay #(.delayTime(10)) delay_13 (.in(driver_29_out), .out(delay_13_out));
  Delay #(.delayTime(10)) delay_14 (.in(pulldown_17_out), .out(delay_14_out));
  assign pulldown_19_out = ~and_16_out ? and_4_out : 1'bz;  // DriverInvSel driverinvsel_7
  assign pulldown_21_out = pulldown_19_out ? pulldown_19_out : 1'bz;  // Driver driver_47
  assign pulldown_21_out = delay_16_out ? delay_16_out : 1'bz;  // Driver driver_48
  assign pulldown_5_out = DIV ? W_DIVQ : 8'bz;  // Driver driver_49
  assign pulldown_8_out = M_TYB ? M_TYB : 1'bz;  // Driver driver_50
  assign pulldown_7_out = TYB ? Y_2 : 8'bz;  // Driver driver_51
  assign pulldown_26_out = delay_15_out ? delay_15_out : 1'bz;  // Driver driver_52
  Delay #(.delayTime(10)) delay_15 (.in(and_12_out), .out(delay_15_out));
  Register #(.Bits(4)) register_2 (.D(driverinvsel_5_out), .C(delay_13_out), .en(driver_29_out), .Q(register_2_q));
  Add #(.Bits(4)) add_1 (.a(out_57), .b(4'b0001), .c_i(1'b0), .s(add_1_s));  // open: c_o
  Register #(.Bits(4)) register_3 (.D(pulldown_18_out), .C(delay_14_out), .en(pulldown_17_out), .Q(out_57));
  assign pulldown_17_out = and_6_out ? and_6_out : 1'bz;  // Driver driver_53
  assign pulldown_18_out = and_6_out ? 4'b0000 : 4'bz;  // Driver driver_54
  assign pulldown_22_out = delay_16_out ? delay_16_out : 1'bz;  // Driver driver_55
  Delay #(.delayTime(10)) delay_16 (.in(and_16_out), .out(delay_16_out));
  assign pulldown_6_out = M_DIV ? M_DIV : 1'bz;  // Driver driver_56
  assign pulldown_7_out = M_TYB ? Y_2 : 8'bz;  // Driver driver_57
  Counter #(.Bits(2)) counter_1 (
    .en(pulldown_25_out), .C(pulldown_25_out), .clr(pulldown_26_out), .out(out_50), .ovf(counter_1_ovf));
  assign pulldown_18_out = ~and_6_out ? add_1_s : 4'bz;  // DriverInvSel driverinvsel_8
  Counter #(.Bits(2)) counter_2 (
    .en(pulldown_21_out), .C(pulldown_21_out), .clr(pulldown_22_out), .out(out_53), .ovf(counter_2_ovf));
  assign pulldown_5_out = M_DIV ? W_DIVQ : 8'bz;  // Driver driver_58
  assign pulldown_8_out = TXB ? TXB : 1'bz;  // Driver driver_59
  Add #(.Bits(4)) add_2 (.a(4'b0001), .b(register_2_q), .c_i(1'b0), .s(out_56));  // open: c_o
  and and_6 (and_6_out, and_15_out, ~delay_17_out);  // And
  and and_7 (and_7_out, and_14_out, ~delay_19_out);  // And
  and and_8 (and_8_out, comparator_1_eq, ~delay_21_out);  // And
  assign pulldown_6_out = MLC ? MLC : 1'bz;  // Driver driver_60
  assign pulldown_7_out = TXB ? {X_t, X_2} : 8'bz;  // Driver driver_61
  not not_1 (not_1_out, out_50[0]);
  not not_2 (not_2_out, out_50[1]);
  not not_3 (not_3_out, out_50[1]);
  not not_4 (not_4_out, out_50[0]);
  Comparator #(.Bits(4)) comparator_1 (
    .a(out_56), .b(out_57), .gt(comparator_1_gt), .eq(comparator_1_eq), .lt(comparator_1_lt));
  Delay #(.delayTime(20)) delay_17 (.in(delay_18_out), .out(delay_17_out));
  Delay #(.delayTime(20)) delay_18 (.in(delay_23_out), .out(delay_18_out));
  Delay #(.delayTime(20)) delay_19 (.in(delay_20_out), .out(delay_19_out));
  Delay #(.delayTime(20)) delay_20 (.in(delay_24_out), .out(delay_20_out));
  Delay #(.delayTime(20)) delay_21 (.in(delay_22_out), .out(delay_21_out));
  Delay #(.delayTime(20)) delay_22 (.in(delay_25_out), .out(delay_22_out));
  not not_5 (not_5_out, out_53[0]);
  not not_6 (not_6_out, out_53[1]);
  not not_7 (not_7_out, out_53[1]);
  not not_8 (not_8_out, out_53[0]);
  assign pulldown_6_out = M_MLC ? M_MLC : 1'bz;  // Driver driver_62
  assign pulldown_5_out = MLC ? W_MUL : 8'bz;  // Driver driver_63
  assign pulldown_8_out = M_TXB ? M_TXB : 1'bz;  // Driver driver_64
  and and_9 (and_9_out, not_1_out, not_2_out);
  and and_10 (and_10_out, out_50[0], not_3_out);
  and and_11 (and_11_out, not_4_out, out_50[1]);
  and and_12 (and_12_out, out_50[0], out_50[1]);
  Delay #(.delayTime(20)) delay_23 (.in(and_15_out), .out(delay_23_out));
  Delay #(.delayTime(20)) delay_24 (.in(and_14_out), .out(delay_24_out));
  Delay #(.delayTime(20)) delay_25 (.in(comparator_1_eq), .out(delay_25_out));
  and and_13 (and_13_out, not_5_out, not_6_out);
  and and_14 (and_14_out, out_53[0], not_7_out);
  and and_15 (and_15_out, not_8_out, out_53[1]);
  and and_16 (and_16_out, out_53[0], out_53[1]);
  assign pulldown_5_out = M_MLC ? W_MUL : 8'bz;  // Driver driver_65
  assign pulldown_7_out = M_TXB ? {X_t, X_2} : 8'bz;  // Driver driver_66
  assign pulldown_6_out = MUL ? MUL : 1'bz;  // Driver driver_67
  assign pulldown_8_out = TAB ? TAB : 1'bz;  // Driver driver_68
  assign INTST = and_11_out ? and_11_out : 1'bz;  // Driver driver_69
  assign pulldown_5_out = MUL ? W_MUL : 8'bz;  // Driver driver_70
  assign pulldown_8_out = M_TAB ? M_TAB : 1'bz;  // Driver driver_71
  assign pulldown_7_out = TAB ? {out_327, A_t[0]} : 8'bz;  // Driver driver_72
  assign INTST = and_15_out ? and_15_out : 1'bz;  // Driver driver_73
  assign pulldown_6_out = M_MUL ? M_MUL : 1'bz;  // Driver driver_74
  assign pulldown_7_out = M_TAB ? {out_327, A_t[0]} : 8'bz;  // Driver driver_75
  assign pulldown_5_out = M_MUL ? W_MUL : 8'bz;  // Driver driver_76
  assign pulldown_8_out = INV ? INV : 1'bz;  // Driver driver_77
  assign pulldown_6_out = SBC ? SBC : 1'bz;  // Driver driver_78
  assign pulldown_7_out = INV ? W_INV : 8'bz;  // Driver driver_79
  assign pulldown_6_out = M_SBC ? M_SBC : 1'bz;  // Driver driver_80
  assign pulldown_5_out = SBC ? W_SBC : 8'bz;  // Driver driver_81
  assign pulldown_8_out = M_INV ? M_INV : 1'bz;  // Driver driver_82
  assign pulldown_5_out = M_SBC ? W_SBC : 8'bz;  // Driver driver_83
  assign pulldown_7_out = M_INV ? W_INV : 8'bz;  // Driver driver_84
  assign pulldown_6_out = SUB ? SUB : 1'bz;  // Driver driver_85
  assign pulldown_8_out = CNT ? CNT : 1'bz;  // Driver driver_86
  assign pulldown_5_out = SUB ? W_SUB : 8'bz;  // Driver driver_87
  assign pulldown_8_out = M_CNT ? M_CNT : 1'bz;  // Driver driver_88
  assign pulldown_7_out = CNT ? {4'b0000, W_CNT} : 8'bz;  // Driver driver_89
  assign pulldown_6_out = M_SUB ? M_SUB : 1'bz;  // Driver driver_90
  assign pulldown_7_out = M_CNT ? {4'b0000, W_CNT} : 8'bz;  // Driver driver_91
  assign pulldown_5_out = M_SUB ? W_SUB : 8'bz;  // Driver driver_92
  assign pulldown_8_out = XNOR ? XNOR : 1'bz;  // Driver driver_93
  assign pulldown_6_out = ADC ? ADC : 1'bz;  // Driver driver_94
  assign pulldown_7_out = XNOR ? W_XNOR : 8'bz;  // Driver driver_95
  assign pulldown_6_out = M_ADC ? M_ADC : 1'bz;  // Driver driver_96
  assign pulldown_5_out = ADC ? W_ADC : 8'bz;  // Driver driver_97
  assign pulldown_8_out = M_XNOR ? M_XNOR : 1'bz;  // Driver driver_98
  assign pulldown_5_out = M_ADC ? W_ADC : 8'bz;  // Driver driver_99
  assign pulldown_7_out = M_XNOR ? W_XNOR : 8'bz;  // Driver driver_100
  assign pulldown_6_out = ADD ? ADD : 1'bz;  // Driver driver_101
  assign pulldown_8_out = XOR ? XOR : 1'bz;  // Driver driver_102
  assign pulldown_5_out = ADD ? W_ADD : 8'bz;  // Driver driver_103
  assign pulldown_8_out = M_XOR ? M_XOR : 1'bz;  // Driver driver_104
  assign pulldown_7_out = XOR ? W_XOR : 8'bz;  // Driver driver_105
  assign pulldown_6_out = M_ADD ? M_ADD : 1'bz;  // Driver driver_106
  assign pulldown_7_out = M_XOR ? W_XOR : 8'bz;  // Driver driver_107
  assign pulldown_5_out = M_ADD ? W_ADD : 8'bz;  // Driver driver_108
  assign pulldown_8_out = NOR ? NOR : 1'bz;  // Driver driver_109
  assign pulldown_6_out = ASL ? ASL : 1'bz;  // Driver driver_110
  assign pulldown_7_out = NOR ? W_NOR : 8'bz;  // Driver driver_111
  assign pulldown_6_out = M_ASL ? M_ASL : 1'bz;  // Driver driver_112
  assign pulldown_5_out = ASL ? W_ASL : 8'bz;  // Driver driver_113
  assign pulldown_8_out = M_NOR ? M_NOR : 1'bz;  // Driver driver_114
  assign pulldown_5_out = M_ASL ? W_ASL : 8'bz;  // Driver driver_115
  assign pulldown_7_out = M_NOR ? W_NOR : 8'bz;  // Driver driver_116
  assign pulldown_6_out = ASR ? ASR : 1'bz;  // Driver driver_117
  assign pulldown_8_out = OR ? OR : 1'bz;  // Driver driver_118
  assign pulldown_5_out = ASR ? W_ASR : 8'bz;  // Driver driver_119
  assign pulldown_8_out = M_OR ? M_OR : 1'bz;  // Driver driver_120
  assign pulldown_7_out = OR ? W_OR : 8'bz;  // Driver driver_121
  assign pulldown_6_out = M_ASR ? M_ASR : 1'bz;  // Driver driver_122
  assign pulldown_7_out = M_OR ? W_OR : 8'bz;  // Driver driver_123
  assign pulldown_9_out = op_sel_1__105 ? out_331 : 8'bz;  // Driver driver_124
  assign pulldown_5_out = M_ASR ? W_ASR : 8'bz;  // Driver driver_125
  assign pulldown_8_out = NAND ? NAND : 1'bz;  // Driver driver_126
  assign X_EN = op_sel_1__105 ? op_sel_1__105 : 1'bz;  // Driver driver_127
  assign pulldown_6_out = ROL ? ROL : 1'bz;  // Driver driver_128
  assign pulldown_7_out = NAND ? W_NAND : 8'bz;  // Driver driver_129
  assign X_EN = TYX ? TYX : 1'bz;  // Driver driver_130
  assign pulldown_6_out = M_ROL ? M_ROL : 1'bz;  // Driver driver_131
  assign pulldown_5_out = ROL ? W_ROL : 8'bz;  // Driver driver_132
  assign pulldown_8_out = M_NAND ? M_NAND : 1'bz;  // Driver driver_133
  assign X_EN = M_TYX ? M_TYX : 1'bz;  // Driver driver_134
  assign pulldown_9_out = TYX ? Y_2 : 8'bz;  // Driver driver_135
  assign Y_EN = op_sel_1__103 ? op_sel_1__103 : 1'bz;  // Driver driver_136
  assign pulldown_5_out = M_ROL ? W_ROL : 8'bz;  // Driver driver_137
  assign pulldown_7_out = M_NAND ? W_NAND : 8'bz;  // Driver driver_138
  assign pulldown_9_out = M_TYX ? Y_2 : 8'bz;  // Driver driver_139
  assign pulldown_11_out = op_sel_1__103 ? {1'b0, driver_700_out} : 8'bz;  // Driver driver_140
  assign pulldown_6_out = ROR ? ROR : 1'bz;  // Driver driver_141
  assign pulldown_8_out = AND ? AND : 1'bz;  // Driver driver_142
  assign X_EN = TBX ? TBX : 1'bz;  // Driver driver_143
  assign Y_EN = TXY ? TXY : 1'bz;  // Driver driver_144
  assign pulldown_5_out = ROR ? W_ROR : 8'bz;  // Driver driver_145
  assign pulldown_8_out = M_AND ? M_AND : 1'bz;  // Driver driver_146
  assign pulldown_7_out = AND ? W_AND : 8'bz;  // Driver driver_147
  assign pulldown_9_out = TBX ? B_t : 8'bz;  // Driver driver_148
  assign pulldown_11_out = TXY ? {X_t, X_2} : 8'bz;  // Driver driver_149
  Button u_SBRM (.out(SBRM_out));
  Button u_BRM (.out(BRM_out));
  Button MAN_M_NEXT (.out(MAN_M_NEXT_out));
  Button MAN_M_READ (.out(MAN_M_READ_out));
  Button MAN_TGL_K_or_M (.out(MAN_TGL_K_or_M_out));
  Button MAN_NEXT (.out(MAN_NEXT_out));
  Button MAN_COPY (.out(MAN_COPY_out));
  Button MAN_RUN (.out(MAN_RUN_out));
  Button u_SBRK (.out(SBRK_out));
  Button u_BRK (.out(BRK_out));
  Button MAN_K_NEXT (.out(MAN_K_NEXT_out));
  Button MAN_K_READ (.out(MAN_K_READ_out));
  assign pulldown_6_out = M_ROR ? M_ROR : 1'bz;  // Driver driver_150
  assign pulldown_7_out = M_AND ? W_AND : 8'bz;  // Driver driver_151
  assign X_EN = M_TBX ? M_TBX : 1'bz;  // Driver driver_152
  assign Y_EN = M_TXY ? M_TXY : 1'bz;  // Driver driver_153
  assign driver_154_out = SBRM_out ? BRMADDR : 8'bz;  // Driver driver_154
  assign driver_155_out = SBRM_out ? SBRM_out : 1'bz;  // Driver driver_155
  assign driver_156_out = BRM_out ? BRM_out : 1'bz;  // Driver driver_156
  assign driver_157_out = MAN_M_NEXT_out ? MAN_M_NEXT_out : 1'bz;  // Driver driver_157
  assign driver_158_out = MAN_M_READ_out ? MAN_M_READ_out : 1'bz;  // Driver driver_158
  assign driver_159_out = MAN_TGL_K_or_M_out ? MAN_TGL_K_or_M_out : 1'bz;  // Driver driver_159
  assign driver_160_out = MAN_NEXT_out ? MAN_NEXT_out : 1'bz;  // Driver driver_160
  assign driver_161_out = MAN_COPY_out ? MAN_COPY_out : 1'bz;  // Driver driver_161
  assign driver_162_out = MAN_RUN_out ? MAN_RUN_out : 1'bz;  // Driver driver_162
  assign driver_163_out = SBRK_out ? BRKADDR : 16'bz;  // Driver driver_163
  assign driver_164_out = SBRK_out ? SBRK_out : 1'bz;  // Driver driver_164
  assign driver_165_out = BRK_out ? BRK_out : 1'bz;  // Driver driver_165
  assign driver_166_out = MAN_K_NEXT_out ? MAN_K_NEXT_out : 1'bz;  // Driver driver_166
  assign driver_167_out = MAN_K_READ_out ? MAN_K_READ_out : 1'bz;  // Driver driver_167
  assign pulldown_5_out = M_ROR ? W_ROR : 8'bz;  // Driver driver_168
  assign pulldown_8_out = NOT ? NOT : 1'bz;  // Driver driver_169
  assign pulldown_9_out = M_TBX ? B_t : 8'bz;  // Driver driver_170
  assign pulldown_11_out = M_TXY ? {X_t, X_2} : 8'bz;  // Driver driver_171
  assign driver_154_out = SBRM ? {X_t, X_2} : 8'bz;  // Driver driver_172
  assign driver_159_out = KMSWP ? KMSWP : 1'bz;  // Driver driver_173
  PullDown pulldown_30 (.out(driver_159_out));
  PullDown pulldown_31 (.out(driver_160_out));
  PullDown pulldown_32 (.out(driver_161_out));
  PullDown pulldown_33 (.out(driver_162_out));
  assign driver_163_out = SBRK ? {Y_2, X_t, X_2} : 16'bz;  // Driver driver_174
  assign pulldown_6_out = LSL ? LSL : 1'bz;  // Driver driver_175
  assign pulldown_7_out = NOT ? W_NOT : 8'bz;  // Driver driver_176
  assign X_EN = TAX ? TAX : 1'bz;  // Driver driver_177
  assign Y_EN = TBY ? TBY : 1'bz;  // Driver driver_178
  assign driver_155_out = SBRM ? SBRM : 1'bz;  // Driver driver_179
  Button WR2M (.out(WR2M_out));
  assign driver_162_out = RUN ? RUN : 1'bz;  // Driver driver_180
  assign driver_164_out = SBRK ? SBRK : 1'bz;  // Driver driver_181
  assign pulldown_6_out = M_LSL ? M_LSL : 1'bz;  // Driver driver_182
  assign pulldown_5_out = LSL ? W_LSL : 8'bz;  // Driver driver_183
  assign pulldown_8_out = M_NOT ? M_NOT : 1'bz;  // Driver driver_184
  assign X_EN = M_TAX ? M_TAX : 1'bz;  // Driver driver_185
  assign pulldown_9_out = TAX ? {out_327, A_t[0]} : 8'bz;  // Driver driver_186
  assign Y_EN = M_TBY ? M_TBY : 1'bz;  // Driver driver_187
  assign pulldown_11_out = TBY ? B_t : 8'bz;  // Driver driver_188
  assign driver_156_out = BRM ? BRM : 1'bz;  // Driver driver_189
  assign driver_190_out = WR2M_out ? WR2M_out : 1'bz;  // Driver driver_190
  Delay #(.delayTime(10)) delay_26 (.in(WR2M_out), .out(delay_26_out));
  assign driver_191_out = WR2M_out ? ADDR : 8'bz;  // Driver driver_191
  assign driver_161_out = COPY ? COPY : 1'bz;  // Driver driver_192
  assign driver_160_out = NEXT ? NEXT : 1'bz;  // Driver driver_193
  assign driver_165_out = BRK ? BRK : 1'bz;  // Driver driver_194
  assign pulldown_5_out = M_LSL ? W_LSL : 8'bz;  // Driver driver_195
  assign pulldown_7_out = M_NOT ? W_NOT : 8'bz;  // Driver driver_196
  assign pulldown_9_out = M_TAX ? {out_327, A_t[0]} : 8'bz;  // Driver driver_197
  assign pulldown_11_out = M_TBY ? B_t : 8'bz;  // Driver driver_198
  assign driver_199_out = delay_26_out ? VAL : 25'bz;  // Driver driver_199
  Delay #(.delayTime(10)) delay_27 (.in(driver_159_out), .out(delay_27_out));
  assign pulldown_6_out = LSR ? LSR : 1'bz;  // Driver driver_200
  assign pulldown_8_out = DIV ? DIV : 1'bz;  // Driver driver_201
  assign Y_EN = TAY ? TAY : 1'bz;  // Driver driver_202
  assign driver_190_out = WR2_MRAM ? WR2_MRAM : 1'bz;  // Driver driver_203
  T_FF t_ff_4 (.T(driver_159_out), .C(delay_27_out), .Q(K_M));  // open: nQ
  assign pulldown_5_out = LSR ? W_LSR : 8'bz;  // Driver driver_204
  assign pulldown_8_out = M_DIV ? M_DIV : 1'bz;  // Driver driver_205
  assign pulldown_7_out = DIV ? W_DIVR : 8'bz;  // Driver driver_206
  assign driver_207_out = M_TSX ? M_TSX : 1'bz;  // Driver driver_207
  assign driver_207_out = TSX ? TSX : 1'bz;  // Driver driver_208
  PullDown pulldown_34 (.out(driver_207_out));
  assign X_EN = driver_207_out ? driver_207_out : 1'bz;  // Driver driver_209
  assign pulldown_11_out = TAY ? {out_327, A_t[0]} : 8'bz;  // Driver driver_210
  Delay #(.delayTime(10)) delay_28 (.in(WR2_MRAM), .out(delay_28_out));
  assign driver_199_out = delay_28_out ? {A_t[0], C, B_t} : 25'bz;  // Driver driver_211
  assign pulldown_6_out = M_LSR ? M_LSR : 1'bz;  // Driver driver_212
  assign pulldown_7_out = M_DIV ? W_DIVR : 8'bz;  // Driver driver_213
  assign pulldown_9_out = driver_207_out ? SP : 8'bz;  // Driver driver_214
  assign Y_EN = M_TAY ? M_TAY : 1'bz;  // Driver driver_215
  assign driver_191_out = WR2_MRAM ? {X_t, X_2} : 8'bz;  // Driver driver_216
  and and_17 (and_17_out, driver_160_out, K_M);
  and and_18 (and_18_out, driver_160_out, ~K_M);  // And
  and and_19 (and_19_out, driver_161_out, K_M);
  and and_20 (and_20_out, driver_161_out, ~K_M);  // And
  assign pulldown_5_out = M_LSR ? W_LSR : 8'bz;  // Driver driver_217
  assign pulldown_11_out = M_TAY ? {out_327, A_t[0]} : 8'bz;  // Driver driver_218
  assign driver_157_out = and_17_out ? and_17_out : 1'bz;  // Driver driver_219
  assign driver_166_out = and_18_out ? and_18_out : 1'bz;  // Driver driver_220
  assign pulldown_6_out = STC ? STC : 1'bz;  // Driver driver_221
  assign pulldown_8_out = STC ? STC : 1'bz;  // Driver driver_222
  assign X_EN = STZ ? STZ : 1'bz;  // Driver driver_223
  assign Y_EN = STZ ? STZ : 1'bz;  // Driver driver_224
  assign driver_158_out = and_19_out ? and_19_out : 1'bz;  // Driver driver_225
  assign driver_226_out = and_19_out ? and_19_out : 1'bz;  // Driver driver_226
  assign driver_167_out = and_20_out ? and_20_out : 1'bz;  // Driver driver_227
  assign pulldown_5_out = STC ? C[15:8] : 8'bz;  // Driver driver_228
  assign pulldown_7_out = STC ? C[7:0] : 8'bz;  // Driver driver_229
  assign pulldown_9_out = STZ ? Z2 : 8'bz;  // Driver driver_230
  assign pulldown_11_out = STZ ? Z1 : 8'bz;  // Driver driver_231
  or or_1 (or_1_out, BR, CBR);
  PullDown pulldown_35 (.out(driver_226_out));
  assign driver_226_out = and_20_out ? and_20_out : 1'bz;  // Driver driver_232
  and and_21 (LDA_t, tunnel, LDA);
  assign pulldown_6_out = LDA_t ? LDA_t : 1'bz;  // Driver driver_233
  and and_22 (LDB_t, tunnel, LDB);
  assign pulldown_8_out = LDB_t ? LDB_t : 1'bz;  // Driver driver_234
  and and_23 (LDX_t, tunnel, LDX);
  assign X_EN = LDX_t ? LDX_t : 1'bz;  // Driver driver_235
  and and_24 (LDY_t, tunnel, LDY);
  assign Y_EN = LDY_t ? LDY_t : 1'bz;  // Driver driver_236
  and and_25 (BRK, ~K_M, or_1_out);  // And
  and and_26 (BRM, K_M, or_1_out);
  assign pulldown_5_out = LDA_t ? LDA___D : 8'bz;  // Driver driver_237
  assign pulldown_7_out = LDB_t ? LDB___D : 8'bz;  // Driver driver_238
  assign pulldown_9_out = LDX_t ? LDX___D : 8'bz;  // Driver driver_239
  assign pulldown_11_out = LDY_t ? LDY___D : 8'bz;  // Driver driver_240
  assign pulldown_6_out = and_27_out ? and_27_out : 1'bz;  // Driver driver_241
  assign pulldown_8_out = and_28_out ? and_28_out : 1'bz;  // Driver driver_242
  assign X_EN = and_29_out ? and_29_out : 1'bz;  // Driver driver_243
  assign Y_EN = and_30_out ? and_30_out : 1'bz;  // Driver driver_244
  Button SCLK1 (.out(SCLK1_out));
  Button CPR_START_STOP (.out(CPR_START_STOP_out));
  Button CPR_CLK_MAN (.out(CPR_CLK_MAN_out));
  Button CPR_MANUAL (.out(CPR_MANUAL_out));
  Button CPR_CLEAR (.out(CPR_CLEAR_out));
  PullDown #(.Bits(8)) pulldown_36 (.out(pulldown_36_out));
  PullDown pulldown_37 (.out(pulldown_37_out));
  PullDown #(.Bits(8)) pulldown_38 (.out(pulldown_38_out));
  PullDown pulldown_39 (.out(pulldown_39_out));
  PullDown #(.Bits(8)) pulldown_40 (.out(pulldown_40_out));
  PullDown pulldown_41 (.out(pulldown_41_out));
  PullDown pulldown_42 (.out(pulldown_42_out));
  PullDown pulldown_43 (.out(pulldown_43_out));
  PullDown #(.Bits(16)) pulldown_44 (.out(pulldown_44_out));
  PullDown pulldown_45 (.out(pulldown_45_out));
  PullDown #(.Bits(16)) pulldown_46 (.out(pulldown_46_out));
  PullDown pulldown_47 (.out(pulldown_47_out));
  PullDown #(.Bits(16)) pulldown_48 (.out(pulldown_48_out));
  PullDown pulldown_49 (.out(pulldown_49_out));
  PullDown pulldown_50 (.out(pulldown_50_out));
  PullDown pulldown_51 (.out(pulldown_51_out));
  and and_27 (and_27_out, ~tunnel, LDA);  // And
  assign pulldown_5_out = and_27_out ? out_46[15:8] : 8'bz;  // Driver driver_245
  and and_28 (and_28_out, ~tunnel, LDB);  // And
  assign pulldown_7_out = and_28_out ? out_46[15:8] : 8'bz;  // Driver driver_246
  and and_29 (and_29_out, ~tunnel, LDX);  // And
  assign pulldown_9_out = and_29_out ? out_46[15:8] : 8'bz;  // Driver driver_247
  and and_30 (and_30_out, ~tunnel, LDY);  // And
  assign pulldown_11_out = and_30_out ? out_46[15:8] : 8'bz;  // Driver driver_248
  assign driver_249_out = CPR_START_STOP_out ? CPR_START_STOP_out : 1'bz;  // Driver driver_249
  assign driver_250_out = CPR_CLK_MAN_out ? CPR_CLK_MAN_out : 1'bz;  // Driver driver_250
  assign driver_251_out = CPR_MANUAL_out ? CPR_MANUAL_out : 1'bz;  // Driver driver_251
  assign driver_252_out = CPR_CLEAR_out ? CPR_CLEAR_out : 1'bz;  // Driver driver_252
  assign pulldown_36_out = driver_155_out ? driver_154_out : 8'bz;  // Driver driver_253
  assign pulldown_44_out = driver_164_out ? driver_163_out : 16'bz;  // Driver driver_254
  PullDown pulldown_52 (.out(driver_249_out));
  PullDown pulldown_53 (.out(driver_250_out));
  assign pulldown_37_out = driver_155_out ? driver_155_out : 1'bz;  // Driver driver_255
  assign pulldown_45_out = driver_164_out ? driver_164_out : 1'bz;  // Driver driver_256
  assign pulldown_6_out = M_LDA_t ? M_LDA_t : 1'bz;  // Driver driver_257
  assign pulldown_8_out = M_LDB_t ? M_LDB_t : 1'bz;  // Driver driver_258
  assign X_EN = M_LDX_t ? M_LDX_t : 1'bz;  // Driver driver_259
  assign Y_EN = M_LDY_t ? M_LDY_t : 1'bz;  // Driver driver_260
  assign pulldown_14_out = LDC ? LDC : 1'bz;  // Driver driver_261
  assign Z_EN = LDZ ? LDZ : 1'bz;  // Driver driver_262
  PullDown pulldown_54 (.out(driver_251_out));
  PullDown pulldown_55 (.out(driver_252_out));
  PullDown pulldown_56 (.out(INTST));
  Delay #(.delayTime(10)) delay_29 (.in(pulldown_37_out), .out(delay_29_out));
  Delay #(.delayTime(10)) delay_30 (.in(pulldown_45_out), .out(delay_30_out));
  assign pulldown_5_out = M_LDA_t ? M_LD___D : 8'bz;  // Driver driver_263
  assign pulldown_7_out = M_LDB_t ? M_LD___D : 8'bz;  // Driver driver_264
  assign pulldown_9_out = M_LDX_t ? M_LD___D : 8'bz;  // Driver driver_265
  assign pulldown_11_out = M_LDY_t ? M_LD___D : 8'bz;  // Driver driver_266
  assign pulldown_13_out = LDC ? {out_327, A_t[0], B_t} : 16'bz;  // Driver driver_267
  assign pulldown_15_out = LDZ ? {X_t, X_2, Y_2} : 16'bz;  // Driver driver_268
  assign driver_249_out = INTST ? INTST : 1'bz;  // Driver driver_269
  Delay #(.delayTime(20)) delay_31 (.in(K_ON), .out(delay_31_out));
  Delay #(.delayTime(20)) delay_32 (.in(K_OFF), .out(delay_32_out));
  Register #(.Bits(8)) M_BRANCH (.D(pulldown_36_out), .C(delay_29_out), .en(pulldown_37_out), .Q(out_45));
  Register #(.Bits(16)) K_BRANCH (.D(pulldown_44_out), .C(delay_30_out), .en(pulldown_45_out), .Q(out_39));
  not not_9 (not_9_out, O_INTDIS);
  not not_10 (not_10_out, delay_31_out);
  not not_11 (not_11_out, delay_32_out);
  PullDown #(.Bits(16)) pulldown_57 (.out(driver_163_out));
  PullDown pulldown_58 (.out(driver_164_out));
  PullDown pulldown_59 (.out(driver_165_out));
  PullDown pulldown_60 (.out(driver_166_out));
  PullDown pulldown_61 (.out(driver_167_out));
  assign pulldown_6_out = M_LDA ? M_LDA : 1'bz;  // Driver driver_270
  assign pulldown_8_out = M_LDB ? M_LDB : 1'bz;  // Driver driver_271
  assign X_EN = M_LDX ? M_LDX : 1'bz;  // Driver driver_272
  assign Y_EN = M_LDY ? M_LDY : 1'bz;  // Driver driver_273
  assign pulldown_14_out = M_LDC ? M_LDC : 1'bz;  // Driver driver_274
  assign Z_EN = M_LDZ ? M_LDZ : 1'bz;  // Driver driver_275
  and and_31 (and_31_out, not_9_out, driver_249_out);
  and and_32 (and_32_out, K_ON, not_10_out);
  and and_33 (and_33_out, K_OFF, not_11_out);
  assign pulldown_39_out = driver_156_out ? driver_156_out : 1'bz;  // Driver driver_276
  assign pulldown_47_out = driver_165_out ? driver_165_out : 1'bz;  // Driver driver_277
  assign pulldown_5_out = M_LDA ? M_LD8___D_t : 8'bz;  // Driver driver_278
  assign pulldown_7_out = M_LDB ? M_LD8___D_t : 8'bz;  // Driver driver_279
  assign pulldown_9_out = M_LDX ? M_LD8___D_t : 8'bz;  // Driver driver_280
  assign pulldown_11_out = M_LDY ? M_LD8___D_t : 8'bz;  // Driver driver_281
  assign pulldown_13_out = M_LDC ? M_LD16___D_t : 16'bz;  // Driver driver_282
  assign pulldown_15_out = M_LDZ ? M_LD16___D_t : 16'bz;  // Driver driver_283
  DipSwitch dipswitch_1 (.out(dipswitch_1_out));
  assign pulldown_38_out = driver_156_out ? out_45 : 8'bz;  // Driver driver_284
  assign pulldown_40_out = driver_190_out ? driver_191_out : 8'bz;  // Driver driver_285
  PullDown #(.Bits(8)) pulldown_62 (.out(driver_154_out));
  PullDown pulldown_63 (.out(driver_155_out));
  PullDown pulldown_64 (.out(driver_156_out));
  PullDown pulldown_65 (.out(driver_157_out));
  PullDown pulldown_66 (.out(driver_158_out));
  PullDown pulldown_67 (.out(driver_190_out));
  PullDown #(.Bits(25)) pulldown_68 (.out(driver_199_out));
  PullDown #(.Bits(8)) pulldown_69 (.out(driver_191_out));
  assign pulldown_46_out = driver_165_out ? out_39 : 16'bz;  // Driver driver_286
  and and_34 (A_EN, pulldown_6_out, ~driver_5_out);  // And
  and and_35 (B_EN, pulldown_8_out, ~driver_5_out);  // And
  and and_36 (C_EN, pulldown_14_out, ~driver_5_out);  // And
  D_FF d_ff_1 (.D(d_ff_1_nq), .C(CLK1), .Q(_8192), .nQ(d_ff_1_nq));
  D_FF d_ff_2 (.D(d_ff_2_nq), .C(d_ff_1_nq), .Q(f2_2_4092), .nQ(d_ff_2_nq));
  D_FF d_ff_3 (.D(d_ff_3_nq), .C(d_ff_2_nq), .Q(_2048), .nQ(d_ff_3_nq));
  D_FF d_ff_4 (.D(d_ff_4_nq), .C(d_ff_3_nq), .Q(f4_2_1024), .nQ(d_ff_4_nq));
  D_FF d_ff_5 (.D(d_ff_5_nq), .C(d_ff_4_nq), .Q(f4_2_512), .nQ(d_ff_5_nq));
  D_FF d_ff_6 (.D(d_ff_6_nq), .C(d_ff_5_nq), .Q(_256), .nQ(d_ff_6_nq));
  D_FF d_ff_7 (.D(d_ff_7_nq), .C(d_ff_6_nq), .Q(f6_2_128), .nQ(d_ff_7_nq));
  D_FF d_ff_8 (.D(d_ff_8_nq), .C(d_ff_7_nq), .Q(f7_2_64), .nQ(d_ff_8_nq));
  D_FF d_ff_9 (.D(d_ff_9_nq), .C(d_ff_8_nq), .Q(_32), .nQ(d_ff_9_nq));
  D_FF d_ff_10 (.D(d_ff_10_nq), .C(d_ff_9_nq), .Q(_16), .nQ(d_ff_10_nq));
  D_FF d_ff_11 (.D(d_ff_11_nq), .C(d_ff_10_nq), .Q(_8), .nQ(d_ff_11_nq));
  D_FF d_ff_12 (.D(d_ff_12_nq), .C(d_ff_11_nq), .Q(_4), .nQ(d_ff_12_nq));
  D_FF d_ff_13 (.D(d_ff_13_nq), .C(d_ff_12_nq), .Q(_2), .nQ(d_ff_13_nq));
  D_FF d_ff_14 (.D(d_ff_14_nq), .C(d_ff_13_nq), .Q(f8_2_1), .nQ(d_ff_14_nq));
  Register #(.Bits(3)) register_4 (.D({in_28, in_29, in_30}), .C(SCLK1_out), .en(SCLK1_out), .Q(out_31));
  and and_37 (VGA_C, dipswitch_1_out, VGA_clock);
  assign driver_287_out = and_32_out ? and_32_out : 1'bz;  // Driver driver_287
  assign driver_288_out = and_33_out ? and_33_out : 1'bz;  // Driver driver_288
  assign pulldown_41_out = driver_190_out ? driver_190_out : 1'bz;  // Driver driver_289
  Register #(.Bits(8)) u_A (.D(pulldown_5_out), .C(delay_33_out), .en(pulldown_6_out), .Q({out_327, A_t[0]}));
  Delay #(.delayTime(20)) delay_33 (.in(pulldown_6_out), .out(delay_33_out));
  Register #(.Bits(8)) u_B (.D(pulldown_7_out), .C(delay_34_out), .en(pulldown_8_out), .Q(B_t));
  Delay #(.delayTime(20)) delay_34 (.in(pulldown_8_out), .out(delay_34_out));
  Register #(.Bits(8)) u_X (.D(pulldown_9_out), .C(delay_35_out), .en(X_EN), .Q({X_t, X_2}));
  Delay #(.delayTime(20)) delay_35 (.in(X_EN), .out(delay_35_out));
  Register #(.Bits(8)) u_Y (.D(pulldown_11_out), .C(delay_36_out), .en(Y_EN), .Q(Y_2));
  Delay #(.delayTime(20)) delay_36 (.in(Y_EN), .out(delay_36_out));
  Register #(.Bits(16)) u_C (.D(pulldown_13_out), .C(delay_37_out), .en(pulldown_14_out), .Q(C));
  Delay #(.delayTime(20)) delay_37 (.in(pulldown_14_out), .out(delay_37_out));
  Register #(.Bits(16)) u_Z (.D(pulldown_15_out), .C(delay_38_out), .en(Z_EN), .Q({Z2, Z1}));
  Delay #(.delayTime(20)) delay_38 (.in(Z_EN), .out(delay_38_out));
  Delay #(.delayTime(10)) delay_39 (.in(and_31_out), .out(delay_39_out));
  Add #(.Bits(8)) M_ADDER (.a(out_44), .b(8'h1), .c_i(1'b0), .s(M_ADDER_s), .c_o(out_43));
  assign pulldown_39_out = driver_157_out ? driver_157_out : 1'bz;  // Driver driver_290
  Delay #(.delayTime(10)) delay_40 (.in(pulldown_39_out), .out(delay_40_out));
  PullDown pulldown_70 (.out(pulldown_39_out));
  PullDown #(.Bits(8)) pulldown_71 (.out(pulldown_38_out));
  assign pulldown_42_out = driver_190_out ? delay_41_out : 1'bz;  // Driver driver_291
  Delay #(.delayTime(10)) delay_41 (.in(driver_190_out), .out(delay_41_out));
  Add #(.Bits(16)) K_ADDER (.a(PC), .b(16'h1), .c_i(1'b0), .s(K_ADDER_s), .c_o(out_37));
  assign pulldown_47_out = driver_166_out ? driver_166_out : 1'bz;  // Driver driver_292
  Delay #(.delayTime(10)) delay_42 (.in(pulldown_47_out), .out(delay_42_out));
  PullDown pulldown_72 (.out(pulldown_47_out));
  PullDown #(.Bits(16)) pulldown_73 (.out(pulldown_46_out));
  T_FF t_ff_5 (.T(and_31_out), .C(delay_39_out), .Q(t_ff_5_q), .nQ(t_ff_5_nq));
  assign driver_287_out = delay_45_out ? delay_45_out : 1'bz;  // Driver driver_293
  Delay #(.delayTime(20)) delay_43 (.in(driver_287_out), .out(delay_43_out));
  PullDown pulldown_74 (.out(driver_287_out));
  assign driver_288_out = delay_46_out ? delay_46_out : 1'bz;  // Driver driver_294
  Delay #(.delayTime(20)) delay_44 (.in(driver_288_out), .out(delay_44_out));
  PullDown pulldown_75 (.out(driver_288_out));
  assign pulldown_38_out = driver_157_out ? M_ADDER_s : 8'bz;  // Driver driver_295
  Register #(.Bits(8)) M_CUR_ADDR (.D(pulldown_38_out), .C(delay_40_out), .en(pulldown_39_out), .Q(out_44));
  assign pulldown_46_out = driver_166_out ? K_ADDER_s : 16'bz;  // Driver driver_296
  Register #(.Bits(16)) K_CUR_ADDR (.D(pulldown_46_out), .C(delay_42_out), .en(pulldown_47_out), .Q(PC));
  T_FF t_ff_6 (.T(driver_287_out), .C(delay_43_out), .Q(t_ff_6_q));  // open: nQ
  T_FF t_ff_7 (.T(driver_288_out), .C(delay_44_out), .Q(t_ff_7_q));  // open: nQ
  assign pulldown_41_out = driver_158_out ? driver_158_out : 1'bz;  // Driver driver_297
  assign pulldown_49_out = driver_167_out ? driver_167_out : 1'bz;  // Driver driver_298
  T_FF t_ff_8 (.T(driver_250_out), .C(driver_250_out), .Q(t_ff_8_q), .nQ(t_ff_8_nq));
  Delay #(.delayTime(10)) delay_45 (.in(and_38_out), .out(delay_45_out));
  Delay #(.delayTime(10)) delay_46 (.in(and_39_out), .out(delay_46_out));
  assign pulldown_40_out = driver_158_out ? out_44 : 8'bz;  // Driver driver_299
  assign pulldown_43_out = driver_158_out ? driver_158_out : 1'bz;  // Driver driver_300
  assign pulldown_48_out = driver_167_out ? PC : 16'bz;  // Driver driver_301
  assign pulldown_51_out = driver_167_out ? driver_167_out : 1'bz;  // Driver driver_302
  Delay #(.delayTime(20)) delay_47 (.in(and_31_out), .out(delay_47_out));
  and and_38 (and_38_out, t_ff_6_q, and_41_out);
  and and_39 (and_39_out, t_ff_7_q, and_42_out);
  EEPROM #(.AddrBits(8), .Bits(25)) eeprom_2 (
    .A(pulldown_40_out), .CS(pulldown_41_out), .WE(pulldown_42_out), .OE(pulldown_43_out), .D(eeprom_2_d));
  EEPROM #(.AddrBits(16), .Bits(25)) K_ROM (
    .A(pulldown_48_out), .CS(pulldown_49_out), .WE(pulldown_50_out), .OE(pulldown_51_out), .D(K_ROM_d));
  PullDown pulldown_76 (.out(HEARTBEAT));
  Register register_5 (.D(t_ff_5_q), .C(delay_47_out), .en(and_31_out), .Q(INTERUPT));
  Delay #(.delayTime(10)) delay_48 (.in(driver_190_out), .out(delay_48_out));
  assign driver_303_out = driver_167_out ? K_ROM_d : 25'bz;  // Driver driver_303
  assign HEARTBEAT = clkdecode_1_o8 ? CLK1 : 1'bz;  // Driver driver_304
  assign HEARTBEAT = clkdecode_1_o7 ? f2_2_4092 : 1'bz;  // Driver driver_305
  and and_40 (and_40_out, HEARTBEAT, INTERUPT);
  and and_41 (and_41_out, delay_49_out, clk_5);
  Delay #(.delayTime(10)) delay_49 (.in(t_ff_6_q), .out(delay_49_out));
  and and_42 (and_42_out, delay_50_out, clk_5);
  Delay #(.delayTime(10)) delay_50 (.in(t_ff_7_q), .out(delay_50_out));
  assign eeprom_2_d = delay_48_out ? driver_199_out : 25'bz;  // Driver driver_306
  assign driver_303_out = driver_158_out ? eeprom_2_d : 25'bz;  // Driver driver_307
  PullDown #(.Bits(25)) pulldown_77 (.out(eeprom_2_d));
  assign HEARTBEAT = clkdecode_1_o6 ? f4_2_1024 : 1'bz;  // Driver driver_308
  assign HEARTBEAT = clkdecode_1_o5 ? f4_2_512 : 1'bz;  // Driver driver_309
  assign INTST = t_ff_6_q ? t_ff_6_q : 1'bz;  // Driver driver_310
  assign INTST = t_ff_7_q ? t_ff_7_q : 1'bz;  // Driver driver_311
  assign HEARTBEAT = clkdecode_1_o4 ? f6_2_128 : 1'bz;  // Driver driver_312
  assign HEARTBEAT = clkdecode_1_o3 ? f7_2_64 : 1'bz;  // Driver driver_313
  PullDown #(.Bits(25)) pulldown_78 (.out(driver_303_out));
  assign HEARTBEAT = clkdecode_1_o2 ? f8_2_1 : 1'bz;  // Driver driver_314
  assign HEARTBEAT = clkdecode_1_o1 ? 1'b0 : 1'bz;  // Driver driver_315
  CPR cpr_1 (
    .clock(and_40_out), .clock_manual(t_ff_8_q), .manual(driver_251_out), .clear(driver_252_out),
    .ovfl(out_33), .count(out_34), .\null (out_35), .next(NEXT), .copy(COPY), .run(RUN));
  Delay #(.delayTime(10)) delay_51 (.in(driver_226_out), .out(delay_51_out));
  Seven_Seg_Hex seven_seg_hex_1 (.d(out_327[6:3]), .dp(pulldown_81_out));
  Register #(.Bits(25)) u_COPY (.D(driver_303_out), .C(delay_51_out), .en(driver_226_out), .Q(out_46));
  Seven_Seg_Hex seven_seg_hex_2 (.d({out_327[2:0], A_t[0]}), .dp(pulldown_81_out));
  clkdecode clkdecode_1 (
    .i(out_31), .o1(clkdecode_1_o1), .o2(clkdecode_1_o2), .o3(clkdecode_1_o3), .o4(clkdecode_1_o4),
    .o5(clkdecode_1_o5), .o6(clkdecode_1_o6), .o7(clkdecode_1_o7), .o8(clkdecode_1_o8));
  PullDown #(.Bits(8)) pulldown_79 (.out(out_46[7:0]));
  PullDown #(.Bits(16)) pulldown_80 (.out(out_46[23:8]));
  PullDown pulldown_81 (.out(pulldown_81_out));
  PullDown pulldown_82 (.out(out_46[24]));
  Seven_Seg_Hex seven_seg_hex_3 (.d(B_t[7:4]), .dp(pulldown_84_out));
  Seven_Seg_Hex seven_seg_hex_4 (.d(B_t[3:0]), .dp(pulldown_84_out));
  not not_12 (tunnel, out_46[24]);
  assign OP = driver_162_out ? out_46[7:0] : 8'bz;  // Driver driver_316
  PullDown #(.Bits(8)) pulldown_83 (.out(OP));
  PullDown pulldown_84 (.out(pulldown_84_out));
  Seven_Seg_Hex seven_seg_hex_5 (.d({X_t, X_2[5:4]}), .dp(pulldown_85_out));
  Seven_Seg_Hex seven_seg_hex_6 (.d(X_2[3:0]), .dp(pulldown_85_out));
  PullDown pulldown_85 (.out(pulldown_85_out));
  Seven_Seg_Hex seven_seg_hex_7 (.d(Y_2[7:4]), .dp(pulldown_86_out));
  Seven_Seg_Hex seven_seg_hex_8 (.d(Y_2[3:0]), .dp(pulldown_86_out));
  PullDown pulldown_86 (.out(pulldown_86_out));
  Seven_Seg_Hex seven_seg_hex_9 (.d(C[15:12]), .dp(pulldown_89_out));
  Seven_Seg_Hex seven_seg_hex_10 (.d(C[11:8]), .dp(pulldown_89_out));
  Button MAN_OP_SEND (.out(MAN_OP_SEND_out));
  PullDown #(.Bits(8)) pulldown_87 (.out(pulldown_87_out));
  Seven_Seg_Hex seven_seg_hex_11 (.d(C[7:4]), .dp(pulldown_89_out));
  PullDown #(.Bits(8)) pulldown_88 (.out(pulldown_88_out));
  assign pulldown_88_out = ~MAN_OP_EN ? OP : 8'bz;  // DriverInvSel driverinvsel_9
  assign pulldown_88_out = MAN_OP_SEND_out ? pulldown_87_out : 8'bz;  // Driver driver_317
  assign pulldown_87_out = MAN_OP_EN ? MAN_OP_DATA : 8'bz;  // Driver driver_318
  Seven_Seg_Hex seven_seg_hex_12 (.d(C[3:0]), .dp(pulldown_89_out));
  INT_DECIDER int_decider_1 (.LOC({X_t, X_2}), .INT(INT), .INT_FULL(INT_FULL), .INT_DEL(INT_DEL), .CHNG_MODE(CHGMD));
  OP_SEL op_sel_1 (
    .OP(pulldown_88_out), ._0_NULL(NULL), ._1_KMSWP(KMSWP), ._2_INT(INT), ._3_SIDEL(SIDEL), ._4_SBRM(SBRM),
    ._5_SBRK(SBRK), ._6_BR(BR), ._7_LDA(LDA), ._8_LDB(LDB), ._9_LDX(LDX), ._10_LDY(LDY), ._11_LDC(LDC),
    ._12_LDZ(LDZ), ._13_STA(STA), ._14_STB(STB), ._15_STX(STX), ._16_STY(STY), ._17_STC(STC), ._18_STZ(STZ),
    ._19_SSP(SSP), ._20_SPP(SPP), ._21_SMM(SMM), ._22_TXS(TXS), ._23_TSX(TSX), ._24_PHA(PHA), ._25_PLA(PLA),
    ._26_PHP(PHP), ._27_PLP(PLP), ._28_LSR(LSR), ._29_LSL(LSL), ._30_ROR(ROR), ._31_ROL(ROL), ._32_ASR(ASR),
    ._33_ASL(ASL), ._34_ADD(ADD), ._35_ADC(ADC), ._36_SUB(SUB), ._37_SBC(SBC), ._38_MUL(MUL), ._39_MLC(MLC),
    ._40_DIV(DIV), ._41_NOT(NOT), ._42_AND(AND), ._43_NAND(NAND), ._44_OR(OR), ._45_XOR(XOR), ._46_NOR(NOR),
    ._47_XNOR(XNOR), ._48_NEG(INV), ._49_CMP(CMP), ._50_CNT(CNT), ._52_SEC(SEC), ._53_CLC(CLC),
    ._54_SEV(SEV), ._55_CLV(CLV), ._56_SEZ(SEZ), ._57_CLZ(CLZ), ._58_SEN(SEN), ._59_CLN(CLN), ._60_SES(SES),
    ._61_CLS(CLS), ._62_SEE(SEE), ._63_CLE(CLE), ._64_SEB(SEB), ._65_CLB(CLB), ._66_TGLDEC(TGLDEC),
    ._67_TGLINTDIS(TGLINTDIS), ._68_BNN(BNN), ._69_BNG(BNG), ._70_BNZ(BNZ), ._71_BZE(BZE), ._72_BNO(BNO),
    ._73_BOV(BOV), ._74_BNC(BNC), ._75_BCA(BCA), ._76_BBE(BBE), ._77_BSE(BSE), ._78_BCC(BCC), ._79_BCS(BCS),
    ._80_BNE(BNE), ._81_BEQ(BEQ), ._82_BPL(BPL), ._83_BMI(BMI), ._84_LEDD_SET(LEDD_SET),
    ._85_TGLZADDR(TGLZADDR), ._86(TAB), ._87(TAX), ._88(TAY), ._89(TBA), ._90(TBX), ._91(TBY), ._92(TXA),
    ._93(TXB), ._94(TXY), ._95(TYA), ._96(TYB), ._97(TYX), ._98(op_sel_1__98), ._99(op_sel_1__99),
    ._100(op_sel_1__100), ._101(op_sel_1__101), ._102(op_sel_1__102), ._103(op_sel_1__103),
    ._104(op_sel_1__104), ._105(op_sel_1__105), ._106(op_sel_1__106), ._107(WR2_MRAM), ._108(EXT_L),
    ._109(op_sel_1__109), ._110(op_sel_1__110), ._111(op_sel_1__111), ._112(op_sel_1__112),
    ._113(op_sel_1__113), ._114(op_sel_1__114), ._115(op_sel_1__115), ._116(op_sel_1__116),
    ._117(op_sel_1__117));
  PullDown pulldown_89 (.out(pulldown_89_out));
  Seven_Seg_Hex seven_seg_hex_13 (.d(Z2[7:4]), .dp(pulldown_90_out));
  Seven_Seg_Hex seven_seg_hex_14 (.d(Z2[3:0]), .dp(pulldown_90_out));
  Seven_Seg_Hex seven_seg_hex_15 (.d(Z1[7:4]), .dp(pulldown_90_out));
  Seven_Seg_Hex seven_seg_hex_16 (.d(Z1[3:0]), .dp(pulldown_90_out));
  PullDown pulldown_90 (.out(pulldown_90_out));
  PullDown #(.Bits(8)) pulldown_91 (.out(M_LD8___D_t));
  PullDown pulldown_92 (.out(M_LDA));
  PullDown pulldown_93 (.out(M_LDB));
  PullDown pulldown_94 (.out(M_LDX));
  PullDown pulldown_95 (.out(M_LDY));
  assign M_LD8___D_t = M_LD8___EN ? M_LD8___D : 8'bz;  // Driver driver_319
  Button u_M_LDA (.out(M_LDA_out));
  assign M_LDA = M_LD8___EN ? M_LDA_out : 1'bz;  // Driver driver_320
  Button u_M_LDB (.out(M_LDB_out));
  assign M_LDB = M_LD8___EN ? M_LDB_out : 1'bz;  // Driver driver_321
  Button u_M_LDX (.out(M_LDX_out));
  assign M_LDX = M_LD8___EN ? M_LDX_out : 1'bz;  // Driver driver_322
  Button u_M_LDY (.out(M_LDY_out));
  assign M_LDY = M_LD8___EN ? M_LDY_out : 1'bz;  // Driver driver_323
  assign M_LD16___D_t = M_LD16___EN ? M_LD16___D : 16'bz;  // Driver driver_324
  PullDown #(.Bits(16)) pulldown_96 (.out(M_LD16___D_t));
  PullDown pulldown_97 (.out(M_LDC));
  PullDown pulldown_98 (.out(M_LDZ));
  Button u_M_LDC (.out(M_LDC_out));
  assign M_LDC = M_LD16___EN ? M_LDC_out : 1'bz;  // Driver driver_325
  Button u_M_LDZ (.out(M_LDZ_out));
  assign M_LDZ = M_LD16___EN ? M_LDZ_out : 1'bz;  // Driver driver_326
  PullDown #(.Bits(16)) pulldown_99 (.out(pulldown_99_out));
  PullDown pulldown_100 (.out(pulldown_100_out));
  PullDown pulldown_101 (.out(pulldown_101_out));
  PullDown pulldown_102 (.out(pulldown_102_out));
  PullDown #(.Bits(16)) pulldown_103 (.out(M_LD___A_t));
  PullDown pulldown_104 (.out(M_LDA_t));
  PullDown pulldown_105 (.out(M_LDB_t));
  PullDown pulldown_106 (.out(M_LDX_t));
  PullDown pulldown_107 (.out(M_LDY_t));
  assign M_LD___A_t = M_LD___EN ? M_LD___A : 16'bz;  // Driver driver_327
  or or_2 (M_LD___EN_t, M_LDY_t, M_LDX_t, M_LDB_t, M_LDA_t);
  Button M_LDA_2 (.out(M_LDA_2_out));
  assign M_LDA_t = M_LD___EN ? M_LDA_2_out : 1'bz;  // Driver driver_328
  Button M_LDB_2 (.out(M_LDB_2_out));
  assign M_LDB_t = M_LD___EN ? M_LDB_2_out : 1'bz;  // Driver driver_329
  Button M_LDX_2 (.out(M_LDX_2_out));
  assign M_LDX_t = M_LD___EN ? M_LDX_2_out : 1'bz;  // Driver driver_330
  Button M_LDY_2 (.out(M_LDY_2_out));
  assign M_LDY_t = M_LD___EN ? M_LDY_2_out : 1'bz;  // Driver driver_331
  assign pulldown_99_out = LDY_t ? out_46[23:8] : 16'bz;  // Driver driver_332
  PullDown #(.Bits(8)) pulldown_108 (.out(pulldown_108_out));
  PullDown pulldown_109 (.out(pulldown_109_out));
  PullDown #(.Bits(8)) pulldown_110 (.out(pulldown_110_out));
  PullDown pulldown_111 (.out(pulldown_111_out));
  assign pulldown_100_out = LDY_t ? LDY_t : 1'bz;  // Driver driver_333
  Add #(.Bits(16)) add_3 (.a(_8_16decoder_1__8_16_out), .b(16'h100), .c_i(1'b0), .s(SP_DECODED), .c_o(out_86));
  assign pulldown_102_out = LDY_t ? LDY_t : 1'bz;  // Driver driver_334
  assign M_ST___A_t = M_ST___EN ? M_ST___A : 16'bz;  // Driver driver_335
  PullDown #(.Bits(16)) pulldown_112 (.out(M_ST___A_t));
  PullDown #(.Bits(8)) pulldown_113 (.out(M_ST___D_t));
  PullDown pulldown_114 (.out(M_ST___EN_t));
  assign pulldown_99_out = LDX_t ? out_46[23:8] : 16'bz;  // Driver driver_336
  _8_16decoder _8_16decoder_1 (._8_16_in(SP), ._8_16_out(_8_16decoder_1__8_16_out));
  assign M_ST___D_t = M_ST___EN ? M_ST___D : 8'bz;  // Driver driver_337
  assign pulldown_100_out = LDX_t ? LDX_t : 1'bz;  // Driver driver_338
  assign pulldown_102_out = LDX_t ? LDX_t : 1'bz;  // Driver driver_339
  assign driver_340_out = SSP ? Y_2 : 8'bz;  // Driver driver_340
  assign driver_341_out = SSP ? SSP : 1'bz;  // Driver driver_341
  assign driver_340_out = M_SSP ? M_Y : 8'bz;  // Driver driver_342
  assign driver_341_out = M_SSP ? M_SSP : 1'bz;  // Driver driver_343
  assign driver_344_out = TXS ? TXS : 1'bz;  // Driver driver_344
  assign driver_344_out = M_TXS ? M_TXS : 1'bz;  // Driver driver_345
  assign pulldown_111_out = driver_341_out ? driver_341_out : 1'bz;  // Driver driver_346
  Button M_ST (.out(M_ST_out));
  assign M_ST___EN_t = M_ST___EN ? M_ST_out : 1'bz;  // Driver driver_347
  PullDown pulldown_115 (.out(driver_341_out));
  assign pulldown_110_out = driver_341_out ? driver_340_out : 8'bz;  // Driver driver_348
  assign pulldown_99_out = driver_352_out ? SP_DECODED : 16'bz;  // Driver driver_349
  assign pulldown_99_out = LDB_t ? out_46[23:8] : 16'bz;  // Driver driver_350
  PullDown #(.Bits(8)) pulldown_116 (.out(driver_340_out));
  PullDown pulldown_117 (.out(driver_344_out));
  assign pulldown_111_out = driver_344_out ? driver_344_out : 1'bz;  // Driver driver_351
  assign driver_352_out = M_PLP ? M_PLP : 1'bz;  // Driver driver_352
  assign pulldown_100_out = driver_352_out ? driver_352_out : 1'bz;  // Driver driver_353
  assign pulldown_100_out = LDB_t ? LDB_t : 1'bz;  // Driver driver_354
  assign pulldown_108_out = pulldown_109_out ? W_PS : 8'bz;  // Driver driver_355
  assign driver_356_out = PLA ? PLA : 1'bz;  // Driver driver_356
  assign driver_356_out = PLP ? PLP : 1'bz;  // Driver driver_357
  assign driver_356_out = M_PLA ? M_PLA : 1'bz;  // Driver driver_358
  assign driver_356_out = M_PLP ? M_PLP : 1'bz;  // Driver driver_359
  assign driver_360_out = M_SPP ? M_SPP : 1'bz;  // Driver driver_360
  assign driver_360_out = SPP ? SPP : 1'bz;  // Driver driver_361
  assign driver_362_out = M_SMM ? M_SMM : 1'bz;  // Driver driver_362
  assign driver_362_out = SMM ? SMM : 1'bz;  // Driver driver_363
  assign pulldown_110_out = driver_344_out ? {X_t, X_2} : 8'bz;  // Driver driver_364
  assign pulldown_110_out = driver_362_out ? sub_1_s : 8'bz;  // Driver driver_365
  assign M_ST___A_t_t = M_ST___EN_2 ? M_ST___A_2 : 16'bz;  // Driver driver_366
  PullDown #(.Bits(16)) pulldown_118 (.out(M_ST___A_t_t));
  PullDown #(.Bits(8)) pulldown_119 ();  // open: out
  PullDown pulldown_120 (.out(M_STA));
  PullDown pulldown_121 (.out(M_STB));
  PullDown pulldown_122 (.out(M_STX));
  PullDown pulldown_123 (.out(M_STY));
  assign driver_352_out = PLP ? PLP : 1'bz;  // Driver driver_367
  PullDown pulldown_124 (.out(driver_352_out));
  assign pulldown_102_out = driver_352_out ? driver_352_out : 1'bz;  // Driver driver_368
  assign pulldown_102_out = LDB_t ? LDB_t : 1'bz;  // Driver driver_369
  assign pulldown_109_out = PLP ? PLP : 1'bz;  // Driver driver_370
  PullDown pulldown_125 (.out(driver_356_out));
  assign driver_362_out = driver_356_out ? driver_356_out : 1'bz;  // Driver driver_371
  PullDown pulldown_126 (.out(driver_362_out));
  assign pulldown_110_out = driver_360_out ? add_4_s : 8'bz;  // Driver driver_372
  assign pulldown_111_out = driver_362_out ? driver_362_out : 1'bz;  // Driver driver_373
  assign pulldown_99_out = driver_384_out ? SP_DECODED : 16'bz;  // Driver driver_374
  assign pulldown_99_out = LDA_t ? out_46[23:8] : 16'bz;  // Driver driver_375
  assign pulldown_109_out = M_PLP ? M_PLP : 1'bz;  // Driver driver_376
  PullDown pulldown_127 (.out(pulldown_127_out));
  assign pulldown_127_out = PHA ? PHA : 1'bz;  // Driver driver_377
  assign pulldown_127_out = PHP ? PHP : 1'bz;  // Driver driver_378
  assign pulldown_127_out = M_PHA ? M_PHA : 1'bz;  // Driver driver_379
  assign pulldown_127_out = M_PHP ? M_PHP : 1'bz;  // Driver driver_380
  assign driver_360_out = pulldown_127_out ? pulldown_127_out : 1'bz;  // Driver driver_381
  PullDown pulldown_128 (.out(driver_360_out));
  assign pulldown_111_out = driver_360_out ? driver_360_out : 1'bz;  // Driver driver_382
  Button u_M_STA (.out(M_STA_out));
  assign M_STA = M_ST___EN_2 ? M_STA_out : 1'bz;  // Driver driver_383
  assign driver_384_out = M_PLA ? M_PLA : 1'bz;  // Driver driver_384
  assign pulldown_100_out = driver_384_out ? driver_384_out : 1'bz;  // Driver driver_385
  assign pulldown_100_out = LDA_t ? LDA_t : 1'bz;  // Driver driver_386
  Seven_Seg_Hex seven_seg_hex_17 (.d(PS[7:4]), .dp(pulldown_132_out));
  Register #(.Bits(8)) register_6 (.D(pulldown_108_out), .C(delay_52_out), .en(pulldown_109_out), .Q(PS));
  Delay #(.delayTime(20)) delay_52 (.in(pulldown_109_out), .out(delay_52_out));
  Seven_Seg_Hex seven_seg_hex_18 (.d(SP[7:4]), .dp(pulldown_133_out));
  PullDown pulldown_129 (.out(pulldown_111_out));
  PullDown #(.Bits(8)) pulldown_130 (.out(pulldown_110_out));
  Delay #(.delayTime(20)) delay_53 (.in(pulldown_111_out), .out(delay_53_out));
  Button u_M_STB (.out(M_STB_out));
  assign M_STB = M_ST___EN_2 ? M_STB_out : 1'bz;  // Driver driver_387
  assign driver_384_out = PLA ? PLA : 1'bz;  // Driver driver_388
  PullDown pulldown_131 (.out(driver_384_out));
  assign pulldown_102_out = driver_384_out ? driver_384_out : 1'bz;  // Driver driver_389
  assign pulldown_102_out = LDA_t ? LDA_t : 1'bz;  // Driver driver_390
  Seven_Seg_Hex seven_seg_hex_19 (.d(PS[3:0]), .dp(pulldown_132_out));
  Seven_Seg_Hex seven_seg_hex_20 (.d(SP[3:0]), .dp(pulldown_133_out));
  Sub #(.Bits(8)) sub_1 (.a(SP), .b(8'h1), .c_i(1'b0), .s(sub_1_s), .c_o(out_84));
  Add #(.Bits(8)) add_4 (.a(SP), .b(8'h1), .c_i(1'b0), .s(add_4_s), .c_o(out_85));
  Register #(.Bits(8)) register_7 (.D(pulldown_110_out), .C(delay_53_out), .en(pulldown_111_out), .Q(SP));
  Button u_M_STX (.out(M_STX_out));
  assign M_STX = M_ST___EN_2 ? M_STX_out : 1'bz;  // Driver driver_391
  PullDown pulldown_132 (.out(pulldown_132_out));
  PullDown pulldown_133 (.out(pulldown_133_out));
  Button u_M_STY (.out(M_STY_out));
  assign M_STY = M_ST___EN_2 ? M_STY_out : 1'bz;  // Driver driver_392
  assign pulldown_99_out = driver_395_out ? SP_DECODED : 16'bz;  // Driver driver_393
  assign pulldown_99_out = M_LD___EN_t ? M_LD___A_t : 16'bz;  // Driver driver_394
  assign driver_395_out = M_PHP ? M_PHP : 1'bz;  // Driver driver_395
  assign pulldown_100_out = driver_395_out ? driver_395_out : 1'bz;  // Driver driver_396
  assign pulldown_100_out = M_LD___EN_t ? M_LD___EN_t : 1'bz;  // Driver driver_397
  assign driver_395_out = PHP ? PHP : 1'bz;  // Driver driver_398
  PullDown pulldown_134 (.out(driver_395_out));
  assign pulldown_101_out = driver_395_out ? driver_395_out : 1'bz;  // Driver driver_399
  assign pulldown_102_out = M_LD___EN_t ? M_LD___EN_t : 1'bz;  // Driver driver_400
  assign pulldown_99_out = driver_403_out ? SP_DECODED : 16'bz;  // Driver driver_401
  assign pulldown_99_out = M_STY ? M_ST___A_t_t : 16'bz;  // Driver driver_402
  Button u_M_SSP (.out(M_SSP));
  assign driver_403_out = M_PHA ? M_PHA : 1'bz;  // Driver driver_403
  assign pulldown_100_out = driver_403_out ? driver_403_out : 1'bz;  // Driver driver_404
  assign pulldown_100_out = M_STY ? M_STY : 1'bz;  // Driver driver_405
  Button u_M_SPP (.out(M_SPP));
  assign driver_403_out = PHA ? PHA : 1'bz;  // Driver driver_406
  PullDown pulldown_135 (.out(driver_403_out));
  assign pulldown_101_out = driver_403_out ? driver_403_out : 1'bz;  // Driver driver_407
  assign pulldown_101_out = M_STY ? M_STY : 1'bz;  // Driver driver_408
  Button u_M_SMM (.out(M_SMM));
  Button u_M_TSX (.out(M_TSX));
  assign pulldown_99_out = STY ? out_46[23:8] : 16'bz;  // Driver driver_409
  assign pulldown_99_out = M_STX ? M_ST___A_t_t : 16'bz;  // Driver driver_410
  Button u_M_TXS (.out(M_TXS));
  assign pulldown_100_out = STY ? STY : 1'bz;  // Driver driver_411
  assign pulldown_100_out = M_STX ? M_STX : 1'bz;  // Driver driver_412
  Button u_M_PHA (.out(M_PHA));
  assign pulldown_101_out = STY ? STY : 1'bz;  // Driver driver_413
  assign pulldown_101_out = M_STX ? M_STX : 1'bz;  // Driver driver_414
  Button u_M_PLA (.out(M_PLA));
  Button u_M_PHP (.out(M_PHP));
  Button u_M_PLP (.out(M_PLP));
  assign pulldown_99_out = STX ? out_46[23:8] : 16'bz;  // Driver driver_415
  assign pulldown_100_out = STX ? STX : 1'bz;  // Driver driver_416
  assign pulldown_99_out = M_STB ? M_ST___A_t_t : 16'bz;  // Driver driver_417
  assign pulldown_100_out = M_STB ? M_STB : 1'bz;  // Driver driver_418
  assign pulldown_101_out = STX ? STX : 1'bz;  // Driver driver_419
  assign pulldown_101_out = M_STB ? M_STB : 1'bz;  // Driver driver_420
  assign pulldown_99_out = STB ? out_46[23:8] : 16'bz;  // Driver driver_421
  assign pulldown_99_out = M_STA ? M_ST___A_t_t : 16'bz;  // Driver driver_422
  Button u_M_ADD (.out(M_ADD));
  Button u_M_ADC (.out(M_ADC));
  Button u_M_LSR (.out(M_LSR));
  Button u_M_LSL (.out(M_LSL));
  Button u_M_NOT (.out(M_NOT));
  Button u_M_AND (.out(M_AND));
  assign pulldown_100_out = STB ? STB : 1'bz;  // Driver driver_423
  assign pulldown_100_out = M_STA ? M_STA : 1'bz;  // Driver driver_424
  Button u_M_SUB (.out(M_SUB));
  Button u_M_ROR (.out(M_ROR));
  Button u_M_NAND (.out(M_NAND));
  assign pulldown_101_out = STB ? STB : 1'bz;  // Driver driver_425
  assign pulldown_101_out = M_STA ? M_STA : 1'bz;  // Driver driver_426
  Button u_M_SBC (.out(M_SBC));
  Button u_M_ROL (.out(M_ROL));
  Button u_M_OR (.out(M_OR));
  assign pulldown_99_out = STA ? out_46[23:8] : 16'bz;  // Driver driver_427
  assign pulldown_99_out = M_ST___EN_t ? M_ST___A_t : 16'bz;  // Driver driver_428
  Button u_M_MUL (.out(M_MUL));
  Button u_M_MLC (.out(M_MLC));
  Button u_M_ASR (.out(M_ASR));
  Button u_M_ASL (.out(M_ASL));
  Button u_M_NOR (.out(M_NOR));
  Button u_M_XOR (.out(M_XOR));
  assign pulldown_100_out = STA ? STA : 1'bz;  // Driver driver_429
  assign pulldown_100_out = M_ST___EN_t ? M_ST___EN_t : 1'bz;  // Driver driver_430
  Button u_M_DIV (.out(M_DIV));
  Button u_M_CMP (.out(M_CMP));
  Button u_M_XNOR (.out(M_XNOR));
  assign pulldown_101_out = STA ? STA : 1'bz;  // Driver driver_431
  Delay #(.delayTime(10)) delay_54 (.in(pulldown_100_out), .out(delay_54_out));
  assign pulldown_101_out = M_ST___EN_t ? M_ST___EN_t : 1'bz;  // Driver driver_432
  Button u_M_INV (.out(M_INV));
  assign driver_433_out = O_ZADDR ? {Z2, Z1} : 16'bz;  // Driver driver_433
  EEPROM #(.AddrBits(16), .Bits(8)) eeprom_3 (
    .A(driver_433_out), .CS(delay_54_out), .WE(pulldown_101_out), .OE(pulldown_102_out), .D(eeprom_3_d));
  assign driver_433_out = ~O_ZADDR ? pulldown_99_out : 16'bz;  // DriverInvSel driverinvsel_10
  PullDown #(.Bits(16)) pulldown_136 (.out(driver_433_out));
  Button u_M_CNT (.out(M_CNT));
  PullDown #(.Bits(8)) pulldown_137 (.out(eeprom_3_d));
  assign eeprom_3_d = delay_55_out ? PS : 8'bz;  // Driver driver_434
  assign eeprom_3_d = pulldown_141_out ? {out_327, A_t[0]} : 8'bz;  // Driver driver_435
  assign eeprom_3_d = delay_57_out ? Y_2 : 8'bz;  // Driver driver_436
  assign eeprom_3_d = delay_58_out ? {X_t, X_2} : 8'bz;  // Driver driver_437
  assign eeprom_3_d = delay_59_out ? B_t : 8'bz;  // Driver driver_438
  assign eeprom_3_d = delay_60_out ? {out_327, A_t[0]} : 8'bz;  // Driver driver_439
  assign eeprom_3_d = delay_61_out ? M_ST___D_t : 8'bz;  // Driver driver_440
  assign eeprom_3_d = delay_62_out ? {out_327, A_t[0]} : 8'bz;  // Driver driver_441
  assign eeprom_3_d = delay_63_out ? B_t : 8'bz;  // Driver driver_442
  assign eeprom_3_d = delay_64_out ? {X_t, X_2} : 8'bz;  // Driver driver_443
  assign eeprom_3_d = delay_65_out ? Y_2 : 8'bz;  // Driver driver_444
  assign M_LD___D = M_LD___EN_t ? eeprom_3_d : 8'bz;  // Driver driver_445
  assign LDA___D = LDA_t ? eeprom_3_d : 8'bz;  // Driver driver_446
  assign LDB___D = LDB_t ? eeprom_3_d : 8'bz;  // Driver driver_447
  assign LDX___D = LDX_t ? eeprom_3_d : 8'bz;  // Driver driver_448
  assign LDY___D = LDY_t ? eeprom_3_d : 8'bz;  // Driver driver_449
  PullDown pulldown_138 (.out(pulldown_138_out));
  assign W_PS = pulldown_138_out ? eeprom_3_d : 8'bz;  // Driver driver_450
  PullDown pulldown_139 (.out(pulldown_139_out));
  assign W_A = pulldown_139_out ? eeprom_3_d : 8'bz;  // Driver driver_451
  Button u_M_SEC (.out(M_SEC));
  Button u_M_SES (.out(M_SES));
  PullDown pulldown_140 (.out(pulldown_140_out));
  Delay #(.delayTime(10)) delay_55 (.in(pulldown_140_out), .out(delay_55_out));
  Delay #(.delayTime(10)) delay_56 (.in(pulldown_150_out), .out(delay_55_out));
  PullDown pulldown_141 (.out(pulldown_141_out));
  PullDown pulldown_142 (.out(pulldown_141_out));
  Delay #(.delayTime(10)) delay_57 (.in(STY), .out(delay_57_out));
  Delay #(.delayTime(10)) delay_58 (.in(STX), .out(delay_58_out));
  Delay #(.delayTime(10)) delay_59 (.in(STB), .out(delay_59_out));
  Delay #(.delayTime(10)) delay_60 (.in(STA), .out(delay_60_out));
  Delay #(.delayTime(10)) delay_61 (.in(M_ST___EN_t), .out(delay_61_out));
  Delay #(.delayTime(10)) delay_62 (.in(M_STA), .out(delay_62_out));
  Delay #(.delayTime(10)) delay_63 (.in(M_STB), .out(delay_63_out));
  Delay #(.delayTime(10)) delay_64 (.in(M_STX), .out(delay_64_out));
  Delay #(.delayTime(10)) delay_65 (.in(M_STY), .out(delay_65_out));
  PullDown #(.Bits(8)) pulldown_143 (.out(M_LD___D));
  PullDown #(.Bits(8)) pulldown_144 (.out(LDA___D));
  PullDown #(.Bits(8)) pulldown_145 (.out(LDB___D));
  PullDown #(.Bits(8)) pulldown_146 (.out(LDX___D));
  PullDown #(.Bits(8)) pulldown_147 (.out(LDY___D));
  assign pulldown_138_out = PLP ? PLP : 1'bz;  // Driver driver_452
  assign pulldown_138_out = M_PLP ? M_PLP : 1'bz;  // Driver driver_453
  PullDown #(.Bits(8)) pulldown_148 (.out(W_PS));
  assign pulldown_139_out = PLA ? PLA : 1'bz;  // Driver driver_454
  assign pulldown_139_out = M_PLA ? M_PLA : 1'bz;  // Driver driver_455
  PullDown #(.Bits(8)) pulldown_149 (.out(W_A));
  Button u_M_CLC (.out(M_CLC));
  Button u_M_CLS (.out(M_CLS));
  PullDown pulldown_150 (.out(pulldown_150_out));
  assign pulldown_140_out = PHP ? PHP : 1'bz;  // Driver driver_456
  assign pulldown_150_out = M_PHP ? M_PHP : 1'bz;  // Driver driver_457
  assign pulldown_141_out = delay_66_out ? delay_66_out : 1'bz;  // Driver driver_458
  assign pulldown_141_out = delay_67_out ? delay_67_out : 1'bz;  // Driver driver_459
  Button u_M_SEV (.out(M_SEV));
  Button u_M_SEE (.out(M_SEE));
  Delay #(.delayTime(10)) delay_66 (.in(PHA), .out(delay_66_out));
  Delay #(.delayTime(10)) delay_67 (.in(M_PHA), .out(delay_67_out));
  Button u_M_CLV (.out(M_CLV));
  Button u_M_CLE (.out(M_CLE));
  LEDDISPLAY leddisplay_1 (
    .LEDD_EN(LEDD_SET), .LEDD_X({X_t, X_2}), .LEDD_Y(Y_2), .LEDD_D(leddisplay_1_ledd_d),
    .LEDD_0(leddisplay_1_ledd_0), .LEDD_1(leddisplay_1_ledd_1), .LEDD_2(leddisplay_1_ledd_2),
    .LEDD_3(leddisplay_1_ledd_3), .LEDD_4(leddisplay_1_ledd_4), .LEDD_5(leddisplay_1_ledd_5),
    .LEDD_6(leddisplay_1_ledd_6), .LEDD_7(leddisplay_1_ledd_7));
  Button u_M_SEZ (.out(M_SEZ));
  Button u_M_SEB (.out(M_SEB));
  Button u_M_CLZ (.out(M_CLZ));
  Button u_M_CLB (.out(M_CLB));
  Button u_M_SEN (.out(M_SEN));
  Button u_M_CLN (.out(M_CLN));
  BarrelShifter #(.Bits(8), .direction("right")) barrelshifter_1 (
    .in({out_327, A_t[0]}), .shift(B_t[3:0]), .out(W_LSR));
  BarrelShifter #(.Bits(8)) barrelshifter_2 (.in({out_327, A_t[0]}), .shift(B_t[3:0]), .out(W_LSL));
  BarrelShifter #(.barrelShifterMode("rotate"), .Bits(8), .direction("right")) barrelshifter_3 (
    .in({out_327, A_t[0]}), .shift(B_t[3:0]), .out(W_ROR));
  BarrelShifter #(.Bits(8), .barrelShifterMode("rotate")) barrelshifter_4 (
    .in({out_327, A_t[0]}), .shift(B_t[3:0]), .out(W_ROL));
  BarrelShifter #(.barrelShifterMode("arithmetic"), .Bits(8), .direction("right")) barrelshifter_5 (
    .in({out_327, A_t[0]}), .shift(B_t[3:0]), .out(W_ASR));
  BarrelShifter #(.barrelShifterMode("arithmetic"), .Bits(8)) barrelshifter_6 (
    .in({out_327, A_t[0]}), .shift(B_t[3:0]), .out(W_ASL));
  Delay #(.delayTime(10)) delay_68 (.in(leddisplay_1_ledd_0), .out(delay_68_out));
  Delay #(.delayTime(10)) delay_69 (.in(leddisplay_1_ledd_1), .out(delay_69_out));
  Delay #(.delayTime(10)) delay_70 (.in(leddisplay_1_ledd_2), .out(delay_70_out));
  Delay #(.delayTime(10)) delay_71 (.in(leddisplay_1_ledd_3), .out(delay_71_out));
  Delay #(.delayTime(10)) delay_72 (.in(leddisplay_1_ledd_4), .out(delay_72_out));
  Delay #(.delayTime(10)) delay_73 (.in(leddisplay_1_ledd_5), .out(delay_73_out));
  Delay #(.delayTime(10)) delay_74 (.in(leddisplay_1_ledd_6), .out(delay_74_out));
  Delay #(.delayTime(10)) delay_75 (.in(leddisplay_1_ledd_7), .out(delay_75_out));
  assign driver_460_out = in_99 ? in_99 : 1'bz;  // Driver driver_460
  Register #(.Bits(8)) register_8 (.D(leddisplay_1_ledd_d), .C(delay_68_out), .en(leddisplay_1_ledd_0), .Q(out_102));
  Register #(.Bits(8)) register_9 (
    .D(leddisplay_1_ledd_d), .C(delay_69_out), .en(leddisplay_1_ledd_1), .Q(register_9_q));
  Register #(.Bits(8)) register_10 (
    .D(leddisplay_1_ledd_d), .C(delay_70_out), .en(leddisplay_1_ledd_2), .Q(register_10_q));
  Register #(.Bits(8)) register_11 (
    .D(leddisplay_1_ledd_d), .C(delay_71_out), .en(leddisplay_1_ledd_3), .Q(register_11_q));
  Register #(.Bits(8)) register_12 (
    .D(leddisplay_1_ledd_d), .C(delay_72_out), .en(leddisplay_1_ledd_4), .Q(register_12_q));
  Register #(.Bits(8)) register_13 (
    .D(leddisplay_1_ledd_d), .C(delay_73_out), .en(leddisplay_1_ledd_5), .Q(register_13_q));
  Register #(.Bits(8)) register_14 (
    .D(leddisplay_1_ledd_d), .C(delay_74_out), .en(leddisplay_1_ledd_6), .Q(register_14_q));
  Register #(.Bits(8)) register_15 (
    .D(leddisplay_1_ledd_d), .C(delay_75_out), .en(leddisplay_1_ledd_7), .Q(register_15_q));
  Button M_TZA (.out(M_TGLZADDR));
  and and_43 (and_43_out, clk, in_97);
  assign driver_460_out = ~in_99 ? and_43_out : 1'bz;  // DriverInvSel driverinvsel_11
  Delay #(.delayTime(10)) delay_76 (.in(driver_460_out), .out(delay_76_out));
  Button M_TID (.out(M_TGLINTDIS));
  Counter #(.Bits(3)) counter_3 (.en(driver_460_out), .C(delay_76_out), .clr(in_99), .out(out_98), .ovf(counter_3_ovf));
  assign DISP_OUT = DISP_C1 ? out_102 : 8'bz;  // Driver driver_461
  assign DISP_OUT = DISP_C2 ? register_9_q : 8'bz;  // Driver driver_462
  assign DISP_OUT = DISP_C3 ? register_10_q : 8'bz;  // Driver driver_463
  assign DISP_OUT = DISP_C4 ? register_11_q : 8'bz;  // Driver driver_464
  assign DISP_OUT = DISP_C5 ? register_12_q : 8'bz;  // Driver driver_465
  assign DISP_OUT = DISP_C6 ? register_13_q : 8'bz;  // Driver driver_466
  assign DISP_OUT = DISP_C7 ? register_14_q : 8'bz;  // Driver driver_467
  assign DISP_OUT = DISP_C8 ? register_15_q : 8'bz;  // Driver driver_468
  Button M_TD (.out(M_TGLDEC));
  Add #(.Bits(8)) add_5 (.a({out_327, A_t[0]}), .b(B_t), .c_i(1'b0), .s(W_ADD), .c_o(W_C_ADD));
  Add #(.Bits(8)) add_6 (.a({out_327, A_t[0]}), .b(B_t), .c_i(O_CARRY), .s(W_ADC), .c_o(W_C_ADC));
  Sub #(.Bits(8)) sub_2 (.a({out_327, A_t[0]}), .b(B_t), .c_i(1'b0), .s(W_SUB), .c_o(W_C_SUB));
  Sub #(.Bits(8)) sub_3 (.a({out_327, A_t[0]}), .b(B_t), .c_i(O_CARRY), .s(W_SBC), .c_o(W_C_SBC));
  Mul #(.Bits(8)) mul_1 (.a({out_327, A_t[0]}), .b(B_t), .mul(O_MUL));
  Div #(.Bits(8)) div_1 (.a({out_327, A_t[0]}), .b(B_t), .q(W_DIVQ), .r(W_DIVR));
  Button u_M_CHGMD (.out(M_CHGMD));
  not not_13 (not_13_out, out_98[0]);
  not not_14 (not_14_out, out_98[1]);
  not not_15 (not_15_out, out_98[0]);
  not not_16 (not_16_out, out_98[1]);
  not not_17 (not_17_out, out_98[2]);
  not not_18 (not_18_out, out_98[0]);
  not not_19 (not_19_out, out_98[2]);
  not not_20 (not_20_out, out_98[1]);
  not not_21 (not_21_out, out_98[2]);
  not not_22 (not_22_out, out_98[0]);
  not not_23 (not_23_out, out_98[1]);
  not not_24 (not_24_out, out_98[2]);
  LedMatrix #(.ledPersistence("true")) ledmatrix_1 (.rows(DISP_OUT), .column(out_98));
  and and_44 (DISP_C8, out_98[0], out_98[1], out_98[2]);
  and and_45 (DISP_C7, not_13_out, out_98[1], out_98[2]);
  and and_46 (DISP_C6, out_98[0], not_14_out, out_98[2]);
  and and_47 (DISP_C5, not_15_out, not_16_out, out_98[2]);
  and and_48 (DISP_C4, out_98[0], out_98[1], not_17_out);
  and and_49 (DISP_C3, not_18_out, out_98[1], not_19_out);
  and and_50 (DISP_C2, out_98[0], not_20_out, not_21_out);
  and and_51 (DISP_C1, not_22_out, not_23_out, not_24_out);
  Button u_M_TAB (.out(M_TAB));
  Button u_M_TXA (.out(M_TXA));
  assign W_NOT = ~{out_327, A_t[0]};  // Not not_25, 8 bits wide
  assign W_AND = {out_327, A_t[0]} & B_t;  // And and_52, 8 bits wide
  assign W_NAND = ~({out_327, A_t[0]} & B_t);  // NAnd nand_1, 8 bits wide
  assign W_OR = {out_327, A_t[0]} | B_t;  // Or or_3, 8 bits wide
  assign W_NOR = ~({out_327, A_t[0]} | B_t);  // NOr nor_1, 8 bits wide
  assign W_XOR = {out_327, A_t[0]} ^ B_t;  // XOr xor_1, 8 bits wide
  assign W_XNOR = ~({out_327, A_t[0]} ^ B_t);  // XNOr xnor_1, 8 bits wide
  Button u_M_TAX (.out(M_TAX));
  Button u_M_TXB (.out(M_TXB));
  Button u_M_TAY (.out(M_TAY));
  Button u_M_TXY (.out(M_TXY));
  Button u_M_TBA (.out(M_TBA));
  Button u_M_TYA (.out(M_TYA));
  Button u_M_TBX (.out(M_TBX));
  Button u_M_TBY (.out(M_TBY));
  Button u_M_TYB (.out(M_TYB));
  Button u_M_TYX (.out(M_TYX));
  and and_53 (and_53_out, BNN, O_NEG);
  assign CBR = and_53_out ? and_53_out : 1'bz;  // Driver driver_469
  assign CBR = and_54_out ? and_54_out : 1'bz;  // Driver driver_470
  Comparator #(.Bits(8)) comparator_2 (.a({out_327, A_t[0]}), .b(B_t), .gt(W__gt), .eq(W__eq), .lt(W__lt));
  Neg #(.Bits(8)) neg_1 (.in({out_327, A_t[0]}), .out(W_INV));
  BitCount #(.Bits(8)) bitcount_1 (.in({out_327, A_t[0]}), .out(W_CNT));
  and and_54 (and_54_out, BNG, O_NEG);
  assign driver_471_out = CHGMD ? CHGMD : 1'bz;  // Driver driver_471
  PullDown #(.Bits(2)) pulldown_151 (.out(pulldown_151_out));
  PullDown pulldown_152 (.out(driver_471_out));
  assign driver_472_out = TGLZADDR ? TGLZADDR : 1'bz;  // Driver driver_472
  PullDown pulldown_153 (.out(driver_472_out));
  assign driver_473_out = TGLDEC ? TGLDEC : 1'bz;  // Driver driver_473
  PullDown pulldown_154 (.out(driver_473_out));
  assign driver_474_out = TGLINTDIS ? TGLINTDIS : 1'bz;  // Driver driver_474
  PullDown pulldown_155 (.out(driver_474_out));
  assign driver_475_out = CLC ? CLC : 1'bz;  // Driver driver_475
  PullDown pulldown_156 (.out(pulldown_156_out));
  PullDown pulldown_157 (.out(driver_475_out));
  assign driver_476_out = CLV ? CLV : 1'bz;  // Driver driver_476
  PullDown pulldown_158 (.out(pulldown_158_out));
  PullDown pulldown_159 (.out(driver_476_out));
  assign driver_477_out = CLZ ? CLZ : 1'bz;  // Driver driver_477
  PullDown pulldown_160 (.out(pulldown_160_out));
  PullDown pulldown_161 (.out(driver_477_out));
  assign driver_478_out = CLN ? CLN : 1'bz;  // Driver driver_478
  PullDown pulldown_162 (.out(pulldown_162_out));
  PullDown pulldown_163 (.out(driver_478_out));
  assign driver_479_out = CLS ? CLS : 1'bz;  // Driver driver_479
  PullDown pulldown_164 (.out(pulldown_164_out));
  PullDown pulldown_165 (.out(driver_479_out));
  assign driver_480_out = CLE ? CLE : 1'bz;  // Driver driver_480
  PullDown pulldown_166 (.out(pulldown_166_out));
  PullDown pulldown_167 (.out(driver_480_out));
  assign driver_481_out = CLB ? CLB : 1'bz;  // Driver driver_481
  PullDown pulldown_168 (.out(pulldown_168_out));
  PullDown pulldown_169 (.out(driver_481_out));
  not not_26 (not_26_out, O_ZERO);
  and and_55 (and_55_out, BNZ, not_26_out);
  assign CBR = and_55_out ? and_55_out : 1'bz;  // Driver driver_482
  assign pulldown_151_out = CHGMD ? Y_2[1:0] : 2'bz;  // Driver driver_483
  assign pulldown_156_out = CLC ? 1'b0 : 1'bz;  // Driver driver_484
  assign pulldown_158_out = CLV ? 1'b0 : 1'bz;  // Driver driver_485
  assign pulldown_160_out = CLZ ? 1'b0 : 1'bz;  // Driver driver_486
  assign pulldown_162_out = CLN ? 1'b0 : 1'bz;  // Driver driver_487
  assign pulldown_164_out = CLS ? 1'b0 : 1'bz;  // Driver driver_488
  assign pulldown_166_out = CLE ? 1'b0 : 1'bz;  // Driver driver_489
  assign pulldown_168_out = CLB ? 1'b0 : 1'bz;  // Driver driver_490
  and and_56 (and_56_out, BZE, O_ZERO);
  assign CBR = and_56_out ? and_56_out : 1'bz;  // Driver driver_491
  assign driver_471_out = M_CHGMD ? M_CHGMD : 1'bz;  // Driver driver_492
  assign driver_472_out = M_TGLZADDR ? M_TGLZADDR : 1'bz;  // Driver driver_493
  assign driver_473_out = M_TGLDEC ? M_TGLDEC : 1'bz;  // Driver driver_494
  assign driver_474_out = M_TGLINTDIS ? M_TGLINTDIS : 1'bz;  // Driver driver_495
  assign driver_475_out = M_CLC ? M_CLC : 1'bz;  // Driver driver_496
  assign driver_476_out = M_CLV ? M_CLV : 1'bz;  // Driver driver_497
  assign driver_477_out = M_CLZ ? M_CLZ : 1'bz;  // Driver driver_498
  assign driver_478_out = M_CLN ? M_CLN : 1'bz;  // Driver driver_499
  assign driver_479_out = M_CLS ? M_CLS : 1'bz;  // Driver driver_500
  assign driver_480_out = M_CLE ? M_CLE : 1'bz;  // Driver driver_501
  assign driver_481_out = M_CLB ? M_CLB : 1'bz;  // Driver driver_502
  not not_27 (not_27_out, O_OVFL);
  Delay #(.delayTime(20)) delay_77 (.in(in_89), .out(delay_77_out));
  assign driver_503_out = delay_77_out ? delay_77_out : 1'bz;  // Driver driver_503
  assign pulldown_151_out = M_CHGMD ? M_GHGMD_D : 2'bz;  // Driver driver_504
  assign pulldown_156_out = M_CLC ? 1'b0 : 1'bz;  // Driver driver_505
  assign pulldown_158_out = M_CLV ? 1'b0 : 1'bz;  // Driver driver_506
  assign pulldown_160_out = M_CLZ ? 1'b0 : 1'bz;  // Driver driver_507
  assign pulldown_162_out = M_CLN ? 1'b0 : 1'bz;  // Driver driver_508
  assign pulldown_164_out = M_CLS ? 1'b0 : 1'bz;  // Driver driver_509
  assign pulldown_166_out = M_CLE ? 1'b0 : 1'bz;  // Driver driver_510
  assign pulldown_168_out = M_CLB ? 1'b0 : 1'bz;  // Driver driver_511
  and and_57 (and_57_out, BNO, not_27_out);
  assign CBR = and_57_out ? and_57_out : 1'bz;  // Driver driver_512
  assign driver_513_out = delay_77_out ? in_90 : 1'bz;  // Driver driver_513
  assign driver_475_out = SEC ? SEC : 1'bz;  // Driver driver_514
  assign driver_476_out = SEV ? SEV : 1'bz;  // Driver driver_515
  assign driver_477_out = SEZ ? SEZ : 1'bz;  // Driver driver_516
  assign driver_478_out = SEN ? SEN : 1'bz;  // Driver driver_517
  assign driver_479_out = SES ? SES : 1'bz;  // Driver driver_518
  assign driver_480_out = SEE ? SEE : 1'bz;  // Driver driver_519
  assign driver_481_out = SEB ? SEB : 1'bz;  // Driver driver_520
  and and_58 (and_58_out, and_59_out, and_62_out);
  and and_59 (and_59_out, not_28_out, not_29_out);
  not not_28 (not_28_out, driver_521_out[0]);
  not not_29 (not_29_out, driver_521_out[1]);
  assign driver_521_out = and_65_out ? {out_327, A_t[0]} : 8'bz;  // Driver driver_521
  assign driver_521_out = and_66_out ? B_t : 8'bz;  // Driver driver_522
  assign driver_521_out = and_67_out ? {X_t, X_2} : 8'bz;  // Driver driver_523
  assign driver_521_out = and_68_out ? Y_2 : 8'bz;  // Driver driver_524
  PullDown #(.Bits(8)) pulldown_170 (.out(driver_521_out));
  and and_60 (and_60_out, BOV, O_OVFL);
  assign CBR = and_60_out ? and_60_out : 1'bz;  // Driver driver_525
  Delay #(.delayTime(20)) delay_78 (.in(in_91), .out(delay_78_out));
  assign driver_503_out = delay_78_out ? delay_78_out : 1'bz;  // Driver driver_526
  assign pulldown_156_out = SEC ? 1'b1 : 1'bz;  // Driver driver_527
  assign driver_475_out = M_SEC ? M_SEC : 1'bz;  // Driver driver_528
  assign pulldown_158_out = SEV ? 1'b1 : 1'bz;  // Driver driver_529
  assign driver_476_out = M_SEV ? M_SEV : 1'bz;  // Driver driver_530
  assign pulldown_160_out = SEZ ? 1'b1 : 1'bz;  // Driver driver_531
  assign driver_477_out = M_SEZ ? M_SEZ : 1'bz;  // Driver driver_532
  assign pulldown_162_out = SEN ? 1'b1 : 1'bz;  // Driver driver_533
  assign driver_478_out = M_SEN ? M_SEN : 1'bz;  // Driver driver_534
  assign pulldown_164_out = SES ? 1'b1 : 1'bz;  // Driver driver_535
  assign driver_479_out = M_SES ? M_SES : 1'bz;  // Driver driver_536
  assign pulldown_166_out = SEE ? 1'b1 : 1'bz;  // Driver driver_537
  assign driver_480_out = M_SEE ? M_SEE : 1'bz;  // Driver driver_538
  assign pulldown_168_out = SEB ? 1'b1 : 1'bz;  // Driver driver_539
  assign driver_481_out = M_SEB ? M_SEB : 1'bz;  // Driver driver_540
  assign W_ZERO = driver_551_out ? and_61_out : 1'bz;  // Driver driver_541
  and and_61 (and_61_out, and_58_out, and_63_out);
  and and_62 (and_62_out, not_30_out, not_31_out);
  not not_30 (not_30_out, driver_521_out[2]);
  not not_31 (not_31_out, driver_521_out[3]);
  not not_32 (not_32_out, O_CARRY);
  assign CBR = and_69_out ? and_69_out : 1'bz;  // Driver driver_542
  assign driver_513_out = delay_78_out ? in_92 : 1'bz;  // Driver driver_543
  assign pulldown_156_out = M_SEC ? 1'b1 : 1'bz;  // Driver driver_544
  assign pulldown_158_out = M_SEV ? 1'b1 : 1'bz;  // Driver driver_545
  assign pulldown_160_out = M_SEZ ? 1'b1 : 1'bz;  // Driver driver_546
  assign pulldown_162_out = M_SEN ? 1'b1 : 1'bz;  // Driver driver_547
  assign pulldown_164_out = M_SES ? 1'b1 : 1'bz;  // Driver driver_548
  assign pulldown_166_out = M_SEE ? 1'b1 : 1'bz;  // Driver driver_549
  assign pulldown_168_out = M_SEB ? 1'b1 : 1'bz;  // Driver driver_550
  assign driver_551_out = A_EN ? A_EN : 1'bz;  // Driver driver_551
  assign driver_551_out = B_EN ? B_EN : 1'bz;  // Driver driver_552
  and and_63 (and_63_out, and_64_out, and_70_out);
  and and_64 (and_64_out, not_33_out, not_34_out);
  not not_33 (not_33_out, driver_521_out[4]);
  not not_34 (not_34_out, driver_521_out[5]);
  and and_65 (and_65_out, ~STC, A_EN);  // And
  and and_66 (and_66_out, B_EN, ~STC);  // And
  and and_67 (and_67_out, ~STZ, X_EN);  // And
  and and_68 (and_68_out, Y_EN, ~STZ);  // And
  and and_69 (and_69_out, BNC, not_32_out);
  assign driver_551_out = X_EN ? X_EN : 1'bz;  // Driver driver_553
  assign driver_551_out = Y_EN ? Y_EN : 1'bz;  // Driver driver_554
  and and_70 (and_70_out, not_35_out, not_36_out);
  not not_35 (not_35_out, driver_521_out[6]);
  not not_36 (not_36_out, driver_521_out[7]);
  and and_71 (and_71_out, BCA, O_CARRY);
  assign CBR = and_71_out ? and_71_out : 1'bz;  // Driver driver_555
  PullDown pulldown_171 (.out(driver_551_out));
  or or_4 (or_4_out, O__eq, O__lt);
  and and_72 (and_72_out, BBE, or_4_out);
  assign CBR = and_72_out ? and_72_out : 1'bz;  // Driver driver_556
  and and_73 (and_73_out, not_37_out, not_38_out);
  not not_37 (not_37_out, pulldown_172_out[0]);
  PullDown #(.Bits(16)) pulldown_172 (.out(pulldown_172_out));
  or or_5 (or_5_out, O__gt, O__eq);
  assign CBR = and_76_out ? and_76_out : 1'bz;  // Driver driver_557
  PullDown pulldown_173 (.out(W_ZERO));
  and and_74 (and_74_out, and_73_out, and_75_out);
  and and_75 (and_75_out, not_39_out, not_40_out);
  not not_38 (not_38_out, pulldown_172_out[1]);
  not not_39 (not_39_out, pulldown_172_out[2]);
  assign pulldown_172_out = C_EN ? C : 16'bz;  // Driver driver_558
  assign pulldown_172_out = Z_EN ? {Z2, Z1} : 16'bz;  // Driver driver_559
  and and_76 (and_76_out, BSE, or_5_out);
  and and_77 (and_77_out, and_74_out, and_80_out);
  and and_78 (and_78_out, not_41_out, not_43_out);
  not not_40 (not_40_out, pulldown_172_out[3]);
  not not_41 (not_41_out, pulldown_172_out[4]);
  not not_42 (not_42_out, O__gt);
  and and_79 (and_79_out, BCC, not_42_out);
  assign CBR = and_79_out ? and_79_out : 1'bz;  // Driver driver_560
  PullDown pulldown_174 (.out(pulldown_174_out));
  assign pulldown_174_out = Z_EN ? Z_EN : 1'bz;  // Driver driver_561
  assign pulldown_174_out = C_EN ? C_EN : 1'bz;  // Driver driver_562
  and and_80 (and_80_out, and_78_out, and_81_out);
  and and_81 (and_81_out, not_44_out, not_45_out);
  not not_43 (not_43_out, pulldown_172_out[5]);
  not not_44 (not_44_out, pulldown_172_out[6]);
  and and_82 (and_82_out, BCS, O__gt);
  assign CBR = and_82_out ? and_82_out : 1'bz;  // Driver driver_563
  assign W_ZERO = pulldown_174_out ? and_83_out : 1'bz;  // Driver driver_564
  and and_83 (and_83_out, and_77_out, and_88_out);
  and and_84 (and_84_out, not_46_out, not_48_out);
  not not_45 (not_45_out, pulldown_172_out[7]);
  not not_46 (not_46_out, pulldown_172_out[8]);
  not not_47 (not_47_out, O__eq);
  Delay #(.delayTime(20)) delay_79 (.in(M_SBC), .out(delay_79_out));
  assign driver_475_out = delay_79_out ? delay_79_out : 1'bz;  // Driver driver_565
  and and_85 (and_85_out, and_84_out, and_86_out);
  and and_86 (and_86_out, not_49_out, not_50_out);
  not not_48 (not_48_out, pulldown_172_out[9]);
  not not_49 (not_49_out, pulldown_172_out[10]);
  and and_87 (and_87_out, BNE, not_47_out);
  assign CBR = and_87_out ? and_87_out : 1'bz;  // Driver driver_566
  assign pulldown_156_out = delay_79_out ? W_C_SBC : 1'bz;  // Driver driver_567
  and and_88 (and_88_out, and_85_out, and_91_out);
  and and_89 (and_89_out, not_51_out, not_52_out);
  not not_50 (not_50_out, pulldown_172_out[11]);
  not not_51 (not_51_out, pulldown_172_out[12]);
  and and_90 (and_90_out, BEQ, O__eq);
  assign CBR = and_90_out ? and_90_out : 1'bz;  // Driver driver_568
  Delay #(.delayTime(20)) delay_80 (.in(SBC), .out(delay_80_out));
  assign driver_475_out = delay_80_out ? delay_80_out : 1'bz;  // Driver driver_569
  and and_91 (and_91_out, and_89_out, and_92_out);
  and and_92 (and_92_out, not_53_out, not_55_out);
  not not_52 (not_52_out, pulldown_172_out[13]);
  not not_53 (not_53_out, pulldown_172_out[14]);
  not not_54 (not_54_out, O__lt);
  assign CBR = and_93_out ? and_93_out : 1'bz;  // Driver driver_570
  assign pulldown_156_out = delay_80_out ? W_C_SBC : 1'bz;  // Driver driver_571
  not not_55 (not_55_out, pulldown_172_out[15]);
  and and_93 (and_93_out, BPL, not_54_out);
  Delay #(.delayTime(20)) delay_81 (.in(M_SUB), .out(delay_81_out));
  assign driver_475_out = delay_81_out ? delay_81_out : 1'bz;  // Driver driver_572
  Delay #(.delayTime(20)) delay_82 (.in(driver_573_out), .out(EN_ZERO));
  assign driver_573_out = LDA ? LDA : 1'bz;  // Driver driver_573
  assign driver_573_out = LDB ? LDB : 1'bz;  // Driver driver_574
  assign driver_573_out = LDC ? LDC : 1'bz;  // Driver driver_575
  assign driver_573_out = LDX ? LDX : 1'bz;  // Driver driver_576
  assign driver_573_out = LDY ? LDY : 1'bz;  // Driver driver_577
  assign driver_573_out = LDZ ? LDZ : 1'bz;  // Driver driver_578
  assign driver_573_out = M_LDA ? M_LDA : 1'bz;  // Driver driver_579
  assign driver_573_out = M_LDB ? M_LDB : 1'bz;  // Driver driver_580
  assign driver_573_out = M_LDC ? M_LDC : 1'bz;  // Driver driver_581
  assign driver_573_out = M_LDX ? M_LDX : 1'bz;  // Driver driver_582
  assign driver_573_out = M_LDY ? M_LDY : 1'bz;  // Driver driver_583
  assign driver_573_out = M_LDZ ? M_LDZ : 1'bz;  // Driver driver_584
  PullDown pulldown_175 (.out(driver_573_out));
  and and_94 (and_94_out, BMI, O__lt);
  assign CBR = and_94_out ? and_94_out : 1'bz;  // Driver driver_585
  PullDown pulldown_176 (.out(CBR));
  Delay #(.delayTime(20)) delay_83 (.in(SUB), .out(delay_83_out));
  assign driver_475_out = delay_83_out ? delay_83_out : 1'bz;  // Driver driver_586
  assign pulldown_156_out = delay_81_out ? W_C_SUB : 1'bz;  // Driver driver_587
  assign pulldown_156_out = delay_83_out ? W_C_SUB : 1'bz;  // Driver driver_588
  Delay #(.delayTime(20)) delay_84 (.in(M_ADC), .out(delay_84_out));
  assign driver_475_out = delay_84_out ? delay_84_out : 1'bz;  // Driver driver_589
  Delay #(.delayTime(20)) delay_85 (.in(M_MLC), .out(delay_85_out));
  assign driver_476_out = delay_85_out ? delay_85_out : 1'bz;  // Driver driver_590
  PullDown #(.Bits(8)) pulldown_177 (.out(pulldown_177_out));
  assign pulldown_156_out = delay_84_out ? W_C_ADC : 1'bz;  // Driver driver_591
  assign pulldown_158_out = delay_85_out ? W_MUL_OVFL : 1'bz;  // Driver driver_592
  assign pulldown_177_out = and_95_out ? {out_327, A_t[0]} : 8'bz;  // Driver driver_593
  assign pulldown_177_out = and_96_out ? B_t : 8'bz;  // Driver driver_594
  assign pulldown_177_out = and_97_out ? {X_t, X_2} : 8'bz;  // Driver driver_595
  assign pulldown_177_out = and_98_out ? Y_2 : 8'bz;  // Driver driver_596
  or or_6 (or_6_out, O_MUL[14], O_MUL[15]);
  Delay #(.delayTime(20)) delay_86 (.in(ADC), .out(delay_86_out));
  assign driver_475_out = delay_86_out ? delay_86_out : 1'bz;  // Driver driver_597
  Delay #(.delayTime(20)) delay_87 (.in(MLC), .out(delay_87_out));
  assign driver_476_out = delay_87_out ? delay_87_out : 1'bz;  // Driver driver_598
  assign W_NEG = driver_600_out ? pulldown_177_out[7] : 1'bz;  // Driver driver_599
  assign driver_600_out = A_EN ? A_EN : 1'bz;  // Driver driver_600
  and and_95 (and_95_out, ~STC, A_EN);  // And
  and and_96 (and_96_out, B_EN, ~STC);  // And
  and and_97 (and_97_out, ~STZ, X_EN);  // And
  and and_98 (and_98_out, Y_EN, ~STZ);  // And
  or or_7 (or_7_out, O_MUL[12], O_MUL[13]);
  or or_8 (or_8_out, or_7_out, or_6_out);
  Delay delay_88 (.in(driver_471_out), .out(delay_88_out));
  assign pulldown_156_out = delay_86_out ? W_C_ADC : 1'bz;  // Driver driver_601
  assign pulldown_158_out = delay_87_out ? W_MUL_OVFL : 1'bz;  // Driver driver_602
  Delay #(.delayTime(20)) delay_89 (.in(M_CMP), .out(delay_89_out));
  assign driver_479_out = delay_89_out ? delay_89_out : 1'bz;  // Driver driver_603
  Delay #(.delayTime(20)) delay_90 (.in(M_CMP), .out(delay_90_out));
  assign driver_480_out = delay_90_out ? delay_90_out : 1'bz;  // Driver driver_604
  Delay #(.delayTime(20)) delay_91 (.in(M_CMP), .out(delay_91_out));
  assign driver_481_out = delay_91_out ? delay_91_out : 1'bz;  // Driver driver_605
  assign driver_600_out = B_EN ? B_EN : 1'bz;  // Driver driver_606
  assign driver_600_out = X_EN ? X_EN : 1'bz;  // Driver driver_607
  or or_9 (or_9_out, O_MUL[10], O_MUL[11]);
  or or_10 (W_MUL_OVFL, or_12_out, or_8_out);
  Register #(.Bits(2)) register_16 (.D(pulldown_151_out), .C(delay_88_out), .en(driver_471_out), .Q(O_MODE));
  Delay #(.delayTime(20)) delay_92 (.in(M_ADD), .out(delay_92_out));
  assign driver_475_out = delay_92_out ? delay_92_out : 1'bz;  // Driver driver_608
  Delay #(.delayTime(20)) delay_93 (.in(M_MUL), .out(delay_93_out));
  assign driver_476_out = delay_93_out ? delay_93_out : 1'bz;  // Driver driver_609
  assign pulldown_164_out = delay_89_out ? W__lt : 1'bz;  // Driver driver_610
  assign pulldown_166_out = delay_90_out ? W__eq : 1'bz;  // Driver driver_611
  assign pulldown_168_out = delay_91_out ? W__gt : 1'bz;  // Driver driver_612
  PullDown pulldown_178 (.out(driver_600_out));
  assign driver_600_out = Y_EN ? Y_EN : 1'bz;  // Driver driver_613
  PullDown #(.Bits(16)) pulldown_179 (.out(pulldown_179_out));
  or or_11 (or_11_out, O_MUL[8], O_MUL[9]);
  or or_12 (or_12_out, or_11_out, or_9_out);
  Delay #(.delayTime(20)) delay_94 (.in(ADD), .out(delay_94_out));
  assign driver_475_out = delay_94_out ? delay_94_out : 1'bz;  // Driver driver_614
  assign pulldown_156_out = delay_92_out ? W_C_ADD : 1'bz;  // Driver driver_615
  Delay #(.delayTime(20)) delay_95 (.in(MUL), .out(delay_95_out));
  assign driver_476_out = delay_95_out ? delay_95_out : 1'bz;  // Driver driver_616
  assign pulldown_158_out = delay_93_out ? W_MUL_OVFL : 1'bz;  // Driver driver_617
  Delay #(.delayTime(20)) delay_96 (.in(EN_ZERO), .out(delay_96_out));
  assign driver_477_out = delay_96_out ? delay_96_out : 1'bz;  // Driver driver_618
  Delay #(.delayTime(20)) delay_97 (.in(EN_NEG), .out(delay_97_out));
  assign driver_478_out = delay_97_out ? delay_97_out : 1'bz;  // Driver driver_619
  Delay #(.delayTime(20)) delay_98 (.in(CMP), .out(delay_98_out));
  assign driver_479_out = delay_98_out ? delay_98_out : 1'bz;  // Driver driver_620
  Delay #(.delayTime(20)) delay_99 (.in(CMP), .out(delay_99_out));
  assign driver_480_out = delay_99_out ? delay_99_out : 1'bz;  // Driver driver_621
  Delay #(.delayTime(20)) delay_100 (.in(CMP), .out(delay_100_out));
  assign driver_481_out = delay_100_out ? delay_100_out : 1'bz;  // Driver driver_622
  PullDown pulldown_180 (.out(W_NEG));
  assign pulldown_179_out = C_EN ? C : 16'bz;  // Driver driver_623
  assign pulldown_179_out = Z_EN ? {Z2, Z1} : 16'bz;  // Driver driver_624
  not not_56 (not_56_out, O_MODE[0]);
  not not_57 (not_57_out, O_MODE[1]);
  not not_58 (not_58_out, O_MODE[1]);
  not not_59 (not_59_out, O_MODE[0]);
  assign pulldown_156_out = delay_94_out ? W_C_ADD : 1'bz;  // Driver driver_625
  assign pulldown_158_out = delay_95_out ? W_MUL_OVFL : 1'bz;  // Driver driver_626
  assign pulldown_160_out = delay_96_out ? W_ZERO : 1'bz;  // Driver driver_627
  assign pulldown_162_out = delay_97_out ? W_NEG : 1'bz;  // Driver driver_628
  assign pulldown_164_out = delay_98_out ? W__lt : 1'bz;  // Driver driver_629
  assign pulldown_166_out = delay_99_out ? W__eq : 1'bz;  // Driver driver_630
  assign pulldown_168_out = delay_100_out ? W__gt : 1'bz;  // Driver driver_631
  PullDown pulldown_181 (.out(pulldown_181_out));
  assign pulldown_181_out = Z_EN ? Z_EN : 1'bz;  // Driver driver_632
  Add #(.Bits(8)) add_7 (.a({8{1'b0}}), .b(O_MUL[7:0]), .c_i(O_CARRY), .s(add_7_s), .c_o(add_7_c_o));
  and and_99 (O_MD8, not_56_out, not_57_out);
  and and_100 (O_MD16, O_MODE[0], not_58_out);
  and and_101 (O_MD32, not_59_out, O_MODE[1]);
  and and_102 (O_MD64, O_MODE[0], O_MODE[1]);
  T_FF t_ff_9 (.T(driver_472_out), .C(delay_101_out), .Q(O_ZADDR));  // open: nQ
  Delay delay_101 (.in(driver_472_out), .out(delay_101_out));
  T_FF t_ff_10 (.T(driver_473_out), .C(delay_102_out), .Q(O_DEC));  // open: nQ
  Delay delay_102 (.in(driver_473_out), .out(delay_102_out));
  T_FF t_ff_11 (.T(driver_474_out), .C(delay_103_out), .Q(O_INTDIS));  // open: nQ
  Delay delay_103 (.in(driver_474_out), .out(delay_103_out));
  Register register_17 (.D(pulldown_156_out), .C(delay_104_out), .en(driver_475_out), .Q(O_CARRY));
  Delay delay_104 (.in(driver_475_out), .out(delay_104_out));
  Register register_18 (.D(pulldown_158_out), .C(delay_105_out), .en(driver_476_out), .Q(O_OVFL));
  Delay delay_105 (.in(driver_476_out), .out(delay_105_out));
  Register register_19 (.D(pulldown_160_out), .C(delay_106_out), .en(driver_477_out), .Q(O_ZERO));
  Delay delay_106 (.in(driver_477_out), .out(delay_106_out));
  Register register_20 (.D(pulldown_162_out), .C(delay_107_out), .en(driver_478_out), .Q(O_NEG));
  Delay delay_107 (.in(driver_478_out), .out(delay_107_out));
  Register register_21 (.D(pulldown_164_out), .C(delay_108_out), .en(driver_479_out), .Q(O__lt));
  Delay delay_108 (.in(driver_479_out), .out(delay_108_out));
  Register register_22 (.D(pulldown_166_out), .C(delay_109_out), .en(driver_480_out), .Q(O__eq));
  Delay delay_109 (.in(driver_480_out), .out(delay_109_out));
  Register register_23 (.D(pulldown_168_out), .C(delay_110_out), .en(driver_481_out), .Q(O__gt));
  Delay delay_110 (.in(driver_481_out), .out(delay_110_out));
  assign pulldown_181_out = C_EN ? C_EN : 1'bz;  // Driver driver_633
  assign driver_634_out = M_MLC ? M_MLC : 1'bz;  // Driver driver_634
  PullDown pulldown_182 (.out(driver_634_out));
  assign driver_634_out = MLC ? MLC : 1'bz;  // Driver driver_635
  assign W_MUL = driver_634_out ? add_7_s : 8'bz;  // Driver driver_636
  assign W_MUL = pulldown_183_out ? O_MUL[7:0] : 8'bz;  // Driver driver_637
  PullDown pulldown_183 (.out(pulldown_183_out));
  assign pulldown_183_out = MUL ? MUL : 1'bz;  // Driver driver_638
  assign pulldown_183_out = M_MUL ? M_MUL : 1'bz;  // Driver driver_639
  not not_60 (O_INT_BRK, INTERUPT);
  assign W_NEG = pulldown_181_out ? pulldown_179_out[15] : 1'bz;  // Driver driver_640
  Delay #(.delayTime(20)) delay_111 (.in(pulldown_184_out), .out(EN_NEG));
  PullDown pulldown_184 (.out(pulldown_184_out));
  PullDown #(.Bits(8)) pulldown_185 (.out(W_MUL));
  LED INT_BRK (.in(O_INT_BRK));
  LED MODE_8b (.in(O_MD8));
  LED MODE_16b (.in(O_MD16));
  LED MODE_32b (.in(O_MD32));
  LED MODE_64b (.in(O_MD64));
  LED ZADDR (.in(O_ZADDR));
  LED DEC (.in(O_DEC));
  LED INTDIS (.in(O_INTDIS));
  LED CARRY (.in(O_CARRY));
  LED OVERFLOW (.in(O_OVFL));
  LED ZERO (.in(O_ZERO));
  LED NEG_2 (.in(O_NEG));
  LED lt (.in(O__lt));
  LED eq (.in(O__eq));
  LED gt (.in(O__gt));
  assign pulldown_184_out = LDA ? LDA : 1'bz;  // Driver driver_641
  assign pulldown_184_out = LDB ? LDB : 1'bz;  // Driver driver_642
  assign pulldown_184_out = LDC ? LDC : 1'bz;  // Driver driver_643
  assign pulldown_184_out = LDX ? LDX : 1'bz;  // Driver driver_644
  assign pulldown_184_out = LDY ? LDY : 1'bz;  // Driver driver_645
  assign pulldown_184_out = LDZ ? LDZ : 1'bz;  // Driver driver_646
  assign pulldown_184_out = M_LDA ? M_LDA : 1'bz;  // Driver driver_647
  assign pulldown_184_out = M_LDB ? M_LDB : 1'bz;  // Driver driver_648
  assign pulldown_184_out = M_LDC ? M_LDC : 1'bz;  // Driver driver_649
  assign pulldown_184_out = M_LDX ? M_LDX : 1'bz;  // Driver driver_650
  assign pulldown_184_out = M_LDY ? M_LDY : 1'bz;  // Driver driver_651
  assign pulldown_184_out = M_LDZ ? M_LDZ : 1'bz;  // Driver driver_652
  Button MAN_INT_FULL_2 (.out(MAN_INT_FULL_2_out));
  PullDown pulldown_186 (.out(pulldown_186_out));
  PullDown pulldown_187 (.out(pulldown_187_out));
  PullDown pulldown_188 (.out(pulldown_188_out));
  PullDown pulldown_189 (.out(pulldown_189_out));
  Button MAN_INT_FULL_3 (.out(INT_TEST));
  Delay #(.delayTime(10)) delay_112 (.in(INT_TEST), .out(delay_112_out));
  assign pulldown_187_out = delay_112_out ? delay_112_out : 1'bz;  // Driver driver_653
  assign pulldown_187_out = MAN_INT_FULL_2_out ? MAN_INT_FULL_2_out : 1'bz;  // Driver driver_654
  assign pulldown_187_out = and_115_out ? and_115_out : 1'bz;  // Driver driver_655
  assign pulldown_187_out = out_326 ? out_326 : 1'bz;  // Driver driver_656
  T_FF t_ff_12 (.T(pulldown_187_out), .C(delay_113_out), .Q(t_ff_12_q));  // open: nQ
  Delay #(.delayTime(10)) delay_113 (.in(pulldown_187_out), .out(delay_113_out));
  and and_103 (and_103_out, t_ff_12_q, clk_6);
  assign pulldown_186_out = ~and_115_out ? and_103_out : 1'bz;  // DriverInvSel driverinvsel_12
  assign pulldown_188_out = pulldown_186_out ? pulldown_186_out : 1'bz;  // Driver driver_657
  assign pulldown_188_out = delay_114_out ? delay_114_out : 1'bz;  // Driver driver_658
  Delay #(.delayTime(10)) delay_114 (.in(and_115_out), .out(delay_114_out));
  Counter #(.Bits(4)) counter_4 (
    .en(pulldown_188_out), .C(pulldown_188_out), .clr(pulldown_189_out), .out(out_328), .ovf(counter_4_ovf));
  assign pulldown_189_out = delay_114_out ? delay_114_out : 1'bz;  // Driver driver_659
  not not_61 (not_61_out, out_328[0]);
  not not_62 (not_62_out, out_328[1]);
  not not_63 (not_63_out, out_328[2]);
  not not_64 (not_64_out, out_328[3]);
  not not_65 (not_65_out, out_328[1]);
  not not_66 (not_66_out, out_328[2]);
  not not_67 (not_67_out, out_328[3]);
  not not_68 (not_68_out, out_328[0]);
  not not_69 (not_69_out, out_328[2]);
  not not_70 (not_70_out, out_328[3]);
  not not_71 (not_71_out, out_328[2]);
  not not_72 (not_72_out, out_328[3]);
  not not_73 (not_73_out, out_328[0]);
  not not_74 (not_74_out, out_328[1]);
  not not_75 (not_75_out, out_328[3]);
  not not_76 (not_76_out, out_328[1]);
  not not_77 (not_77_out, out_328[3]);
  not not_78 (not_78_out, out_328[0]);
  not not_79 (not_79_out, out_328[3]);
  not not_80 (not_80_out, out_328[3]);
  not not_81 (not_81_out, out_328[0]);
  not not_82 (not_82_out, out_328[1]);
  not not_83 (not_83_out, out_328[2]);
  not not_84 (not_84_out, out_328[1]);
  not not_85 (not_85_out, out_328[2]);
  not not_86 (not_86_out, out_328[0]);
  and and_104 (and_104_out, not_61_out, not_62_out, not_63_out, not_64_out);
  and and_105 (and_105_out, out_328[0], not_65_out, not_66_out, not_67_out);
  and and_106 (and_106_out, not_68_out, out_328[1], not_69_out, not_70_out);
  and and_107 (and_107_out, out_328[0], out_328[1], not_71_out, not_72_out);
  and and_108 (and_108_out, not_73_out, not_74_out, out_328[2], not_75_out);
  and and_109 (and_109_out, out_328[0], not_76_out, out_328[2], not_77_out);
  and and_110 (and_110_out, not_78_out, out_328[1], out_328[2], not_79_out);
  and and_111 (and_111_out, out_328[0], out_328[1], out_328[2], not_80_out);
  and and_112 (and_112_out, not_81_out, not_82_out, not_83_out, out_328[3]);
  and and_113 (and_113_out, out_328[0], not_84_out, not_85_out, out_328[3]);
  and and_114 (and_114_out, not_86_out, out_328[1], out_328[2], out_328[3]);
  and and_115 (and_115_out, out_328[0], out_328[1], out_328[2], out_328[3]);
  LED led_1 (.in(and_104_out));
  assign driver_660_out = and_105_out ? and_105_out : 1'bz;  // Driver driver_660
  assign driver_661_out = and_106_out ? and_106_out : 1'bz;  // Driver driver_661
  assign driver_662_out = and_107_out ? and_107_out : 1'bz;  // Driver driver_662
  assign driver_663_out = and_108_out ? and_108_out : 1'bz;  // Driver driver_663
  assign driver_664_out = and_109_out ? and_109_out : 1'bz;  // Driver driver_664
  assign driver_660_out = and_110_out ? and_110_out : 1'bz;  // Driver driver_665
  assign driver_664_out = and_111_out ? and_111_out : 1'bz;  // Driver driver_666
  assign driver_667_out = and_112_out ? and_112_out : 1'bz;  // Driver driver_667
  LED led_2 (.in(and_113_out));
  LED led_3 (.in(and_114_out));
  Delay #(.delayTime(20)) delay_115 (.in(op_sel_1__106), .out(delay_115_out));
  Delay #(.delayTime(20)) delay_116 (.in(in_330), .out(delay_116_out));
  assign driver_668_out = M_C ? M_IN : 8'bz;  // Driver driver_668
  assign driver_669_out = M_C ? M_C : 1'bz;  // Driver driver_669
  assign driver_670_out = M_C ? M_WR : 1'bz;  // Driver driver_670
  assign driver_671_out = M_C ? M_RD : 1'bz;  // Driver driver_671
  assign driver_671_out = pulldown_191_out ? in_330 : 1'bz;  // Driver driver_672
  PullDown pulldown_190 (.out(driver_671_out));
  PullDown pulldown_191 (.out(pulldown_191_out));
  assign pulldown_191_out = delay_115_out ? delay_115_out : 1'bz;  // Driver driver_673
  assign pulldown_191_out = delay_116_out ? delay_116_out : 1'bz;  // Driver driver_674
  assign driver_669_out = pulldown_191_out ? pulldown_191_out : 1'bz;  // Driver driver_675
  assign driver_670_out = pulldown_191_out ? op_sel_1__106 : 1'bz;  // Driver driver_676
  PullDown pulldown_192 (.out(driver_670_out));
  PullDown pulldown_193 (.out(driver_669_out));
  assign driver_668_out = pulldown_191_out ? {X_t, X_2} : 8'bz;  // Driver driver_677
  PullDown #(.Bits(8)) pulldown_194 (.out(driver_668_out));
  assign driver_669_out = rs_ff_as_1_q ? rs_ff_as_1_q : 1'bz;  // Driver driver_678
  RS_FF_AS rs_ff_as_1 (.S(driver_660_out), .R(driver_664_out), .Q(rs_ff_as_1_q));  // open: nQ
  PullDown pulldown_195 (.out(driver_660_out));
  PullDown pulldown_196 (.out(driver_664_out));
  assign driver_671_out = rs_ff_as_2_q ? rs_ff_as_2_q : 1'bz;  // Driver driver_679
  RS_FF_AS rs_ff_as_2 (.S(driver_661_out), .R(driver_667_out), .Q(rs_ff_as_2_q));  // open: nQ
  PullDown pulldown_197 (.out(driver_661_out));
  PullDown pulldown_198 (.out(driver_667_out));
  assign INTST = and_116_out ? and_116_out : 1'bz;  // Driver driver_680
  Telnet telnet_1 (
    .in(driver_668_out), .C(driver_669_out), .wr(driver_670_out), .rd(driver_671_out), .out(out_325),
    .av(out_326));
  RS_FF_AS rs_ff_as_3 (.S(driver_662_out), .R(driver_663_out), .Q(rs_ff_as_3_q));  // open: nQ
  PullDown pulldown_199 (.out(driver_662_out));
  PullDown pulldown_200 (.out(driver_663_out));
  and and_116 (and_116_out, out_326, not_87_out);
  Register #(.Bits(8)) register_24 (.D(out_325), .C(rs_ff_as_3_q), .en(rs_ff_as_3_q), .Q(out_331));
  not not_87 (not_87_out, INTERUPT);
  Button u_EN (.out(EN_out));
  assign driverinvsel_13_out = ~EN_out ? B_t : 8'bz;  // DriverInvSel driverinvsel_13
  assign driverinvsel_14_out = ~EN_out ? op_sel_1__102 : 1'bz;  // DriverInvSel driverinvsel_14
  assign driverinvsel_14_out = EN_out ? EN_out : 1'bz;  // Driver driver_681
  Button WR (.out(WR_out));
  Button RE (.out(RE_out));
  Register #(.Bits(16)) register_25 (.D(keyboard_1_d), .C(and_117_out), .en(keyboard_1_av), .Q(out_162));
  and and_117 (and_117_out, keyboard_1_av, driverinvsel_15_out);
  Keyboard keyboard_1 (.C(delay_117_out), .en(driverinvsel_15_out), .D(keyboard_1_d), .av(keyboard_1_av));
  Delay #(.delayTime(10)) delay_117 (.in(driverinvsel_15_out), .out(delay_117_out));
  assign driverinvsel_15_out = ~EN_EN ? clk_4 : 1'bz;  // DriverInvSel driverinvsel_15
  assign driverinvsel_15_out = EN_EN ? EN : 1'bz;  // Driver driver_682
  assign driverinvsel_13_out = EN_out ? LOC : 8'bz;  // Driver driver_683
  and and_118 (K_ON, O_INT_BRK, comparator_3_eq);
  Comparator #(.Bits(7)) comparator_3 (
    .a(out_162[6:0]), .b(in_164), .gt(comparator_3_gt), .eq(comparator_3_eq), .lt(comparator_3_lt));
  and and_119 (K_OFF, ~O_INT_BRK, comparator_4_eq);  // And
  Comparator #(.Bits(7)) comparator_4 (
    .a(out_162[6:0]), .b(in_166), .gt(comparator_4_gt), .eq(comparator_4_eq), .lt(comparator_4_lt));
  and and_120 (and_120_out, ~EN_EN, keyboard_1_av);  // And
  and and_121 (and_121_out, and_120_out, ~clk_4);  // And
  Delay #(.delayTime(10)) delay_118 (.in(and_121_out), .out(delay_118_out));
  Delay #(.Bits(8), .delayTime(20)) delay_119 (.in(out_159), .out(delay_119_out));
  assign driver_684_out = delay_118_out ? delay_118_out : 1'bz;  // Driver driver_684
  Register #(.Bits(8)) register_26 (.D(driverinvsel_16_out), .C(delay_120_out), .en(driver_684_out), .Q(out_159));
  Delay #(.delayTime(10)) delay_120 (.in(driver_684_out), .out(delay_120_out));
  assign driverinvsel_16_out = ~driverinvsel_14_out ? add_8_s : 8'bz;  // DriverInvSel driverinvsel_16
  Add #(.Bits(8)) add_8 (.a(out_159), .b(8'h1), .c_i(1'b0), .s(add_8_s), .c_o(out_160));
  Add #(.Bits(8)) add_9 (.a(out_114), .b(8'h1), .c_i(1'b0), .s(add_9_s), .c_o(add_9_c_o));
  assign driver_685_out = WR_out ? A : 8'bz;  // Driver driver_685
  assign {out_121, out_122[6:0]} = WR_out ? D : 8'bz;  // Driver driver_686
  assign driverinvsel_17_out = ~WR_out ? op_sel_1__101 : 1'bz;  // DriverInvSel driverinvsel_17
  assign driverinvsel_17_out = WR_out ? WR_out : 1'bz;  // Driver driver_687
  assign {out_163, driver_688_out} = delay_121_out ? out_162 : 16'bz;  // Driver driver_688
  Delay #(.delayTime(10)) delay_121 (.in(driver_684_out), .out(delay_121_out));
  PullDown pulldown_201 (.out(driver_684_out));
  assign driver_684_out = driverinvsel_14_out ? driverinvsel_14_out : 1'bz;  // Driver driver_689
  assign driverinvsel_16_out = driverinvsel_14_out ? driverinvsel_13_out : 8'bz;  // Driver driver_690
  vgasync vgasync_1 (
    .clock(VGA_C), .H(vgasync_1_h), .V(vgasync_1_v), .pic(vgasync_1_pic), .X(vgasync_1_x), .Y(vgasync_1_y));
  Delay #(.delayTime(10)) delay_122 (.in(clk_2), .out(delay_122_out));
  assign driver_685_out = ~WR_out ? {X_t, X_2} : 8'bz;  // DriverInvSel driverinvsel_18
  assign {out_121, out_122[6:0]} = ~WR_out ? Y_2 : 8'bz;  // DriverInvSel driverinvsel_19
  Delay #(.delayTime(10)) delay_123 (.in(driverinvsel_17_out), .out(delay_123_out));
  assign driver_691_out = RE_out ? A_3 : 8'bz;  // Driver driver_691
  Register #(.Bits(8)) register_27 (.D(add_9_s), .C(delay_122_out), .en(clk_2), .Q(out_114));
  assign driver_692_out = RE_out ? RE_out : 1'bz;  // Driver driver_692
  assign driver_692_out = ~RE_out ? op_sel_1__103 : 1'bz;  // DriverInvSel driverinvsel_20
  Register #(.Bits(7)) register_28 (.D(driver_700_out), .C(delay_124_out), .en(or_13_out), .Q(out_240));
  Add #(.Bits(6)) add_10 (.a(out_119), .b(6'b000001), .c_i(1'b0), .s(add_10_s), .c_o(add_10_c_o));
  // vgacharpos vgacharpos_1: pin names not known; wires that end beside it: vgasync_1_x, vgasync_1_y, vgacharpos_1_p3, vgacharpos_1_p4, vgacharpos_1_p5, vgacharpos_1_p6
  assign driverinvsel_21_out = ~delay_123_out ? out_114 : 8'bz;  // DriverInvSel driverinvsel_21
  assign driver_691_out = ~RE_out ? {X_t, X_2} : 8'bz;  // DriverInvSel driverinvsel_22
  Delay #(.delayTime(10)) delay_124 (.in(or_13_out), .out(delay_124_out));
  Delay #(.delayTime(10)) delay_125 (.in(delay_123_out), .out(delay_125_out));
  not not_88 (not_88_out, delay_123_out);
  assign driverinvsel_21_out = delay_123_out ? driver_685_out : 8'bz;  // Driver driver_693
  assign driverinvsel_23_out = ~driver_692_out ? driver_695_out : 8'bz;  // DriverInvSel driverinvsel_23
  assign driverinvsel_23_out = driver_692_out ? driver_691_out : 8'bz;  // Driver driver_694
  or or_13 (or_13_out, driver_692_out, op_sel_1__103);
  Delay #(.delayTime(10)) delay_126 (.in(clk_3), .out(delay_126_out));
  Button WR_2 (.out(WR_2_out));
  Register #(.Bits(6)) register_29 (.D(add_10_s), .C(delay_126_out), .en(clk_3), .Q(out_119));
  assign driverinvsel_24_out = ~keyboard_1_av ? delay_125_out : 1'bz;  // DriverInvSel driverinvsel_24
  Delay #(.delayTime(10)) delay_127 (.in(delay_125_out), .out(delay_127_out));
  and and_122 (and_122_out, not_88_out, ~keyboard_1_av);  // And
  assign driverinvsel_25_out = ~driver_692_out ? driverinvsel_24_out : 1'bz;  // DriverInvSel driverinvsel_25
  assign driverinvsel_26_out = ~driver_692_out ? and_122_out : 1'bz;  // DriverInvSel driverinvsel_26
  assign driverinvsel_27_out = ~op_sel_1__98 ? out_119 : 6'bz;  // DriverInvSel driverinvsel_27
  Register #(.Bits(3)) register_30 (.D(B_t[2:0]), .C(delay_128_out), .en(op_sel_1__99), .Q(out_237));
  Delay #(.delayTime(10)) delay_128 (.in(op_sel_1__99), .out(delay_128_out));
  Register #(.Bits(3)) register_31 (.D(B_t[2:0]), .C(delay_129_out), .en(op_sel_1__100), .Q(out_238));
  Delay #(.delayTime(10)) delay_129 (.in(op_sel_1__100), .out(delay_129_out));
  assign driver_695_out = keyboard_1_av ? delay_119_out : 8'bz;  // Driver driver_695
  assign driver_695_out = ~keyboard_1_av ? driverinvsel_21_out : 8'bz;  // DriverInvSel driverinvsel_28
  Delay #(.delayTime(10)) delay_130 (.in(op_sel_1__98), .out(delay_130_out));
  not not_89 (not_89_out, op_sel_1__98);
  assign driverinvsel_27_out = op_sel_1__98 ? B_t[5:0] : 6'bz;  // Driver driver_696
  assign driverinvsel_24_out = keyboard_1_av ? delay_121_out : 1'bz;  // Driver driver_697
  EEPROM #(.AddrBits(8), .Bits(7)) eeprom_4 (
    .A(driverinvsel_23_out), .CS(1'b1), .WE(driverinvsel_25_out), .OE(driverinvsel_26_out), .D(out_115));
  assign driverinvsel_25_out = driver_692_out ? 1'b0 : 1'bz;  // Driver driver_698
  assign driverinvsel_26_out = driver_692_out ? 1'b1 : 1'bz;  // Driver driver_699
  EEPROM #(.AddrBits(6), .Bits(14)) eeprom_5 (
    .A(driverinvsel_27_out), .CS(delay_131_out), .WE(delay_130_out), .OE(not_89_out), .D(out_120));
  Delay #(.delayTime(20)) delay_131 (.in(1'b1), .out(delay_131_out));
  ROM #(.AddrBits(3), .Bits(12)) rom_2 (.A(out_237), .sel(1'b1), .D(FG_c0));
  ROM #(.AddrBits(3), .Bits(12)) rom_3 (.A(out_238), .sel(1'b1), .D(BG_c0));
  _16_BASCII_TO_7_BASCII _16_bascii_to_7_bascii_1 (
    .IN(pulldown_203_out), .OUT(_16_bascii_to_7_bascii_1_out), .IN_OUT(out_170));
  Delay #(.delayTime(10)) delay_132 (.in(keyboard_1_av), .out(delay_132_out));
  assign driver_700_out = driver_692_out ? out_115 : 7'bz;  // Driver driver_700
  PullDown #(.Bits(14)) pulldown_202 (.out(pulldown_202_out));
  PullDown #(.Bits(7)) pulldown_203 (.out(pulldown_203_out));
  assign pulldown_203_out = not_88_out ? out_115 : 7'bz;  // Driver driver_701
  assign out_115 = delay_127_out ? out_122[6:0] : 7'bz;  // Driver driver_702
  assign pulldown_202_out = not_89_out ? out_120 : 14'bz;  // Driver driver_703
  assign out_120 = delay_130_out ? {Y_2, X_2} : 14'bz;  // Driver driver_704
  assign out_115 = delay_132_out ? driver_688_out : 7'bz;  // Driver driver_705
  PullDown #(.Bits(7)) pulldown_204 (.out(out_115));
  Comparator #(.Bits(8)) comparator_5 (.a(out_114), .b({8{1'b0}}), .eq(comparator_5_eq));  // open: gt, lt
  Comparator #(.Bits(8)) comparator_6 (.a(out_114), .b(8'h1), .eq(comparator_6_eq));  // open: gt, lt
  Comparator #(.Bits(8)) comparator_7 (.a(out_114), .b(8'h2), .eq(comparator_7_eq));  // open: gt, lt
  Comparator #(.Bits(8)) comparator_8 (.a(out_114), .b(8'h3), .eq(comparator_8_eq));  // open: gt, lt
  Comparator #(.Bits(8)) comparator_9 (.a(out_114), .b(8'h28), .eq(comparator_9_eq));  // open: gt, lt
  Comparator #(.Bits(8)) comparator_10 (.a(out_114), .b(8'h29), .eq(comparator_10_eq));  // open: gt, lt
  Comparator #(.Bits(8)) comparator_11 (.a(out_114), .b(8'h2a), .eq(comparator_11_eq));  // open: gt, lt
  Comparator #(.Bits(8)) comparator_12 (.a(out_114), .b(8'h2b), .eq(comparator_12_eq));  // open: gt, lt
  Comparator #(.Bits(8)) comparator_13 (.a(out_114), .b(8'h50), .eq(comparator_13_eq));  // open: gt, lt
  Comparator #(.Bits(8)) comparator_14 (.a(out_114), .b(8'h51), .eq(comparator_14_eq));  // open: gt, lt
  Comparator #(.Bits(8)) comparator_15 (.a(out_114), .b(8'h52), .eq(comparator_15_eq));  // open: gt, lt
  Comparator #(.Bits(8)) comparator_16 (.a(out_114), .b(8'h53), .eq(comparator_16_eq));  // open: gt, lt
  Comparator #(.Bits(8)) comparator_17 (.a(out_114), .b(8'h78), .eq(comparator_17_eq));  // open: gt, lt
  Comparator #(.Bits(8)) comparator_18 (.a(out_114), .b(8'h79), .eq(comparator_18_eq));  // open: gt, lt
  Comparator #(.Bits(8)) comparator_19 (.a(out_114), .b(8'h7a), .eq(comparator_19_eq));  // open: gt, lt
  Comparator #(.Bits(8)) comparator_20 (.a(out_114), .b(8'h7b), .eq(comparator_20_eq));  // open: gt, lt
  Comparator #(.Bits(6)) comparator_21 (
    .a(out_119), .b({6{1'b0}}), .gt(comparator_21_gt), .eq(comparator_21_eq), .lt(comparator_21_lt));
  Comparator #(.Bits(6)) comparator_22 (
    .a(out_119), .b(6'b001010), .gt(comparator_22_gt), .eq(comparator_22_eq), .lt(comparator_22_lt));
  Comparator #(.Bits(6)) comparator_23 (
    .a(out_119), .b(6'b010100), .gt(comparator_23_gt), .eq(comparator_23_eq), .lt(comparator_23_lt));
  Comparator #(.Bits(6)) comparator_24 (
    .a(out_119), .b(6'b100100), .gt(comparator_24_gt), .eq(comparator_24_eq), .lt(comparator_24_lt));
  Register #(.Bits(7)) register_32 (
    .D(_16_bascii_to_7_bascii_1_out), .C(delay_133_out), .en(comparator_5_eq), .Q(out_169));
  Delay #(.delayTime(10)) delay_133 (.in(comparator_5_eq), .out(delay_133_out));
  Register #(.Bits(7)) register_33 (
    .D(_16_bascii_to_7_bascii_1_out), .C(delay_134_out), .en(comparator_6_eq), .Q(register_33_q));
  Delay #(.delayTime(10)) delay_134 (.in(comparator_6_eq), .out(delay_134_out));
  Register #(.Bits(7)) register_34 (
    .D(_16_bascii_to_7_bascii_1_out), .C(delay_135_out), .en(comparator_7_eq), .Q(register_34_q));
  Delay #(.delayTime(10)) delay_135 (.in(comparator_7_eq), .out(delay_135_out));
  Register #(.Bits(7)) register_35 (
    .D(_16_bascii_to_7_bascii_1_out), .C(delay_136_out), .en(comparator_8_eq), .Q(out_244));
  Delay #(.delayTime(10)) delay_136 (.in(comparator_8_eq), .out(delay_136_out));
  Register #(.Bits(7)) register_36 (
    .D(_16_bascii_to_7_bascii_1_out), .C(delay_137_out), .en(comparator_9_eq), .Q(out_315));
  Delay #(.delayTime(10)) delay_137 (.in(comparator_9_eq), .out(delay_137_out));
  Register #(.Bits(7)) register_37 (
    .D(_16_bascii_to_7_bascii_1_out), .C(delay_138_out), .en(comparator_10_eq), .Q(register_37_q));
  Delay #(.delayTime(10)) delay_138 (.in(comparator_10_eq), .out(delay_138_out));
  Register #(.Bits(7)) register_38 (
    .D(_16_bascii_to_7_bascii_1_out), .C(delay_139_out), .en(comparator_11_eq), .Q(register_38_q));
  Delay #(.delayTime(10)) delay_139 (.in(comparator_11_eq), .out(delay_139_out));
  Register #(.Bits(7)) register_39 (
    .D(_16_bascii_to_7_bascii_1_out), .C(delay_140_out), .en(comparator_12_eq), .Q(out_316));
  Delay #(.delayTime(10)) delay_140 (.in(comparator_12_eq), .out(delay_140_out));
  Register #(.Bits(7)) register_40 (
    .D(_16_bascii_to_7_bascii_1_out), .C(delay_141_out), .en(comparator_13_eq), .Q(out_285));
  Delay #(.delayTime(10)) delay_141 (.in(comparator_13_eq), .out(delay_141_out));
  Register #(.Bits(7)) register_41 (
    .D(_16_bascii_to_7_bascii_1_out), .C(delay_142_out), .en(comparator_14_eq), .Q(register_41_q));
  Delay #(.delayTime(10)) delay_142 (.in(comparator_14_eq), .out(delay_142_out));
  Register #(.Bits(7)) register_42 (
    .D(_16_bascii_to_7_bascii_1_out), .C(delay_143_out), .en(comparator_15_eq), .Q(register_42_q));
  Delay #(.delayTime(10)) delay_143 (.in(comparator_15_eq), .out(delay_143_out));
  Register #(.Bits(7)) register_43 (
    .D(_16_bascii_to_7_bascii_1_out), .C(delay_144_out), .en(comparator_16_eq), .Q(out_286));
  Delay #(.delayTime(10)) delay_144 (.in(comparator_16_eq), .out(delay_144_out));
  Register #(.Bits(7)) register_44 (
    .D(_16_bascii_to_7_bascii_1_out), .C(delay_145_out), .en(comparator_17_eq), .Q(out_287));
  Delay #(.delayTime(10)) delay_145 (.in(comparator_17_eq), .out(delay_145_out));
  Register #(.Bits(7)) register_45 (
    .D(_16_bascii_to_7_bascii_1_out), .C(delay_146_out), .en(comparator_18_eq), .Q(register_45_q));
  Delay #(.delayTime(10)) delay_146 (.in(comparator_18_eq), .out(delay_146_out));
  Register #(.Bits(7)) register_46 (
    .D(_16_bascii_to_7_bascii_1_out), .C(delay_147_out), .en(comparator_19_eq), .Q(register_46_q));
  Delay #(.delayTime(10)) delay_147 (.in(comparator_19_eq), .out(delay_147_out));
  Register #(.Bits(7)) register_47 (
    .D(_16_bascii_to_7_bascii_1_out), .C(delay_148_out), .en(comparator_20_eq), .Q(out_288));
  Delay #(.delayTime(10)) delay_148 (.in(comparator_20_eq), .out(delay_148_out));
  Delay #(.delayTime(10)) delay_149 (.in(comparator_21_eq), .out(delay_149_out));
  Delay #(.delayTime(10)) delay_150 (.in(comparator_21_eq), .out(delay_150_out));
  Delay #(.delayTime(10)) delay_151 (.in(comparator_22_eq), .out(delay_151_out));
  Delay #(.delayTime(10)) delay_152 (.in(comparator_22_eq), .out(delay_152_out));
  Delay #(.delayTime(10)) delay_153 (.in(comparator_23_eq), .out(delay_153_out));
  Delay #(.delayTime(10)) delay_154 (.in(comparator_23_eq), .out(delay_154_out));
  Delay #(.delayTime(10)) delay_155 (.in(comparator_24_eq), .out(delay_155_out));
  Delay #(.delayTime(10)) delay_156 (.in(comparator_24_eq), .out(delay_156_out));
  Register #(.Bits(6)) register_48 (.D(pulldown_202_out[5:0]), .C(delay_149_out), .en(comparator_21_eq), .Q(CX_c0));
  Register #(.Bits(8)) register_49 (.D(pulldown_202_out[13:6]), .C(delay_150_out), .en(comparator_21_eq), .Q(CY_c0));
  Register #(.Bits(6)) register_50 (.D(pulldown_202_out[5:0]), .C(delay_151_out), .en(comparator_22_eq), .Q(CX_c10));
  Register #(.Bits(8)) register_51 (.D(pulldown_202_out[13:6]), .C(delay_152_out), .en(comparator_22_eq), .Q(CY_c10));
  Register #(.Bits(6)) register_52 (.D(pulldown_202_out[5:0]), .C(delay_153_out), .en(comparator_23_eq), .Q(CX_c20));
  Register #(.Bits(8)) register_53 (.D(pulldown_202_out[13:6]), .C(delay_154_out), .en(comparator_23_eq), .Q(CY_c20));
  Register #(.Bits(6)) register_54 (.D(pulldown_202_out[5:0]), .C(delay_155_out), .en(comparator_24_eq), .Q(CX_c30));
  Register #(.Bits(8)) register_55 (.D(pulldown_202_out[13:6]), .C(delay_156_out), .en(comparator_24_eq), .Q(CY_c30));
  vgastring vgastring_1 (
    .CX_i(vgacharpos_1_p5), .CY_i(vgacharpos_1_p6), .C_i({7{1'b0}}), .FG_i(FG_c0), .BG_i(BG_c0),
    .FG_c(FG_c0), .BG_c(BG_c0), .CX_c(CX_c0), .CY_c(CY_c0), .C_0(out_169), .C_1(register_33_q),
    .C_2(register_34_q), .C_3(out_244), .EN(1'b1), .CX_o(vgastring_1_cx_o), .CY_o(vgastring_1_cy_o),
    .C_o(vgastring_1_c_o), .FG_o(vgastring_1_fg_o), .BG_o(vgastring_1_bg_o));
  vgastring vgastring_2 (
    .CX_i(vgastring_37_cx_o), .CY_i(vgastring_37_cy_o), .C_i(vgastring_37_c_o), .FG_i(vgastring_37_fg_o),
    .BG_i(vgastring_37_bg_o), .FG_c(FG_c0), .BG_c(BG_c0), .CX_c(CX_c10), .CY_c(CY_c10), .C_0(out_315),
    .C_1(register_37_q), .C_2(register_38_q), .C_3(out_316), .EN(1'b1), .CX_o(vgastring_2_cx_o),
    .CY_o(vgastring_2_cy_o), .C_o(vgastring_2_c_o), .FG_o(vgastring_2_fg_o), .BG_o(vgastring_2_bg_o));
  vgastring vgastring_3 (
    .CX_i(vgastring_38_cx_o), .CY_i(vgastring_38_cy_o), .C_i(vgastring_38_c_o), .FG_i(vgastring_38_fg_o),
    .BG_i(vgastring_38_bg_o), .FG_c(FG_c0), .BG_c(BG_c0), .CX_c(CX_c20), .CY_c(CY_c20), .C_0(out_285),
    .C_1(register_41_q), .C_2(register_42_q), .C_3(out_286), .EN(1'b1), .CX_o(vgastring_3_cx_o),
    .CY_o(vgastring_3_cy_o), .C_o(vgastring_3_c_o), .FG_o(vgastring_3_fg_o), .BG_o(vgastring_3_bg_o));
  vgastring vgastring_4 (
    .CX_i(vgastring_39_cx_o), .CY_i(vgastring_39_cy_o), .C_i(vgastring_39_c_o), .FG_i(vgastring_39_fg_o),
    .BG_i(vgastring_39_bg_o), .FG_c(FG_c0), .BG_c(BG_c0), .CX_c(CX_c30), .CY_c(CY_c30), .C_0(out_287),
    .C_1(register_45_q), .C_2(register_46_q), .C_3(out_288), .EN(1'b1), .CX_o(vgastring_4_cx_o),
    .CY_o(vgastring_4_cy_o), .C_o(vgastring_4_c_o), .FG_o(vgastring_4_fg_o), .BG_o(vgastring_4_bg_o));
  Comparator #(.Bits(8)) comparator_25 (.a(out_114), .b(8'h4), .eq(comparator_25_eq));  // open: gt, lt
  Comparator #(.Bits(8)) comparator_26 (.a(out_114), .b(8'h5), .eq(comparator_26_eq));  // open: gt, lt
  Comparator #(.Bits(8)) comparator_27 (.a(out_114), .b(8'h6), .eq(comparator_27_eq));  // open: gt, lt
  Comparator #(.Bits(8)) comparator_28 (.a(out_114), .b(8'h7), .eq(comparator_28_eq));  // open: gt, lt
  Comparator #(.Bits(8)) comparator_29 (.a(out_114), .b(8'h2c), .eq(comparator_29_eq));  // open: gt, lt
  Comparator #(.Bits(8)) comparator_30 (.a(out_114), .b(8'h2d), .eq(comparator_30_eq));  // open: gt, lt
  Comparator #(.Bits(8)) comparator_31 (.a(out_114), .b(8'h2e), .eq(comparator_31_eq));  // open: gt, lt
  Comparator #(.Bits(8)) comparator_32 (.a(out_114), .b(8'h2f), .eq(comparator_32_eq));  // open: gt, lt
  Comparator #(.Bits(8)) comparator_33 (.a(out_114), .b(8'h54), .eq(comparator_33_eq));  // open: gt, lt
  Comparator #(.Bits(8)) comparator_34 (.a(out_114), .b(8'h55), .eq(comparator_34_eq));  // open: gt, lt
  Comparator #(.Bits(8)) comparator_35 (.a(out_114), .b(8'h56), .eq(comparator_35_eq));  // open: gt, lt
  Comparator #(.Bits(8)) comparator_36 (.a(out_114), .b(8'h57), .eq(comparator_36_eq));  // open: gt, lt
  Comparator #(.Bits(8)) comparator_37 (.a(out_114), .b(8'h7c), .eq(comparator_37_eq));  // open: gt, lt
  Comparator #(.Bits(8)) comparator_38 (.a(out_114), .b(8'h7d), .eq(comparator_38_eq));  // open: gt, lt
  Comparator #(.Bits(8)) comparator_39 (.a(out_114), .b(8'h7e), .eq(comparator_39_eq));  // open: gt, lt
  Comparator #(.Bits(8)) comparator_40 (.a(out_114), .b(8'h7f), .eq(comparator_40_eq));  // open: gt, lt
  Comparator #(.Bits(6)) comparator_41 (
    .a(out_119), .b(6'b000001), .gt(comparator_41_gt), .eq(comparator_41_eq), .lt(comparator_41_lt));
  Comparator #(.Bits(6)) comparator_42 (
    .a(out_119), .b(6'b001011), .gt(comparator_42_gt), .eq(comparator_42_eq), .lt(comparator_42_lt));
  Comparator #(.Bits(6)) comparator_43 (
    .a(out_119), .b(6'b010101), .gt(comparator_43_gt), .eq(comparator_43_eq), .lt(comparator_43_lt));
  Comparator #(.Bits(6)) comparator_44 (
    .a(out_119), .b(6'b100101), .gt(comparator_44_gt), .eq(comparator_44_eq), .lt(comparator_44_lt));
  Register #(.Bits(7)) register_56 (
    .D(_16_bascii_to_7_bascii_1_out), .C(delay_157_out), .en(comparator_25_eq), .Q(out_245));
  Delay #(.delayTime(10)) delay_157 (.in(comparator_25_eq), .out(delay_157_out));
  Register #(.Bits(7)) register_57 (
    .D(_16_bascii_to_7_bascii_1_out), .C(delay_158_out), .en(comparator_26_eq), .Q(register_57_q));
  Delay #(.delayTime(10)) delay_158 (.in(comparator_26_eq), .out(delay_158_out));
  Register #(.Bits(7)) register_58 (
    .D(_16_bascii_to_7_bascii_1_out), .C(delay_159_out), .en(comparator_27_eq), .Q(register_58_q));
  Delay #(.delayTime(10)) delay_159 (.in(comparator_27_eq), .out(delay_159_out));
  Register #(.Bits(7)) register_59 (
    .D(_16_bascii_to_7_bascii_1_out), .C(delay_160_out), .en(comparator_28_eq), .Q(out_246));
  Delay #(.delayTime(10)) delay_160 (.in(comparator_28_eq), .out(delay_160_out));
  Register #(.Bits(7)) register_60 (
    .D(_16_bascii_to_7_bascii_1_out), .C(delay_161_out), .en(comparator_29_eq), .Q(out_317));
  Delay #(.delayTime(10)) delay_161 (.in(comparator_29_eq), .out(delay_161_out));
  Register #(.Bits(7)) register_61 (
    .D(_16_bascii_to_7_bascii_1_out), .C(delay_162_out), .en(comparator_30_eq), .Q(register_61_q));
  Delay #(.delayTime(10)) delay_162 (.in(comparator_30_eq), .out(delay_162_out));
  Register #(.Bits(7)) register_62 (
    .D(_16_bascii_to_7_bascii_1_out), .C(delay_163_out), .en(comparator_31_eq), .Q(register_62_q));
  Delay #(.delayTime(10)) delay_163 (.in(comparator_31_eq), .out(delay_163_out));
  Register #(.Bits(7)) register_63 (
    .D(_16_bascii_to_7_bascii_1_out), .C(delay_164_out), .en(comparator_32_eq), .Q(out_318));
  Delay #(.delayTime(10)) delay_164 (.in(comparator_32_eq), .out(delay_164_out));
  Register #(.Bits(7)) register_64 (
    .D(_16_bascii_to_7_bascii_1_out), .C(delay_165_out), .en(comparator_33_eq), .Q(out_281));
  Delay #(.delayTime(10)) delay_165 (.in(comparator_33_eq), .out(delay_165_out));
  Register #(.Bits(7)) register_65 (
    .D(_16_bascii_to_7_bascii_1_out), .C(delay_166_out), .en(comparator_34_eq), .Q(register_65_q));
  Delay #(.delayTime(10)) delay_166 (.in(comparator_34_eq), .out(delay_166_out));
  Register #(.Bits(7)) register_66 (
    .D(_16_bascii_to_7_bascii_1_out), .C(delay_167_out), .en(comparator_35_eq), .Q(register_66_q));
  Delay #(.delayTime(10)) delay_167 (.in(comparator_35_eq), .out(delay_167_out));
  Register #(.Bits(7)) register_67 (
    .D(_16_bascii_to_7_bascii_1_out), .C(delay_168_out), .en(comparator_36_eq), .Q(out_282));
  Delay #(.delayTime(10)) delay_168 (.in(comparator_36_eq), .out(delay_168_out));
  Register #(.Bits(7)) register_68 (
    .D(_16_bascii_to_7_bascii_1_out), .C(delay_169_out), .en(comparator_37_eq), .Q(out_289));
  Delay #(.delayTime(10)) delay_169 (.in(comparator_37_eq), .out(delay_169_out));
  Register #(.Bits(7)) register_69 (
    .D(_16_bascii_to_7_bascii_1_out), .C(delay_170_out), .en(comparator_38_eq), .Q(register_69_q));
  Delay #(.delayTime(10)) delay_170 (.in(comparator_38_eq), .out(delay_170_out));
  Register #(.Bits(7)) register_70 (
    .D(_16_bascii_to_7_bascii_1_out), .C(delay_171_out), .en(comparator_39_eq), .Q(register_70_q));
  Delay #(.delayTime(10)) delay_171 (.in(comparator_39_eq), .out(delay_171_out));
  Register #(.Bits(7)) register_71 (
    .D(_16_bascii_to_7_bascii_1_out), .C(delay_172_out), .en(comparator_40_eq), .Q(out_290));
  Delay #(.delayTime(10)) delay_172 (.in(comparator_40_eq), .out(delay_172_out));
  Delay #(.delayTime(10)) delay_173 (.in(comparator_41_eq), .out(delay_173_out));
  Delay #(.delayTime(10)) delay_174 (.in(comparator_41_eq), .out(delay_174_out));
  Delay #(.delayTime(10)) delay_175 (.in(comparator_42_eq), .out(delay_175_out));
  Delay #(.delayTime(10)) delay_176 (.in(comparator_42_eq), .out(delay_176_out));
  Delay #(.delayTime(10)) delay_177 (.in(comparator_43_eq), .out(delay_177_out));
  Delay #(.delayTime(10)) delay_178 (.in(comparator_43_eq), .out(delay_178_out));
  Delay #(.delayTime(10)) delay_179 (.in(comparator_44_eq), .out(delay_179_out));
  Delay #(.delayTime(10)) delay_180 (.in(comparator_44_eq), .out(delay_180_out));
  Register #(.Bits(6)) register_72 (.D(pulldown_202_out[5:0]), .C(delay_173_out), .en(comparator_41_eq), .Q(CX_c1));
  Register #(.Bits(8)) register_73 (.D(pulldown_202_out[13:6]), .C(delay_174_out), .en(comparator_41_eq), .Q(CY_c1));
  Register #(.Bits(6)) register_74 (.D(pulldown_202_out[5:0]), .C(delay_175_out), .en(comparator_42_eq), .Q(CX_c11));
  Register #(.Bits(8)) register_75 (.D(pulldown_202_out[13:6]), .C(delay_176_out), .en(comparator_42_eq), .Q(CY_c11));
  Register #(.Bits(6)) register_76 (.D(pulldown_202_out[5:0]), .C(delay_177_out), .en(comparator_43_eq), .Q(CX_c21));
  Register #(.Bits(8)) register_77 (.D(pulldown_202_out[13:6]), .C(delay_178_out), .en(comparator_43_eq), .Q(CY_c21));
  Register #(.Bits(6)) register_78 (.D(pulldown_202_out[5:0]), .C(delay_179_out), .en(comparator_44_eq), .Q(CX_c31));
  Register #(.Bits(8)) register_79 (.D(pulldown_202_out[13:6]), .C(delay_180_out), .en(comparator_44_eq), .Q(CY_c31));
  vgastring vgastring_5 (
    .CX_i(vgastring_1_cx_o), .CY_i(vgastring_1_cy_o), .C_i(vgastring_1_c_o), .FG_i(vgastring_1_fg_o),
    .BG_i(vgastring_1_bg_o), .FG_c(FG_c0), .BG_c(BG_c0), .CX_c(CX_c1), .CY_c(CY_c1), .C_0(out_245),
    .C_1(register_57_q), .C_2(register_58_q), .C_3(out_246), .EN(1'b1), .CX_o(vgastring_5_cx_o),
    .CY_o(vgastring_5_cy_o), .C_o(vgastring_5_c_o), .FG_o(vgastring_5_fg_o), .BG_o(vgastring_5_bg_o));
  vgastring vgastring_6 (
    .CX_i(vgastring_2_cx_o), .CY_i(vgastring_2_cy_o), .C_i(vgastring_2_c_o), .FG_i(vgastring_2_fg_o),
    .BG_i(vgastring_2_bg_o), .FG_c(FG_c0), .BG_c(BG_c0), .CX_c(CX_c11), .CY_c(CY_c11), .C_0(out_317),
    .C_1(register_61_q), .C_2(register_62_q), .C_3(out_318), .EN(1'b1), .CX_o(vgastring_6_cx_o),
    .CY_o(vgastring_6_cy_o), .C_o(vgastring_6_c_o), .FG_o(vgastring_6_fg_o), .BG_o(vgastring_6_bg_o));
  vgastring vgastring_7 (
    .CX_i(vgastring_3_cx_o), .CY_i(vgastring_3_cy_o), .C_i(vgastring_3_c_o), .FG_i(vgastring_3_fg_o),
    .BG_i(vgastring_3_bg_o), .FG_c(FG_c0), .BG_c(BG_c0), .CX_c(CX_c21), .CY_c(CY_c21), .C_0(out_281),
    .C_1(register_65_q), .C_2(register_66_q), .C_3(out_282), .EN(1'b1), .CX_o(vgastring_7_cx_o),
    .CY_o(vgastring_7_cy_o), .C_o(vgastring_7_c_o), .FG_o(vgastring_7_fg_o), .BG_o(vgastring_7_bg_o));
  vgastring vgastring_8 (
    .CX_i(vgastring_4_cx_o), .CY_i(vgastring_4_cy_o), .C_i(vgastring_4_c_o), .FG_i(vgastring_4_fg_o),
    .BG_i(vgastring_4_bg_o), .FG_c(FG_c0), .BG_c(BG_c0), .CX_c(CX_c31), .CY_c(CY_c31), .C_0(out_289),
    .C_1(register_69_q), .C_2(register_70_q), .C_3(out_290), .EN(1'b1), .CX_o(vgastring_8_cx_o),
    .CY_o(vgastring_8_cy_o), .C_o(vgastring_8_c_o), .FG_o(vgastring_8_fg_o), .BG_o(vgastring_8_bg_o));
  Comparator #(.Bits(8)) comparator_45 (.a(out_114), .b(8'h8), .eq(comparator_45_eq));  // open: gt, lt
  Comparator #(.Bits(8)) comparator_46 (.a(out_114), .b(8'h9), .eq(comparator_46_eq));  // open: gt, lt
  Comparator #(.Bits(8)) comparator_47 (.a(out_114), .b(8'ha), .eq(comparator_47_eq));  // open: gt, lt
  Comparator #(.Bits(8)) comparator_48 (.a(out_114), .b(8'hb), .eq(comparator_48_eq));  // open: gt, lt
  Comparator #(.Bits(8)) comparator_49 (.a(out_114), .b(8'h30), .eq(comparator_49_eq));  // open: gt, lt
  Comparator #(.Bits(8)) comparator_50 (.a(out_114), .b(8'h31), .eq(comparator_50_eq));  // open: gt, lt
  Comparator #(.Bits(8)) comparator_51 (.a(out_114), .b(8'h32), .eq(comparator_51_eq));  // open: gt, lt
  Comparator #(.Bits(8)) comparator_52 (.a(out_114), .b(8'h33), .eq(comparator_52_eq));  // open: gt, lt
  Comparator #(.Bits(8)) comparator_53 (.a(out_114), .b(8'h58), .eq(comparator_53_eq));  // open: gt, lt
  Comparator #(.Bits(8)) comparator_54 (.a(out_114), .b(8'h59), .eq(comparator_54_eq));  // open: gt, lt
  Comparator #(.Bits(8)) comparator_55 (.a(out_114), .b(8'h5a), .eq(comparator_55_eq));  // open: gt, lt
  Comparator #(.Bits(8)) comparator_56 (.a(out_114), .b(8'h5b), .eq(comparator_56_eq));  // open: gt, lt
  Comparator #(.Bits(8)) comparator_57 (.a(out_114), .b(8'h80), .eq(comparator_57_eq));  // open: gt, lt
  Comparator #(.Bits(8)) comparator_58 (.a(out_114), .b(8'h81), .eq(comparator_58_eq));  // open: gt, lt
  Comparator #(.Bits(8)) comparator_59 (.a(out_114), .b(8'h82), .eq(comparator_59_eq));  // open: gt, lt
  Comparator #(.Bits(8)) comparator_60 (.a(out_114), .b(8'h83), .eq(comparator_60_eq));  // open: gt, lt
  Comparator #(.Bits(6)) comparator_61 (
    .a(out_119), .b(6'b000010), .gt(comparator_61_gt), .eq(comparator_61_eq), .lt(comparator_61_lt));
  Comparator #(.Bits(6)) comparator_62 (
    .a(out_119), .b(6'b001100), .gt(comparator_62_gt), .eq(comparator_62_eq), .lt(comparator_62_lt));
  Comparator #(.Bits(6)) comparator_63 (
    .a(out_119), .b(6'b010110), .gt(comparator_63_gt), .eq(comparator_63_eq), .lt(comparator_63_lt));
  Comparator #(.Bits(6)) comparator_64 (
    .a(out_119), .b(6'b100110), .gt(comparator_64_gt), .eq(comparator_64_eq), .lt(comparator_64_lt));
  Register #(.Bits(7)) register_80 (
    .D(_16_bascii_to_7_bascii_1_out), .C(delay_181_out), .en(comparator_45_eq), .Q(out_247));
  Delay #(.delayTime(10)) delay_181 (.in(comparator_45_eq), .out(delay_181_out));
  Register #(.Bits(7)) register_81 (
    .D(_16_bascii_to_7_bascii_1_out), .C(delay_182_out), .en(comparator_46_eq), .Q(register_81_q));
  Delay #(.delayTime(10)) delay_182 (.in(comparator_46_eq), .out(delay_182_out));
  Register #(.Bits(7)) register_82 (
    .D(_16_bascii_to_7_bascii_1_out), .C(delay_183_out), .en(comparator_47_eq), .Q(register_82_q));
  Delay #(.delayTime(10)) delay_183 (.in(comparator_47_eq), .out(delay_183_out));
  Register #(.Bits(7)) register_83 (
    .D(_16_bascii_to_7_bascii_1_out), .C(delay_184_out), .en(comparator_48_eq), .Q(out_248));
  Delay #(.delayTime(10)) delay_184 (.in(comparator_48_eq), .out(delay_184_out));
  Register #(.Bits(7)) register_84 (
    .D(_16_bascii_to_7_bascii_1_out), .C(delay_185_out), .en(comparator_49_eq), .Q(out_319));
  Delay #(.delayTime(10)) delay_185 (.in(comparator_49_eq), .out(delay_185_out));
  Register #(.Bits(7)) register_85 (
    .D(_16_bascii_to_7_bascii_1_out), .C(delay_186_out), .en(comparator_50_eq), .Q(register_85_q));
  Delay #(.delayTime(10)) delay_186 (.in(comparator_50_eq), .out(delay_186_out));
  Register #(.Bits(7)) register_86 (
    .D(_16_bascii_to_7_bascii_1_out), .C(delay_187_out), .en(comparator_51_eq), .Q(register_86_q));
  Delay #(.delayTime(10)) delay_187 (.in(comparator_51_eq), .out(delay_187_out));
  Register #(.Bits(7)) register_87 (
    .D(_16_bascii_to_7_bascii_1_out), .C(delay_188_out), .en(comparator_52_eq), .Q(out_320));
  Delay #(.delayTime(10)) delay_188 (.in(comparator_52_eq), .out(delay_188_out));
  Register #(.Bits(7)) register_88 (
    .D(_16_bascii_to_7_bascii_1_out), .C(delay_189_out), .en(comparator_53_eq), .Q(out_283));
  Delay #(.delayTime(10)) delay_189 (.in(comparator_53_eq), .out(delay_189_out));
  Register #(.Bits(7)) register_89 (
    .D(_16_bascii_to_7_bascii_1_out), .C(delay_190_out), .en(comparator_54_eq), .Q(register_89_q));
  Delay #(.delayTime(10)) delay_190 (.in(comparator_54_eq), .out(delay_190_out));
  Register #(.Bits(7)) register_90 (
    .D(_16_bascii_to_7_bascii_1_out), .C(delay_191_out), .en(comparator_55_eq), .Q(register_90_q));
  Delay #(.delayTime(10)) delay_191 (.in(comparator_55_eq), .out(delay_191_out));
  Register #(.Bits(7)) register_91 (
    .D(_16_bascii_to_7_bascii_1_out), .C(delay_192_out), .en(comparator_56_eq), .Q(out_284));
  Delay #(.delayTime(10)) delay_192 (.in(comparator_56_eq), .out(delay_192_out));
  Register #(.Bits(7)) register_92 (
    .D(_16_bascii_to_7_bascii_1_out), .C(delay_193_out), .en(comparator_57_eq), .Q(out_291));
  Delay #(.delayTime(10)) delay_193 (.in(comparator_57_eq), .out(delay_193_out));
  Register #(.Bits(7)) register_93 (
    .D(_16_bascii_to_7_bascii_1_out), .C(delay_194_out), .en(comparator_58_eq), .Q(register_93_q));
  Delay #(.delayTime(10)) delay_194 (.in(comparator_58_eq), .out(delay_194_out));
  Register #(.Bits(7)) register_94 (
    .D(_16_bascii_to_7_bascii_1_out), .C(delay_195_out), .en(comparator_59_eq), .Q(register_94_q));
  Delay #(.delayTime(10)) delay_195 (.in(comparator_59_eq), .out(delay_195_out));
  Register #(.Bits(7)) register_95 (
    .D(_16_bascii_to_7_bascii_1_out), .C(delay_196_out), .en(comparator_60_eq), .Q(out_292));
  Delay #(.delayTime(10)) delay_196 (.in(comparator_60_eq), .out(delay_196_out));
  Delay #(.delayTime(10)) delay_197 (.in(comparator_61_eq), .out(delay_197_out));
  Delay #(.delayTime(10)) delay_198 (.in(comparator_61_eq), .out(delay_198_out));
  Delay #(.delayTime(10)) delay_199 (.in(comparator_62_eq), .out(delay_199_out));
  Delay #(.delayTime(10)) delay_200 (.in(comparator_62_eq), .out(delay_200_out));
  Delay #(.delayTime(10)) delay_201 (.in(comparator_63_eq), .out(delay_201_out));
  Delay #(.delayTime(10)) delay_202 (.in(comparator_63_eq), .out(delay_202_out));
  Delay #(.delayTime(10)) delay_203 (.in(comparator_64_eq), .out(delay_203_out));
  Delay #(.delayTime(10)) delay_204 (.in(comparator_64_eq), .out(delay_204_out));
  Register #(.Bits(6)) register_96 (.D(pulldown_202_out[5:0]), .C(delay_197_out), .en(comparator_61_eq), .Q(CX_c2));
  Register #(.Bits(8)) register_97 (.D(pulldown_202_out[13:6]), .C(delay_198_out), .en(comparator_61_eq), .Q(CY_c2));
  Register #(.Bits(6)) register_98 (.D(pulldown_202_out[5:0]), .C(delay_199_out), .en(comparator_62_eq), .Q(CX_c12));
  Register #(.Bits(8)) register_99 (.D(pulldown_202_out[13:6]), .C(delay_200_out), .en(comparator_62_eq), .Q(CY_c12));
  Register #(.Bits(6)) register_100 (.D(pulldown_202_out[5:0]), .C(delay_201_out), .en(comparator_63_eq), .Q(CX_c22));
  Register #(.Bits(8)) register_101 (.D(pulldown_202_out[13:6]), .C(delay_202_out), .en(comparator_63_eq), .Q(CY_c22));
  Register #(.Bits(6)) register_102 (.D(pulldown_202_out[5:0]), .C(delay_203_out), .en(comparator_64_eq), .Q(CX_c32));
  Register #(.Bits(8)) register_103 (.D(pulldown_202_out[13:6]), .C(delay_204_out), .en(comparator_64_eq), .Q(CY_c32));
  vgastring vgastring_9 (
    .CX_i(vgastring_5_cx_o), .CY_i(vgastring_5_cy_o), .C_i(vgastring_5_c_o), .FG_i(vgastring_5_fg_o),
    .BG_i(vgastring_5_bg_o), .FG_c(FG_c0), .BG_c(BG_c0), .CX_c(CX_c2), .CY_c(CY_c2), .C_0(out_247),
    .C_1(register_81_q), .C_2(register_82_q), .C_3(out_248), .EN(1'b1), .CX_o(vgastring_9_cx_o),
    .CY_o(vgastring_9_cy_o), .C_o(vgastring_9_c_o), .FG_o(vgastring_9_fg_o), .BG_o(vgastring_9_bg_o));
  vgastring vgastring_10 (
    .CX_i(vgastring_6_cx_o), .CY_i(vgastring_6_cy_o), .C_i(vgastring_6_c_o), .FG_i(vgastring_6_fg_o),
    .BG_i(vgastring_6_bg_o), .FG_c(FG_c0), .BG_c(BG_c0), .CX_c(CX_c12), .CY_c(CY_c12), .C_0(out_319),
    .C_1(register_85_q), .C_2(register_86_q), .C_3(out_320), .EN(1'b1), .CX_o(vgastring_10_cx_o),
    .CY_o(vgastring_10_cy_o), .C_o(vgastring_10_c_o), .FG_o(vgastring_10_fg_o), .BG_o(vgastring_10_bg_o));
  vgastring vgastring_11 (
    .CX_i(vgastring_7_cx_o), .CY_i(vgastring_7_cy_o), .C_i(vgastring_7_c_o), .FG_i(vgastring_7_fg_o),
    .BG_i(vgastring_7_bg_o), .FG_c(FG_c0), .BG_c(BG_c0), .CX_c(CX_c22), .CY_c(CY_c22), .C_0(out_283),
    .C_1(register_89_q), .C_2(register_90_q), .C_3(out_284), .EN(1'b1), .CX_o(vgastring_11_cx_o),
    .CY_o(vgastring_11_cy_o), .C_o(vgastring_11_c_o), .FG_o(vgastring_11_fg_o), .BG_o(vgastring_11_bg_o));
  vgastring vgastring_12 (
    .CX_i(vgastring_8_cx_o), .CY_i(vgastring_8_cy_o), .C_i(vgastring_8_c_o), .FG_i(vgastring_8_fg_o),
    .BG_i(vgastring_8_bg_o), .FG_c(FG_c0), .BG_c(BG_c0), .CX_c(CX_c32), .CY_c(CY_c32), .C_0(out_291),
    .C_1(register_93_q), .C_2(register_94_q), .C_3(out_292), .EN(1'b1), .CX_o(vgastring_12_cx_o),
    .CY_o(vgastring_12_cy_o), .C_o(vgastring_12_c_o), .FG_o(vgastring_12_fg_o), .BG_o(vgastring_12_bg_o));
  Comparator #(.Bits(8)) comparator_65 (.a(out_114), .b(8'hc), .eq(comparator_65_eq));  // open: gt, lt
  Comparator #(.Bits(8)) comparator_66 (.a(out_114), .b(8'hd), .eq(comparator_66_eq));  // open: gt, lt
  Comparator #(.Bits(8)) comparator_67 (.a(out_114), .b(8'he), .eq(comparator_67_eq));  // open: gt, lt
  Comparator #(.Bits(8)) comparator_68 (.a(out_114), .b(8'hf), .eq(comparator_68_eq));  // open: gt, lt
  Comparator #(.Bits(8)) comparator_69 (.a(out_114), .b(8'h34), .eq(comparator_69_eq));  // open: gt, lt
  Comparator #(.Bits(8)) comparator_70 (.a(out_114), .b(8'h35), .eq(comparator_70_eq));  // open: gt, lt
  Comparator #(.Bits(8)) comparator_71 (.a(out_114), .b(8'h36), .eq(comparator_71_eq));  // open: gt, lt
  Comparator #(.Bits(8)) comparator_72 (.a(out_114), .b(8'h37), .eq(comparator_72_eq));  // open: gt, lt
  Comparator #(.Bits(8)) comparator_73 (.a(out_114), .b(8'h5c), .eq(comparator_73_eq));  // open: gt, lt
  Comparator #(.Bits(8)) comparator_74 (.a(out_114), .b(8'h5d), .eq(comparator_74_eq));  // open: gt, lt
  Comparator #(.Bits(8)) comparator_75 (.a(out_114), .b(8'h5e), .eq(comparator_75_eq));  // open: gt, lt
  Comparator #(.Bits(8)) comparator_76 (.a(out_114), .b(8'h5f), .eq(comparator_76_eq));  // open: gt, lt
  Comparator #(.Bits(8)) comparator_77 (.a(out_114), .b(8'h84), .eq(comparator_77_eq));  // open: gt, lt
  Comparator #(.Bits(8)) comparator_78 (.a(out_114), .b(8'h85), .eq(comparator_78_eq));  // open: gt, lt
  Comparator #(.Bits(8)) comparator_79 (.a(out_114), .b(8'h86), .eq(comparator_79_eq));  // open: gt, lt
  Comparator #(.Bits(8)) comparator_80 (.a(out_114), .b(8'h87), .eq(comparator_80_eq));  // open: gt, lt
  Comparator #(.Bits(6)) comparator_81 (
    .a(out_119), .b(6'b000011), .gt(comparator_81_gt), .eq(comparator_81_eq), .lt(comparator_81_lt));
  Comparator #(.Bits(6)) comparator_82 (
    .a(out_119), .b(6'b001101), .gt(comparator_82_gt), .eq(comparator_82_eq), .lt(comparator_82_lt));
  Comparator #(.Bits(6)) comparator_83 (
    .a(out_119), .b(6'b010111), .gt(comparator_83_gt), .eq(comparator_83_eq), .lt(comparator_83_lt));
  Comparator #(.Bits(6)) comparator_84 (
    .a(out_119), .b(6'b100111), .gt(comparator_84_gt), .eq(comparator_84_eq), .lt(comparator_84_lt));
  Register #(.Bits(7)) register_104 (
    .D(_16_bascii_to_7_bascii_1_out), .C(delay_205_out), .en(comparator_65_eq), .Q(out_249));
  Delay #(.delayTime(10)) delay_205 (.in(comparator_65_eq), .out(delay_205_out));
  Register #(.Bits(7)) register_105 (
    .D(_16_bascii_to_7_bascii_1_out), .C(delay_206_out), .en(comparator_66_eq), .Q(register_105_q));
  Delay #(.delayTime(10)) delay_206 (.in(comparator_66_eq), .out(delay_206_out));
  Register #(.Bits(7)) register_106 (
    .D(_16_bascii_to_7_bascii_1_out), .C(delay_207_out), .en(comparator_67_eq), .Q(register_106_q));
  Delay #(.delayTime(10)) delay_207 (.in(comparator_67_eq), .out(delay_207_out));
  Register #(.Bits(7)) register_107 (
    .D(_16_bascii_to_7_bascii_1_out), .C(delay_208_out), .en(comparator_68_eq), .Q(out_250));
  Delay #(.delayTime(10)) delay_208 (.in(comparator_68_eq), .out(delay_208_out));
  Register #(.Bits(7)) register_108 (
    .D(_16_bascii_to_7_bascii_1_out), .C(delay_209_out), .en(comparator_69_eq), .Q(out_273));
  Delay #(.delayTime(10)) delay_209 (.in(comparator_69_eq), .out(delay_209_out));
  Register #(.Bits(7)) register_109 (
    .D(_16_bascii_to_7_bascii_1_out), .C(delay_210_out), .en(comparator_70_eq), .Q(register_109_q));
  Delay #(.delayTime(10)) delay_210 (.in(comparator_70_eq), .out(delay_210_out));
  Register #(.Bits(7)) register_110 (
    .D(_16_bascii_to_7_bascii_1_out), .C(delay_211_out), .en(comparator_71_eq), .Q(register_110_q));
  Delay #(.delayTime(10)) delay_211 (.in(comparator_71_eq), .out(delay_211_out));
  Register #(.Bits(7)) register_111 (
    .D(_16_bascii_to_7_bascii_1_out), .C(delay_212_out), .en(comparator_72_eq), .Q(out_274));
  Delay #(.delayTime(10)) delay_212 (.in(comparator_72_eq), .out(delay_212_out));
  Register #(.Bits(7)) register_112 (
    .D(_16_bascii_to_7_bascii_1_out), .C(delay_213_out), .en(comparator_73_eq), .Q(out_313));
  Delay #(.delayTime(10)) delay_213 (.in(comparator_73_eq), .out(delay_213_out));
  Register #(.Bits(7)) register_113 (
    .D(_16_bascii_to_7_bascii_1_out), .C(delay_214_out), .en(comparator_74_eq), .Q(register_113_q));
  Delay #(.delayTime(10)) delay_214 (.in(comparator_74_eq), .out(delay_214_out));
  Register #(.Bits(7)) register_114 (
    .D(_16_bascii_to_7_bascii_1_out), .C(delay_215_out), .en(comparator_75_eq), .Q(register_114_q));
  Delay #(.delayTime(10)) delay_215 (.in(comparator_75_eq), .out(delay_215_out));
  Register #(.Bits(7)) register_115 (
    .D(_16_bascii_to_7_bascii_1_out), .C(delay_216_out), .en(comparator_76_eq), .Q(out_314));
  Delay #(.delayTime(10)) delay_216 (.in(comparator_76_eq), .out(delay_216_out));
  Register #(.Bits(7)) register_116 (
    .D(_16_bascii_to_7_bascii_1_out), .C(delay_217_out), .en(comparator_77_eq), .Q(out_293));
  Delay #(.delayTime(10)) delay_217 (.in(comparator_77_eq), .out(delay_217_out));
  Register #(.Bits(7)) register_117 (
    .D(_16_bascii_to_7_bascii_1_out), .C(delay_218_out), .en(comparator_78_eq), .Q(register_117_q));
  Delay #(.delayTime(10)) delay_218 (.in(comparator_78_eq), .out(delay_218_out));
  Register #(.Bits(7)) register_118 (
    .D(_16_bascii_to_7_bascii_1_out), .C(delay_219_out), .en(comparator_79_eq), .Q(register_118_q));
  Delay #(.delayTime(10)) delay_219 (.in(comparator_79_eq), .out(delay_219_out));
  Register #(.Bits(7)) register_119 (
    .D(_16_bascii_to_7_bascii_1_out), .C(delay_220_out), .en(comparator_80_eq), .Q(out_294));
  Delay #(.delayTime(10)) delay_220 (.in(comparator_80_eq), .out(delay_220_out));
  Register #(.Bits(6)) register_120 (.D(pulldown_202_out[5:0]), .C(delay_221_out), .en(comparator_81_eq), .Q(CX_c3));
  Delay #(.delayTime(10)) delay_221 (.in(comparator_81_eq), .out(delay_221_out));
  Register #(.Bits(8)) register_121 (.D(pulldown_202_out[13:6]), .C(delay_222_out), .en(comparator_81_eq), .Q(CY_c3));
  Delay #(.delayTime(10)) delay_222 (.in(comparator_81_eq), .out(delay_222_out));
  Register #(.Bits(6)) register_122 (.D(pulldown_202_out[5:0]), .C(delay_223_out), .en(comparator_82_eq), .Q(CX_c13));
  Delay #(.delayTime(10)) delay_223 (.in(comparator_82_eq), .out(delay_223_out));
  Register #(.Bits(8)) register_123 (.D(pulldown_202_out[13:6]), .C(delay_224_out), .en(comparator_82_eq), .Q(CY_c13));
  Delay #(.delayTime(10)) delay_224 (.in(comparator_82_eq), .out(delay_224_out));
  Register #(.Bits(6)) register_124 (.D(pulldown_202_out[5:0]), .C(delay_225_out), .en(comparator_83_eq), .Q(CX_c23));
  Delay #(.delayTime(10)) delay_225 (.in(comparator_83_eq), .out(delay_225_out));
  Register #(.Bits(8)) register_125 (.D(pulldown_202_out[13:6]), .C(delay_226_out), .en(comparator_83_eq), .Q(CY_c23));
  Delay #(.delayTime(10)) delay_226 (.in(comparator_83_eq), .out(delay_226_out));
  Register #(.Bits(6)) register_126 (.D(pulldown_202_out[5:0]), .C(delay_227_out), .en(comparator_84_eq), .Q(CX_c33));
  Delay #(.delayTime(10)) delay_227 (.in(comparator_84_eq), .out(delay_227_out));
  Register #(.Bits(8)) register_127 (.D(pulldown_202_out[13:6]), .C(delay_228_out), .en(comparator_84_eq), .Q(CY_c33));
  Delay #(.delayTime(10)) delay_228 (.in(comparator_84_eq), .out(delay_228_out));
  vgastring vgastring_13 (
    .CX_i(vgastring_9_cx_o), .CY_i(vgastring_9_cy_o), .C_i(vgastring_9_c_o), .FG_i(vgastring_9_fg_o),
    .BG_i(vgastring_9_bg_o), .FG_c(FG_c0), .BG_c(BG_c0), .CX_c(CX_c3), .CY_c(CY_c3), .C_0(out_249),
    .C_1(register_105_q), .C_2(register_106_q), .C_3(out_250), .EN(1'b1), .CX_o(vgastring_13_cx_o),
    .CY_o(vgastring_13_cy_o), .C_o(vgastring_13_c_o), .FG_o(vgastring_13_fg_o), .BG_o(vgastring_13_bg_o));
  vgastring vgastring_14 (
    .CX_i(vgastring_10_cx_o), .CY_i(vgastring_10_cy_o), .C_i(vgastring_10_c_o), .FG_i(vgastring_10_fg_o),
    .BG_i(vgastring_10_bg_o), .FG_c(FG_c0), .BG_c(BG_c0), .CX_c(CX_c13), .CY_c(CY_c13), .C_0(out_273),
    .C_1(register_109_q), .C_2(register_110_q), .C_3(out_274), .EN(1'b1), .CX_o(vgastring_14_cx_o),
    .CY_o(vgastring_14_cy_o), .C_o(vgastring_14_c_o), .FG_o(vgastring_14_fg_o), .BG_o(vgastring_14_bg_o));
  vgastring vgastring_15 (
    .CX_i(vgastring_11_cx_o), .CY_i(vgastring_11_cy_o), .C_i(vgastring_11_c_o), .FG_i(vgastring_11_fg_o),
    .BG_i(vgastring_11_bg_o), .FG_c(FG_c0), .BG_c(BG_c0), .CX_c(CX_c23), .CY_c(CY_c23), .C_0(out_313),
    .C_1(register_113_q), .C_2(register_114_q), .C_3(out_314), .EN(1'b1), .CX_o(vgastring_15_cx_o),
    .CY_o(vgastring_15_cy_o), .C_o(vgastring_15_c_o), .FG_o(vgastring_15_fg_o), .BG_o(vgastring_15_bg_o));
  vgastring vgastring_16 (
    .CX_i(vgastring_12_cx_o), .CY_i(vgastring_12_cy_o), .C_i(vgastring_12_c_o), .FG_i(vgastring_12_fg_o),
    .BG_i(vgastring_12_bg_o), .FG_c(FG_c0), .BG_c(BG_c0), .CX_c(CX_c33), .CY_c(CY_c33), .C_0(out_293),
    .C_1(register_117_q), .C_2(register_118_q), .C_3(out_294), .EN(1'b1), .CX_o(vgastring_16_cx_o),
    .CY_o(vgastring_16_cy_o), .C_o(vgastring_16_c_o), .FG_o(vgastring_16_fg_o), .BG_o(vgastring_16_bg_o));
  Comparator #(.Bits(8)) comparator_85 (.a(out_114), .b(8'h10), .eq(comparator_85_eq));  // open: gt, lt
  Comparator #(.Bits(8)) comparator_86 (.a(out_114), .b(8'h11), .eq(comparator_86_eq));  // open: gt, lt
  Comparator #(.Bits(8)) comparator_87 (.a(out_114), .b(8'h12), .eq(comparator_87_eq));  // open: gt, lt
  Comparator #(.Bits(8)) comparator_88 (.a(out_114), .b(8'h13), .eq(comparator_88_eq));  // open: gt, lt
  Comparator #(.Bits(8)) comparator_89 (.a(out_114), .b(8'h38), .eq(comparator_89_eq));  // open: gt, lt
  Comparator #(.Bits(8)) comparator_90 (.a(out_114), .b(8'h39), .eq(comparator_90_eq));  // open: gt, lt
  Comparator #(.Bits(8)) comparator_91 (.a(out_114), .b(8'h3a), .eq(comparator_91_eq));  // open: gt, lt
  Comparator #(.Bits(8)) comparator_92 (.a(out_114), .b(8'h3b), .eq(comparator_92_eq));  // open: gt, lt
  Comparator #(.Bits(8)) comparator_93 (.a(out_114), .b(8'h60), .eq(comparator_93_eq));  // open: gt, lt
  Comparator #(.Bits(8)) comparator_94 (.a(out_114), .b(8'h61), .eq(comparator_94_eq));  // open: gt, lt
  Comparator #(.Bits(8)) comparator_95 (.a(out_114), .b(8'h62), .eq(comparator_95_eq));  // open: gt, lt
  Comparator #(.Bits(8)) comparator_96 (.a(out_114), .b(8'h63), .eq(comparator_96_eq));  // open: gt, lt
  Comparator #(.Bits(8)) comparator_97 (.a(out_114), .b(8'h88), .eq(comparator_97_eq));  // open: gt, lt
  Comparator #(.Bits(8)) comparator_98 (.a(out_114), .b(8'h89), .eq(comparator_98_eq));  // open: gt, lt
  Comparator #(.Bits(8)) comparator_99 (.a(out_114), .b(8'h8a), .eq(comparator_99_eq));  // open: gt, lt
  Comparator #(.Bits(8)) comparator_100 (.a(out_114), .b(8'h8b), .eq(comparator_100_eq));  // open: gt, lt
  Comparator #(.Bits(6)) comparator_101 (
    .a(out_119), .b(6'b000100), .gt(comparator_101_gt), .eq(comparator_101_eq), .lt(comparator_101_lt));
  Comparator #(.Bits(6)) comparator_102 (
    .a(out_119), .b(6'b001110), .gt(comparator_102_gt), .eq(comparator_102_eq), .lt(comparator_102_lt));
  Comparator #(.Bits(6)) comparator_103 (
    .a(out_119), .b(6'b011000), .gt(comparator_103_gt), .eq(comparator_103_eq), .lt(comparator_103_lt));
  Comparator #(.Bits(6)) comparator_104 (
    .a(out_119), .b(6'b101000), .gt(comparator_104_gt), .eq(comparator_104_eq), .lt(comparator_104_lt));
  Register #(.Bits(7)) register_128 (
    .D(_16_bascii_to_7_bascii_1_out), .C(delay_229_out), .en(comparator_85_eq), .Q(out_251));
  Delay #(.delayTime(10)) delay_229 (.in(comparator_85_eq), .out(delay_229_out));
  Register #(.Bits(7)) register_129 (
    .D(_16_bascii_to_7_bascii_1_out), .C(delay_230_out), .en(comparator_86_eq), .Q(register_129_q));
  Delay #(.delayTime(10)) delay_230 (.in(comparator_86_eq), .out(delay_230_out));
  Register #(.Bits(7)) register_130 (
    .D(_16_bascii_to_7_bascii_1_out), .C(delay_231_out), .en(comparator_87_eq), .Q(register_130_q));
  Delay #(.delayTime(10)) delay_231 (.in(comparator_87_eq), .out(delay_231_out));
  Register #(.Bits(7)) register_131 (
    .D(_16_bascii_to_7_bascii_1_out), .C(delay_232_out), .en(comparator_88_eq), .Q(out_252));
  Delay #(.delayTime(10)) delay_232 (.in(comparator_88_eq), .out(delay_232_out));
  Register #(.Bits(7)) register_132 (
    .D(_16_bascii_to_7_bascii_1_out), .C(delay_233_out), .en(comparator_89_eq), .Q(out_275));
  Delay #(.delayTime(10)) delay_233 (.in(comparator_89_eq), .out(delay_233_out));
  Register #(.Bits(7)) register_133 (
    .D(_16_bascii_to_7_bascii_1_out), .C(delay_234_out), .en(comparator_90_eq), .Q(register_133_q));
  Delay #(.delayTime(10)) delay_234 (.in(comparator_90_eq), .out(delay_234_out));
  Register #(.Bits(7)) register_134 (
    .D(_16_bascii_to_7_bascii_1_out), .C(delay_235_out), .en(comparator_91_eq), .Q(register_134_q));
  Delay #(.delayTime(10)) delay_235 (.in(comparator_91_eq), .out(delay_235_out));
  Register #(.Bits(7)) register_135 (
    .D(_16_bascii_to_7_bascii_1_out), .C(delay_236_out), .en(comparator_92_eq), .Q(out_276));
  Delay #(.delayTime(10)) delay_236 (.in(comparator_92_eq), .out(delay_236_out));
  Register #(.Bits(7)) register_136 (
    .D(_16_bascii_to_7_bascii_1_out), .C(delay_237_out), .en(comparator_93_eq), .Q(out_278));
  Delay #(.delayTime(10)) delay_237 (.in(comparator_93_eq), .out(delay_237_out));
  Register #(.Bits(7)) register_137 (
    .D(_16_bascii_to_7_bascii_1_out), .C(delay_238_out), .en(comparator_94_eq), .Q(register_137_q));
  Delay #(.delayTime(10)) delay_238 (.in(comparator_94_eq), .out(delay_238_out));
  Register #(.Bits(7)) register_138 (
    .D(_16_bascii_to_7_bascii_1_out), .C(delay_239_out), .en(comparator_95_eq), .Q(register_138_q));
  Delay #(.delayTime(10)) delay_239 (.in(comparator_95_eq), .out(delay_239_out));
  Register #(.Bits(7)) register_139 (
    .D(_16_bascii_to_7_bascii_1_out), .C(delay_240_out), .en(comparator_96_eq), .Q(out_277));
  Delay #(.delayTime(10)) delay_240 (.in(comparator_96_eq), .out(delay_240_out));
  Register #(.Bits(7)) register_140 (
    .D(_16_bascii_to_7_bascii_1_out), .C(delay_241_out), .en(comparator_97_eq), .Q(out_279));
  Delay #(.delayTime(10)) delay_241 (.in(comparator_97_eq), .out(delay_241_out));
  Register #(.Bits(7)) register_141 (
    .D(_16_bascii_to_7_bascii_1_out), .C(delay_242_out), .en(comparator_98_eq), .Q(register_141_q));
  Delay #(.delayTime(10)) delay_242 (.in(comparator_98_eq), .out(delay_242_out));
  Register #(.Bits(7)) register_142 (
    .D(_16_bascii_to_7_bascii_1_out), .C(delay_243_out), .en(comparator_99_eq), .Q(register_142_q));
  Delay #(.delayTime(10)) delay_243 (.in(comparator_99_eq), .out(delay_243_out));
  Register #(.Bits(7)) register_143 (
    .D(_16_bascii_to_7_bascii_1_out), .C(delay_244_out), .en(comparator_100_eq), .Q(out_280));
  Delay #(.delayTime(10)) delay_244 (.in(comparator_100_eq), .out(delay_244_out));
  Delay #(.delayTime(10)) delay_245 (.in(comparator_101_eq), .out(delay_245_out));
  Delay #(.delayTime(10)) delay_246 (.in(comparator_101_eq), .out(delay_246_out));
  Delay #(.delayTime(10)) delay_247 (.in(comparator_102_eq), .out(delay_247_out));
  Delay #(.delayTime(10)) delay_248 (.in(comparator_102_eq), .out(delay_248_out));
  Delay #(.delayTime(10)) delay_249 (.in(comparator_103_eq), .out(delay_249_out));
  Delay #(.delayTime(10)) delay_250 (.in(comparator_103_eq), .out(delay_250_out));
  Delay #(.delayTime(10)) delay_251 (.in(comparator_104_eq), .out(delay_251_out));
  Delay #(.delayTime(10)) delay_252 (.in(comparator_104_eq), .out(delay_252_out));
  vgastring vgastring_17 (
    .CX_i(vgastring_13_cx_o), .CY_i(vgastring_13_cy_o), .C_i(vgastring_13_c_o), .FG_i(vgastring_13_fg_o),
    .BG_i(vgastring_13_bg_o), .FG_c(FG_c0), .BG_c(BG_c0), .CX_c(CX_c4), .CY_c(CY_c4), .C_0(out_251),
    .C_1(register_129_q), .C_2(register_130_q), .C_3(out_252), .EN(1'b1), .CX_o(vgastring_17_cx_o),
    .CY_o(vgastring_17_cy_o), .C_o(vgastring_17_c_o), .FG_o(vgastring_17_fg_o), .BG_o(vgastring_17_bg_o));
  vgastring vgastring_18 (
    .CX_i(vgastring_14_cx_o), .CY_i(vgastring_14_cy_o), .C_i(vgastring_14_c_o), .FG_i(vgastring_14_fg_o),
    .BG_i(vgastring_14_bg_o), .FG_c(FG_c0), .BG_c(BG_c0), .CX_c(CX_c14), .CY_c(CY_c14), .C_0(out_275),
    .C_1(register_133_q), .C_2(register_134_q), .C_3(out_276), .EN(1'b1), .CX_o(vgastring_18_cx_o),
    .CY_o(vgastring_18_cy_o), .C_o(vgastring_18_c_o), .FG_o(vgastring_18_fg_o), .BG_o(vgastring_18_bg_o));
  vgastring vgastring_19 (
    .CX_i(vgastring_15_cx_o), .CY_i(vgastring_15_cy_o), .C_i(vgastring_15_c_o), .FG_i(vgastring_15_fg_o),
    .BG_i(vgastring_15_bg_o), .FG_c(FG_c0), .BG_c(BG_c0), .CX_c(CX_c24), .CY_c(CY_c24), .C_0(out_278),
    .C_1(register_137_q), .C_2(register_138_q), .C_3(out_277), .EN(1'b1), .CX_o(vgastring_19_cx_o),
    .CY_o(vgastring_19_cy_o), .C_o(vgastring_19_c_o), .FG_o(vgastring_19_fg_o), .BG_o(vgastring_19_bg_o));
  vgastring vgastring_20 (
    .CX_i(vgastring_16_cx_o), .CY_i(vgastring_16_cy_o), .C_i(vgastring_16_c_o), .FG_i(vgastring_16_fg_o),
    .BG_i(vgastring_16_bg_o), .FG_c(FG_c0), .BG_c(BG_c0), .CX_c(CX_c34), .CY_c(CY_c34), .C_0(out_279),
    .C_1(register_141_q), .C_2(register_142_q), .C_3(out_280), .EN(1'b1), .CX_o(vgastring_20_cx_o),
    .CY_o(vgastring_20_cy_o), .C_o(vgastring_20_c_o), .FG_o(vgastring_20_fg_o), .BG_o(vgastring_20_bg_o));
  Register #(.Bits(6)) register_144 (.D(pulldown_202_out[5:0]), .C(delay_245_out), .en(comparator_101_eq), .Q(CX_c4));
  Register #(.Bits(8)) register_145 (.D(pulldown_202_out[13:6]), .C(delay_246_out), .en(comparator_101_eq), .Q(CY_c4));
  Register #(.Bits(6)) register_146 (.D(pulldown_202_out[5:0]), .C(delay_247_out), .en(comparator_102_eq), .Q(CX_c14));
  Register #(.Bits(8)) register_147 (.D(pulldown_202_out[13:6]), .C(delay_248_out), .en(comparator_102_eq), .Q(CY_c14));
  Register #(.Bits(6)) register_148 (.D(pulldown_202_out[5:0]), .C(delay_249_out), .en(comparator_103_eq), .Q(CX_c24));
  Register #(.Bits(8)) register_149 (.D(pulldown_202_out[13:6]), .C(delay_250_out), .en(comparator_103_eq), .Q(CY_c24));
  Register #(.Bits(6)) register_150 (.D(pulldown_202_out[5:0]), .C(delay_251_out), .en(comparator_104_eq), .Q(CX_c34));
  Register #(.Bits(8)) register_151 (.D(pulldown_202_out[13:6]), .C(delay_252_out), .en(comparator_104_eq), .Q(CY_c34));
  Comparator #(.Bits(8)) comparator_105 (.a(out_114), .b(8'h14), .eq(comparator_105_eq));  // open: gt, lt
  Comparator #(.Bits(8)) comparator_106 (.a(out_114), .b(8'h15), .eq(comparator_106_eq));  // open: gt, lt
  Comparator #(.Bits(8)) comparator_107 (.a(out_114), .b(8'h16), .eq(comparator_107_eq));  // open: gt, lt
  Comparator #(.Bits(8)) comparator_108 (.a(out_114), .b(8'h17), .eq(comparator_108_eq));  // open: gt, lt
  Comparator #(.Bits(8)) comparator_109 (.a(out_114), .b(8'h3c), .eq(comparator_109_eq));  // open: gt, lt
  Comparator #(.Bits(8)) comparator_110 (.a(out_114), .b(8'h3d), .eq(comparator_110_eq));  // open: gt, lt
  Comparator #(.Bits(8)) comparator_111 (.a(out_114), .b(8'h3e), .eq(comparator_111_eq));  // open: gt, lt
  Comparator #(.Bits(8)) comparator_112 (.a(out_114), .b(8'h3f), .eq(comparator_112_eq));  // open: gt, lt
  Comparator #(.Bits(8)) comparator_113 (.a(out_114), .b(8'h64), .eq(comparator_113_eq));  // open: gt, lt
  Comparator #(.Bits(8)) comparator_114 (.a(out_114), .b(8'h65), .eq(comparator_114_eq));  // open: gt, lt
  Comparator #(.Bits(8)) comparator_115 (.a(out_114), .b(8'h66), .eq(comparator_115_eq));  // open: gt, lt
  Comparator #(.Bits(8)) comparator_116 (.a(out_114), .b(8'h67), .eq(comparator_116_eq));  // open: gt, lt
  Comparator #(.Bits(8)) comparator_117 (.a(out_114), .b(8'h8c), .eq(comparator_117_eq));  // open: gt, lt
  Comparator #(.Bits(8)) comparator_118 (.a(out_114), .b(8'h8d), .eq(comparator_118_eq));  // open: gt, lt
  Comparator #(.Bits(8)) comparator_119 (.a(out_114), .b(8'h8e), .eq(comparator_119_eq));  // open: gt, lt
  Comparator #(.Bits(8)) comparator_120 (.a(out_114), .b(8'h8f), .eq(comparator_120_eq));  // open: gt, lt
  Delay #(.delayTime(10)) delay_253 (.in(comparator_105_eq), .out(delay_253_out));
  Delay #(.delayTime(10)) delay_254 (.in(comparator_106_eq), .out(delay_254_out));
  Delay #(.delayTime(10)) delay_255 (.in(comparator_107_eq), .out(delay_255_out));
  Delay #(.delayTime(10)) delay_256 (.in(comparator_108_eq), .out(delay_256_out));
  Delay #(.delayTime(10)) delay_257 (.in(comparator_109_eq), .out(delay_257_out));
  Delay #(.delayTime(10)) delay_258 (.in(comparator_110_eq), .out(delay_258_out));
  Delay #(.delayTime(10)) delay_259 (.in(comparator_111_eq), .out(delay_259_out));
  Delay #(.delayTime(10)) delay_260 (.in(comparator_112_eq), .out(delay_260_out));
  Delay #(.delayTime(10)) delay_261 (.in(comparator_113_eq), .out(delay_261_out));
  Delay #(.delayTime(10)) delay_262 (.in(comparator_114_eq), .out(delay_262_out));
  Delay #(.delayTime(10)) delay_263 (.in(comparator_115_eq), .out(delay_263_out));
  Delay #(.delayTime(10)) delay_264 (.in(comparator_116_eq), .out(delay_264_out));
  Delay #(.delayTime(10)) delay_265 (.in(comparator_117_eq), .out(delay_265_out));
  Delay #(.delayTime(10)) delay_266 (.in(comparator_118_eq), .out(delay_266_out));
  Delay #(.delayTime(10)) delay_267 (.in(comparator_119_eq), .out(delay_267_out));
  Delay #(.delayTime(10)) delay_268 (.in(comparator_120_eq), .out(delay_268_out));
  Comparator #(.Bits(6)) comparator_121 (
    .a(out_119), .b(6'b000101), .gt(comparator_121_gt), .eq(comparator_121_eq), .lt(comparator_121_lt));
  Comparator #(.Bits(6)) comparator_122 (
    .a(out_119), .b(6'b001111), .gt(comparator_122_gt), .eq(comparator_122_eq), .lt(comparator_122_lt));
  Comparator #(.Bits(6)) comparator_123 (
    .a(out_119), .b(6'b011001), .gt(comparator_123_gt), .eq(comparator_123_eq), .lt(comparator_123_lt));
  Comparator #(.Bits(6)) comparator_124 (
    .a(out_119), .b(6'b101001), .gt(comparator_124_gt), .eq(comparator_124_eq), .lt(comparator_124_lt));
  Register #(.Bits(7)) register_152 (
    .D(_16_bascii_to_7_bascii_1_out), .C(delay_253_out), .en(comparator_105_eq), .Q(out_253));
  Register #(.Bits(7)) register_153 (
    .D(_16_bascii_to_7_bascii_1_out), .C(delay_254_out), .en(comparator_106_eq), .Q(register_153_q));
  Register #(.Bits(7)) register_154 (
    .D(_16_bascii_to_7_bascii_1_out), .C(delay_255_out), .en(comparator_107_eq), .Q(register_154_q));
  Register #(.Bits(7)) register_155 (
    .D(_16_bascii_to_7_bascii_1_out), .C(delay_256_out), .en(comparator_108_eq), .Q(out_254));
  Register #(.Bits(7)) register_156 (
    .D(_16_bascii_to_7_bascii_1_out), .C(delay_257_out), .en(comparator_109_eq), .Q(out_271));
  Register #(.Bits(7)) register_157 (
    .D(_16_bascii_to_7_bascii_1_out), .C(delay_258_out), .en(comparator_110_eq), .Q(register_157_q));
  Register #(.Bits(7)) register_158 (
    .D(_16_bascii_to_7_bascii_1_out), .C(delay_259_out), .en(comparator_111_eq), .Q(register_158_q));
  Register #(.Bits(7)) register_159 (
    .D(_16_bascii_to_7_bascii_1_out), .C(delay_260_out), .en(comparator_112_eq), .Q(out_272));
  Register #(.Bits(7)) register_160 (
    .D(_16_bascii_to_7_bascii_1_out), .C(delay_261_out), .en(comparator_113_eq), .Q(out_311));
  Register #(.Bits(7)) register_161 (
    .D(_16_bascii_to_7_bascii_1_out), .C(delay_262_out), .en(comparator_114_eq), .Q(register_161_q));
  Register #(.Bits(7)) register_162 (
    .D(_16_bascii_to_7_bascii_1_out), .C(delay_263_out), .en(comparator_115_eq), .Q(register_162_q));
  Register #(.Bits(7)) register_163 (
    .D(_16_bascii_to_7_bascii_1_out), .C(delay_264_out), .en(comparator_116_eq), .Q(out_312));
  Register #(.Bits(7)) register_164 (
    .D(_16_bascii_to_7_bascii_1_out), .C(delay_265_out), .en(comparator_117_eq), .Q(out_295));
  Register #(.Bits(7)) register_165 (
    .D(_16_bascii_to_7_bascii_1_out), .C(delay_266_out), .en(comparator_118_eq), .Q(register_165_q));
  Register #(.Bits(7)) register_166 (
    .D(_16_bascii_to_7_bascii_1_out), .C(delay_267_out), .en(comparator_119_eq), .Q(register_166_q));
  Register #(.Bits(7)) register_167 (
    .D(_16_bascii_to_7_bascii_1_out), .C(delay_268_out), .en(comparator_120_eq), .Q(out_296));
  Delay #(.delayTime(10)) delay_269 (.in(comparator_121_eq), .out(delay_269_out));
  Delay #(.delayTime(10)) delay_270 (.in(comparator_121_eq), .out(delay_270_out));
  Delay #(.delayTime(10)) delay_271 (.in(comparator_122_eq), .out(delay_271_out));
  Delay #(.delayTime(10)) delay_272 (.in(comparator_122_eq), .out(delay_272_out));
  Delay #(.delayTime(10)) delay_273 (.in(comparator_123_eq), .out(delay_273_out));
  Delay #(.delayTime(10)) delay_274 (.in(comparator_123_eq), .out(delay_274_out));
  Delay #(.delayTime(10)) delay_275 (.in(comparator_124_eq), .out(delay_275_out));
  Delay #(.delayTime(10)) delay_276 (.in(comparator_124_eq), .out(delay_276_out));
  vgastring vgastring_21 (
    .CX_i(vgastring_17_cx_o), .CY_i(vgastring_17_cy_o), .C_i(vgastring_17_c_o), .FG_i(vgastring_17_fg_o),
    .BG_i(vgastring_17_bg_o), .FG_c(FG_c0), .BG_c(BG_c0), .CX_c(CX_c5), .CY_c(CY_c5), .C_0(out_253),
    .C_1(register_153_q), .C_2(register_154_q), .C_3(out_254), .EN(1'b1), .CX_o(vgastring_21_cx_o),
    .CY_o(vgastring_21_cy_o), .C_o(vgastring_21_c_o), .FG_o(vgastring_21_fg_o), .BG_o(vgastring_21_bg_o));
  vgastring vgastring_22 (
    .CX_i(vgastring_18_cx_o), .CY_i(vgastring_18_cy_o), .C_i(vgastring_18_c_o), .FG_i(vgastring_18_fg_o),
    .BG_i(vgastring_18_bg_o), .FG_c(FG_c0), .BG_c(BG_c0), .CX_c(CX_c15), .CY_c(CY_c15), .C_0(out_271),
    .C_1(register_157_q), .C_2(register_158_q), .C_3(out_272), .EN(1'b1), .CX_o(vgastring_22_cx_o),
    .CY_o(vgastring_22_cy_o), .C_o(vgastring_22_c_o), .FG_o(vgastring_22_fg_o), .BG_o(vgastring_22_bg_o));
  vgastring vgastring_23 (
    .CX_i(vgastring_19_cx_o), .CY_i(vgastring_19_cy_o), .C_i(vgastring_19_c_o), .FG_i(vgastring_19_fg_o),
    .BG_i(vgastring_19_bg_o), .FG_c(FG_c0), .BG_c(BG_c0), .CX_c(CX_c25), .CY_c(CY_c25), .C_0(out_311),
    .C_1(register_161_q), .C_2(register_162_q), .C_3(out_312), .EN(1'b1), .CX_o(vgastring_23_cx_o),
    .CY_o(vgastring_23_cy_o), .C_o(vgastring_23_c_o), .FG_o(vgastring_23_fg_o), .BG_o(vgastring_23_bg_o));
  vgastring vgastring_24 (
    .CX_i(vgastring_20_cx_o), .CY_i(vgastring_20_cy_o), .C_i(vgastring_20_c_o), .FG_i(vgastring_20_fg_o),
    .BG_i(vgastring_20_bg_o), .FG_c(FG_c0), .BG_c(BG_c0), .CX_c(CX_c35), .CY_c(CY_c35), .C_0(out_295),
    .C_1(register_165_q), .C_2(register_166_q), .C_3(out_296), .EN(1'b1), .CX_o(vgastring_24_cx_o),
    .CY_o(vgastring_24_cy_o), .C_o(vgastring_24_c_o), .FG_o(vgastring_24_fg_o), .BG_o(vgastring_24_bg_o));
  Register #(.Bits(6)) register_168 (.D(pulldown_202_out[5:0]), .C(delay_269_out), .en(comparator_121_eq), .Q(CX_c5));
  Register #(.Bits(8)) register_169 (.D(pulldown_202_out[13:6]), .C(delay_270_out), .en(comparator_121_eq), .Q(CY_c5));
  Register #(.Bits(6)) register_170 (.D(pulldown_202_out[5:0]), .C(delay_271_out), .en(comparator_122_eq), .Q(CX_c15));
  Register #(.Bits(8)) register_171 (.D(pulldown_202_out[13:6]), .C(delay_272_out), .en(comparator_122_eq), .Q(CY_c15));
  Register #(.Bits(6)) register_172 (.D(pulldown_202_out[5:0]), .C(delay_273_out), .en(comparator_123_eq), .Q(CX_c25));
  Register #(.Bits(8)) register_173 (.D(pulldown_202_out[13:6]), .C(delay_274_out), .en(comparator_123_eq), .Q(CY_c25));
  Register #(.Bits(6)) register_174 (.D(pulldown_202_out[5:0]), .C(delay_275_out), .en(comparator_124_eq), .Q(CX_c35));
  Register #(.Bits(8)) register_175 (.D(pulldown_202_out[13:6]), .C(delay_276_out), .en(comparator_124_eq), .Q(CY_c35));
  Comparator #(.Bits(8)) comparator_125 (.a(out_114), .b(8'h18), .eq(comparator_125_eq));  // open: gt, lt
  Comparator #(.Bits(8)) comparator_126 (.a(out_114), .b(8'h19), .eq(comparator_126_eq));  // open: gt, lt
  Comparator #(.Bits(8)) comparator_127 (.a(out_114), .b(8'h1a), .eq(comparator_127_eq));  // open: gt, lt
  Comparator #(.Bits(8)) comparator_128 (.a(out_114), .b(8'h1b), .eq(comparator_128_eq));  // open: gt, lt
  Comparator #(.Bits(8)) comparator_129 (.a(out_114), .b(8'h40), .eq(comparator_129_eq));  // open: gt, lt
  Comparator #(.Bits(8)) comparator_130 (.a(out_114), .b(8'h41), .eq(comparator_130_eq));  // open: gt, lt
  Comparator #(.Bits(8)) comparator_131 (.a(out_114), .b(8'h42), .eq(comparator_131_eq));  // open: gt, lt
  Comparator #(.Bits(8)) comparator_132 (.a(out_114), .b(8'h43), .eq(comparator_132_eq));  // open: gt, lt
  Comparator #(.Bits(8)) comparator_133 (.a(out_114), .b(8'h68), .eq(comparator_133_eq));  // open: gt, lt
  Comparator #(.Bits(8)) comparator_134 (.a(out_114), .b(8'h69), .eq(comparator_134_eq));  // open: gt, lt
  Comparator #(.Bits(8)) comparator_135 (.a(out_114), .b(8'h6a), .eq(comparator_135_eq));  // open: gt, lt
  Comparator #(.Bits(8)) comparator_136 (.a(out_114), .b(8'h6b), .eq(comparator_136_eq));  // open: gt, lt
  Comparator #(.Bits(8)) comparator_137 (.a(out_114), .b(8'h90), .eq(comparator_137_eq));  // open: gt, lt
  Comparator #(.Bits(8)) comparator_138 (.a(out_114), .b(8'h91), .eq(comparator_138_eq));  // open: gt, lt
  Comparator #(.Bits(8)) comparator_139 (.a(out_114), .b(8'h92), .eq(comparator_139_eq));  // open: gt, lt
  Comparator #(.Bits(8)) comparator_140 (.a(out_114), .b(8'h93), .eq(comparator_140_eq));  // open: gt, lt
  Delay #(.delayTime(10)) delay_277 (.in(comparator_125_eq), .out(delay_277_out));
  Delay #(.delayTime(10)) delay_278 (.in(comparator_126_eq), .out(delay_278_out));
  Delay #(.delayTime(10)) delay_279 (.in(comparator_127_eq), .out(delay_279_out));
  Delay #(.delayTime(10)) delay_280 (.in(comparator_128_eq), .out(delay_280_out));
  Delay #(.delayTime(10)) delay_281 (.in(comparator_129_eq), .out(delay_281_out));
  Delay #(.delayTime(10)) delay_282 (.in(comparator_130_eq), .out(delay_282_out));
  Delay #(.delayTime(10)) delay_283 (.in(comparator_131_eq), .out(delay_283_out));
  Delay #(.delayTime(10)) delay_284 (.in(comparator_132_eq), .out(delay_284_out));
  Delay #(.delayTime(10)) delay_285 (.in(comparator_133_eq), .out(delay_285_out));
  Delay #(.delayTime(10)) delay_286 (.in(comparator_134_eq), .out(delay_286_out));
  Delay #(.delayTime(10)) delay_287 (.in(comparator_135_eq), .out(delay_287_out));
  Delay #(.delayTime(10)) delay_288 (.in(comparator_136_eq), .out(delay_288_out));
  Delay #(.delayTime(10)) delay_289 (.in(comparator_137_eq), .out(delay_289_out));
  Delay #(.delayTime(10)) delay_290 (.in(comparator_138_eq), .out(delay_290_out));
  Delay #(.delayTime(10)) delay_291 (.in(comparator_139_eq), .out(delay_291_out));
  Delay #(.delayTime(10)) delay_292 (.in(comparator_140_eq), .out(delay_292_out));
  Comparator #(.Bits(6)) comparator_141 (
    .a(out_119), .b(6'b000110), .gt(comparator_141_gt), .eq(comparator_141_eq), .lt(comparator_141_lt));
  Comparator #(.Bits(6)) comparator_142 (
    .a(out_119), .b(6'b010000), .gt(comparator_142_gt), .eq(comparator_142_eq), .lt(comparator_142_lt));
  Comparator #(.Bits(6)) comparator_143 (
    .a(out_119), .b(6'b100000), .gt(comparator_143_gt), .eq(comparator_143_eq), .lt(comparator_143_lt));
  Comparator #(.Bits(6)) comparator_144 (
    .a(out_119), .b(6'b101010), .gt(comparator_144_gt), .eq(comparator_144_eq), .lt(comparator_144_lt));
  Register #(.Bits(7)) register_176 (
    .D(_16_bascii_to_7_bascii_1_out), .C(delay_277_out), .en(comparator_125_eq), .Q(out_255));
  Register #(.Bits(7)) register_177 (
    .D(_16_bascii_to_7_bascii_1_out), .C(delay_278_out), .en(comparator_126_eq), .Q(register_177_q));
  Register #(.Bits(7)) register_178 (
    .D(_16_bascii_to_7_bascii_1_out), .C(delay_279_out), .en(comparator_127_eq), .Q(register_178_q));
  Register #(.Bits(7)) register_179 (
    .D(_16_bascii_to_7_bascii_1_out), .C(delay_280_out), .en(comparator_128_eq), .Q(out_256));
  Register #(.Bits(7)) register_180 (
    .D(_16_bascii_to_7_bascii_1_out), .C(delay_281_out), .en(comparator_129_eq), .Q(out_269));
  Register #(.Bits(7)) register_181 (
    .D(_16_bascii_to_7_bascii_1_out), .C(delay_282_out), .en(comparator_130_eq), .Q(register_181_q));
  Register #(.Bits(7)) register_182 (
    .D(_16_bascii_to_7_bascii_1_out), .C(delay_283_out), .en(comparator_131_eq), .Q(register_182_q));
  Register #(.Bits(7)) register_183 (
    .D(_16_bascii_to_7_bascii_1_out), .C(delay_284_out), .en(comparator_132_eq), .Q(out_270));
  Register #(.Bits(7)) register_184 (
    .D(_16_bascii_to_7_bascii_1_out), .C(delay_285_out), .en(comparator_133_eq), .Q(out_309));
  Register #(.Bits(7)) register_185 (
    .D(_16_bascii_to_7_bascii_1_out), .C(delay_286_out), .en(comparator_134_eq), .Q(register_185_q));
  Register #(.Bits(7)) register_186 (
    .D(_16_bascii_to_7_bascii_1_out), .C(delay_287_out), .en(comparator_135_eq), .Q(register_186_q));
  Register #(.Bits(7)) register_187 (
    .D(_16_bascii_to_7_bascii_1_out), .C(delay_288_out), .en(comparator_136_eq), .Q(out_310));
  Register #(.Bits(7)) register_188 (
    .D(_16_bascii_to_7_bascii_1_out), .C(delay_289_out), .en(comparator_137_eq), .Q(register_188_q));
  Register #(.Bits(7)) register_189 (
    .D(_16_bascii_to_7_bascii_1_out), .C(delay_290_out), .en(comparator_138_eq), .Q(register_189_q));
  Register #(.Bits(7)) register_190 (
    .D(_16_bascii_to_7_bascii_1_out), .C(delay_291_out), .en(comparator_139_eq), .Q(register_190_q));
  Register #(.Bits(7)) register_191 (
    .D(_16_bascii_to_7_bascii_1_out), .C(delay_292_out), .en(comparator_140_eq), .Q(register_191_q));
  Delay #(.delayTime(10)) delay_293 (.in(comparator_141_eq), .out(delay_293_out));
  Delay #(.delayTime(10)) delay_294 (.in(comparator_141_eq), .out(delay_294_out));
  Delay #(.delayTime(10)) delay_295 (.in(comparator_142_eq), .out(delay_295_out));
  Delay #(.delayTime(10)) delay_296 (.in(comparator_142_eq), .out(delay_296_out));
  Delay #(.delayTime(10)) delay_297 (.in(comparator_143_eq), .out(delay_297_out));
  Delay #(.delayTime(10)) delay_298 (.in(comparator_143_eq), .out(delay_298_out));
  Delay #(.delayTime(10)) delay_299 (.in(comparator_144_eq), .out(delay_299_out));
  Delay #(.delayTime(10)) delay_300 (.in(comparator_144_eq), .out(delay_300_out));
  vgastring vgastring_25 (
    .CX_i(vgastring_21_cx_o), .CY_i(vgastring_21_cy_o), .C_i(vgastring_21_c_o), .FG_i(vgastring_21_fg_o),
    .BG_i(vgastring_21_bg_o), .FG_c(FG_c0), .BG_c(BG_c0), .CX_c(CX_c6), .CY_c(CY_c6), .C_0(out_255),
    .C_1(register_177_q), .C_2(register_178_q), .C_3(out_256), .EN(1'b1), .CX_o(vgastring_25_cx_o),
    .CY_o(vgastring_25_cy_o), .C_o(vgastring_25_c_o), .FG_o(vgastring_25_fg_o), .BG_o(vgastring_25_bg_o));
  vgastring vgastring_26 (
    .CX_i(vgastring_22_cx_o), .CY_i(vgastring_22_cy_o), .C_i(vgastring_22_c_o), .FG_i(vgastring_22_fg_o),
    .BG_i(vgastring_22_bg_o), .FG_c(FG_c0), .BG_c(BG_c0), .CX_c(CX_c16), .CY_c(CY_c16), .C_0(out_269),
    .C_1(register_181_q), .C_2(register_182_q), .C_3(out_270), .EN(1'b1), .CX_o(vgastring_26_cx_o),
    .CY_o(vgastring_26_cy_o), .C_o(vgastring_26_c_o), .FG_o(vgastring_26_fg_o), .BG_o(vgastring_26_bg_o));
  vgastring vgastring_27 (
    .CX_i(vgastring_23_cx_o), .CY_i(vgastring_23_cy_o), .C_i(vgastring_23_c_o), .FG_i(vgastring_23_fg_o),
    .BG_i(vgastring_23_bg_o), .FG_c(FG_c0), .BG_c(BG_c0), .CX_c(CX_c26), .CY_c(CY_c26), .C_0(out_309),
    .C_1(register_185_q), .C_2(register_186_q), .C_3(out_310), .EN(1'b1), .CX_o(vgastring_27_cx_o),
    .CY_o(vgastring_27_cy_o), .C_o(vgastring_27_c_o), .FG_o(vgastring_27_fg_o), .BG_o(vgastring_27_bg_o));
  vgastring vgastring_28 (
    .CX_i(vgastring_24_cx_o), .CY_i(vgastring_24_cy_o), .C_i(vgastring_24_c_o), .FG_i(vgastring_24_fg_o),
    .BG_i(vgastring_24_bg_o), .FG_c(FG_c0), .BG_c(BG_c0), .CX_c(CX_c36), .CY_c(CY_c36), .C_0(register_188_q),
    .C_1(register_189_q), .C_2(register_190_q), .C_3(register_191_q), .EN(1'b1), .CX_o(vgastring_28_cx_o),
    .CY_o(vgastring_28_cy_o), .C_o(vgastring_28_c_o), .FG_o(vgastring_28_fg_o), .BG_o(vgastring_28_bg_o));
  Register #(.Bits(6)) register_192 (.D(pulldown_202_out[5:0]), .C(delay_293_out), .en(comparator_141_eq), .Q(CX_c6));
  Register #(.Bits(8)) register_193 (.D(pulldown_202_out[13:6]), .C(delay_294_out), .en(comparator_141_eq), .Q(CY_c6));
  Register #(.Bits(6)) register_194 (.D(pulldown_202_out[5:0]), .C(delay_295_out), .en(comparator_142_eq), .Q(CX_c16));
  Register #(.Bits(8)) register_195 (.D(pulldown_202_out[13:6]), .C(delay_296_out), .en(comparator_142_eq), .Q(CY_c16));
  Register #(.Bits(6)) register_196 (.D(pulldown_202_out[5:0]), .C(delay_297_out), .en(comparator_143_eq), .Q(CX_c26));
  Register #(.Bits(8)) register_197 (.D(pulldown_202_out[13:6]), .C(delay_298_out), .en(comparator_143_eq), .Q(CY_c26));
  Register #(.Bits(6)) register_198 (.D(pulldown_202_out[5:0]), .C(delay_299_out), .en(comparator_144_eq), .Q(CX_c36));
  Register #(.Bits(8)) register_199 (.D(pulldown_202_out[13:6]), .C(delay_300_out), .en(comparator_144_eq), .Q(CY_c36));
  Comparator #(.Bits(8)) comparator_145 (.a(out_114), .b(8'h1c), .eq(comparator_145_eq));  // open: gt, lt
  Comparator #(.Bits(8)) comparator_146 (.a(out_114), .b(8'h1d), .eq(comparator_146_eq));  // open: gt, lt
  Comparator #(.Bits(8)) comparator_147 (.a(out_114), .b(8'h1e), .eq(comparator_147_eq));  // open: gt, lt
  Comparator #(.Bits(8)) comparator_148 (.a(out_114), .b(8'h1f), .eq(comparator_148_eq));  // open: gt, lt
  Comparator #(.Bits(8)) comparator_149 (.a(out_114), .b(8'h44), .eq(comparator_149_eq));  // open: gt, lt
  Comparator #(.Bits(8)) comparator_150 (.a(out_114), .b(8'h45), .eq(comparator_150_eq));  // open: gt, lt
  Comparator #(.Bits(8)) comparator_151 (.a(out_114), .b(8'h46), .eq(comparator_151_eq));  // open: gt, lt
  Comparator #(.Bits(8)) comparator_152 (.a(out_114), .b(8'h47), .eq(comparator_152_eq));  // open: gt, lt
  Comparator #(.Bits(8)) comparator_153 (.a(out_114), .b(8'h6c), .eq(comparator_153_eq));  // open: gt, lt
  Comparator #(.Bits(8)) comparator_154 (.a(out_114), .b(8'h6d), .eq(comparator_154_eq));  // open: gt, lt
  Comparator #(.Bits(8)) comparator_155 (.a(out_114), .b(8'h6e), .eq(comparator_155_eq));  // open: gt, lt
  Comparator #(.Bits(8)) comparator_156 (.a(out_114), .b(8'h6f), .eq(comparator_156_eq));  // open: gt, lt
  Comparator #(.Bits(8)) comparator_157 (.a(out_114), .b(8'h94), .eq(comparator_157_eq));  // open: gt, lt
  Comparator #(.Bits(8)) comparator_158 (.a(out_114), .b(8'h95), .eq(comparator_158_eq));  // open: gt, lt
  Comparator #(.Bits(8)) comparator_159 (.a(out_114), .b(8'h96), .eq(comparator_159_eq));  // open: gt, lt
  Comparator #(.Bits(8)) comparator_160 (.a(out_114), .b(8'h97), .eq(comparator_160_eq));  // open: gt, lt
  Delay #(.delayTime(10)) delay_301 (.in(comparator_145_eq), .out(delay_301_out));
  Delay #(.delayTime(10)) delay_302 (.in(comparator_146_eq), .out(delay_302_out));
  Delay #(.delayTime(10)) delay_303 (.in(comparator_147_eq), .out(delay_303_out));
  Delay #(.delayTime(10)) delay_304 (.in(comparator_148_eq), .out(delay_304_out));
  Delay #(.delayTime(10)) delay_305 (.in(comparator_149_eq), .out(delay_305_out));
  Delay #(.delayTime(10)) delay_306 (.in(comparator_150_eq), .out(delay_306_out));
  Delay #(.delayTime(10)) delay_307 (.in(comparator_151_eq), .out(delay_307_out));
  Delay #(.delayTime(10)) delay_308 (.in(comparator_152_eq), .out(delay_308_out));
  Delay #(.delayTime(10)) delay_309 (.in(comparator_153_eq), .out(delay_309_out));
  Delay #(.delayTime(10)) delay_310 (.in(comparator_154_eq), .out(delay_310_out));
  Delay #(.delayTime(10)) delay_311 (.in(comparator_155_eq), .out(delay_311_out));
  Delay #(.delayTime(10)) delay_312 (.in(comparator_156_eq), .out(delay_312_out));
  Delay #(.delayTime(10)) delay_313 (.in(comparator_157_eq), .out(delay_313_out));
  Delay #(.delayTime(10)) delay_314 (.in(comparator_158_eq), .out(delay_314_out));
  Delay #(.delayTime(10)) delay_315 (.in(comparator_159_eq), .out(delay_315_out));
  Delay #(.delayTime(10)) delay_316 (.in(comparator_160_eq), .out(delay_316_out));
  Comparator #(.Bits(6)) comparator_161 (
    .a(out_119), .b(6'b000111), .gt(comparator_161_gt), .eq(comparator_161_eq), .lt(comparator_161_lt));
  Comparator #(.Bits(6)) comparator_162 (
    .a(out_119), .b(6'b010001), .gt(comparator_162_gt), .eq(comparator_162_eq), .lt(comparator_162_lt));
  Comparator #(.Bits(6)) comparator_163 (
    .a(out_119), .b(6'b100001), .gt(comparator_163_gt), .eq(comparator_163_eq), .lt(comparator_163_lt));
  Comparator #(.Bits(6)) comparator_164 (
    .a(out_119), .b(6'b101011), .gt(comparator_164_gt), .eq(comparator_164_eq), .lt(comparator_164_lt));
  Register #(.Bits(7)) register_200 (
    .D(_16_bascii_to_7_bascii_1_out), .C(delay_301_out), .en(comparator_145_eq), .Q(out_257));
  Register #(.Bits(7)) register_201 (
    .D(_16_bascii_to_7_bascii_1_out), .C(delay_302_out), .en(comparator_146_eq), .Q(register_201_q));
  Register #(.Bits(7)) register_202 (
    .D(_16_bascii_to_7_bascii_1_out), .C(delay_303_out), .en(comparator_147_eq), .Q(register_202_q));
  Register #(.Bits(7)) register_203 (
    .D(_16_bascii_to_7_bascii_1_out), .C(delay_304_out), .en(comparator_148_eq), .Q(out_258));
  Register #(.Bits(7)) register_204 (
    .D(_16_bascii_to_7_bascii_1_out), .C(delay_305_out), .en(comparator_149_eq), .Q(out_267));
  Register #(.Bits(7)) register_205 (
    .D(_16_bascii_to_7_bascii_1_out), .C(delay_306_out), .en(comparator_150_eq), .Q(register_205_q));
  Register #(.Bits(7)) register_206 (
    .D(_16_bascii_to_7_bascii_1_out), .C(delay_307_out), .en(comparator_151_eq), .Q(register_206_q));
  Register #(.Bits(7)) register_207 (
    .D(_16_bascii_to_7_bascii_1_out), .C(delay_308_out), .en(comparator_152_eq), .Q(out_268));
  Register #(.Bits(7)) register_208 (
    .D(_16_bascii_to_7_bascii_1_out), .C(delay_309_out), .en(comparator_153_eq), .Q(out_307));
  Register #(.Bits(7)) register_209 (
    .D(_16_bascii_to_7_bascii_1_out), .C(delay_310_out), .en(comparator_154_eq), .Q(register_209_q));
  Register #(.Bits(7)) register_210 (
    .D(_16_bascii_to_7_bascii_1_out), .C(delay_311_out), .en(comparator_155_eq), .Q(register_210_q));
  Register #(.Bits(7)) register_211 (
    .D(_16_bascii_to_7_bascii_1_out), .C(delay_312_out), .en(comparator_156_eq), .Q(out_308));
  Register #(.Bits(7)) register_212 (
    .D(_16_bascii_to_7_bascii_1_out), .C(delay_313_out), .en(comparator_157_eq), .Q(out_297));
  Register #(.Bits(7)) register_213 (
    .D(_16_bascii_to_7_bascii_1_out), .C(delay_314_out), .en(comparator_158_eq), .Q(register_213_q));
  Register #(.Bits(7)) register_214 (
    .D(_16_bascii_to_7_bascii_1_out), .C(delay_315_out), .en(comparator_159_eq), .Q(register_214_q));
  Register #(.Bits(7)) register_215 (
    .D(_16_bascii_to_7_bascii_1_out), .C(delay_316_out), .en(comparator_160_eq), .Q(out_298));
  Delay #(.delayTime(10)) delay_317 (.in(comparator_161_eq), .out(delay_317_out));
  Delay #(.delayTime(10)) delay_318 (.in(comparator_161_eq), .out(delay_318_out));
  Delay #(.delayTime(10)) delay_319 (.in(comparator_162_eq), .out(delay_319_out));
  Delay #(.delayTime(10)) delay_320 (.in(comparator_162_eq), .out(delay_320_out));
  Delay #(.delayTime(10)) delay_321 (.in(comparator_163_eq), .out(delay_321_out));
  Delay #(.delayTime(10)) delay_322 (.in(comparator_163_eq), .out(delay_322_out));
  Delay #(.delayTime(10)) delay_323 (.in(comparator_164_eq), .out(delay_323_out));
  Delay #(.delayTime(10)) delay_324 (.in(comparator_164_eq), .out(delay_324_out));
  vgastring vgastring_29 (
    .CX_i(vgastring_25_cx_o), .CY_i(vgastring_25_cy_o), .C_i(vgastring_25_c_o), .FG_i(vgastring_25_fg_o),
    .BG_i(vgastring_25_bg_o), .FG_c(FG_c0), .BG_c(BG_c0), .CX_c(CX_c7), .CY_c(CY_c7), .C_0(out_257),
    .C_1(register_201_q), .C_2(register_202_q), .C_3(out_258), .EN(1'b1), .CX_o(vgastring_29_cx_o),
    .CY_o(vgastring_29_cy_o), .C_o(vgastring_29_c_o), .FG_o(vgastring_29_fg_o), .BG_o(vgastring_29_bg_o));
  vgastring vgastring_30 (
    .CX_i(vgastring_26_cx_o), .CY_i(vgastring_26_cy_o), .C_i(vgastring_26_c_o), .FG_i(vgastring_26_fg_o),
    .BG_i(vgastring_26_bg_o), .FG_c(FG_c0), .BG_c(BG_c0), .CX_c(CX_c17), .CY_c(CY_c17), .C_0(out_267),
    .C_1(register_205_q), .C_2(register_206_q), .C_3(out_268), .EN(1'b1), .CX_o(vgastring_30_cx_o),
    .CY_o(vgastring_30_cy_o), .C_o(vgastring_30_c_o), .FG_o(vgastring_30_fg_o), .BG_o(vgastring_30_bg_o));
  vgastring vgastring_31 (
    .CX_i(vgastring_27_cx_o), .CY_i(vgastring_27_cy_o), .C_i(vgastring_27_c_o), .FG_i(vgastring_27_fg_o),
    .BG_i(vgastring_27_bg_o), .FG_c(FG_c0), .BG_c(BG_c0), .CX_c(CX_c27), .CY_c(CY_c27), .C_0(out_307),
    .C_1(register_209_q), .C_2(register_210_q), .C_3(out_308), .EN(1'b1), .CX_o(vgastring_31_cx_o),
    .CY_o(vgastring_31_cy_o), .C_o(vgastring_31_c_o), .FG_o(vgastring_31_fg_o), .BG_o(vgastring_31_bg_o));
  vgastring vgastring_32 (
    .CX_i(vgastring_28_cx_o), .CY_i(vgastring_28_cy_o), .C_i(vgastring_28_c_o), .FG_i(vgastring_28_fg_o),
    .BG_i(vgastring_28_bg_o), .FG_c(FG_c0), .BG_c(BG_c0), .CX_c(CX_c37), .CY_c(CY_c37), .C_0(out_297),
    .C_1(register_213_q), .C_2(register_214_q), .C_3(out_298), .EN(1'b1), .CX_o(vgastring_32_cx_o),
    .CY_o(vgastring_32_cy_o), .C_o(vgastring_32_c_o), .FG_o(vgastring_32_fg_o), .BG_o(vgastring_32_bg_o));
  Register #(.Bits(6)) register_216 (.D(pulldown_202_out[5:0]), .C(delay_317_out), .en(comparator_161_eq), .Q(CX_c7));
  Register #(.Bits(8)) register_217 (.D(pulldown_202_out[13:6]), .C(delay_318_out), .en(comparator_161_eq), .Q(CY_c7));
  Register #(.Bits(6)) register_218 (.D(pulldown_202_out[5:0]), .C(delay_319_out), .en(comparator_162_eq), .Q(CX_c17));
  Register #(.Bits(8)) register_219 (.D(pulldown_202_out[13:6]), .C(delay_320_out), .en(comparator_162_eq), .Q(CY_c17));
  Register #(.Bits(6)) register_220 (.D(pulldown_202_out[5:0]), .C(delay_321_out), .en(comparator_163_eq), .Q(CX_c27));
  Register #(.Bits(8)) register_221 (.D(pulldown_202_out[13:6]), .C(delay_322_out), .en(comparator_163_eq), .Q(CY_c27));
  Register #(.Bits(6)) register_222 (.D(pulldown_202_out[5:0]), .C(delay_323_out), .en(comparator_164_eq), .Q(CX_c37));
  Register #(.Bits(8)) register_223 (.D(pulldown_202_out[13:6]), .C(delay_324_out), .en(comparator_164_eq), .Q(CY_c37));
  Comparator #(.Bits(8)) comparator_165 (.a(out_114), .b(8'h20), .eq(comparator_165_eq));  // open: gt, lt
  Comparator #(.Bits(8)) comparator_166 (.a(out_114), .b(8'h21), .eq(comparator_166_eq));  // open: gt, lt
  Comparator #(.Bits(8)) comparator_167 (.a(out_114), .b(8'h22), .eq(comparator_167_eq));  // open: gt, lt
  Comparator #(.Bits(8)) comparator_168 (.a(out_114), .b(8'h23), .eq(comparator_168_eq));  // open: gt, lt
  Comparator #(.Bits(8)) comparator_169 (.a(out_114), .b(8'h48), .eq(comparator_169_eq));  // open: gt, lt
  Comparator #(.Bits(8)) comparator_170 (.a(out_114), .b(8'h49), .eq(comparator_170_eq));  // open: gt, lt
  Comparator #(.Bits(8)) comparator_171 (.a(out_114), .b(8'h4a), .eq(comparator_171_eq));  // open: gt, lt
  Comparator #(.Bits(8)) comparator_172 (.a(out_114), .b(8'h4b), .eq(comparator_172_eq));  // open: gt, lt
  Comparator #(.Bits(8)) comparator_173 (.a(out_114), .b(8'h70), .eq(comparator_173_eq));  // open: gt, lt
  Comparator #(.Bits(8)) comparator_174 (.a(out_114), .b(8'h71), .eq(comparator_174_eq));  // open: gt, lt
  Comparator #(.Bits(8)) comparator_175 (.a(out_114), .b(8'h72), .eq(comparator_175_eq));  // open: gt, lt
  Comparator #(.Bits(8)) comparator_176 (.a(out_114), .b(8'h73), .eq(comparator_176_eq));  // open: gt, lt
  Comparator #(.Bits(8)) comparator_177 (.a(out_114), .b(8'h98), .eq(comparator_177_eq));  // open: gt, lt
  Comparator #(.Bits(8)) comparator_178 (.a(out_114), .b(8'h99), .eq(comparator_178_eq));  // open: gt, lt
  Comparator #(.Bits(8)) comparator_179 (.a(out_114), .b(8'h9a), .eq(comparator_179_eq));  // open: gt, lt
  Comparator #(.Bits(8)) comparator_180 (.a(out_114), .b(8'h9b), .eq(comparator_180_eq));  // open: gt, lt
  Delay #(.delayTime(10)) delay_325 (.in(comparator_165_eq), .out(delay_325_out));
  Delay #(.delayTime(10)) delay_326 (.in(comparator_166_eq), .out(delay_326_out));
  Delay #(.delayTime(10)) delay_327 (.in(comparator_167_eq), .out(delay_327_out));
  Delay #(.delayTime(10)) delay_328 (.in(comparator_168_eq), .out(delay_328_out));
  Delay #(.delayTime(10)) delay_329 (.in(comparator_169_eq), .out(delay_329_out));
  Delay #(.delayTime(10)) delay_330 (.in(comparator_170_eq), .out(delay_330_out));
  Delay #(.delayTime(10)) delay_331 (.in(comparator_171_eq), .out(delay_331_out));
  Delay #(.delayTime(10)) delay_332 (.in(comparator_172_eq), .out(delay_332_out));
  Delay #(.delayTime(10)) delay_333 (.in(comparator_173_eq), .out(delay_333_out));
  Delay #(.delayTime(10)) delay_334 (.in(comparator_174_eq), .out(delay_334_out));
  Delay #(.delayTime(10)) delay_335 (.in(comparator_175_eq), .out(delay_335_out));
  Delay #(.delayTime(10)) delay_336 (.in(comparator_176_eq), .out(delay_336_out));
  Delay #(.delayTime(10)) delay_337 (.in(comparator_177_eq), .out(delay_337_out));
  Delay #(.delayTime(10)) delay_338 (.in(comparator_178_eq), .out(delay_338_out));
  Delay #(.delayTime(10)) delay_339 (.in(comparator_179_eq), .out(delay_339_out));
  Delay #(.delayTime(10)) delay_340 (.in(comparator_180_eq), .out(delay_340_out));
  Comparator #(.Bits(6)) comparator_181 (
    .a(out_119), .b(6'b001000), .gt(comparator_181_gt), .eq(comparator_181_eq), .lt(comparator_181_lt));
  Comparator #(.Bits(6)) comparator_182 (
    .a(out_119), .b(6'b010010), .gt(comparator_182_gt), .eq(comparator_182_eq), .lt(comparator_182_lt));
  Comparator #(.Bits(6)) comparator_183 (
    .a(out_119), .b(6'b100010), .gt(comparator_183_gt), .eq(comparator_183_eq), .lt(comparator_183_lt));
  Comparator #(.Bits(6)) comparator_184 (
    .a(out_119), .b(6'b101100), .gt(comparator_184_gt), .eq(comparator_184_eq), .lt(comparator_184_lt));
  Register #(.Bits(7)) register_224 (
    .D(_16_bascii_to_7_bascii_1_out), .C(delay_325_out), .en(comparator_165_eq), .Q(out_259));
  Register #(.Bits(7)) register_225 (
    .D(_16_bascii_to_7_bascii_1_out), .C(delay_326_out), .en(comparator_166_eq), .Q(register_225_q));
  Register #(.Bits(7)) register_226 (
    .D(_16_bascii_to_7_bascii_1_out), .C(delay_327_out), .en(comparator_167_eq), .Q(register_226_q));
  Register #(.Bits(7)) register_227 (
    .D(_16_bascii_to_7_bascii_1_out), .C(delay_328_out), .en(comparator_168_eq), .Q(out_260));
  Register #(.Bits(7)) register_228 (
    .D(_16_bascii_to_7_bascii_1_out), .C(delay_329_out), .en(comparator_169_eq), .Q(out_265));
  Register #(.Bits(7)) register_229 (
    .D(_16_bascii_to_7_bascii_1_out), .C(delay_330_out), .en(comparator_170_eq), .Q(register_229_q));
  Register #(.Bits(7)) register_230 (
    .D(_16_bascii_to_7_bascii_1_out), .C(delay_331_out), .en(comparator_171_eq), .Q(register_230_q));
  Register #(.Bits(7)) register_231 (
    .D(_16_bascii_to_7_bascii_1_out), .C(delay_332_out), .en(comparator_172_eq), .Q(out_266));
  Register #(.Bits(7)) register_232 (
    .D(_16_bascii_to_7_bascii_1_out), .C(delay_333_out), .en(comparator_173_eq), .Q(out_305));
  Register #(.Bits(7)) register_233 (
    .D(_16_bascii_to_7_bascii_1_out), .C(delay_334_out), .en(comparator_174_eq), .Q(register_233_q));
  Register #(.Bits(7)) register_234 (
    .D(_16_bascii_to_7_bascii_1_out), .C(delay_335_out), .en(comparator_175_eq), .Q(register_234_q));
  Register #(.Bits(7)) register_235 (
    .D(_16_bascii_to_7_bascii_1_out), .C(delay_336_out), .en(comparator_176_eq), .Q(out_306));
  Register #(.Bits(7)) register_236 (
    .D(_16_bascii_to_7_bascii_1_out), .C(delay_337_out), .en(comparator_177_eq), .Q(out_299));
  Register #(.Bits(7)) register_237 (
    .D(_16_bascii_to_7_bascii_1_out), .C(delay_338_out), .en(comparator_178_eq), .Q(register_237_q));
  Register #(.Bits(7)) register_238 (
    .D(_16_bascii_to_7_bascii_1_out), .C(delay_339_out), .en(comparator_179_eq), .Q(register_238_q));
  Register #(.Bits(7)) register_239 (
    .D(_16_bascii_to_7_bascii_1_out), .C(delay_340_out), .en(comparator_180_eq), .Q(out_300));
  Delay #(.delayTime(10)) delay_341 (.in(comparator_181_eq), .out(delay_341_out));
  Delay #(.delayTime(10)) delay_342 (.in(comparator_181_eq), .out(delay_342_out));
  Delay #(.delayTime(10)) delay_343 (.in(comparator_182_eq), .out(delay_343_out));
  Delay #(.delayTime(10)) delay_344 (.in(comparator_182_eq), .out(delay_344_out));
  Delay #(.delayTime(10)) delay_345 (.in(comparator_183_eq), .out(delay_345_out));
  Delay #(.delayTime(10)) delay_346 (.in(comparator_183_eq), .out(delay_346_out));
  Delay #(.delayTime(10)) delay_347 (.in(comparator_184_eq), .out(delay_347_out));
  Delay #(.delayTime(10)) delay_348 (.in(comparator_184_eq), .out(delay_348_out));
  vgastring vgastring_33 (
    .CX_i(vgastring_29_cx_o), .CY_i(vgastring_29_cy_o), .C_i(vgastring_29_c_o), .FG_i(vgastring_29_fg_o),
    .BG_i(vgastring_29_bg_o), .FG_c(FG_c0), .BG_c(BG_c0), .CX_c(CX_c8), .CY_c(CY_c8), .C_0(out_259),
    .C_1(register_225_q), .C_2(register_226_q), .C_3(out_260), .EN(1'b1), .CX_o(vgastring_33_cx_o),
    .CY_o(vgastring_33_cy_o), .C_o(vgastring_33_c_o), .FG_o(vgastring_33_fg_o), .BG_o(vgastring_33_bg_o));
  vgastring vgastring_34 (
    .CX_i(vgastring_30_cx_o), .CY_i(vgastring_30_cy_o), .C_i(vgastring_30_c_o), .FG_i(vgastring_30_fg_o),
    .BG_i(vgastring_30_bg_o), .FG_c(FG_c0), .BG_c(BG_c0), .CX_c(CX_c18), .CY_c(CY_c18), .C_0(out_265),
    .C_1(register_229_q), .C_2(register_230_q), .C_3(out_266), .EN(1'b1), .CX_o(vgastring_34_cx_o),
    .CY_o(vgastring_34_cy_o), .C_o(vgastring_34_c_o), .FG_o(vgastring_34_fg_o), .BG_o(vgastring_34_bg_o));
  vgastring vgastring_35 (
    .CX_i(vgastring_31_cx_o), .CY_i(vgastring_31_cy_o), .C_i(vgastring_31_c_o), .FG_i(vgastring_31_fg_o),
    .BG_i(vgastring_31_bg_o), .FG_c(FG_c0), .BG_c(BG_c0), .CX_c(CX_c28), .CY_c(CY_c28), .C_0(out_305),
    .C_1(register_233_q), .C_2(register_234_q), .C_3(out_306), .EN(1'b1), .CX_o(vgastring_35_cx_o),
    .CY_o(vgastring_35_cy_o), .C_o(vgastring_35_c_o), .FG_o(vgastring_35_fg_o), .BG_o(vgastring_35_bg_o));
  vgastring vgastring_36 (
    .CX_i(vgastring_32_cx_o), .CY_i(vgastring_32_cy_o), .C_i(vgastring_32_c_o), .FG_i(vgastring_32_fg_o),
    .BG_i(vgastring_32_bg_o), .FG_c(FG_c0), .BG_c(BG_c0), .CX_c(CX_c38), .CY_c(CY_c38), .C_0(out_299),
    .C_1(register_237_q), .C_2(register_238_q), .C_3(out_300), .EN(1'b1), .CX_o(vgastring_36_cx_o),
    .CY_o(vgastring_36_cy_o), .C_o(vgastring_36_c_o), .FG_o(vgastring_36_fg_o), .BG_o(vgastring_36_bg_o));
  Register #(.Bits(6)) register_240 (.D(pulldown_202_out[5:0]), .C(delay_341_out), .en(comparator_181_eq), .Q(CX_c8));
  Register #(.Bits(8)) register_241 (.D(pulldown_202_out[13:6]), .C(delay_342_out), .en(comparator_181_eq), .Q(CY_c8));
  Register #(.Bits(6)) register_242 (.D(pulldown_202_out[5:0]), .C(delay_343_out), .en(comparator_182_eq), .Q(CX_c18));
  Register #(.Bits(8)) register_243 (.D(pulldown_202_out[13:6]), .C(delay_344_out), .en(comparator_182_eq), .Q(CY_c18));
  Register #(.Bits(6)) register_244 (.D(pulldown_202_out[5:0]), .C(delay_345_out), .en(comparator_183_eq), .Q(CX_c28));
  Register #(.Bits(8)) register_245 (.D(pulldown_202_out[13:6]), .C(delay_346_out), .en(comparator_183_eq), .Q(CY_c28));
  Register #(.Bits(6)) register_246 (.D(pulldown_202_out[5:0]), .C(delay_347_out), .en(comparator_184_eq), .Q(CX_c38));
  Register #(.Bits(8)) register_247 (.D(pulldown_202_out[13:6]), .C(delay_348_out), .en(comparator_184_eq), .Q(CY_c38));
  Comparator #(.Bits(8)) comparator_185 (.a(out_114), .b(8'h24), .eq(comparator_185_eq));  // open: gt, lt
  Comparator #(.Bits(8)) comparator_186 (.a(out_114), .b(8'h25), .eq(comparator_186_eq));  // open: gt, lt
  Comparator #(.Bits(8)) comparator_187 (.a(out_114), .b(8'h26), .eq(comparator_187_eq));  // open: gt, lt
  Comparator #(.Bits(8)) comparator_188 (.a(out_114), .b(8'h27), .eq(comparator_188_eq));  // open: gt, lt
  Comparator #(.Bits(8)) comparator_189 (.a(out_114), .b(8'h4c), .eq(comparator_189_eq));  // open: gt, lt
  Comparator #(.Bits(8)) comparator_190 (.a(out_114), .b(8'h4d), .eq(comparator_190_eq));  // open: gt, lt
  Comparator #(.Bits(8)) comparator_191 (.a(out_114), .b(8'h4e), .eq(comparator_191_eq));  // open: gt, lt
  Comparator #(.Bits(8)) comparator_192 (.a(out_114), .b(8'h4f), .eq(comparator_192_eq));  // open: gt, lt
  Comparator #(.Bits(8)) comparator_193 (.a(out_114), .b(8'h74), .eq(comparator_193_eq));  // open: gt, lt
  Comparator #(.Bits(8)) comparator_194 (.a(out_114), .b(8'h75), .eq(comparator_194_eq));  // open: gt, lt
  Comparator #(.Bits(8)) comparator_195 (.a(out_114), .b(8'h76), .eq(comparator_195_eq));  // open: gt, lt
  Comparator #(.Bits(8)) comparator_196 (.a(out_114), .b(8'h77), .eq(comparator_196_eq));  // open: gt, lt
  Comparator #(.Bits(8)) comparator_197 (.a(out_114), .b(8'h9c), .eq(comparator_197_eq));  // open: gt, lt
  Comparator #(.Bits(8)) comparator_198 (.a(out_114), .b(8'h9d), .eq(comparator_198_eq));  // open: gt, lt
  Comparator #(.Bits(8)) comparator_199 (.a(out_114), .b(8'h9e), .eq(comparator_199_eq));  // open: gt, lt
  Comparator #(.Bits(8)) comparator_200 (.a(out_114), .b(8'h9f), .eq(comparator_200_eq));  // open: gt, lt
  Delay #(.delayTime(10)) delay_349 (.in(comparator_185_eq), .out(delay_349_out));
  Delay #(.delayTime(10)) delay_350 (.in(comparator_186_eq), .out(delay_350_out));
  Delay #(.delayTime(10)) delay_351 (.in(comparator_187_eq), .out(delay_351_out));
  Delay #(.delayTime(10)) delay_352 (.in(comparator_188_eq), .out(delay_352_out));
  Delay #(.delayTime(10)) delay_353 (.in(comparator_189_eq), .out(delay_353_out));
  Delay #(.delayTime(10)) delay_354 (.in(comparator_190_eq), .out(delay_354_out));
  Delay #(.delayTime(10)) delay_355 (.in(comparator_191_eq), .out(delay_355_out));
  Delay #(.delayTime(10)) delay_356 (.in(comparator_192_eq), .out(delay_356_out));
  Delay #(.delayTime(10)) delay_357 (.in(comparator_193_eq), .out(delay_357_out));
  Delay #(.delayTime(10)) delay_358 (.in(comparator_194_eq), .out(delay_358_out));
  Delay #(.delayTime(10)) delay_359 (.in(comparator_195_eq), .out(delay_359_out));
  Delay #(.delayTime(10)) delay_360 (.in(comparator_196_eq), .out(delay_360_out));
  Delay #(.delayTime(10)) delay_361 (.in(comparator_197_eq), .out(delay_361_out));
  Delay #(.delayTime(10)) delay_362 (.in(comparator_198_eq), .out(delay_362_out));
  Delay #(.delayTime(10)) delay_363 (.in(comparator_199_eq), .out(delay_363_out));
  Delay #(.delayTime(10)) delay_364 (.in(comparator_200_eq), .out(delay_364_out));
  Comparator #(.Bits(6)) comparator_201 (
    .a(out_119), .b(6'b001001), .gt(comparator_201_gt), .eq(comparator_201_eq), .lt(comparator_201_lt));
  Comparator #(.Bits(6)) comparator_202 (
    .a(out_119), .b(6'b010011), .gt(comparator_202_gt), .eq(comparator_202_eq), .lt(comparator_202_lt));
  Comparator #(.Bits(6)) comparator_203 (
    .a(out_119), .b(6'b100011), .gt(comparator_203_gt), .eq(comparator_203_eq), .lt(comparator_203_lt));
  Comparator #(.Bits(6)) comparator_204 (
    .a(out_119), .b(6'b101101), .gt(comparator_204_gt), .eq(comparator_204_eq), .lt(comparator_204_lt));
  Register #(.Bits(7)) register_248 (
    .D(_16_bascii_to_7_bascii_1_out), .C(delay_349_out), .en(comparator_185_eq), .Q(out_261));
  Register #(.Bits(7)) register_249 (
    .D(_16_bascii_to_7_bascii_1_out), .C(delay_350_out), .en(comparator_186_eq), .Q(register_249_q));
  Register #(.Bits(7)) register_250 (
    .D(_16_bascii_to_7_bascii_1_out), .C(delay_351_out), .en(comparator_187_eq), .Q(register_250_q));
  Register #(.Bits(7)) register_251 (
    .D(_16_bascii_to_7_bascii_1_out), .C(delay_352_out), .en(comparator_188_eq), .Q(out_262));
  Register #(.Bits(7)) register_252 (
    .D(_16_bascii_to_7_bascii_1_out), .C(delay_353_out), .en(comparator_189_eq), .Q(out_263));
  Register #(.Bits(7)) register_253 (
    .D(_16_bascii_to_7_bascii_1_out), .C(delay_354_out), .en(comparator_190_eq), .Q(register_253_q));
  Register #(.Bits(7)) register_254 (
    .D(_16_bascii_to_7_bascii_1_out), .C(delay_355_out), .en(comparator_191_eq), .Q(register_254_q));
  Register #(.Bits(7)) register_255 (
    .D(_16_bascii_to_7_bascii_1_out), .C(delay_356_out), .en(comparator_192_eq), .Q(out_264));
  Register #(.Bits(7)) register_256 (
    .D(_16_bascii_to_7_bascii_1_out), .C(delay_357_out), .en(comparator_193_eq), .Q(out_303));
  Register #(.Bits(7)) register_257 (
    .D(_16_bascii_to_7_bascii_1_out), .C(delay_358_out), .en(comparator_194_eq), .Q(register_257_q));
  Register #(.Bits(7)) register_258 (
    .D(_16_bascii_to_7_bascii_1_out), .C(delay_359_out), .en(comparator_195_eq), .Q(register_258_q));
  Register #(.Bits(7)) register_259 (
    .D(_16_bascii_to_7_bascii_1_out), .C(delay_360_out), .en(comparator_196_eq), .Q(out_304));
  Register #(.Bits(7)) register_260 (
    .D(_16_bascii_to_7_bascii_1_out), .C(delay_361_out), .en(comparator_197_eq), .Q(out_301));
  Register #(.Bits(7)) register_261 (
    .D(_16_bascii_to_7_bascii_1_out), .C(delay_362_out), .en(comparator_198_eq), .Q(register_261_q));
  Register #(.Bits(7)) register_262 (
    .D(_16_bascii_to_7_bascii_1_out), .C(delay_363_out), .en(comparator_199_eq), .Q(register_262_q));
  Register #(.Bits(7)) register_263 (
    .D(_16_bascii_to_7_bascii_1_out), .C(delay_364_out), .en(comparator_200_eq), .Q(out_302));
  Delay #(.delayTime(10)) delay_365 (.in(comparator_201_eq), .out(delay_365_out));
  Delay #(.delayTime(10)) delay_366 (.in(comparator_201_eq), .out(delay_366_out));
  Delay #(.delayTime(10)) delay_367 (.in(comparator_202_eq), .out(delay_367_out));
  Delay #(.delayTime(10)) delay_368 (.in(comparator_202_eq), .out(delay_368_out));
  Delay #(.delayTime(10)) delay_369 (.in(comparator_203_eq), .out(delay_369_out));
  Delay #(.delayTime(10)) delay_370 (.in(comparator_203_eq), .out(delay_370_out));
  Delay #(.delayTime(10)) delay_371 (.in(comparator_204_eq), .out(delay_371_out));
  Delay #(.delayTime(10)) delay_372 (.in(comparator_204_eq), .out(delay_372_out));
  vgastring vgastring_37 (
    .CX_i(vgastring_33_cx_o), .CY_i(vgastring_33_cy_o), .C_i(vgastring_33_c_o), .FG_i(vgastring_33_fg_o),
    .BG_i(vgastring_33_bg_o), .FG_c(FG_c0), .BG_c(BG_c0), .CX_c(CX_c9), .CY_c(CY_c9), .C_0(out_261),
    .C_1(register_249_q), .C_2(register_250_q), .C_3(out_262), .EN(1'b1), .CX_o(vgastring_37_cx_o),
    .CY_o(vgastring_37_cy_o), .C_o(vgastring_37_c_o), .FG_o(vgastring_37_fg_o), .BG_o(vgastring_37_bg_o));
  vgastring vgastring_38 (
    .CX_i(vgastring_34_cx_o), .CY_i(vgastring_34_cy_o), .C_i(vgastring_34_c_o), .FG_i(vgastring_34_fg_o),
    .BG_i(vgastring_34_bg_o), .FG_c(FG_c0), .BG_c(BG_c0), .CX_c(CX_c19), .CY_c(CY_c19), .C_0(out_263),
    .C_1(register_253_q), .C_2(register_254_q), .C_3(out_264), .EN(1'b1), .CX_o(vgastring_38_cx_o),
    .CY_o(vgastring_38_cy_o), .C_o(vgastring_38_c_o), .FG_o(vgastring_38_fg_o), .BG_o(vgastring_38_bg_o));
  vgastring vgastring_39 (
    .CX_i(vgastring_35_cx_o), .CY_i(vgastring_35_cy_o), .C_i(vgastring_35_c_o), .FG_i(vgastring_35_fg_o),
    .BG_i(vgastring_35_bg_o), .FG_c(FG_c0), .BG_c(BG_c0), .CX_c(CX_c29), .CY_c(CY_c29), .C_0(out_303),
    .C_1(register_257_q), .C_2(register_258_q), .C_3(out_304), .EN(1'b1), .CX_o(vgastring_39_cx_o),
    .CY_o(vgastring_39_cy_o), .C_o(vgastring_39_c_o), .FG_o(vgastring_39_fg_o), .BG_o(vgastring_39_bg_o));
  vgastring vgastring_40 (
    .CX_i(vgastring_36_cx_o), .CY_i(vgastring_36_cy_o), .C_i(vgastring_36_c_o), .FG_i(vgastring_36_fg_o),
    .BG_i(vgastring_36_bg_o), .FG_c(FG_c0), .BG_c(BG_c0), .CX_c(CX_c39), .CY_c(CY_c39), .C_0(out_301),
    .C_1(register_261_q), .C_2(register_262_q), .C_3(out_302), .EN(1'b1), .CX_o(vgastring_40_cx_o),
    .CY_o(vgastring_40_cy_o), .C_o(vgastring_40_c_o), .FG_o(vgastring_40_fg_o), .BG_o(vgastring_40_bg_o));
  Register #(.Bits(6)) register_264 (.D(pulldown_202_out[5:0]), .C(delay_365_out), .en(comparator_201_eq), .Q(CX_c9));
  Register #(.Bits(8)) register_265 (.D(pulldown_202_out[13:6]), .C(delay_366_out), .en(comparator_201_eq), .Q(CY_c9));
  Register #(.Bits(6)) register_266 (.D(pulldown_202_out[5:0]), .C(delay_367_out), .en(comparator_202_eq), .Q(CX_c19));
  Register #(.Bits(8)) register_267 (.D(pulldown_202_out[13:6]), .C(delay_368_out), .en(comparator_202_eq), .Q(CY_c19));
  Register #(.Bits(6)) register_268 (.D(pulldown_202_out[5:0]), .C(delay_369_out), .en(comparator_203_eq), .Q(CX_c29));
  Register #(.Bits(8)) register_269 (.D(pulldown_202_out[13:6]), .C(delay_370_out), .en(comparator_203_eq), .Q(CY_c29));
  Register #(.Bits(6)) register_270 (.D(pulldown_202_out[5:0]), .C(delay_371_out), .en(comparator_204_eq), .Q(CX_c39));
  Register #(.Bits(8)) register_271 (.D(pulldown_202_out[13:6]), .C(delay_372_out), .en(comparator_204_eq), .Q(CY_c39));
  // vgatext vgatext_1: pin names not known; wires that end beside it: vgasync_1_h, vgasync_1_v, vgasync_1_pic, vgacharpos_1_p3, vgacharpos_1_p4, vgatext_1_p6, VGA_C, vgastring_40_c_o, vgastring_40_fg_o, vgastring_40_bg_o, R, G, B, hs, vs, de, CA
  ROM #(.AddrBits(11), .Bits(16)) Char_ROM (.A(CA), .sel(1'b1), .D(Char_ROM_d));
  D_FF #(.Bits(16)) d_ff_15 (.D(Char_ROM_d), .C(VGA_C), .Q(vgatext_1_p6));  // open: nQ
  VGA vga_1 (.R(R), .G(G), .B(B), .H(hs), .V(vs), .C(VGA_C));

  assign f1_16384 = CLK1;
  assign out_47 = out_46[24];
  assign out_48 = out_46[23:8];
  assign out_49 = out_46[7:0];
  assign out_83 = {in_82, in_66, in_67, in_68, in_69, in_70, in_71, in_72, in_73, in_74, in_75, in_76, in_77, in_78, in_79, in_80, in_81, in_58, in_59, in_60, in_61, in_62, in_63, in_64, in_65};
  assign out_100 = {in_58, in_59, in_60, in_61, in_62, in_63, in_64, in_65};
  assign out_101 = {in_66, in_67, in_68, in_69, in_70, in_71, in_72, in_73, in_74, in_75, in_76, in_77, in_78, in_79, in_80, in_81};
  assign out_122[7] = out_121;
  assign out_126 = X[7:6];
  assign out_127 = X[5:0];
  assign out_128 = Y;
  assign out_129 = {Y, X[5:0]};
  assign out_130 = in_155[7];
  assign out_131 = in_155[24];
  assign out_132 = in_155[6];
  assign out_133 = in_155[5];
  assign out_134 = in_155[4];
  assign out_135 = in_155[3];
  assign out_136 = in_155[2];
  assign out_137 = in_155[1];
  assign out_138 = in_155[0];
  assign out_139 = in_155[23];
  assign out_140 = in_155[22];
  assign out_141 = in_155[21];
  assign out_142 = in_155[20];
  assign out_143 = in_155[19];
  assign out_144 = in_155[18];
  assign out_145 = in_155[17];
  assign out_146 = in_155[16];
  assign out_147 = in_155[15];
  assign out_148 = in_155[14];
  assign out_149 = in_155[13];
  assign out_150 = in_155[12];
  assign out_151 = in_155[11];
  assign out_152 = in_155[10];
  assign out_153 = in_155[9];
  assign out_154 = in_155[8];
  assign out_165 = out_162[15:7];
  assign out_167 = out_162[15:7];
  assign out_184 = {in_176, in_177, in_178, in_179, in_180, in_181, in_182, in_183, in_185, in_186, in_187, in_188, in_189, in_190, in_191, in_192};
  assign out_193 = {in_194, in_195, in_196, in_197, in_198, in_199, in_200, in_201};
  assign out_202 = {in_194, in_195, in_196, in_197, in_198, in_199, in_200, in_201};
  assign out_203 = in_219[0];
  assign out_204 = in_219[1];
  assign out_205 = in_219[2];
  assign out_206 = in_219[3];
  assign out_207 = in_219[4];
  assign out_208 = in_219[5];
  assign out_209 = in_219[6];
  assign out_210 = in_219[7];
  assign out_211 = in_219[8];
  assign out_212 = in_219[9];
  assign out_213 = in_219[10];
  assign out_214 = in_219[11];
  assign out_215 = in_219[12];
  assign out_216 = in_219[13];
  assign out_217 = in_219[14];
  assign out_218 = in_219[15];
  assign out_220 = in_219[7:0];
  assign out_221 = in_219[15:8];
  assign out_222 = {in_185, in_186, in_187, in_188, in_189, in_190, in_191, in_192};
  assign out_223 = {in_176, in_177, in_178, in_179, in_180, in_181, in_182, in_183};
  assign out_233 = in_232;
  assign out_234 = in_232[6:0];
  assign out_236 = in_235[6:0];
  assign out_243 = {in_242, in_241};
  assign Z = {Y_3, X_3[5:0]};

  // Other names for the same wires on the sheet: A_t[7:1] = out_327; C1[7:0] = C[7:0]; C2[7:0] = C[15:8];
  //   DISP_CNT[2:0] = out_98; op_dec[7:0] = {in_58, in_59, in_60, in_61, in_62, in_63, in_64, in_65};
  //   op_addr_data[15:0] = {in_66, in_67, in_68, in_69, in_70, in_71, in_72, in_73, in_74, in_75, in_76, in_77, in_78, in_79, in_80, in_81};
  //   M_CHGMD_D[1:0] = M_GHGMD_D; NOU1 = in_89; NOU2 = in_90; NOU3 = in_91; NOU4 = in_92;
  //   ADDR_VAL[15:0] = out_46[23:8]; X_t[5:0] = X_2; Y_t[7:0] = Y_2; Z_t[15:0] = {Z2, Z1}

  // Notes on the sheet:
  //   CLK1: Hz: 16384
  //   _100: Hz: 100
  //   clk: Hz: 10000
  //   VGA_clock: Hz: 2147483647
  //   clk_2: Hz: 50
  //   clk_3: Hz: 50
  //   clk_4: Hz: 10
  //   in_164: default 10
  //   in_166: default 27
  //   clk_5: Hz: 100
  //   clk_6: Hz: 5000
  //   contents of eeprom_1 (hex, n*v repeats v):
  //   1,1,0,1
  //   SEGLOC CALC
  //   contents of rom_1 (hex, n*v repeats v):
  //   0,1111109
  //   INT-FULL
  //   INT-DELAY
  //   REGISTERS
  //   contents of eeprom_2 (hex, n*v repeats v):
  //   0,100ff07,100ff08,100ff09,100ff0a,0,b,c,0,1000009,2
  //   contents of K_ROM (hex, n*v repeats v):
  //   0,0,0,1000007,200d,0,1000107,220d,1000007,230d,0,1000007,250d
  //   ,1000007,260d,0,1000007,d0d,1000007,e0d,0,1000007,130d,0,1000007
  //   ,140d,38*0,1000009,2,5*0,68,a0f,0,a08,1003d07,31,0,1008009,100000a
  //   ,5,50,0,0,2209,230a,c,a09,54,f,54,0,2307,1000108,22,230d,0,a09
  //   ,69,0,1003f09,100000a,5,6,32*0,10007,1004508,31,0,100d009,100000a
  //   ,5,4f,4*0,10107,1004308,31,0,100d009,100000a,5,4f,4*0,10207,1004808
  //   ,31,0,100d009,100000a,5,4f,4*0,10307,1004f08,31,0,100d009,100000a
  //   ,5,4f,4*0,1000009,100020a,5,6,4*0,100d00a,1000009,2,21*0,10007
  //   ,1004c08,31,0,1002009,100010a,5,4f,4*0,10107,1004f08,31,0,1002009
  //   ,100010a,5,4f,4*0,10207,1004108,31,0,1002009,100010a,5,4f,4*0
  //   ,10307,1004408,31,0,1002009,100010a,5,4f,4*0,1006009,100020a,5
  //   ,6,4*0,100d10a,1000009,2,141*0,1000a09,69,69,0,1000809,20*69,0
  //   ,1005509,69,0,1004e09,69,0,1004b09,69,0,1002009,69,0,1004309,69
  //   ,0,1004d09,69,0,1004409,69,0,0,1000009,100030a,5,6,4*0,100cc0a
  //   ,1000009,2,38*0,1000a09,69,0,1000809,19*69,0,0,2307,300d,1000507
  //   ,310d,12*0,3007,3108,31,0,1000009,100030a,5,50,0,1000109,310a
  //   ,c,0,54,9,54,0,69,0,3107,1000108,22,310d,0,1002009,100020a,5,6
  //   ,4*0,100f70a,1000009,2,20*0,1000a09,69,0,1000809,19*69,0,1004c09
  //   ,69,1004f09,69,1004109,69,1004409,69,1004909,69,1004e09,69,1004709
  //   ,69,0,0,1000009,100040a,5,6,4*0,1000009,100060a,5,6,4*0,1007,1001008
  //   ,26,130d,0,1107,140d,0,1307,1408,22,e0d,15*0,1000009,100080a,5
  //   ,6,20*0,1000009,2,51*0,1000a09,69,69,0,1000809,20*69,0,1000009
  //   ,100000a,5,6,17*0,100f50a,1000009,2,206*0,10507,1004008,31,0,1006009
  //   ,100040a,5,4e,7*0,10507,1003008,31,0,1000009,100050a,5,50,10507
  //   ,1003108,31,0,1000809,100050a,5,50,10507,1003208,31,0,1001009
  //   ,100050a,5,50,10507,1003308,31,0,1001809,100050a,5,50,10507,1003408
  //   ,31,0,1002009,100050a,5,50,10507,1003508,31,0,1002809,100050a
  //   ,5,50,10507,1003608,31,0,1003009,100050a,5,50,10507,1003708,31
  //   ,0,1003809,100050a,5,50,10507,1003808,31,0,1004009,100050a,5,50
  //   ,10507,1003908,31,0,1004809,100050a,5,50,0,10507,1004108,31,1006009
  //   ,100050a,5,50,0,10507,1004208,31,1006809,100050a,5,50,0,10507
  //   ,1004308,31,1007009,100050a,5,50,0,10507,1004408,31,1007809,100050a
  //   ,5,50,0,10507,1004508,31,1008009,100050a,5,50,0,10507,1004608
  //   ,31,1008809,100050a,5,50,9*0,100a50a,1000009,2,101*0,1000007,100d
  //   ,0,1008f09,100020a,5,6,0,1000107,100d,0,1008f09,100020a,5,6,0
  //   ,1000207,100d,0,1008f09,100020a,5,6,0,1000307,100d,0,1008f09,100020a
  //   ,5,6,0,1000407,100d,0,1008f09,100020a,5,6,0,1000507,100d,0,1008f09
  //   ,100020a,5,6,0,1000607,100d,0,1008f09,100020a,5,6,0,1000707,100d
  //   ,0,1008f09,100020a,5,6,0,1000807,100d,0,1008f09,100020a,5,6,0
  //   ,1000907,100d,0,1008f09,100020a,5,6,17*0,1000a07,100d,0,1008f09
  //   ,100020a,5,6,0,1000b07,100d,0,1008f09,100020a,5,6,0,1000c07,100d
  //   ,0,1008f09,100020a,5,6,0,1000d07,100d,0,1008f09,100020a,5,6,0
  //   ,1000e07,100d,0,1008f09,100020a,5,6,0,1000f07,100d,0,1008f09,100020a
  //   ,5,6,9*0,100b50a,1000009,2,101*0,10607,1004008,31,0,1006009,100060a
  //   ,5,4e,7*0,10607,1003008,31,0,1000009,100070a,5,50,10607,1003108
  //   ,31,0,1000809,100070a,5,50,10607,1003208,31,0,1001009,100070a
  //   ,5,50,10607,1003308,31,0,1001809,100070a,5,50,10607,1003408,31
  //   ,0,1002009,100070a,5,50,10607,1003508,31,0,1002809,100070a,5,50
  //   ,10607,1003608,31,0,1003009,100070a,5,50,10607,1003708,31,0,1003809
  //   ,100070a,5,50,10607,1003808,31,0,1004009,100070a,5,50,10607,1003908
  //   ,31,0,1004809,100070a,5,50,0,10607,1004108,31,1006009,100070a
  //   ,5,50,0,10607,1004208,31,1006809,100070a,5,50,0,10607,1004308
  //   ,31,1007009,100070a,5,50,0,10607,1004408,31,1007809,100070a,5
  //   ,50,0,10607,1004508,31,1008009,100070a,5,50,0,10607,1004608,31
  //   ,1008809,100070a,5,50,9*0,100a60a,1000009,2,101*0,1000007,110d
  //   ,0,1009709,100020a,5,6,0,1000107,110d,0,1009709,100020a,5,6,0
  //   ,1000207,110d,0,1009709,100020a,5,6,0,1000307,110d,0,1009709,100020a
  //   ,5,6,0,1000407,110d,0,1009709,100020a,5,6,0,1000507,110d,0,1009709
  //   ,100020a,5,6,0,1000607,110d,0,1009709,100020a,5,6,0,1000707,110d
  //   ,0,1009709,100020a,5,6,0,1000807,110d,0,1009709,100020a,5,6,0
  //   ,1000907,110d,0,1009709,100020a,5,6,17*0,1000a07,110d,0,1009709
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  //   A
  //   B
  //   X
  //   Y
  //   C
  //   Z
  //   ABOVE 50 = - 1
  //   Branch If Not Negative
  //   Branch If Negative
  //   Branch If Not Zero
  //   Branch If Zero
  //   Branch If Not Overflown
  //   Branch If Overflown
  //   Branch If Not Carrying
  //   Branch If Carrying
  //   Branch If Bigger Or Equal
  //   Branch If Smaller Or Equal
  //   Branch If Not Bigger
  //   Branch If Bigger
  //   Branch If Not Equal
  //   Branch If Equal
  //   Branch If Not Smaller
  //   Branch If Smaller
  //   SESEGLOC (Set Segment Location)
  //   SEFGCOL     (Set ForeGround Color)
  //   SEBGCOL     (Set BackGround Color)
  //   SECHLOC     (Set Character With Location)
  //   SEKBLOC (Set Keyboard Location)
  //   GETCHLOC (Get Character With Location)
  //   GETKBLOC (Get Keyboard Location)
  //   TELRECV
  //   TELSEND
  //   R1TOA
  //   ATOR1
  //   R2TOA
  //   ATOR2
  //   R3TOA
  //   ATOR3
  //   R4TOA
  //   ATOR4
  //   R5TOA
  //   ATOR5
  //   R6TOA
  //   ATOR6
  //   R7TOA
  //   ATOR7
  //   R8TOA
  //   ATOR8
  //   LD/#-(8)
  //   LD/#-(16)
  //   MANUAL CONTROL
  //   LD/$
  //   LDY/$
  //   ST/#
  //   LDX/$
  //   PLP
  //   LDB/$
  //   STACK
  //   ST/@
  //   PLA
  //   LDA/$
  //   PS
  //   SP
  //   PHP
  //   M-LD/$
  //   M-STY/@
  //   PHA
  //   M-STX/@
  //   STY
  //   M-STB/@
  //   STX
  //   STB
  //   M-STA/@
  //   ALU
  //   M-ST/#
  //   STA
  //   contents of eeprom_3 (hex, n*v repeats v):
  //   10*0,3d,0,0,0,3e,0,3,e,0,30,e,13*0,1,7,12*0,7,7,206*0,4c,4f,41
  //   ,44,20,33,45,53,54,52,64,65,44,a
  //   RAM
  //   FLAGS
  //   LSR
  //   LSL
  //   ROR
  //   ROL
  //   ASR
  //   ASL
  //   ADD
  //   ADC
  //   SUB
  //   SBC
  //   MUL
  //   DIV
  //   LED-DISPLAY
  //   TRANSFERS
  //   NOT
  //   AND
  //   NAND
  //   OR
  //   NOR
  //   XOR
  //   XNOR
  //   VGDB (VGA DATA BUS)
  //   CMP
  //   INV
  //   CNT
  //   ab(c) xy(z), if stc/stz enabled, ignore.
  //   CONDITIONAL 
  //   BRANCHES
  //   ZERO
  //   MUL/MLC
  //   NEG
  //   MANUAL
  //   NOP
  //   CLK ON
  //   READ ON
  //   REG ON
  //   REG OFF
  //   CLK OFF
  //   READ OFF
  //   ADDR FOR SEG POS
  //   DATA FOR FG
  //   DATA FOR BG
  //   ALL = B
  //   X = DATA0 FOR SEG POS
  //   Y = DATA1 FOR SEG POS
  //   X = ADDR FOR CHAR
  //   Y = CHAR DATA
  //   TAKE OUTPUT AND SEND TO "PAS-BASIC"
  //   ENKEYBOARD FLAG
  //   ENTER
  //   ESC
  //   EN
  //   X = ADDR
  //   Y = DATA
  //   ADDR
  //   DATA
  //   WR
  //   B = ADDR
  //   X + Y = DATA
  //   SEG DAT
  //   SEG LOC
  //   FOREGROUND
  //   BACKGROUND
  //   ONLY TO 0x9F
  //   contents of eeprom_4 (hex, n*v repeats v):
  //   4*0,2d,0,2d,2d,0,2d,0,0,2d,0,0,0,2d,0,0,2d,0,2d,0,2d,0,2d,0,0,0
  //   ,2d,0,5*2d,0,0,2d,0,49,4e,50,0,0,0,20,72,0,74,61,72,0,0,64
  //   contents of eeprom_5 (hex, n*v repeats v):
  //   48,c4,4f,4f,4e,185,4d,44,4f,c8,c8,c8,4a,c8,48,48,173,ca,ca,8a
  //   ,8*88,8c,81,84,89,8e,87,120,81,88,88,88,c,88,88,c8,c8,5,1d3,c8,c8
  //   ,185,88,185,88,88,88,c4,173,4*88,120,88,185,48
  //   contents of rom_2 (hex, n*v repeats v):
  //   0,fff,31f,2af,2ff,2f1,e00,e07
  //   contents of rom_3 (hex, n*v repeats v):
  //   0,fff,31f,2af,2ff,2f1,e00,e07
  //   DELAY?
  //   0, 0 IS INACCESIBLE
  //   contents of Char_ROM (hex, n*v repeats v):
  //   35*0,8*180,0,0,8*180,12*0,3e7c,1e78,30*0,3e7c,3ffc,4182,6*6186
  //   ,4182,3e7c,3e7c,4182,6*6186,4182,3ffc,3e7c,10*0,3e7c,3ff8,4180
  //   ,6*6180,4180,3e7c,3e7c,182,6*186,182,1ffc,3e7c,10*0,3e00,3f00
  //   ,4188,6188,6198,61b0,61b0,61e0,61e0,4180,3e7c,3e7c,182,786,786
  //   ,d86,d86,1986,1186,1182,fc,7c,10*0,3e00,3f00,4180,6*6180,4180
  //   ,3f00,3e00,4000,6060,6060,6030,6030,6018,6008,4000,3e78,3e7c,12*0
  //   ,8,8,18,30,30,60,60,23*0,7c,78,200,600,600,c00,800,1800,1000,4*0
  //   ,1000,1800,800,c00,600,600,200,78,7c,10*0,3e00,1e00,40,60,60,30
  //   ,10,18,8,4*0,8,18,10,30,60,60,40,1e00,3e00,12*0,1188,1188,1998
  //   ,db0,db0,7e0,7e0,180,3e7c,3e7c,180,7e0,7e0,db0,db0,1998,1188,1188
  //   ,14*0,8*180,3e7c,3e7c,8*180,25*0,600,600,c00,c00,1800,1000,1000
  //   ,22*0,3e7c,3e7c,40*0,180,180,12*0,8,8,18,30,30,60,60,4*0,600,600
  //   ,c00,c00,1800,1000,1000,12*0,3e7c,3e7c,4006,600e,601a,6032,6036
  //   ,6066,6066,6006,0,0,6006,6606,6606,6c06,4c06,5806,7006,6002,3e7c,3e7c
  //   ,10*0,3e00,1f00,8*180,0,0,8*180,1ff8,3e7c,10*0,3e7c,1e7c,2,6*6
  //   ,2,3e7c,3e7c,4000,6*6000,4000,3e78,3e7c,10*0,3e7c,1e7c,2,6*6,2
  //   ,3e7c,3e7c,2,6*6,2,1e7c,3e7c,11*0,4002,7*6006,4002,3e7c,3e7c,2
  //   ,7*6,2,11*0,3e7c,3e78,4000,6*6000,4000,3e7c,3e7c,2,6*6,2,1e7c
  //   ,3e7c,10*0,3e7c,3e78,4000,6*6000,4000,3e7c,3e7c,4002,6*6006,4002
  //   ,3e7c,3e7c,10*0,3e7c,1e7c,2,7*6,0,0,8*6,2,11*0,3e7c,3e7c,4002
  //   ,6*6006,4002,3e7c,3e7c,4002,6*6006,4002,3e7c,3e7c,10*0,3e7c,3e7c
  //   ,4002,6*6006,4002,3e7c,3e7c,2,6*6,2,1e7c,3e7c,15*0,180,180,8*0
  //   ,180,180,17*0,8*180,0,0,0,600,600,c00,c00,1800,1000,1000,14*0
  //   ,40,c0,c0,180,180,300,300,4*0,300,300,180,180,c0,c0,40,17*0,3e7c,3e7c
  //   ,8*0,1e78,3e7c,17*0,200,300,300,180,180,c0,c0,4*0,c0,c0,180,180
  //   ,300,300,200,12*0,3e7c,1e7c,2,6*6,2,7c,fc,8*180,12*0,3e7c,3ffc
  //   ,4182,6*6186,6182,fc,7c,7*6000,4000,3e78,3e7c,10*0,3e7c,3e7c,4002
  //   ,6*6006,4002,3e7c,3e7c,4002,7*6006,4002,11*0,3e7c,1ffc,182,6*186
  //   ,182,3e7c,3e7c,182,6*186,182,1ffc,3e7c,10*0,3e7c,3e78,4000,7*6000
  //   ,0,0,7*6000,4000,3e78,3e7c,10*0,3e7c,1ffc,182,7*186,0,0,7*186
  //   ,182,1ffc,3e7c,10*0,3e7c,3e78,4000,6*6000,4000,3e7c,3e7c,4000
  //   ,6*6000,4000,3e78,3e7c,10*0,3e7c,3e78,4000,6*6000,4000,3e7c,3e7c
  //   ,4000,7*6000,4000,11*0,3e7c,3e78,4000,7*6000,7c,7c,6002,6*6006
  //   ,4002,3e7c,3e7c,11*0,4002,7*6006,4002,3e7c,3e7c,4002,7*6006,4002
  //   ,11*0,3e7c,1ff8,8*180,0,0,8*180,1ff8,3e7c,10*0,7c,7c,2,7*6,0,0
  //   ,7*6006,4002,3e7c,3e7c,11*0,4000,6008,6008,6018,6030,6030,6060,6060
  //   ,4000,3e00,3e00,4000,6060,6060,6030,6030,6018,6008,6008,4000,12*0
  //   ,4000,8*6000,0,0,7*6000,4000,3e78,3e7c,11*0,4002,6006,700e,581a
  //   ,4c32,6c36,6666,6666,6006,0,0,8*6186,4002,12*0,4002,6006,7006
  //   ,5806,4c06,6c06,6606,6606,6006,0,0,6006,6066,6066,6036,6032,601a
  //   ,600e,6006,4002,11*0,3e7c,3e7c,4002,7*6006,0,0,7*6006,4002,3e7c,3e7c
  //   ,10*0,3e7c,3e7c,4002,6*6006,4002,3e7c,3e7c,4000,7*6000,4000,11*0
  //   ,3e7c,3e7c,4002,7*6006,0,0,6006,6066,6066,6036,6032,601a,600e
  //   ,4006,3e7c,3e7c,10*0,3e7c,3e7c,4002,6*6006,4006,3e00,3e00,4000
  //   ,6060,6060,6030,6030,6018,6008,6008,4000,11*0,3e7c,3e78,4000,6*6000
  //   ,4000,3e7c,3e7c,2,6*6,2,1e7c,3e7c,10*0,3e7c,1ff8,8*180,0,0,8*180
  //   ,13*0,4002,8*6006,0,0,7*6006,4002,3e7c,3e7c,11*0,4000,6008,6008
  //   ,6018,6030,6030,6060,6060,6000,0,0,6000,6600,6600,6c00,4c00,5800
  //   ,7000,6000,4000,12*0,4002,8*6006,0,0,7*6186,4182,3ffc,3e7c,12*0
  //   ,1008,1008,1818,c30,c30,660,660,4*0,660,660,c30,c30,1818,1008,1008
  //   ,14*0,1008,1008,1818,c30,c30,660,660,0,0,0,8*180,12*0,3e7c,1e78
  //   ,0,8,18,30,30,60,60,4*0,600,600,c00,c00,1800,1000,0,1e78,3e7c
  //   ,10*0,3e00,3e00,4000,7*6000,0,0,7*6000,4000,3e00,3e00,12*0,1000,1000
  //   ,1800,c00,c00,600,600,4*0,60,60,30,30,18,8,8,12*0,7c,7c,2,7*6
  //   ,0,0,7*6,2,7c,7c,12*0,240,660,660,c30,810,1818,1008,43*0,1e78,3e7c
endmodule
