// Digital circuit test.dig as structural Verilog
module test (
  input  [7:0] in_1,
  input  in_2,
  input  in_3,
  input  in_4,
  output [7:0] out_5,
  output out_6
);

  Telnet telnet_1 (.in(in_1), .C(in_2), .wr(in_3), .rd(in_4), .out(out_5), .av(out_6));
endmodule
