// Digital circuit vgaline.dig as structural Verilog
module vgaline (
  input  [7:0] CX_i,
  input  [7:0] CY_i,
  input  [6:0] C_i,
  input  [11:0] FG_i,
  input  [11:0] BG_i,
  input  [6:0] D_ci,
  input  [7:0] POS_i,
  input  [7:0] POS_ci,
  input  [6:0] D,
  input  [7:0] A,
  input  clk,
  input  clock,
  output [7:0] CX_o,
  output [7:0] CY_o,
  output [6:0] C_o,
  output [11:0] FG_o,
  output [11:0] BG_o,
  output [6:0] D_co,
  output [7:0] POS_o,
  output [7:0] POS_co,
  output [6:0] RPOS,
  output [7:0] out_21,
  output [6:0] out_22
);

  wire add_1_c_o, add_2_c_o, add_3_c_o, add_4_c_o, add_5_c_o, add_6_c_o, add_7_c_o, add_8_c_o, add_9_c_o,
       add_10_c_o, add_11_c_o, add_12_c_o, add_13_c_o, add_14_c_o, add_15_c_o, add_16_c_o, add_17_c_o,
       add_18_c_o, add_19_c_o, add_20_c_o, add_21_c_o, add_22_c_o, add_23_c_o, add_24_c_o, add_25_c_o,
       add_26_c_o, add_27_c_o, add_28_c_o, add_29_c_o, add_30_c_o, add_31_c_o, add_32_c_o, add_33_c_o,
       add_34_c_o, add_35_c_o, add_36_c_o, add_37_c_o, add_38_c_o, add_39_c_o, add_40_c_o, comparator_1_eq,
       comparator_1_gt, comparator_1_lt, comparator_2_eq, comparator_2_gt, comparator_2_lt, comparator_3_eq,
       comparator_3_gt, comparator_3_lt, comparator_4_eq, comparator_4_gt, comparator_4_lt, comparator_5_eq,
       comparator_5_gt, comparator_5_lt, comparator_6_eq, comparator_6_gt, comparator_6_lt, comparator_7_eq,
       comparator_7_gt, comparator_7_lt, comparator_8_eq, comparator_8_gt, comparator_8_lt, comparator_9_eq,
       comparator_9_gt, comparator_9_lt, comparator_10_eq, comparator_10_gt, comparator_10_lt,
       comparator_11_eq, comparator_11_gt, comparator_11_lt, comparator_12_eq, comparator_12_gt,
       comparator_12_lt, comparator_13_eq, comparator_13_gt, comparator_13_lt, comparator_14_eq,
       comparator_14_gt, comparator_14_lt, comparator_15_eq, comparator_15_gt, comparator_15_lt,
       comparator_16_eq, comparator_16_gt, comparator_16_lt, comparator_17_eq, comparator_17_gt,
       comparator_17_lt, comparator_18_eq, comparator_18_gt, comparator_18_lt, comparator_19_eq,
       comparator_19_gt, comparator_19_lt, comparator_20_eq, comparator_20_gt, comparator_20_lt,
       comparator_21_eq, comparator_21_gt, comparator_21_lt, comparator_22_eq, comparator_22_gt,
       comparator_22_lt, comparator_23_eq, comparator_23_gt, comparator_23_lt, comparator_24_eq,
       comparator_24_gt, comparator_24_lt, comparator_25_eq, comparator_25_gt, comparator_25_lt,
       comparator_26_eq, comparator_26_gt, comparator_26_lt, comparator_27_eq, comparator_27_gt,
       comparator_27_lt, comparator_28_eq, comparator_28_gt, comparator_28_lt, comparator_29_eq,
       comparator_29_gt, comparator_29_lt, comparator_30_eq, comparator_30_gt, comparator_30_lt,
       comparator_31_eq, comparator_31_gt, comparator_31_lt, comparator_32_eq, comparator_32_gt,
       comparator_32_lt, comparator_33_eq, comparator_33_gt, comparator_33_lt, comparator_34_eq,
       comparator_34_gt, comparator_34_lt, comparator_35_eq, comparator_35_gt, comparator_35_lt,
       comparator_36_eq, comparator_36_gt, comparator_36_lt, comparator_37_eq, comparator_37_gt,
       comparator_37_lt, comparator_38_eq, comparator_38_gt, comparator_38_lt, comparator_39_eq,
       comparator_39_gt, comparator_39_lt, comparator_40_eq, comparator_40_gt, comparator_40_lt, delay_1_out,
       delay_2_out, delay_3_out, delay_4_out, delay_5_out, delay_6_out, delay_7_out, delay_8_out,
       delay_9_out, delay_10_out, delay_11_out, delay_12_out, delay_13_out, delay_14_out, delay_15_out,
       delay_16_out, delay_17_out, delay_18_out, delay_19_out, delay_20_out, delay_21_out, delay_22_out,
       delay_23_out, delay_24_out, delay_25_out, delay_26_out, delay_27_out, delay_28_out, delay_29_out,
       delay_30_out, delay_31_out, delay_32_out, delay_33_out, delay_34_out, delay_35_out, delay_36_out,
       delay_37_out, delay_38_out, delay_39_out, delay_40_out, delay_41_out, delay_42_out, not_1_out,
       vgacharpos_1_p3, vgacharpos_1_p4, vgasync_1_h, vgasync_1_pic, vgasync_1_v, vgatext_1_p11,
       vgatext_1_p12, vgatext_1_p13, vgatext_1_p14, vgatext_1_p15, WR_out;
  wire [6:0] register_3_q, register_4_q, register_5_q, register_6_q, register_7_q, register_8_q,
       register_9_q, register_10_q, register_11_q, register_12_q, register_13_q, register_14_q,
       register_15_q, register_16_q, register_17_q, register_18_q, register_19_q, register_20_q,
       register_21_q, register_22_q, register_23_q, register_24_q, register_25_q, register_26_q,
       register_27_q, register_28_q, register_29_q, register_30_q, register_31_q, register_32_q,
       register_33_q, register_34_q, register_35_q, register_36_q, register_37_q, register_38_q,
       register_39_q, register_40_q, register_41_q, vgastring_1_c_o, vgastring_2_c_o, vgastring_3_c_o,
       vgastring_4_c_o, vgastring_5_c_o, vgastring_6_c_o, vgastring_7_c_o, vgastring_8_c_o, vgastring_9_c_o;
  wire [7:0] add_1_s, add_2_s, add_3_s, add_4_s, add_5_s, add_6_s, add_7_s, add_8_s, add_9_s, add_10_s,
       add_11_s, add_12_s, add_13_s, add_14_s, add_15_s, add_16_s, add_17_s, add_18_s, add_19_s, add_20_s,
       add_21_s, add_22_s, add_23_s, add_24_s, add_25_s, add_26_s, add_27_s, add_28_s, add_29_s, add_30_s,
       add_31_s, add_32_s, add_33_s, add_34_s, add_35_s, add_36_s, add_37_s, add_38_s, add_39_s,
       driverinvsel_1_out, vgacharpos_1_p5, vgacharpos_1_p6, vgastring_1_cx_o, vgastring_1_cy_o,
       vgastring_2_cx_o, vgastring_2_cy_o, vgastring_3_cx_o, vgastring_3_cy_o, vgastring_4_cx_o,
       vgastring_4_cy_o, vgastring_5_cx_o, vgastring_5_cy_o, vgastring_6_cx_o, vgastring_6_cy_o,
       vgastring_7_cx_o, vgastring_7_cy_o, vgastring_8_cx_o, vgastring_8_cy_o, vgastring_9_cx_o,
       vgastring_9_cy_o;
  wire [10:0] vgatext_1_p16;
  wire [11:0] vgastring_1_bg_o, vgastring_1_fg_o, vgastring_2_bg_o, vgastring_2_fg_o, vgastring_3_bg_o,
       vgastring_3_fg_o, vgastring_4_bg_o, vgastring_4_fg_o, vgastring_5_bg_o, vgastring_5_fg_o,
       vgastring_6_bg_o, vgastring_6_fg_o, vgastring_7_bg_o, vgastring_7_fg_o, vgastring_8_bg_o,
       vgastring_8_fg_o, vgastring_9_bg_o, vgastring_9_fg_o;
  wire [15:0] Char_ROM_d, vgasync_1_x, vgasync_1_y, vgatext_1_p6;

  Add #(.Bits(8)) add_1 (.a(out_21), .b(8'h1), .c_i(1'b0), .s(add_1_s), .c_o(add_1_c_o));
  Delay #(.delayTime(10)) delay_1 (.in(clk), .out(delay_1_out));
  Register #(.Bits(8)) register_1 (.D(add_1_s), .C(delay_1_out), .en(clk), .Q(out_21));
  Button WR (.out(WR_out));
  assign driverinvsel_1_out = ~WR_out ? out_21 : 8'bz;  // DriverInvSel driverinvsel_1
  assign driverinvsel_1_out = WR_out ? A : 8'bz;  // Driver driver_1
  Delay #(.delayTime(10)) delay_2 (.in(WR_out), .out(delay_2_out));
  not not_1 (not_1_out, WR_out);
  vgasync vgasync_1 (
    .clock(clock), .H(vgasync_1_h), .V(vgasync_1_v), .pic(vgasync_1_pic), .X(vgasync_1_x), .Y(vgasync_1_y));
  EEPROM #(.AddrBits(8), .Bits(7)) eeprom_1 (
    .A(driverinvsel_1_out), .CS(1'b1), .WE(delay_2_out), .OE(not_1_out), .D(out_22));
  // vgacharpos vgacharpos_1: pin names not known; wires that end beside it: vgasync_1_x, vgasync_1_y, vgacharpos_1_p3, vgacharpos_1_p4, vgacharpos_1_p5, vgacharpos_1_p6
  assign D_co = not_1_out ? out_22 : 7'bz;  // Driver driver_2
  assign out_22 = delay_2_out ? D : 7'bz;  // Driver driver_3
  Add #(.Bits(8)) add_2 (.a(POS_ci), .b(8'h1), .c_i(1'b0), .s(add_2_s), .c_o(add_2_c_o));
  Add #(.Bits(8)) add_3 (.a(add_2_s), .b(8'h1), .c_i(1'b0), .s(add_3_s), .c_o(add_3_c_o));
  Add #(.Bits(8)) add_4 (.a(add_3_s), .b(8'h1), .c_i(1'b0), .s(add_4_s), .c_o(add_4_c_o));
  Comparator #(.Bits(8)) comparator_1 (
    .a(out_21), .b(POS_ci), .gt(comparator_1_gt), .eq(comparator_1_eq), .lt(comparator_1_lt));
  Comparator #(.Bits(8)) comparator_2 (
    .a(out_21), .b(add_2_s), .gt(comparator_2_gt), .eq(comparator_2_eq), .lt(comparator_2_lt));
  Comparator #(.Bits(8)) comparator_3 (
    .a(out_21), .b(add_3_s), .gt(comparator_3_gt), .eq(comparator_3_eq), .lt(comparator_3_lt));
  Comparator #(.Bits(8)) comparator_4 (
    .a(out_21), .b(add_4_s), .gt(comparator_4_gt), .eq(comparator_4_eq), .lt(comparator_4_lt));
  Delay #(.delayTime(10)) delay_3 (.in(comparator_1_eq), .out(delay_3_out));
  Delay #(.delayTime(10)) delay_4 (.in(comparator_2_eq), .out(delay_4_out));
  Delay #(.delayTime(10)) delay_5 (.in(comparator_3_eq), .out(delay_5_out));
  Delay #(.delayTime(10)) delay_6 (.in(comparator_4_eq), .out(delay_6_out));
  Register #(.Bits(7)) register_2 (.D(D_co), .C(delay_3_out), .en(comparator_1_eq), .Q(RPOS));
  Register #(.Bits(7)) register_3 (.D(D_co), .C(delay_4_out), .en(comparator_2_eq), .Q(register_3_q));
  Register #(.Bits(7)) register_4 (.D(D_co), .C(delay_5_out), .en(comparator_3_eq), .Q(register_4_q));
  Register #(.Bits(7)) register_5 (.D(D_co), .C(delay_6_out), .en(comparator_4_eq), .Q(register_5_q));
  vgastring vgastring_1 (
    .CX_i(vgacharpos_1_p5), .CY_i(vgacharpos_1_p6), .C_i(C_i), .FG_i(BG_i), .BG_i(FG_i), .FG_c(12'he07),
    .BG_c({12{1'b0}}), .CX_c({6{1'b0}}), .CY_c(8'he), .C_0(RPOS), .C_1(register_3_q), .C_2(register_4_q),
    .C_3(register_5_q), .EN(1'b1), .CX_o(vgastring_1_cx_o), .CY_o(vgastring_1_cy_o), .C_o(vgastring_1_c_o),
    .FG_o(vgastring_1_fg_o), .BG_o(vgastring_1_bg_o));
  Add #(.Bits(8)) add_5 (.a(add_4_s), .b(8'h1), .c_i(1'b0), .s(add_5_s), .c_o(add_5_c_o));
  Add #(.Bits(8)) add_6 (.a(add_5_s), .b(8'h1), .c_i(1'b0), .s(add_6_s), .c_o(add_6_c_o));
  Add #(.Bits(8)) add_7 (.a(add_6_s), .b(8'h1), .c_i(1'b0), .s(add_7_s), .c_o(add_7_c_o));
  Add #(.Bits(8)) add_8 (.a(add_7_s), .b(8'h1), .c_i(1'b0), .s(add_8_s), .c_o(add_8_c_o));
  Comparator #(.Bits(8)) comparator_5 (
    .a(out_21), .b(add_5_s), .gt(comparator_5_gt), .eq(comparator_5_eq), .lt(comparator_5_lt));
  Comparator #(.Bits(8)) comparator_6 (
    .a(out_21), .b(add_6_s), .gt(comparator_6_gt), .eq(comparator_6_eq), .lt(comparator_6_lt));
  Comparator #(.Bits(8)) comparator_7 (
    .a(out_21), .b(add_7_s), .gt(comparator_7_gt), .eq(comparator_7_eq), .lt(comparator_7_lt));
  Comparator #(.Bits(8)) comparator_8 (
    .a(out_21), .b(add_8_s), .gt(comparator_8_gt), .eq(comparator_8_eq), .lt(comparator_8_lt));
  Delay #(.delayTime(10)) delay_7 (.in(comparator_5_eq), .out(delay_7_out));
  Delay #(.delayTime(10)) delay_8 (.in(comparator_6_eq), .out(delay_8_out));
  Delay #(.delayTime(10)) delay_9 (.in(comparator_7_eq), .out(delay_9_out));
  Delay #(.delayTime(10)) delay_10 (.in(comparator_8_eq), .out(delay_10_out));
  Register #(.Bits(7)) register_6 (.D(D_co), .C(delay_7_out), .en(comparator_5_eq), .Q(register_6_q));
  Register #(.Bits(7)) register_7 (.D(D_co), .C(delay_8_out), .en(comparator_6_eq), .Q(register_7_q));
  Register #(.Bits(7)) register_8 (.D(D_co), .C(delay_9_out), .en(comparator_7_eq), .Q(register_8_q));
  Register #(.Bits(7)) register_9 (.D(D_co), .C(delay_10_out), .en(comparator_8_eq), .Q(register_9_q));
  vgastring vgastring_2 (
    .CX_i(vgastring_1_cx_o), .CY_i(vgastring_1_cy_o), .C_i(vgastring_1_c_o), .FG_i(vgastring_1_fg_o),
    .BG_i(vgastring_1_bg_o), .FG_c(12'he09), .BG_c({12{1'b0}}), .CX_c(6'b000001), .CY_c(8'he),
    .C_0(register_6_q), .C_1(register_7_q), .C_2(register_8_q), .C_3(register_9_q), .EN(1'b1),
    .CX_o(vgastring_2_cx_o), .CY_o(vgastring_2_cy_o), .C_o(vgastring_2_c_o), .FG_o(vgastring_2_fg_o),
    .BG_o(vgastring_2_bg_o));
  Add #(.Bits(8)) add_9 (.a(add_8_s), .b(8'h1), .c_i(1'b0), .s(add_9_s), .c_o(add_9_c_o));
  Add #(.Bits(8)) add_10 (.a(add_9_s), .b(8'h1), .c_i(1'b0), .s(add_10_s), .c_o(add_10_c_o));
  Add #(.Bits(8)) add_11 (.a(add_10_s), .b(8'h1), .c_i(1'b0), .s(add_11_s), .c_o(add_11_c_o));
  Add #(.Bits(8)) add_12 (.a(add_11_s), .b(8'h1), .c_i(1'b0), .s(add_12_s), .c_o(add_12_c_o));
  Comparator #(.Bits(8)) comparator_9 (
    .a(out_21), .b(add_9_s), .gt(comparator_9_gt), .eq(comparator_9_eq), .lt(comparator_9_lt));
  Comparator #(.Bits(8)) comparator_10 (
    .a(out_21), .b(add_10_s), .gt(comparator_10_gt), .eq(comparator_10_eq), .lt(comparator_10_lt));
  Comparator #(.Bits(8)) comparator_11 (
    .a(out_21), .b(add_11_s), .gt(comparator_11_gt), .eq(comparator_11_eq), .lt(comparator_11_lt));
  Comparator #(.Bits(8)) comparator_12 (
    .a(out_21), .b(add_12_s), .gt(comparator_12_gt), .eq(comparator_12_eq), .lt(comparator_12_lt));
  Delay #(.delayTime(10)) delay_11 (.in(comparator_9_eq), .out(delay_11_out));
  Delay #(.delayTime(10)) delay_12 (.in(comparator_10_eq), .out(delay_12_out));
  Delay #(.delayTime(10)) delay_13 (.in(comparator_11_eq), .out(delay_13_out));
  Delay #(.delayTime(10)) delay_14 (.in(comparator_12_eq), .out(delay_14_out));
  Register #(.Bits(7)) register_10 (.D(D_co), .C(delay_11_out), .en(comparator_9_eq), .Q(register_10_q));
  Register #(.Bits(7)) register_11 (.D(D_co), .C(delay_12_out), .en(comparator_10_eq), .Q(register_11_q));
  Register #(.Bits(7)) register_12 (.D(D_co), .C(delay_13_out), .en(comparator_11_eq), .Q(register_12_q));
  Register #(.Bits(7)) register_13 (.D(D_co), .C(delay_14_out), .en(comparator_12_eq), .Q(register_13_q));
  vgastring vgastring_3 (
    .CX_i(vgastring_2_cx_o), .CY_i(vgastring_2_cy_o), .C_i(vgastring_2_c_o), .FG_i(vgastring_2_fg_o),
    .BG_i(vgastring_2_bg_o), .FG_c(12'he09), .BG_c({12{1'b0}}), .CX_c(6'b000010), .CY_c(8'he),
    .C_0(register_10_q), .C_1(register_11_q), .C_2(register_12_q), .C_3(register_13_q), .EN(1'b1),
    .CX_o(vgastring_3_cx_o), .CY_o(vgastring_3_cy_o), .C_o(vgastring_3_c_o), .FG_o(vgastring_3_fg_o),
    .BG_o(vgastring_3_bg_o));
  Add #(.Bits(8)) add_13 (.a(add_12_s), .b(8'h1), .c_i(1'b0), .s(add_13_s), .c_o(add_13_c_o));
  Add #(.Bits(8)) add_14 (.a(add_13_s), .b(8'h1), .c_i(1'b0), .s(add_14_s), .c_o(add_14_c_o));
  Add #(.Bits(8)) add_15 (.a(add_14_s), .b(8'h1), .c_i(1'b0), .s(add_15_s), .c_o(add_15_c_o));
  Add #(.Bits(8)) add_16 (.a(add_15_s), .b(8'h1), .c_i(1'b0), .s(add_16_s), .c_o(add_16_c_o));
  Comparator #(.Bits(8)) comparator_13 (
    .a(out_21), .b(add_13_s), .gt(comparator_13_gt), .eq(comparator_13_eq), .lt(comparator_13_lt));
  Comparator #(.Bits(8)) comparator_14 (
    .a(out_21), .b(add_14_s), .gt(comparator_14_gt), .eq(comparator_14_eq), .lt(comparator_14_lt));
  Comparator #(.Bits(8)) comparator_15 (
    .a(out_21), .b(add_15_s), .gt(comparator_15_gt), .eq(comparator_15_eq), .lt(comparator_15_lt));
  Comparator #(.Bits(8)) comparator_16 (
    .a(out_21), .b(add_16_s), .gt(comparator_16_gt), .eq(comparator_16_eq), .lt(comparator_16_lt));
  Delay #(.delayTime(10)) delay_15 (.in(comparator_13_eq), .out(delay_15_out));
  Delay #(.delayTime(10)) delay_16 (.in(comparator_14_eq), .out(delay_16_out));
  Delay #(.delayTime(10)) delay_17 (.in(comparator_15_eq), .out(delay_17_out));
  Delay #(.delayTime(10)) delay_18 (.in(comparator_16_eq), .out(delay_18_out));
  Register #(.Bits(7)) register_14 (.D(D_co), .C(delay_15_out), .en(comparator_13_eq), .Q(register_14_q));
  Register #(.Bits(7)) register_15 (.D(D_co), .C(delay_16_out), .en(comparator_14_eq), .Q(register_15_q));
  Register #(.Bits(7)) register_16 (.D(D_co), .C(delay_17_out), .en(comparator_15_eq), .Q(register_16_q));
  Register #(.Bits(7)) register_17 (.D(D_co), .C(delay_18_out), .en(comparator_16_eq), .Q(register_17_q));
  vgastring vgastring_4 (
    .CX_i(vgastring_3_cx_o), .CY_i(vgastring_3_cy_o), .C_i(vgastring_3_c_o), .FG_i(vgastring_3_fg_o),
    .BG_i(vgastring_3_bg_o), .FG_c(12'he09), .BG_c({12{1'b0}}), .CX_c(6'b000011), .CY_c(8'he),
    .C_0(register_14_q), .C_1(register_15_q), .C_2(register_16_q), .C_3(register_17_q), .EN(1'b1),
    .CX_o(vgastring_4_cx_o), .CY_o(vgastring_4_cy_o), .C_o(vgastring_4_c_o), .FG_o(vgastring_4_fg_o),
    .BG_o(vgastring_4_bg_o));
  Add #(.Bits(8)) add_17 (.a(add_16_s), .b(8'h1), .c_i(1'b0), .s(add_17_s), .c_o(add_17_c_o));
  Add #(.Bits(8)) add_18 (.a(add_17_s), .b(8'h1), .c_i(1'b0), .s(add_18_s), .c_o(add_18_c_o));
  Add #(.Bits(8)) add_19 (.a(add_18_s), .b(8'h1), .c_i(1'b0), .s(add_19_s), .c_o(add_19_c_o));
  Add #(.Bits(8)) add_20 (.a(add_19_s), .b(8'h1), .c_i(1'b0), .s(add_20_s), .c_o(add_20_c_o));
  Comparator #(.Bits(8)) comparator_17 (
    .a(out_21), .b(add_17_s), .gt(comparator_17_gt), .eq(comparator_17_eq), .lt(comparator_17_lt));
  Comparator #(.Bits(8)) comparator_18 (
    .a(out_21), .b(add_18_s), .gt(comparator_18_gt), .eq(comparator_18_eq), .lt(comparator_18_lt));
  Comparator #(.Bits(8)) comparator_19 (
    .a(out_21), .b(add_19_s), .gt(comparator_19_gt), .eq(comparator_19_eq), .lt(comparator_19_lt));
  Comparator #(.Bits(8)) comparator_20 (
    .a(out_21), .b(add_20_s), .gt(comparator_20_gt), .eq(comparator_20_eq), .lt(comparator_20_lt));
  Delay #(.delayTime(10)) delay_19 (.in(comparator_17_eq), .out(delay_19_out));
  Delay #(.delayTime(10)) delay_20 (.in(comparator_18_eq), .out(delay_20_out));
  Delay #(.delayTime(10)) delay_21 (.in(comparator_19_eq), .out(delay_21_out));
  Delay #(.delayTime(10)) delay_22 (.in(comparator_20_eq), .out(delay_22_out));
  Register #(.Bits(7)) register_18 (.D(D_co), .C(delay_19_out), .en(comparator_17_eq), .Q(register_18_q));
  Register #(.Bits(7)) register_19 (.D(D_co), .C(delay_20_out), .en(comparator_18_eq), .Q(register_19_q));
  Register #(.Bits(7)) register_20 (.D(D_co), .C(delay_21_out), .en(comparator_19_eq), .Q(register_20_q));
  Register #(.Bits(7)) register_21 (.D(D_co), .C(delay_22_out), .en(comparator_20_eq), .Q(register_21_q));
  vgastring vgastring_5 (
    .CX_i(vgastring_4_cx_o), .CY_i(vgastring_4_cy_o), .C_i(vgastring_4_c_o), .FG_i(vgastring_4_fg_o),
    .BG_i(vgastring_4_bg_o), .FG_c(12'he07), .BG_c({12{1'b0}}), .CX_c(6'b000100), .CY_c(8'he),
    .C_0(register_18_q), .C_1(register_19_q), .C_2(register_20_q), .C_3(register_21_q), .EN(1'b1),
    .CX_o(vgastring_5_cx_o), .CY_o(vgastring_5_cy_o), .C_o(vgastring_5_c_o), .FG_o(vgastring_5_fg_o),
    .BG_o(vgastring_5_bg_o));
  Add #(.Bits(8)) add_21 (.a(add_20_s), .b(8'h1), .c_i(1'b0), .s(add_21_s), .c_o(add_21_c_o));
  Add #(.Bits(8)) add_22 (.a(add_21_s), .b(8'h1), .c_i(1'b0), .s(add_22_s), .c_o(add_22_c_o));
  Add #(.Bits(8)) add_23 (.a(add_22_s), .b(8'h1), .c_i(1'b0), .s(add_23_s), .c_o(add_23_c_o));
  Add #(.Bits(8)) add_24 (.a(add_23_s), .b(8'h1), .c_i(1'b0), .s(add_24_s), .c_o(add_24_c_o));
  Comparator #(.Bits(8)) comparator_21 (
    .a(out_21), .b(add_21_s), .gt(comparator_21_gt), .eq(comparator_21_eq), .lt(comparator_21_lt));
  Comparator #(.Bits(8)) comparator_22 (
    .a(out_21), .b(add_22_s), .gt(comparator_22_gt), .eq(comparator_22_eq), .lt(comparator_22_lt));
  Comparator #(.Bits(8)) comparator_23 (
    .a(out_21), .b(add_23_s), .gt(comparator_23_gt), .eq(comparator_23_eq), .lt(comparator_23_lt));
  Comparator #(.Bits(8)) comparator_24 (
    .a(out_21), .b(add_24_s), .gt(comparator_24_gt), .eq(comparator_24_eq), .lt(comparator_24_lt));
  Delay #(.delayTime(10)) delay_23 (.in(comparator_21_eq), .out(delay_23_out));
  Delay #(.delayTime(10)) delay_24 (.in(comparator_22_eq), .out(delay_24_out));
  Delay #(.delayTime(10)) delay_25 (.in(comparator_23_eq), .out(delay_25_out));
  Delay #(.delayTime(10)) delay_26 (.in(comparator_24_eq), .out(delay_26_out));
  Register #(.Bits(7)) register_22 (.D(D_co), .C(delay_23_out), .en(comparator_21_eq), .Q(register_22_q));
  Register #(.Bits(7)) register_23 (.D(D_co), .C(delay_24_out), .en(comparator_22_eq), .Q(register_23_q));
  Register #(.Bits(7)) register_24 (.D(D_co), .C(delay_25_out), .en(comparator_23_eq), .Q(register_24_q));
  Register #(.Bits(7)) register_25 (.D(D_co), .C(delay_26_out), .en(comparator_24_eq), .Q(register_25_q));
  vgastring vgastring_6 (
    .CX_i(vgastring_5_cx_o), .CY_i(vgastring_5_cy_o), .C_i(vgastring_5_c_o), .FG_i(vgastring_5_fg_o),
    .BG_i(vgastring_5_bg_o), .FG_c(12'he09), .BG_c({12{1'b0}}), .CX_c(6'b000101), .CY_c(8'he),
    .C_0(register_22_q), .C_1(register_23_q), .C_2(register_24_q), .C_3(register_25_q), .EN(1'b1),
    .CX_o(vgastring_6_cx_o), .CY_o(vgastring_6_cy_o), .C_o(vgastring_6_c_o), .FG_o(vgastring_6_fg_o),
    .BG_o(vgastring_6_bg_o));
  Add #(.Bits(8)) add_25 (.a(add_24_s), .b(8'h1), .c_i(1'b0), .s(add_25_s), .c_o(add_25_c_o));
  Add #(.Bits(8)) add_26 (.a(add_25_s), .b(8'h1), .c_i(1'b0), .s(add_26_s), .c_o(add_26_c_o));
  Add #(.Bits(8)) add_27 (.a(add_26_s), .b(8'h1), .c_i(1'b0), .s(add_27_s), .c_o(add_27_c_o));
  Add #(.Bits(8)) add_28 (.a(add_27_s), .b(8'h1), .c_i(1'b0), .s(add_28_s), .c_o(add_28_c_o));
  Comparator #(.Bits(8)) comparator_25 (
    .a(out_21), .b(add_25_s), .gt(comparator_25_gt), .eq(comparator_25_eq), .lt(comparator_25_lt));
  Comparator #(.Bits(8)) comparator_26 (
    .a(out_21), .b(add_26_s), .gt(comparator_26_gt), .eq(comparator_26_eq), .lt(comparator_26_lt));
  Comparator #(.Bits(8)) comparator_27 (
    .a(out_21), .b(add_27_s), .gt(comparator_27_gt), .eq(comparator_27_eq), .lt(comparator_27_lt));
  Comparator #(.Bits(8)) comparator_28 (
    .a(out_21), .b(add_28_s), .gt(comparator_28_gt), .eq(comparator_28_eq), .lt(comparator_28_lt));
  Delay #(.delayTime(10)) delay_27 (.in(comparator_25_eq), .out(delay_27_out));
  Delay #(.delayTime(10)) delay_28 (.in(comparator_26_eq), .out(delay_28_out));
  Delay #(.delayTime(10)) delay_29 (.in(comparator_27_eq), .out(delay_29_out));
  Delay #(.delayTime(10)) delay_30 (.in(comparator_28_eq), .out(delay_30_out));
  Register #(.Bits(7)) register_26 (.D(D_co), .C(delay_27_out), .en(comparator_25_eq), .Q(register_26_q));
  Register #(.Bits(7)) register_27 (.D(D_co), .C(delay_28_out), .en(comparator_26_eq), .Q(register_27_q));
  Register #(.Bits(7)) register_28 (.D(D_co), .C(delay_29_out), .en(comparator_27_eq), .Q(register_28_q));
  Register #(.Bits(7)) register_29 (.D(D_co), .C(delay_30_out), .en(comparator_28_eq), .Q(register_29_q));
  vgastring vgastring_7 (
    .CX_i(vgastring_6_cx_o), .CY_i(vgastring_6_cy_o), .C_i(vgastring_6_c_o), .FG_i(vgastring_6_fg_o),
    .BG_i(vgastring_6_bg_o), .FG_c(12'he09), .BG_c({12{1'b0}}), .CX_c(6'b000110), .CY_c(8'he),
    .C_0(register_26_q), .C_1(register_27_q), .C_2(register_28_q), .C_3(register_29_q), .EN(1'b1),
    .CX_o(vgastring_7_cx_o), .CY_o(vgastring_7_cy_o), .C_o(vgastring_7_c_o), .FG_o(vgastring_7_fg_o),
    .BG_o(vgastring_7_bg_o));
  Add #(.Bits(8)) add_29 (.a(add_28_s), .b(8'h1), .c_i(1'b0), .s(add_29_s), .c_o(add_29_c_o));
  Add #(.Bits(8)) add_30 (.a(add_29_s), .b(8'h1), .c_i(1'b0), .s(add_30_s), .c_o(add_30_c_o));
  Add #(.Bits(8)) add_31 (.a(add_30_s), .b(8'h1), .c_i(1'b0), .s(add_31_s), .c_o(add_31_c_o));
  Add #(.Bits(8)) add_32 (.a(add_31_s), .b(8'h1), .c_i(1'b0), .s(add_32_s), .c_o(add_32_c_o));
  Comparator #(.Bits(8)) comparator_29 (
    .a(out_21), .b(add_29_s), .gt(comparator_29_gt), .eq(comparator_29_eq), .lt(comparator_29_lt));
  Comparator #(.Bits(8)) comparator_30 (
    .a(out_21), .b(add_30_s), .gt(comparator_30_gt), .eq(comparator_30_eq), .lt(comparator_30_lt));
  Comparator #(.Bits(8)) comparator_31 (
    .a(out_21), .b(add_31_s), .gt(comparator_31_gt), .eq(comparator_31_eq), .lt(comparator_31_lt));
  Comparator #(.Bits(8)) comparator_32 (
    .a(out_21), .b(add_32_s), .gt(comparator_32_gt), .eq(comparator_32_eq), .lt(comparator_32_lt));
  Delay #(.delayTime(10)) delay_31 (.in(comparator_29_eq), .out(delay_31_out));
  Delay #(.delayTime(10)) delay_32 (.in(comparator_30_eq), .out(delay_32_out));
  Delay #(.delayTime(10)) delay_33 (.in(comparator_31_eq), .out(delay_33_out));
  Delay #(.delayTime(10)) delay_34 (.in(comparator_32_eq), .out(delay_34_out));
  Register #(.Bits(7)) register_30 (.D(D_co), .C(delay_31_out), .en(comparator_29_eq), .Q(register_30_q));
  Register #(.Bits(7)) register_31 (.D(D_co), .C(delay_32_out), .en(comparator_30_eq), .Q(register_31_q));
  Register #(.Bits(7)) register_32 (.D(D_co), .C(delay_33_out), .en(comparator_31_eq), .Q(register_32_q));
  Register #(.Bits(7)) register_33 (.D(D_co), .C(delay_34_out), .en(comparator_32_eq), .Q(register_33_q));
  vgastring vgastring_8 (
    .CX_i(vgastring_7_cx_o), .CY_i(vgastring_7_cy_o), .C_i(vgastring_7_c_o), .FG_i(vgastring_7_fg_o),
    .BG_i(vgastring_7_bg_o), .FG_c(12'he09), .BG_c({12{1'b0}}), .CX_c(6'b000111), .CY_c(8'he),
    .C_0(register_30_q), .C_1(register_31_q), .C_2(register_32_q), .C_3(register_33_q), .EN(1'b1),
    .CX_o(vgastring_8_cx_o), .CY_o(vgastring_8_cy_o), .C_o(vgastring_8_c_o), .FG_o(vgastring_8_fg_o),
    .BG_o(vgastring_8_bg_o));
  Add #(.Bits(8)) add_33 (.a(add_32_s), .b(8'h1), .c_i(1'b0), .s(add_33_s), .c_o(add_33_c_o));
  Add #(.Bits(8)) add_34 (.a(add_33_s), .b(8'h1), .c_i(1'b0), .s(add_34_s), .c_o(add_34_c_o));
  Add #(.Bits(8)) add_35 (.a(add_34_s), .b(8'h1), .c_i(1'b0), .s(add_35_s), .c_o(add_35_c_o));
  Add #(.Bits(8)) add_36 (.a(add_35_s), .b(8'h1), .c_i(1'b0), .s(add_36_s), .c_o(add_36_c_o));
  Comparator #(.Bits(8)) comparator_33 (
    .a(out_21), .b(add_33_s), .gt(comparator_33_gt), .eq(comparator_33_eq), .lt(comparator_33_lt));
  Comparator #(.Bits(8)) comparator_34 (
    .a(out_21), .b(add_34_s), .gt(comparator_34_gt), .eq(comparator_34_eq), .lt(comparator_34_lt));
  Comparator #(.Bits(8)) comparator_35 (
    .a(out_21), .b(add_35_s), .gt(comparator_35_gt), .eq(comparator_35_eq), .lt(comparator_35_lt));
  Comparator #(.Bits(8)) comparator_36 (
    .a(out_21), .b(add_36_s), .gt(comparator_36_gt), .eq(comparator_36_eq), .lt(comparator_36_lt));
  Delay #(.delayTime(10)) delay_35 (.in(comparator_33_eq), .out(delay_35_out));
  Delay #(.delayTime(10)) delay_36 (.in(comparator_34_eq), .out(delay_36_out));
  Delay #(.delayTime(10)) delay_37 (.in(comparator_35_eq), .out(delay_37_out));
  Delay #(.delayTime(10)) delay_38 (.in(comparator_36_eq), .out(delay_38_out));
  Register #(.Bits(7)) register_34 (.D(D_co), .C(delay_35_out), .en(comparator_33_eq), .Q(register_34_q));
  Register #(.Bits(7)) register_35 (.D(D_co), .C(delay_36_out), .en(comparator_34_eq), .Q(register_35_q));
  Register #(.Bits(7)) register_36 (.D(D_co), .C(delay_37_out), .en(comparator_35_eq), .Q(register_36_q));
  Register #(.Bits(7)) register_37 (.D(D_co), .C(delay_38_out), .en(comparator_36_eq), .Q(register_37_q));
  vgastring vgastring_9 (
    .CX_i(vgastring_8_cx_o), .CY_i(vgastring_8_cy_o), .C_i(vgastring_8_c_o), .FG_i(vgastring_8_fg_o),
    .BG_i(vgastring_8_bg_o), .FG_c(12'he09), .BG_c({12{1'b0}}), .CX_c(6'b001000), .CY_c(8'he),
    .C_0(register_34_q), .C_1(register_35_q), .C_2(register_36_q), .C_3(register_37_q), .EN(1'b1),
    .CX_o(vgastring_9_cx_o), .CY_o(vgastring_9_cy_o), .C_o(vgastring_9_c_o), .FG_o(vgastring_9_fg_o),
    .BG_o(vgastring_9_bg_o));
  Add #(.Bits(8)) add_37 (.a(add_36_s), .b(8'h1), .c_i(1'b0), .s(add_37_s), .c_o(add_37_c_o));
  Add #(.Bits(8)) add_38 (.a(add_37_s), .b(8'h1), .c_i(1'b0), .s(add_38_s), .c_o(add_38_c_o));
  Add #(.Bits(8)) add_39 (.a(add_38_s), .b(8'h1), .c_i(1'b0), .s(add_39_s), .c_o(add_39_c_o));
  Add #(.Bits(8)) add_40 (.a(add_39_s), .b(8'h1), .c_i(1'b0), .s(POS_co), .c_o(add_40_c_o));
  Comparator #(.Bits(8)) comparator_37 (
    .a(out_21), .b(add_37_s), .gt(comparator_37_gt), .eq(comparator_37_eq), .lt(comparator_37_lt));
  Comparator #(.Bits(8)) comparator_38 (
    .a(out_21), .b(add_38_s), .gt(comparator_38_gt), .eq(comparator_38_eq), .lt(comparator_38_lt));
  Comparator #(.Bits(8)) comparator_39 (
    .a(out_21), .b(add_39_s), .gt(comparator_39_gt), .eq(comparator_39_eq), .lt(comparator_39_lt));
  Comparator #(.Bits(8)) comparator_40 (
    .a(out_21), .b(POS_co), .gt(comparator_40_gt), .eq(comparator_40_eq), .lt(comparator_40_lt));
  Delay #(.delayTime(10)) delay_39 (.in(comparator_37_eq), .out(delay_39_out));
  Delay #(.delayTime(10)) delay_40 (.in(comparator_38_eq), .out(delay_40_out));
  Delay #(.delayTime(10)) delay_41 (.in(comparator_39_eq), .out(delay_41_out));
  Delay #(.delayTime(10)) delay_42 (.in(comparator_40_eq), .out(delay_42_out));
  Register #(.Bits(7)) register_38 (.D(D_co), .C(delay_39_out), .en(comparator_37_eq), .Q(register_38_q));
  Register #(.Bits(7)) register_39 (.D(D_co), .C(delay_40_out), .en(comparator_38_eq), .Q(register_39_q));
  Register #(.Bits(7)) register_40 (.D(D_co), .C(delay_41_out), .en(comparator_39_eq), .Q(register_40_q));
  Register #(.Bits(7)) register_41 (.D(D_co), .C(delay_42_out), .en(comparator_40_eq), .Q(register_41_q));
  vgastring vgastring_10 (
    .CX_i(vgastring_9_cx_o), .CY_i(vgastring_9_cy_o), .C_i(vgastring_9_c_o), .FG_i(vgastring_9_fg_o),
    .BG_i(vgastring_9_bg_o), .FG_c(12'he09), .BG_c({12{1'b0}}), .CX_c(6'b001001), .CY_c(8'he),
    .C_0(register_38_q), .C_1(register_39_q), .C_2(register_40_q), .C_3(register_41_q), .EN(1'b1),
    .CX_o(CX_o), .CY_o(CY_o), .C_o(C_o), .FG_o(FG_o), .BG_o(BG_o));
  // vgatext vgatext_1: pin names not known; wires that end beside it: vgasync_1_h, vgasync_1_v, vgasync_1_pic, vgacharpos_1_p3, vgacharpos_1_p4, vgatext_1_p6, clock, C_o, FG_o, BG_o, vgatext_1_p11, vgatext_1_p12, vgatext_1_p13, vgatext_1_p14, vgatext_1_p15, vgatext_1_p16
  ROM #(.AddrBits(11), .Bits(16)) Char_ROM (.A(vgatext_1_p16), .sel(1'b1), .D(Char_ROM_d));
  VGA vga_1 (.R(vgatext_1_p11), .G(vgatext_1_p12), .B(vgatext_1_p13), .H(vgatext_1_p14), .V(vgatext_1_p15), .C(clock));
  D_FF #(.Bits(16)) d_ff_1 (.D(Char_ROM_d), .C(clock), .Q(vgatext_1_p6));  // open: nQ

  assign POS_o = out_21;

  // Other names for the same wires on the sheet: C = clock

  // Notes on the sheet:
  //   clk: Hz: 50
  //   clock: Hz: 2147483647
  //   contents of eeprom_1 (hex, n*v repeats v):
  //   7*41,43,41,41,49,41,41,41,45,41
  //   contents of Char_ROM (hex, n*v repeats v):
  //   35*0,8*180,0,0,8*180,12*0,3e7c,1e78,30*0,3e7c,3ffc,4182,6*6186
  //   ,4182,3e7c,3e7c,4182,6*6186,4182,3ffc,3e7c,10*0,3e7c,3ff8,4180
  //   ,6*6180,4180,3e7c,3e7c,182,6*186,182,1ffc,3e7c,10*0,3e00,3f00
  //   ,4188,6188,6198,61b0,61b0,61e0,61e0,4180,3e7c,3e7c,182,786,786
  //   ,d86,d86,1986,1186,1182,fc,7c,10*0,3e00,3f00,4180,6*6180,4180
  //   ,3f00,3e00,4000,6060,6060,6030,6030,6018,6008,4000,3e78,3e7c,12*0
  //   ,8,8,18,30,30,60,60,23*0,7c,78,200,600,600,c00,800,1800,1000,4*0
  //   ,1000,1800,800,c00,600,600,200,78,7c,10*0,3e00,1e00,40,60,60,30
  //   ,10,18,8,4*0,8,18,10,30,60,60,40,1e00,3e00,12*0,1188,1188,1998
  //   ,db0,db0,7e0,7e0,180,3e7c,3e7c,180,7e0,7e0,db0,db0,1998,1188,1188
  //   ,14*0,8*180,3e7c,3e7c,8*180,25*0,600,600,c00,c00,1800,1000,1000
  //   ,22*0,3e7c,3e7c,40*0,180,180,12*0,8,8,18,30,30,60,60,4*0,600,600
  //   ,c00,c00,1800,1000,1000,12*0,3e7c,3e7c,4006,600e,601a,6032,6036
  //   ,6066,6066,6006,0,0,6006,6606,6606,6c06,4c06,5806,7006,6002,3e7c,3e7c
  //   ,10*0,3e00,1f00,8*180,0,0,8*180,1ff8,3e7c,10*0,3e7c,1e7c,2,6*6
  //   ,2,3e7c,3e7c,4000,6*6000,4000,3e78,3e7c,10*0,3e7c,1e7c,2,6*6,2
  //   ,3e7c,3e7c,2,6*6,2,1e7c,3e7c,11*0,4002,7*6006,4002,3e7c,3e7c,2
  //   ,7*6,2,11*0,3e7c,3e78,4000,6*6000,4000,3e7c,3e7c,2,6*6,2,1e7c
  //   ,3e7c,10*0,3e7c,3e78,4000,6*6000,4000,3e7c,3e7c,4002,6*6006,4002
  //   ,3e7c,3e7c,10*0,3e7c,1e7c,2,7*6,0,0,8*6,2,11*0,3e7c,3e7c,4002
  //   ,6*6006,4002,3e7c,3e7c,4002,6*6006,4002,3e7c,3e7c,10*0,3e7c,3e7c
  //   ,4002,6*6006,4002,3e7c,3e7c,2,6*6,2,1e7c,3e7c,15*0,180,180,8*0
  //   ,180,180,17*0,8*180,0,0,0,600,600,c00,c00,1800,1000,1000,14*0
  //   ,40,c0,c0,180,180,300,300,4*0,300,300,180,180,c0,c0,40,17*0,3e7c,3e7c
  //   ,8*0,1e78,3e7c,17*0,200,300,300,180,180,c0,c0,4*0,c0,c0,180,180
  //   ,300,300,200,12*0,3e7c,1e7c,2,6*6,2,7c,fc,8*180,12*0,3e7c,3ffc
  //   ,4182,6*6186,6182,fc,7c,7*6000,4000,3e78,3e7c,10*0,3e7c,3e7c,4002
  //   ,6*6006,4002,3e7c,3e7c,4002,7*6006,4002,11*0,3e7c,1ffc,182,6*186
  //   ,182,3e7c,3e7c,182,6*186,182,1ffc,3e7c,10*0,3e7c,3e78,4000,7*6000
  //   ,0,0,7*6000,4000,3e78,3e7c,10*0,3e7c,1ffc,182,7*186,0,0,7*186
  //   ,182,1ffc,3e7c,10*0,3e7c,3e78,4000,6*6000,4000,3e7c,3e7c,4000
  //   ,6*6000,4000,3e78,3e7c,10*0,3e7c,3e78,4000,6*6000,4000,3e7c,3e7c
  //   ,4000,7*6000,4000,11*0,3e7c,3e78,4000,7*6000,7c,7c,6002,6*6006
  //   ,4002,3e7c,3e7c,11*0,4002,7*6006,4002,3e7c,3e7c,4002,7*6006,4002
  //   ,11*0,3e7c,1ff8,8*180,0,0,8*180,1ff8,3e7c,10*0,7c,7c,2,7*6,0,0
  //   ,7*6006,4002,3e7c,3e7c,11*0,4000,6008,6008,6018,6030,6030,6060,6060
  //   ,4000,3e00,3e00,4000,6060,6060,6030,6030,6018,6008,6008,4000,12*0
  //   ,4000,8*6000,0,0,7*6000,4000,3e78,3e7c,11*0,4002,6006,700e,581a
  //   ,4c32,6c36,6666,6666,6006,0,0,8*6186,4002,12*0,4002,6006,7006
  //   ,5806,4c06,6c06,6606,6606,6006,0,0,6006,6066,6066,6036,6032,601a
  //   ,600e,6006,4002,11*0,3e7c,3e7c,4002,7*6006,0,0,7*6006,4002,3e7c,3e7c
  //   ,10*0,3e7c,3e7c,4002,6*6006,4002,3e7c,3e7c,4000,7*6000,4000,11*0
  //   ,3e7c,3e7c,4002,7*6006,0,0,6006,6066,6066,6036,6032,601a,600e
  //   ,4006,3e7c,3e7c,10*0,3e7c,3e7c,4002,6*6006,4006,3e00,3e00,4000
  //   ,6060,6060,6030,6030,6018,6008,6008,4000,11*0,3e7c,3e78,4000,6*6000
  //   ,4000,3e7c,3e7c,2,6*6,2,1e7c,3e7c,10*0,3e7c,1ff8,8*180,0,0,8*180
  //   ,13*0,4002,8*6006,0,0,7*6006,4002,3e7c,3e7c,11*0,4000,6008,6008
  //   ,6018,6030,6030,6060,6060,6000,0,0,6000,6600,6600,6c00,4c00,5800
  //   ,7000,6000,4000,12*0,4002,8*6006,0,0,7*6186,4182,3ffc,3e7c,12*0
  //   ,1008,1008,1818,c30,c30,660,660,4*0,660,660,c30,c30,1818,1008,1008
  //   ,14*0,1008,1008,1818,c30,c30,660,660,0,0,0,8*180,12*0,3e7c,1e78
  //   ,0,8,18,30,30,60,60,4*0,600,600,c00,c00,1800,1000,0,1e78,3e7c
  //   ,10*0,3e00,3e00,4000,7*6000,0,0,7*6000,4000,3e00,3e00,12*0,1000,1000
  //   ,1800,c00,c00,600,600,4*0,60,60,30,30,18,8,8,12*0,7c,7c,2,7*6
  //   ,0,0,7*6,2,7c,7c,12*0,240,660,660,c30,810,1818,1008,43*0,1e78,3e7c
endmodule
