// Digital circuit vgamain.dig as structural Verilog
module vgamain (
  input  clock,
  input  [6:0] D,
  input  [7:0] A,
  input  clk,
  input  [7:0] in_7,
  output [7:0] out_5,
  output [6:0] out_6,
  output [6:0] out_8
);

  wire add_1_c_o, delay_1_out, delay_2_out, not_1_out, vgacharpos_1_p3, vgacharpos_1_p4, vgasync_1_h,
       vgasync_1_pic, vgasync_1_v, vgatext_1_p15, vgatext_1_p16, vgatext_1_p17, vgatext_1_p18, vgatext_1_p19,
       WR_out;
  wire [6:0] driver_2_out, vgaline_1_c_o, vgaline_1_d_co, vgaline_2_c_o, vgaline_2_d_co, vgaline_3_c_o,
       vgaline_3_d_co, vgaline_4_c_o, vgaline_4_d_co, vgaline_5_c_o, vgaline_5_d_co, vgaline_6_c_o,
       vgaline_6_d_co;
  wire [7:0] add_1_s, driverinvsel_1_out, vgacharpos_1_p5, vgacharpos_1_p6, vgaline_1_cx_o, vgaline_1_cy_o,
       vgaline_1_pos_co, vgaline_1_pos_o, vgaline_2_cx_o, vgaline_2_cy_o, vgaline_2_pos_co, vgaline_2_pos_o,
       vgaline_3_cx_o, vgaline_3_cy_o, vgaline_3_pos_co, vgaline_3_pos_o, vgaline_4_cx_o, vgaline_4_cy_o,
       vgaline_4_pos_co, vgaline_4_pos_o, vgaline_5_cx_o, vgaline_5_cy_o, vgaline_5_pos_co, vgaline_5_pos_o,
       vgaline_6_cx_o, vgaline_6_cy_o, vgaline_6_pos_o;
  wire [10:0] vgatext_1_p20;
  wire [11:0] vgaline_1_bg_o, vgaline_1_fg_o, vgaline_2_bg_o, vgaline_2_fg_o, vgaline_3_bg_o, vgaline_3_fg_o,
       vgaline_4_bg_o, vgaline_4_fg_o, vgaline_5_bg_o, vgaline_5_fg_o, vgaline_6_bg_o, vgaline_6_fg_o;
  wire [15:0] Char_ROM_d, vgasync_1_x, vgasync_1_y, vgatext_1_p10;

  Add #(.Bits(8)) add_1 (.a(out_5), .b(8'h1), .c_i(1'b0), .s(add_1_s), .c_o(add_1_c_o));
  Delay #(.delayTime(10)) delay_1 (.in(clk), .out(delay_1_out));
  Register #(.Bits(8)) register_1 (.D(add_1_s), .C(delay_1_out), .en(clk), .Q(out_5));
  Button WR (.out(WR_out));
  assign driverinvsel_1_out = ~WR_out ? out_5 : 8'bz;  // DriverInvSel driverinvsel_1
  assign driverinvsel_1_out = WR_out ? A : 8'bz;  // Driver driver_1
  Delay #(.delayTime(10)) delay_2 (.in(WR_out), .out(delay_2_out));
  not not_1 (not_1_out, WR_out);
  EEPROM #(.AddrBits(8), .Bits(7)) eeprom_1 (
    .A(driverinvsel_1_out), .CS(1'b1), .WE(delay_2_out), .OE(not_1_out), .D(out_6));
  assign driver_2_out = not_1_out ? out_6 : 7'bz;  // Driver driver_2
  assign out_6 = delay_2_out ? D : 7'bz;  // Driver driver_3
  vgasync vgasync_1 (
    .clock(clock), .H(vgasync_1_h), .V(vgasync_1_v), .pic(vgasync_1_pic), .X(vgasync_1_x), .Y(vgasync_1_y));
  // vgacharpos vgacharpos_1: pin names not known; wires that end beside it: vgasync_1_x, vgasync_1_y, vgacharpos_1_p3, vgacharpos_1_p4, vgacharpos_1_p5, vgacharpos_1_p6
  vgaline vgaline_1 (
    .CX_i(vgacharpos_1_p5), .CY_i(vgacharpos_1_p6), .C_i({7{1'b0}}), .FG_i({12{1'b0}}), .BG_i({12{1'b0}}),
    .D_ci(driver_2_out), .POS_i(out_5), .POS_ci(in_7), .CX_o(vgaline_1_cx_o), .CY_o(vgaline_1_cy_o),
    .C_o(vgaline_1_c_o), .FG_o(vgaline_1_fg_o), .BG_o(vgaline_1_bg_o), .D_co(vgaline_1_d_co),
    .POS_o(vgaline_1_pos_o), .POS_co(vgaline_1_pos_co), .RPOS(out_8));  // open: D, A, clk, clock
  vgaline vgaline_2 (
    .CX_i(vgaline_1_cx_o), .CY_i(vgaline_1_cy_o), .C_i(vgaline_1_c_o), .FG_i(vgaline_1_fg_o),
    .BG_i(vgaline_1_bg_o), .D_ci(vgaline_1_d_co), .POS_i(vgaline_1_pos_o), .POS_ci(vgaline_1_pos_co),
    .CX_o(vgaline_2_cx_o), .CY_o(vgaline_2_cy_o), .C_o(vgaline_2_c_o), .FG_o(vgaline_2_fg_o),
    .BG_o(vgaline_2_bg_o), .D_co(vgaline_2_d_co), .POS_o(vgaline_2_pos_o), .POS_co(vgaline_2_pos_co));  // open: D, A, clk, clock, RPOS
  vgaline vgaline_3 (
    .CX_i(vgaline_2_cx_o), .CY_i(vgaline_2_cy_o), .C_i(vgaline_2_c_o), .FG_i(vgaline_2_fg_o),
    .BG_i(vgaline_2_bg_o), .D_ci(vgaline_2_d_co), .POS_i(vgaline_2_pos_o), .POS_ci(vgaline_2_pos_co),
    .CX_o(vgaline_3_cx_o), .CY_o(vgaline_3_cy_o), .C_o(vgaline_3_c_o), .FG_o(vgaline_3_fg_o),
    .BG_o(vgaline_3_bg_o), .D_co(vgaline_3_d_co), .POS_o(vgaline_3_pos_o), .POS_co(vgaline_3_pos_co));  // open: D, A, clk, clock, RPOS
  vgaline vgaline_4 (
    .CX_i(vgaline_3_cx_o), .CY_i(vgaline_3_cy_o), .C_i(vgaline_3_c_o), .FG_i(vgaline_3_fg_o),
    .BG_i(vgaline_3_bg_o), .D_ci(vgaline_3_d_co), .POS_i(vgaline_3_pos_o), .POS_ci(vgaline_3_pos_co),
    .CX_o(vgaline_4_cx_o), .CY_o(vgaline_4_cy_o), .C_o(vgaline_4_c_o), .FG_o(vgaline_4_fg_o),
    .BG_o(vgaline_4_bg_o), .D_co(vgaline_4_d_co), .POS_o(vgaline_4_pos_o), .POS_co(vgaline_4_pos_co));  // open: D, A, clk, clock, RPOS
  vgaline vgaline_5 (
    .CX_i(vgaline_4_cx_o), .CY_i(vgaline_4_cy_o), .C_i(vgaline_4_c_o), .FG_i(vgaline_4_fg_o),
    .BG_i(vgaline_4_bg_o), .D_ci(vgaline_4_d_co), .POS_i(vgaline_4_pos_o), .POS_ci(vgaline_4_pos_co),
    .CX_o(vgaline_5_cx_o), .CY_o(vgaline_5_cy_o), .C_o(vgaline_5_c_o), .FG_o(vgaline_5_fg_o),
    .BG_o(vgaline_5_bg_o), .D_co(vgaline_5_d_co), .POS_o(vgaline_5_pos_o), .POS_co(vgaline_5_pos_co));  // open: D, A, clk, clock, RPOS
  vgaline vgaline_6 (
    .CX_i(vgaline_5_cx_o), .CY_i(vgaline_5_cy_o), .C_i(vgaline_5_c_o), .FG_i(vgaline_5_fg_o),
    .BG_i(vgaline_5_bg_o), .D_ci(vgaline_5_d_co), .POS_i(vgaline_5_pos_o), .POS_ci(vgaline_5_pos_co),
    .CX_o(vgaline_6_cx_o), .CY_o(vgaline_6_cy_o), .C_o(vgaline_6_c_o), .FG_o(vgaline_6_fg_o),
    .BG_o(vgaline_6_bg_o), .D_co(vgaline_6_d_co), .POS_o(vgaline_6_pos_o));  // open: D, A, clk, clock, POS_co, RPOS
  // vgatext vgatext_1: pin names not known; wires that end beside it: vgaline_6_cx_o, vgaline_6_cy_o, vgaline_6_d_co, vgaline_6_pos_o, vgasync_1_h, vgasync_1_v, vgasync_1_pic, vgacharpos_1_p3, vgacharpos_1_p4, vgatext_1_p10, clock, vgaline_6_c_o, vgaline_6_fg_o, vgaline_6_bg_o, vgatext_1_p15, vgatext_1_p16, vgatext_1_p17, vgatext_1_p18, vgatext_1_p19, vgatext_1_p20
  ROM #(.AddrBits(11), .Bits(16)) Char_ROM (.A(vgatext_1_p20), .sel(1'b1), .D(Char_ROM_d));
  VGA vga_1 (.R(vgatext_1_p15), .G(vgatext_1_p16), .B(vgatext_1_p17), .H(vgatext_1_p18), .V(vgatext_1_p19), .C(clock));
  D_FF #(.Bits(16)) d_ff_1 (.D(Char_ROM_d), .C(clock), .Q(vgatext_1_p10));  // open: nQ

  // Other names for the same wires on the sheet: C = clock

  // Notes on the sheet:
  //   clock: Hz: 2147483647
  //   clk: Hz: 50
  //   contents of eeprom_1 (hex, n*v repeats v):
  //   7*41,43,41,41,49,41,41,41,45,41
  //   contents of Char_ROM (hex, n*v repeats v):
  //   35*0,8*180,0,0,8*180,12*0,3e7c,1e78,30*0,3e7c,3ffc,4182,6*6186
  //   ,4182,3e7c,3e7c,4182,6*6186,4182,3ffc,3e7c,10*0,3e7c,3ff8,4180
  //   ,6*6180,4180,3e7c,3e7c,182,6*186,182,1ffc,3e7c,10*0,3e00,3f00
  //   ,4188,6188,6198,61b0,61b0,61e0,61e0,4180,3e7c,3e7c,182,786,786
  //   ,d86,d86,1986,1186,1182,fc,7c,10*0,3e00,3f00,4180,6*6180,4180
  //   ,3f00,3e00,4000,6060,6060,6030,6030,6018,6008,4000,3e78,3e7c,12*0
  //   ,8,8,18,30,30,60,60,23*0,7c,78,200,600,600,c00,800,1800,1000,4*0
  //   ,1000,1800,800,c00,600,600,200,78,7c,10*0,3e00,1e00,40,60,60,30
  //   ,10,18,8,4*0,8,18,10,30,60,60,40,1e00,3e00,12*0,1188,1188,1998
  //   ,db0,db0,7e0,7e0,180,3e7c,3e7c,180,7e0,7e0,db0,db0,1998,1188,1188
  //   ,14*0,8*180,3e7c,3e7c,8*180,25*0,600,600,c00,c00,1800,1000,1000
  //   ,22*0,3e7c,3e7c,40*0,180,180,12*0,8,8,18,30,30,60,60,4*0,600,600
  //   ,c00,c00,1800,1000,1000,12*0,3e7c,3e7c,4006,600e,601a,6032,6036
  //   ,6066,6066,6006,0,0,6006,6606,6606,6c06,4c06,5806,7006,6002,3e7c,3e7c
  //   ,10*0,3e00,1f00,8*180,0,0,8*180,1ff8,3e7c,10*0,3e7c,1e7c,2,6*6
  //   ,2,3e7c,3e7c,4000,6*6000,4000,3e78,3e7c,10*0,3e7c,1e7c,2,6*6,2
  //   ,3e7c,3e7c,2,6*6,2,1e7c,3e7c,11*0,4002,7*6006,4002,3e7c,3e7c,2
  //   ,7*6,2,11*0,3e7c,3e78,4000,6*6000,4000,3e7c,3e7c,2,6*6,2,1e7c
  //   ,3e7c,10*0,3e7c,3e78,4000,6*6000,4000,3e7c,3e7c,4002,6*6006,4002
  //   ,3e7c,3e7c,10*0,3e7c,1e7c,2,7*6,0,0,8*6,2,11*0,3e7c,3e7c,4002
  //   ,6*6006,4002,3e7c,3e7c,4002,6*6006,4002,3e7c,3e7c,10*0,3e7c,3e7c
  //   ,4002,6*6006,4002,3e7c,3e7c,2,6*6,2,1e7c,3e7c,15*0,180,180,8*0
  //   ,180,180,17*0,8*180,0,0,0,600,600,c00,c00,1800,1000,1000,14*0
  //   ,40,c0,c0,180,180,300,300,4*0,300,300,180,180,c0,c0,40,17*0,3e7c,3e7c
  //   ,8*0,1e78,3e7c,17*0,200,300,300,180,180,c0,c0,4*0,c0,c0,180,180
  //   ,300,300,200,12*0,3e7c,1e7c,2,6*6,2,7c,fc,8*180,12*0,3e7c,3ffc
  //   ,4182,6*6186,6182,fc,7c,7*6000,4000,3e78,3e7c,10*0,3e7c,3e7c,4002
  //   ,6*6006,4002,3e7c,3e7c,4002,7*6006,4002,11*0,3e7c,1ffc,182,6*186
  //   ,182,3e7c,3e7c,182,6*186,182,1ffc,3e7c,10*0,3e7c,3e78,4000,7*6000
  //   ,0,0,7*6000,4000,3e78,3e7c,10*0,3e7c,1ffc,182,7*186,0,0,7*186
  //   ,182,1ffc,3e7c,10*0,3e7c,3e78,4000,6*6000,4000,3e7c,3e7c,4000
  //   ,6*6000,4000,3e78,3e7c,10*0,3e7c,3e78,4000,6*6000,4000,3e7c,3e7c
  //   ,4000,7*6000,4000,11*0,3e7c,3e78,4000,7*6000,7c,7c,6002,6*6006
  //   ,4002,3e7c,3e7c,11*0,4002,7*6006,4002,3e7c,3e7c,4002,7*6006,4002
  //   ,11*0,3e7c,1ff8,8*180,0,0,8*180,1ff8,3e7c,10*0,7c,7c,2,7*6,0,0
  //   ,7*6006,4002,3e7c,3e7c,11*0,4000,6008,6008,6018,6030,6030,6060,6060
  //   ,4000,3e00,3e00,4000,6060,6060,6030,6030,6018,6008,6008,4000,12*0
  //   ,4000,8*6000,0,0,7*6000,4000,3e78,3e7c,11*0,4002,6006,700e,581a
  //   ,4c32,6c36,6666,6666,6006,0,0,8*6186,4002,12*0,4002,6006,7006
  //   ,5806,4c06,6c06,6606,6606,6006,0,0,6006,6066,6066,6036,6032,601a
  //   ,600e,6006,4002,11*0,3e7c,3e7c,4002,7*6006,0,0,7*6006,4002,3e7c,3e7c
  //   ,10*0,3e7c,3e7c,4002,6*6006,4002,3e7c,3e7c,4000,7*6000,4000,11*0
  //   ,3e7c,3e7c,4002,7*6006,0,0,6006,6066,6066,6036,6032,601a,600e
  //   ,4006,3e7c,3e7c,10*0,3e7c,3e7c,4002,6*6006,4006,3e00,3e00,4000
  //   ,6060,6060,6030,6030,6018,6008,6008,4000,11*0,3e7c,3e78,4000,6*6000
  //   ,4000,3e7c,3e7c,2,6*6,2,1e7c,3e7c,10*0,3e7c,1ff8,8*180,0,0,8*180
  //   ,13*0,4002,8*6006,0,0,7*6006,4002,3e7c,3e7c,11*0,4000,6008,6008
  //   ,6018,6030,6030,6060,6060,6000,0,0,6000,6600,6600,6c00,4c00,5800
  //   ,7000,6000,4000,12*0,4002,8*6006,0,0,7*6186,4182,3ffc,3e7c,12*0
  //   ,1008,1008,1818,c30,c30,660,660,4*0,660,660,c30,c30,1818,1008,1008
  //   ,14*0,1008,1008,1818,c30,c30,660,660,0,0,0,8*180,12*0,3e7c,1e78
  //   ,0,8,18,30,30,60,60,4*0,600,600,c00,c00,1800,1000,0,1e78,3e7c
  //   ,10*0,3e00,3e00,4000,7*6000,0,0,7*6000,4000,3e00,3e00,12*0,1000,1000
  //   ,1800,c00,c00,600,600,4*0,60,60,30,30,18,8,8,12*0,7c,7c,2,7*6
  //   ,0,0,7*6,2,7c,7c,12*0,240,660,660,c30,810,1818,1008,43*0,1e78,3e7c
endmodule
