// Digital circuit vgatiming.dig as structural Verilog
module vgatiming (
  input  en,
  input  clock,
  input  [15:0] res,
  input  [15:0] fp,
  input  [15:0] sync,
  input  [15:0] bp,
  input  neg,
  output [15:0] V,
  output pulse,
  output next
);

  wire and_1_out, comparator_2_eq, comparator_3_eq, d_ff_1_q, or_1_out;
  wire [15:0] sub_1_s, sub_2_s, sub_3_s, sub_4_s;

  Sub #(.Bits(16)) sub_1 (.a(res), .b(16'h1), .c_i(1'b0), .s(sub_1_s));  // open: c_o
  Sub #(.Bits(16)) sub_2 (.a({16{1'b0}}), .b(bp), .c_i(1'b0), .s(sub_2_s));  // open: c_o
  Sub #(.Bits(16)) sub_3 (.a(sub_2_s), .b(sync), .c_i(1'b0), .s(sub_3_s));  // open: c_o
  Sub #(.Bits(16)) sub_4 (.a(sub_3_s), .b(fp), .c_i(1'b0), .s(sub_4_s));  // open: c_o
  Comparator #(.Bits(16)) comparator_1 (.a(V), .b(sub_1_s), .eq(next));  // open: gt, lt
  Comparator #(.Bits(16)) comparator_2 (.a(V), .b(sub_2_s), .eq(comparator_2_eq));  // open: gt, lt
  Comparator #(.Bits(16)) comparator_3 (.a(V), .b(sub_3_s), .eq(comparator_3_eq));  // open: gt, lt
  or or_1 (or_1_out, comparator_3_eq, d_ff_1_q);
  and and_1 (and_1_out, ~comparator_2_eq, or_1_out);  // And
  D_FF d_ff_1 (.D(and_1_out), .C(clock), .Q(d_ff_1_q));  // open: nQ
  xor xor_1 (pulse, d_ff_1_q, neg);
  CounterPreset #(.Bits(16)) counterpreset_1 (
    .en(en), .C(clock), .dir(1'b0), .in(sub_4_s), .ld(next), .clr(1'b0), .out(V));  // open: ovf

  // Other names for the same wires on the sheet: C = clock

  // Notes on the sheet:
  //   res: default 5
  //   fp: default 3
  //   sync: default 5
  //   bp: default 4
  //   neg: default 48
endmodule
