// Digital circuit LEDDISPLAY.dig as structural Verilog
module LEDDISPLAY (
  input  LEDD_EN,
  input  [7:0] LEDD_X,
  input  [7:0] LEDD_Y,
  output [7:0] LEDD_D,
  output LEDD_0,
  output LEDD_1,
  output LEDD_2,
  output LEDD_3,
  output LEDD_4,
  output LEDD_5,
  output LEDD_6,
  output LEDD_7
);

  wire and_1_out, and_2_out, and_3_out, and_4_out, and_5_out, and_6_out, and_7_out, and_8_out, not_1_out,
       not_2_out, not_3_out, not_4_out, not_5_out, not_6_out, not_7_out, not_8_out, not_9_out, not_10_out,
       not_11_out, not_12_out;

  not not_1 (not_1_out, LEDD_X[0]);
  not not_2 (not_2_out, LEDD_X[1]);
  not not_3 (not_3_out, LEDD_X[2]);
  not not_4 (not_4_out, LEDD_X[1]);
  not not_5 (not_5_out, LEDD_X[2]);
  not not_6 (not_6_out, LEDD_X[0]);
  not not_7 (not_7_out, LEDD_X[2]);
  not not_8 (not_8_out, LEDD_X[2]);
  not not_9 (not_9_out, LEDD_X[0]);
  not not_10 (not_10_out, LEDD_X[1]);
  not not_11 (not_11_out, LEDD_X[1]);
  not not_12 (not_12_out, LEDD_X[0]);
  and and_1 (and_1_out, not_1_out, not_2_out, not_3_out);
  and and_2 (and_2_out, LEDD_X[0], not_4_out, not_5_out);
  and and_3 (and_3_out, not_6_out, LEDD_X[1], not_7_out);
  and and_4 (and_4_out, LEDD_X[0], LEDD_X[1], not_8_out);
  and and_5 (and_5_out, not_9_out, not_10_out, LEDD_X[2]);
  and and_6 (and_6_out, LEDD_X[0], not_11_out, LEDD_X[2]);
  and and_7 (and_7_out, not_12_out, LEDD_X[1], LEDD_X[2]);
  and and_8 (and_8_out, LEDD_X[0], LEDD_X[1], LEDD_X[2]);
  assign LEDD_0 = LEDD_EN ? and_1_out : 1'bz;  // Driver driver_1
  PullDown pulldown_1 (.out(LEDD_0));
  assign LEDD_1 = LEDD_EN ? and_2_out : 1'bz;  // Driver driver_2
  PullDown pulldown_2 (.out(LEDD_1));
  assign LEDD_2 = LEDD_EN ? and_3_out : 1'bz;  // Driver driver_3
  PullDown pulldown_3 (.out(LEDD_2));
  assign LEDD_3 = LEDD_EN ? and_4_out : 1'bz;  // Driver driver_4
  PullDown pulldown_4 (.out(LEDD_3));
  assign LEDD_4 = LEDD_EN ? and_5_out : 1'bz;  // Driver driver_5
  PullDown pulldown_5 (.out(LEDD_4));
  assign LEDD_5 = LEDD_EN ? and_6_out : 1'bz;  // Driver driver_6
  PullDown pulldown_6 (.out(LEDD_5));
  assign LEDD_6 = LEDD_EN ? and_7_out : 1'bz;  // Driver driver_7
  PullDown pulldown_7 (.out(LEDD_6));
  assign LEDD_7 = LEDD_EN ? and_8_out : 1'bz;  // Driver driver_8
  PullDown pulldown_8 (.out(LEDD_7));
  PullDown #(.Bits(8)) pulldown_9 (.out(LEDD_D));
  assign LEDD_D = LEDD_EN ? LEDD_Y : 8'bz;  // Driver driver_9
endmodule
