// Digital circuit INT-DECIDER.dig as structural Verilog
module INT_DECIDER (
  input  [7:0] LOC,
  input  INT,
  output INT_FULL,
  output INT_DEL,
  output CHNG_MODE,
  output CHNG_BANK
);

  wire and_1_out, and_2_out, and_3_out, and_4_out, and_5_out, and_6_out, and_7_out, and_8_out, and_9_out,
       and_10_out, and_11_out, and_12_out, and_13_out, and_14_out, and_15_out, and_16_out, and_17_out,
       and_18_out, and_19_out, and_20_out, and_21_out, and_22_out, and_23_out, and_24_out, and_25_out,
       and_26_out, and_27_out, and_28_out, not_1_out, not_2_out, not_3_out, not_4_out, not_5_out, not_6_out,
       not_7_out, not_8_out, not_9_out, not_10_out, not_11_out, not_12_out, not_13_out, not_14_out,
       not_15_out, not_16_out, not_17_out, not_18_out, not_19_out, not_20_out, not_21_out, not_22_out,
       not_23_out, not_24_out, not_25_out, not_26_out, not_27_out, not_28_out;

  not not_1 (not_1_out, LOC[0]);
  not not_2 (not_2_out, LOC[1]);
  not not_3 (not_3_out, LOC[2]);
  not not_4 (not_4_out, LOC[3]);
  not not_5 (not_5_out, LOC[4]);
  not not_6 (not_6_out, LOC[5]);
  not not_7 (not_7_out, LOC[6]);
  not not_8 (not_8_out, LOC[7]);
  not not_9 (not_9_out, LOC[1]);
  not not_10 (not_10_out, LOC[2]);
  not not_11 (not_11_out, LOC[3]);
  not not_12 (not_12_out, LOC[4]);
  not not_13 (not_13_out, LOC[5]);
  not not_14 (not_14_out, LOC[6]);
  not not_15 (not_15_out, LOC[7]);
  not not_16 (not_16_out, LOC[0]);
  not not_17 (not_17_out, LOC[2]);
  not not_18 (not_18_out, LOC[3]);
  not not_19 (not_19_out, LOC[4]);
  not not_20 (not_20_out, LOC[5]);
  not not_21 (not_21_out, LOC[6]);
  not not_22 (not_22_out, LOC[7]);
  not not_23 (not_23_out, LOC[2]);
  not not_24 (not_24_out, LOC[3]);
  not not_25 (not_25_out, LOC[4]);
  not not_26 (not_26_out, LOC[5]);
  not not_27 (not_27_out, LOC[6]);
  not not_28 (not_28_out, LOC[7]);
  and and_1 (and_1_out, not_1_out, not_2_out);
  and and_2 (and_2_out, not_3_out, not_4_out);
  and and_3 (and_3_out, not_5_out, not_6_out);
  and and_4 (and_4_out, not_7_out, not_8_out);
  and and_5 (and_5_out, LOC[0], not_9_out);
  and and_6 (and_6_out, not_10_out, not_11_out);
  and and_7 (and_7_out, not_12_out, not_13_out);
  and and_8 (and_8_out, not_14_out, not_15_out);
  and and_9 (and_9_out, not_16_out, LOC[1]);
  and and_10 (and_10_out, not_17_out, not_18_out);
  and and_11 (and_11_out, not_19_out, not_20_out);
  and and_12 (and_12_out, not_21_out, not_22_out);
  and and_13 (and_13_out, LOC[0], LOC[1]);
  and and_14 (and_14_out, not_23_out, not_24_out);
  and and_15 (and_15_out, not_25_out, not_26_out);
  and and_16 (and_16_out, not_27_out, not_28_out);
  and and_17 (and_17_out, and_1_out, and_2_out);
  and and_18 (and_18_out, and_3_out, and_4_out);
  and and_19 (and_19_out, and_5_out, and_6_out);
  and and_20 (and_20_out, and_7_out, and_8_out);
  and and_21 (and_21_out, and_9_out, and_10_out);
  and and_22 (and_22_out, and_11_out, and_12_out);
  and and_23 (and_23_out, and_13_out, and_14_out);
  and and_24 (and_24_out, and_15_out, and_16_out);
  and and_25 (and_25_out, and_17_out, and_18_out);
  and and_26 (and_26_out, and_19_out, and_20_out);
  and and_27 (and_27_out, and_21_out, and_22_out);
  and and_28 (and_28_out, and_23_out, and_24_out);
  and and_29 (INT_FULL, INT, and_25_out);
  and and_30 (INT_DEL, INT, and_26_out);
  and and_31 (CHNG_MODE, INT, and_27_out);
  and and_32 (CHNG_BANK, INT, and_28_out);
endmodule
