// Digital circuit PES.dig as structural Verilog
module PES (
  input  clk,
  input  in_2,
  input  GET_2_CLK,
  input  GET_2_EXT,
  input  GET_2_SEL,
  output [7:0] out_3,
  output [7:0] out_4,
  output [2:0] out_5,
  output out_9,
  output [7:0] out_10,
  output [7:0] out_11
);

  wire and_1_out, and_2_out, and_6_out, and_8_out, and_10_out, delay_1_out, delay_2_out, delay_3_out,
       delay_4_out, delay_5_out, delay_6_out, driver_1_out, driverinvsel_1_out, GEN_RND, GET_2_MAN_out,
       not_1_out, not_2_out, not_3_out, not_4_out, not_5_out, not_6_out, not_7_out, not_8_out, not_9_out,
       not_10_out, not_11_out, not_12_out, NULL, pulldown_1_out, pulldown_3_out, pulldown_4_out, rnd_1_rnd_c,
       ST_RR1, ST_RR2, t_ff_1_q;

  and and_1 (and_1_out, driverinvsel_1_out, ~delay_1_out);  // And
  Delay #(.delayTime(20)) delay_1 (.in(driverinvsel_1_out), .out(delay_1_out));
  RND rnd_1 (.RND_CLK(clk), .EXT_RND(GEN_RND), .MAN_EXT(in_2), .RND_C(rnd_1_rnd_c), .CUR_RND(out_3), .OUT_RND(out_4));
  assign driver_1_out = and_1_out ? and_1_out : 1'bz;  // Driver driver_1
  PullDown pulldown_1 (.out(pulldown_1_out));
  PullDown pulldown_2 (.out(driver_1_out));
  PullDown pulldown_3 (.out(pulldown_3_out));
  PullDown pulldown_4 (.out(pulldown_4_out));
  Button GET_2_MAN (.out(GET_2_MAN_out));
  Delay #(.delayTime(10)) delay_2 (.in(driver_1_out), .out(delay_2_out));
  assign driver_1_out = and_10_out ? and_10_out : 1'bz;  // Driver driver_2
  assign driverinvsel_1_out = ~GET_2_SEL ? GET_2_EXT : 1'bz;  // DriverInvSel driverinvsel_1
  assign driverinvsel_1_out = GET_2_SEL ? GET_2_MAN_out : 1'bz;  // Driver driver_3
  T_FF t_ff_1 (.T(driver_1_out), .C(delay_2_out), .Q(t_ff_1_q));  // open: nQ
  LED led_1 (.in(rnd_1_rnd_c));
  and and_2 (and_2_out, t_ff_1_q, GET_2_CLK);
  assign pulldown_1_out = ~and_10_out ? and_2_out : 1'bz;  // DriverInvSel driverinvsel_2
  assign pulldown_3_out = pulldown_1_out ? pulldown_1_out : 1'bz;  // Driver driver_4
  assign pulldown_3_out = delay_3_out ? delay_3_out : 1'bz;  // Driver driver_5
  Delay #(.delayTime(10)) delay_3 (.in(and_10_out), .out(delay_3_out));
  Counter #(.Bits(3)) counter_1 (
    .en(pulldown_3_out), .C(pulldown_3_out), .clr(pulldown_4_out), .out(out_5), .ovf(out_9));
  assign pulldown_4_out = delay_3_out ? delay_3_out : 1'bz;  // Driver driver_6
  not not_1 (not_1_out, out_5[0]);
  not not_2 (not_2_out, out_5[1]);
  not not_3 (not_3_out, out_5[2]);
  not not_4 (not_4_out, out_5[1]);
  not not_5 (not_5_out, out_5[2]);
  not not_6 (not_6_out, out_5[0]);
  not not_7 (not_7_out, out_5[2]);
  not not_8 (not_8_out, out_5[2]);
  not not_9 (not_9_out, out_5[0]);
  not not_10 (not_10_out, out_5[1]);
  not not_11 (not_11_out, out_5[1]);
  not not_12 (not_12_out, out_5[0]);
  and and_3 (NULL, not_1_out, not_2_out, not_3_out);
  // And and_4 has open pins: In_1=out_5[0], In_2=not_4_out, In_3=not_5_out, out=open
  // And and_5 has open pins: In_1=not_6_out, In_2=out_5[1], In_3=not_7_out, out=open
  and and_6 (and_6_out, out_5[0], out_5[1], not_8_out);
  and and_7 (ST_RR1, not_9_out, not_10_out, out_5[2]);
  and and_8 (and_8_out, out_5[0], not_11_out, out_5[2]);
  and and_9 (ST_RR2, not_12_out, out_5[1], out_5[2]);
  and and_10 (and_10_out, out_5[0], out_5[1], out_5[2]);
  Delay #(.delayTime(20)) delay_4 (.in(and_8_out), .out(delay_4_out));
  Register #(.Bits(8)) RR1 (.D(out_4), .C(delay_5_out), .en(ST_RR1), .Q(out_10));
  Delay #(.delayTime(10)) delay_5 (.in(ST_RR1), .out(delay_5_out));
  Register #(.Bits(8)) RR2 (.D(out_4), .C(delay_6_out), .en(ST_RR2), .Q(out_11));
  Delay #(.delayTime(10)) delay_6 (.in(ST_RR2), .out(delay_6_out));
  assign GEN_RND = and_6_out ? and_6_out : 1'bz;  // Driver driver_7
  PullDown pulldown_5 (.out(GEN_RND));
  assign GEN_RND = delay_4_out ? delay_4_out : 1'bz;  // Driver driver_8
  PullDown pulldown_6 (.out(GEN_RND));

  // Other names for the same wires on the sheet: OUT_RND[7:0] = out_4; RR1[7:0] = out_10; RR2[7:0] = out_11

  // Notes on the sheet:
  //   clk: Hz: 5000
  //   GET_2_CLK: Hz: 100
  //   1213
  //   RND
  //   PES-KEY
  //   GEN-KEY
  //   < ADD 
  //       RND 
  //     DELAY
endmodule
