// Digital circuit RND.dig as structural Verilog
module RND (
  input  RND_CLK,
  input  EXT_RND,
  input  MAN_EXT,
  output RND_C,
  output [7:0] CUR_RND,
  output [7:0] OUT_RND
);

  wire delay_1_out, delay_2_out, driverinvsel_1_out, MAN_RND_out;
  wire [7:0] add_1_s;

  Add #(.Bits(8)) add_1 (.a(CUR_RND), .b(8'h1), .c_i(1'b0), .s(add_1_s), .c_o(RND_C));
  assign driverinvsel_1_out = ~MAN_EXT ? EXT_RND : 1'bz;  // DriverInvSel driverinvsel_1
  Button MAN_RND (.out(MAN_RND_out));
  assign driverinvsel_1_out = MAN_EXT ? MAN_RND_out : 1'bz;  // Driver driver_1
  Delay #(.delayTime(10)) delay_1 (.in(RND_CLK), .out(delay_1_out));
  Register #(.Bits(8)) register_1 (.D(add_1_s), .C(delay_1_out), .en(RND_CLK), .Q(CUR_RND));
  Delay #(.delayTime(10)) delay_2 (.in(driverinvsel_1_out), .out(delay_2_out));
  Register #(.Bits(8)) register_2 (.D(CUR_RND), .C(delay_2_out), .en(driverinvsel_1_out), .Q(OUT_RND));

  // Notes on the sheet:
  //   RND_CLK: Hz: 5000
  //   1213
  //   Random Number Generator
endmodule
