// Digital circuit TEST.dig as structural Verilog
module TEST (
  input  RND_CLK,
  input  EXT_RND,
  input  MAN_EXT,
  output out_1,
  output [7:0] out_2,
  output [7:0] out_5
);

  wire delay_1_out, delay_2_out, driverinvsel_1_out, MAN_RND_out;
  wire [7:0] add_1_s;

  Button MAN_RND (.out(MAN_RND_out));
  Add #(.Bits(8)) add_1 (.a(out_2), .b(8'h1), .c_i(1'b0), .s(add_1_s), .c_o(out_1));
  assign driverinvsel_1_out = ~MAN_EXT ? EXT_RND : 1'bz;  // DriverInvSel driverinvsel_1
  assign driverinvsel_1_out = MAN_EXT ? MAN_RND_out : 1'bz;  // Driver driver_1
  Delay #(.delayTime(10)) delay_1 (.in(RND_CLK), .out(delay_1_out));
  Register #(.Bits(8)) register_1 (.D(add_1_s), .C(delay_1_out), .en(RND_CLK), .Q(out_2));
  Delay #(.delayTime(10)) delay_2 (.in(driverinvsel_1_out), .out(delay_2_out));
  Register #(.Bits(8)) register_2 (.D(out_2), .C(delay_2_out), .en(driverinvsel_1_out), .Q(out_5));

  // Notes on the sheet:
  //   RND_CLK: Hz: 5000
  //   1213
endmodule
