// Digital circuit test.dig as structural Verilog
module test (
  input  [9:0] in_1
);

  wire one_1_p4;
  wire [3:0] one_1_p6, one_1_p6_2;
  wire [9:0] one_1_p3;
  wire [23:0] one_1_p5, rom_1_d;

  ROM #(.AddrBits(10), .Bits(24)) rom_1 (.A(one_1_p3), .sel(one_1_p4), .D(rom_1_d));
  // one one_1: pin names not known; wires that end beside it: in_1, rom_1_d, one_1_p3, one_1_p4, one_1_p5, {one_1_p6_2, one_1_p6}
  Seven_Seg seven_seg_1 (
    .a(one_1_p6_2[0]), .b(one_1_p6_2[1]), .c(one_1_p6_2[2]), .d(one_1_p6_2[3]), .e(one_1_p6[0]),
    .f(one_1_p6[1]), .g(one_1_p6[2]), .dp(one_1_p6[3]));
  Seven_Seg seven_seg_2 (
    .a(one_1_p5[8]), .b(one_1_p5[9]), .c(one_1_p5[10]), .d(one_1_p5[11]), .e(one_1_p5[12]), .f(one_1_p5[13]),
    .g(one_1_p5[14]), .dp(one_1_p5[15]));
  Seven_Seg seven_seg_3 (
    .a(one_1_p5[4]), .b(one_1_p5[5]), .c(one_1_p5[6]), .d(one_1_p5[7]), .e(one_1_p5[16]), .f(one_1_p5[17]),
    .g(one_1_p5[18]), .dp(one_1_p5[19]));
  Seven_Seg seven_seg_4 (
    .a(one_1_p5[0]), .b(one_1_p5[1]), .c(one_1_p5[2]), .d(one_1_p5[3]), .e(one_1_p5[20]), .f(one_1_p5[21]),
    .g(one_1_p5[22]), .dp(one_1_p5[23]));

  // Notes on the sheet:
  //   contents of rom_1 (hex, n*v repeats v):
  //   3f3f3f,3f3f06,3f3f5b,3f3f4f,3f3f66,3f3f6d,3f3f7d,3f3f07,3f3f7f
  //   ,3f3f6f,3f063f,3f0606,3f065b,3f064f,3f0666,3f066d,3f067d,3f0607
  //   ,3f067f,3f066f,3f5b3f,3f5b06,3f5b5b,3f5b4f,3f5b66,3f5b6d,3f5b7d
  //   ,3f5b07,3f5b7f,3f5b6f,3f4f3f,3f4f06,3f4f5b,3f4f4f,3f4f66,3f4f6d
  //   ,3f4f7d,3f4f07,3f4f7f,3f4f6f,3f663f,3f6606,3f665b,3f664f,3f6666
  //   ,3f666d,3f667d,3f6607,3f667f,3f666f,3f6d3f,3f6d06,3f6d5b,3f6d4f
  //   ,3f6d66,3f6d6d,3f6d7d,3f6d07,3f6d7f,3f6d6f,3f7d3f,3f7d06,3f7d5b
  //   ,3f7d4f,3f7d66,3f7d6d,3f7d7d,3f7d07,3f7d7f,3f7d6f,3f073f,3f0706
  //   ,3f075b,3f074f,3f0766,3f076d,3f077d,3f0707,3f077f,3f076f,3f7f3f
  //   ,3f7f06,3f7f5b,3f7f4f,3f7f66,3f7f6d,3f7f7d,3f7f07,3f7f7f,3f7f6f
  //   ,3f6f3f,3f6f06,3f6f5b,3f6f4f,3f6f66,3f6f6d,3f6f7d,3f6f07,3f6f7f
  //   ,3f6f6f,63f3f,63f06,63f5b,63f4f,63f66,63f6d,63f7d,63f07,63f7f
  //   ,63f6f,6063f,60606,6065b,6064f,60666,6066d,6067d,60607,6067f,6066f
  //   ,65b3f,65b06,65b5b,65b4f,65b66,65b6d,65b7d,65b07,65b7f,65b6f,64f3f
  //   ,64f06,64f5b,64f4f,64f66,64f6d,64f7d,64f07,64f7f,64f6f,6663f,66606
  //   ,6665b,6664f,66666,6666d,6667d,66607,6667f,6666f,66d3f,66d06,66d5b
  //   ,66d4f,66d66,66d6d,66d7d,66d07,66d7f,66d6f,67d3f,67d06,67d5b,67d4f
  //   ,67d66,67d6d,67d7d,67d07,67d7f,67d6f,6073f,60706,6075b,6074f,60766
  //   ,6076d,6077d,60707,6077f,6076f,67f3f,67f06,67f5b,67f4f,67f66,67f6d
  //   ,67f7d,67f07,67f7f,67f6f,66f3f,66f06,66f5b,66f4f,66f66,66f6d,66f7d
  //   ,66f07,66f7f,66f6f,5b3f3f,5b3f06,5b3f5b,5b3f4f,5b3f66,5b3f6d,5b3f7d
  //   ,5b3f07,5b3f7f,5b3f6f,5b063f,5b0606,5b065b,5b064f,5b0666,5b066d
  //   ,5b067d,5b0607,5b067f,5b066f,5b5b3f,5b5b06,5b5b5b,5b5b4f,5b5b66
  //   ,5b5b6d,5b5b7d,5b5b07,5b5b7f,5b5b6f,5b4f3f,5b4f06,5b4f5b,5b4f4f
  //   ,5b4f66,5b4f6d,5b4f7d,5b4f07,5b4f7f,5b4f6f,5b663f,5b6606,5b665b
  //   ,5b664f,5b6666,5b666d,5b667d,5b6607,5b667f,5b666f,5b6d3f,5b6d06
  //   ,5b6d5b,5b6d4f,5b6d66,5b6d6d,5b6d7d,5b6d07,5b6d7f,5b6d6f,5b7d3f
  //   ,5b7d06,5b7d5b,5b7d4f,5b7d66,5b7d6d,5b7d7d,5b7d07,5b7d7f,5b7d6f
  //   ,5b073f,5b0706,5b075b,5b074f,5b0766,5b076d,5b077d,5b0707,5b077f
  //   ,5b076f,5b7f3f,5b7f06,5b7f5b,5b7f4f,5b7f66,5b7f6d,5b7f7d,5b7f07
  //   ,5b7f7f,5b7f6f,5b6f3f,5b6f06,5b6f5b,5b6f4f,5b6f66,5b6f6d,5b6f7d
  //   ,5b6f07,5b6f7f,5b6f6f,4f3f3f,4f3f06,4f3f5b,4f3f4f,4f3f66,4f3f6d
  //   ,4f3f7d,4f3f07,4f3f7f,4f3f6f,4f063f,4f0606,4f065b,4f064f,4f0666
  //   ,4f066d,4f067d,4f0607,4f067f,4f066f,4f5b3f,4f5b06,4f5b5b,4f5b4f
  //   ,4f5b66,4f5b6d,4f5b7d,4f5b07,4f5b7f,4f5b6f,4f4f3f,4f4f06,4f4f5b
  //   ,4f4f4f,4f4f66,4f4f6d,4f4f7d,4f4f07,4f4f7f,4f4f6f,4f663f,4f6606
  //   ,4f665b,4f664f,4f6666,4f666d,4f667d,4f6607,4f667f,4f666f,4f6d3f
  //   ,4f6d06,4f6d5b,4f6d4f,4f6d66,4f6d6d,4f6d7d,4f6d07,4f6d7f,4f6d6f
  //   ,4f7d3f,4f7d06,4f7d5b,4f7d4f,4f7d66,4f7d6d,4f7d7d,4f7d07,4f7d7f
  //   ,4f7d6f,4f073f,4f0706,4f075b,4f074f,4f0766,4f076d,4f077d,4f0707
  //   ,4f077f,4f076f,4f7f3f,4f7f06,4f7f5b,4f7f4f,4f7f66,4f7f6d,4f7f7d
  //   ,4f7f07,4f7f7f,4f7f6f,4f6f3f,4f6f06,4f6f5b,4f6f4f,4f6f66,4f6f6d
  //   ,4f6f7d,4f6f07,4f6f7f,4f6f6f,663f3f,663f06,663f5b,663f4f,663f66
  //   ,663f6d,663f7d,663f07,663f7f,663f6f,66063f,660606,66065b,66064f
  //   ,660666,66066d,66067d,660607,66067f,66066f,665b3f,665b06,665b5b
  //   ,665b4f,665b66,665b6d,665b7d,665b07,665b7f,665b6f,664f3f,664f06
  //   ,664f5b,664f4f,664f66,664f6d,664f7d,664f07,664f7f,664f6f,66663f
  //   ,666606,66665b,66664f,666666,66666d,66667d,666607,66667f,66666f
  //   ,666d3f,666d06,666d5b,666d4f,666d66,666d6d,666d7d,666d07,666d7f
  //   ,666d6f,667d3f,667d06,667d5b,667d4f,667d66,667d6d,667d7d,667d07
  //   ,667d7f,667d6f,66073f,660706,66075b,66074f,660766,66076d,66077d
  //   ,660707,66077f,66076f,667f3f,667f06,667f5b,667f4f,667f66,667f6d
  //   ,667f7d,667f07,667f7f,667f6f,666f3f,666f06,666f5b,666f4f,666f66
  //   ,666f6d,666f7d,666f07,666f7f,666f6f,6d3f3f,6d3f06,6d3f5b,6d3f4f
  //   ,6d3f66,6d3f6d,6d3f7d,6d3f07,6d3f7f,6d3f6f,6d063f,6d0606,6d065b
  //   ,6d0606,6d063f,6d3f6f,6d3f7f,6d3f07,6d3f7d,6d3f6d,6d3f66,6d3f4f
  //   ,6d3f5b,6d3f06,6d3f3f,666f6f,666f7f,666f07,666f7d,666f6d,666f66
  //   ,666f4f,666f5b,666f06,666f3f,667f6f,667f7f,667f07,667f7d,667f6d
  //   ,667f66,667f4f,667f5b,667f06,667f3f,66076f,66077f,660707,66077d
  //   ,66076d,660766,66074f,66075b,660706,66073f,667d6f,667d7f,667d07
  //   ,667d7d,667d6d,667d66,667d4f,667d5b,667d06,667d3f,666d6f,666d7f
  //   ,666d07,666d7d,666d6d,666d66,666d4f,666d5b,666d06,666d3f,66666f
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endmodule
