// Digital circuit two.dig as structural Verilog
module two (
  input  [9:0] IN,
  input  [23:0] OUT_IN,
  output [9:0] ADDR,
  output SEL
);

  wire comparator_1_eq, comparator_1_gt, comparator_1_lt;
  wire [2:2] and_1_out;

  Comparator #(.Bits(10)) comparator_1 (
    .a(IN), .b(10'h1ff), .gt(comparator_1_gt), .eq(comparator_1_eq), .lt(comparator_1_lt));
  and and_1 (and_1_out[2], comparator_1_gt, 1'b1);
  Seven_Seg seven_seg_1 (.a(1'b0), .b(1'b0), .c(1'b0), .d(1'b0), .e(1'b0), .f(1'b0), .g(and_1_out[2]), .dp(1'b0));
  // Pins of 1 and 24 bits meet at OUT_IN

  assign ADDR = IN;
  assign SEL = 1'b1;
endmodule
