// Digital circuit HEX2DEC.dig as structural Verilog
module HEX2DEC (
  input  [9:0] IN,
  input  DOT,
  input  [1:0] EXTRA,
  input  [1:0] _1ST_1ST,
  input  [1:0] _1ST_2ND,
  input  [1:0] _1ST_3RD,
  input  [1:0] _1ST_4TH,
  input  [3:0] _2ND_1ST,
  input  [3:0] _2ND_2ND,
  input  [3:0] _2ND_3RD,
  input  [3:0] _2ND_4TH,
  input  [3:0] _2ND_5TH,
  input  [3:0] _2ND_6TH,
  input  [3:0] _2ND_7TH,
  input  [3:0] _2ND_8TH,
  input  [3:0] _2ND_9TH,
  input  [3:0] _2ND_10TH,
  input  [3:0] _3RD_1ST,
  input  [3:0] _3RD_2ND,
  input  [3:0] _3RD_3RD,
  input  [3:0] _3RD_4TH,
  input  [3:0] _3RD_5TH,
  input  [3:0] _3RD_6TH,
  input  [3:0] _3RD_7TH,
  input  [3:0] _3RD_8TH,
  input  [3:0] _3RD_9TH,
  input  [3:0] _3RD_10TH
);

  wire comparator_1_eq, comparator_1_gt, comparator_1_lt, comparator_2_eq, comparator_2_gt, comparator_2_lt,
       comparator_3_eq, comparator_3_gt, comparator_3_lt, comparator_4_eq, comparator_4_gt, comparator_4_lt,
       comparator_5_eq, comparator_5_gt, comparator_5_lt, comparator_6_eq, comparator_6_gt, comparator_6_lt,
       comparator_7_eq, comparator_7_gt, comparator_7_lt, comparator_8_eq, comparator_8_gt, comparator_8_lt,
       comparator_9_eq, comparator_9_gt, comparator_9_lt, comparator_10_eq, comparator_10_gt,
       comparator_10_lt, comparator_11_eq, comparator_11_gt, comparator_11_lt, comparator_12_eq,
       comparator_12_gt, comparator_12_lt, comparator_13_eq, comparator_13_gt, comparator_13_lt,
       comparator_14_eq, comparator_14_gt, comparator_14_lt, comparator_15_eq, comparator_15_gt,
       comparator_15_lt, comparator_16_eq, comparator_16_gt, comparator_16_lt, comparator_17_eq,
       comparator_17_gt, comparator_17_lt, comparator_18_eq, comparator_18_gt, comparator_18_lt,
       comparator_19_eq, comparator_19_gt, comparator_19_lt, comparator_20_eq, comparator_20_gt,
       comparator_20_lt, comparator_21_eq, comparator_21_gt, comparator_21_lt, comparator_22_eq,
       comparator_22_gt, comparator_22_lt, comparator_23_eq, comparator_23_gt, comparator_23_lt,
       comparator_24_eq, comparator_24_gt, comparator_24_lt;

  Seven_Seg_Hex seven_seg_hex_1 (.d({EXTRA, IN[9:8]}), .dp(DOT));
  Seven_Seg_Hex seven_seg_hex_2 (.d(IN[7:4]), .dp(DOT));
  Comparator #(.Bits(2)) comparator_1 (
    .a(IN[9:8]), .b(_1ST_1ST), .gt(comparator_1_gt), .eq(comparator_1_eq), .lt(comparator_1_lt));
  Comparator #(.Bits(2)) comparator_2 (
    .a(IN[9:8]), .b(_1ST_2ND), .gt(comparator_2_gt), .eq(comparator_2_eq), .lt(comparator_2_lt));
  Comparator #(.Bits(2)) comparator_3 (
    .a(IN[9:8]), .b(_1ST_3RD), .gt(comparator_3_gt), .eq(comparator_3_eq), .lt(comparator_3_lt));
  Comparator #(.Bits(2)) comparator_4 (
    .a(IN[9:8]), .b(_1ST_4TH), .gt(comparator_4_gt), .eq(comparator_4_eq), .lt(comparator_4_lt));
  Seven_Seg_Hex seven_seg_hex_3 (.d(IN[3:0]), .dp(DOT));
  Comparator #(.Bits(4)) comparator_5 (
    .a(IN[7:4]), .b(_2ND_1ST), .gt(comparator_5_gt), .eq(comparator_5_eq), .lt(comparator_5_lt));
  Comparator #(.Bits(4)) comparator_6 (
    .a(IN[7:4]), .b(_2ND_2ND), .gt(comparator_6_gt), .eq(comparator_6_eq), .lt(comparator_6_lt));
  Comparator #(.Bits(4)) comparator_7 (
    .a(IN[7:4]), .b(_2ND_3RD), .gt(comparator_7_gt), .eq(comparator_7_eq), .lt(comparator_7_lt));
  Comparator #(.Bits(4)) comparator_8 (
    .a(IN[7:4]), .b(_2ND_4TH), .gt(comparator_8_gt), .eq(comparator_8_eq), .lt(comparator_8_lt));
  Comparator #(.Bits(4)) comparator_9 (
    .a(IN[7:4]), .b(_2ND_5TH), .gt(comparator_9_gt), .eq(comparator_9_eq), .lt(comparator_9_lt));
  Comparator #(.Bits(4)) comparator_10 (
    .a(IN[7:4]), .b(_2ND_6TH), .gt(comparator_10_gt), .eq(comparator_10_eq), .lt(comparator_10_lt));
  Comparator #(.Bits(4)) comparator_11 (
    .a(IN[7:4]), .b(_2ND_7TH), .gt(comparator_11_gt), .eq(comparator_11_eq), .lt(comparator_11_lt));
  Comparator #(.Bits(4)) comparator_12 (
    .a(IN[7:4]), .b(_2ND_8TH), .gt(comparator_12_gt), .eq(comparator_12_eq), .lt(comparator_12_lt));
  Comparator #(.Bits(4)) comparator_13 (
    .a(IN[7:4]), .b(_2ND_9TH), .gt(comparator_13_gt), .eq(comparator_13_eq), .lt(comparator_13_lt));
  Comparator #(.Bits(4)) comparator_14 (
    .a(IN[7:4]), .b(_2ND_10TH), .gt(comparator_14_gt), .eq(comparator_14_eq), .lt(comparator_14_lt));
  Comparator #(.Bits(4)) comparator_15 (
    .a(IN[3:0]), .b(_3RD_1ST), .gt(comparator_15_gt), .eq(comparator_15_eq), .lt(comparator_15_lt));
  Comparator #(.Bits(4)) comparator_16 (
    .a(IN[3:0]), .b(_3RD_2ND), .gt(comparator_16_gt), .eq(comparator_16_eq), .lt(comparator_16_lt));
  Comparator #(.Bits(4)) comparator_17 (
    .a(IN[3:0]), .b(_3RD_3RD), .gt(comparator_17_gt), .eq(comparator_17_eq), .lt(comparator_17_lt));
  Comparator #(.Bits(4)) comparator_18 (
    .a(IN[3:0]), .b(_3RD_4TH), .gt(comparator_18_gt), .eq(comparator_18_eq), .lt(comparator_18_lt));
  Comparator #(.Bits(4)) comparator_19 (
    .a(IN[3:0]), .b(_3RD_5TH), .gt(comparator_19_gt), .eq(comparator_19_eq), .lt(comparator_19_lt));
  Comparator #(.Bits(4)) comparator_20 (
    .a(IN[3:0]), .b(_3RD_6TH), .gt(comparator_20_gt), .eq(comparator_20_eq), .lt(comparator_20_lt));
  Comparator #(.Bits(4)) comparator_21 (
    .a(IN[3:0]), .b(_3RD_7TH), .gt(comparator_21_gt), .eq(comparator_21_eq), .lt(comparator_21_lt));
  Comparator #(.Bits(4)) comparator_22 (
    .a(IN[3:0]), .b(_3RD_8TH), .gt(comparator_22_gt), .eq(comparator_22_eq), .lt(comparator_22_lt));
  Comparator #(.Bits(4)) comparator_23 (
    .a(IN[3:0]), .b(_3RD_9TH), .gt(comparator_23_gt), .eq(comparator_23_eq), .lt(comparator_23_lt));
  Comparator #(.Bits(4)) comparator_24 (
    .a(IN[3:0]), .b(_3RD_10TH), .gt(comparator_24_gt), .eq(comparator_24_eq), .lt(comparator_24_lt));

  // Notes on the sheet:
  //   _1ST_2ND: default 1
  //   _1ST_3RD: default 2
  //   _1ST_4TH: default 3
endmodule
