// Digital circuit PAS-MLP-V1.dig as structural Verilog
module PAS_MLP_V1 (
  input  in_1,
  input  in_2,
  input  in_3,
  input  in_4,
  input  in_5,
  input  in_6,
  input  in_7,
  input  in_8,
  input  in_9,
  input  in_10,
  input  in_11,
  input  in_12,
  input  in_13,
  input  in_14,
  input  in_15,
  input  in_16,
  input  in_21,
  input  in_22,
  input  in_23,
  input  in_24,
  input  in_25,
  input  in_26,
  input  in_27,
  input  in_28,
  input  in_29,
  input  in_30,
  input  in_31,
  input  in_32,
  input  in_33,
  input  in_34,
  input  in_35,
  input  in_36,
  input  [4:0] W_1,
  input  [4:0] W_5,
  input  [4:0] W_9,
  input  [4:0] W_13,
  input  [4:0] W_2,
  input  [4:0] W_6,
  input  [4:0] W_10,
  input  [4:0] W_14,
  input  [4:0] W_3,
  input  [4:0] W_7,
  input  [4:0] W_11,
  input  [4:0] W_15,
  input  [4:0] W_4,
  input  [4:0] W_8,
  input  [4:0] W_12,
  input  [4:0] W_16,
  output [3:0] out_17,
  output [3:0] out_18,
  output [3:0] out_19,
  output [3:0] out_20,
  output [3:0] out_37,
  output [3:0] out_38,
  output [3:0] out_39,
  output [3:0] out_40,
  output [19:0] out_57,
  output [19:0] out_58,
  output [19:0] out_59,
  output [19:0] out_60
);

  wire [3:0] pas_perceron_v3_1_p1_2, pas_perceron_v3_1_p1_3, pas_perceron_v3_1_p3_2, pas_perceron_v3_1_p3_3,
       pas_perceron_v3_2_p1_2, pas_perceron_v3_2_p1_3, pas_perceron_v3_2_p3_2, pas_perceron_v3_2_p3_3;
  wire [7:0] pas_perceron_v3_1_p2, pas_perceron_v3_1_p4, pas_perceron_v3_2_p2, pas_perceron_v3_2_p4;
  wire [15:0] pas_perceron_v3_1_p1, pas_perceron_v3_1_p3, pas_perceron_v3_2_p1, pas_perceron_v3_2_p3;

  // PAS_Perceron_V3 pas_perceron_v3_1: pin names not known; wires that end beside it: {pas_perceron_v3_1_p1_3, pas_perceron_v3_1_p1_2, pas_perceron_v3_1_p1}, pas_perceron_v3_1_p2, {pas_perceron_v3_1_p3_3, pas_perceron_v3_1_p3_2, pas_perceron_v3_1_p3}, pas_perceron_v3_1_p4
  // PAS_Perceron_V3 pas_perceron_v3_2: pin names not known; wires that end beside it: {pas_perceron_v3_2_p1_3, pas_perceron_v3_2_p1_2, pas_perceron_v3_2_p1}, pas_perceron_v3_2_p2, {pas_perceron_v3_2_p3_3, pas_perceron_v3_2_p3_2, pas_perceron_v3_2_p3}, pas_perceron_v3_2_p4
  Seven_Seg seven_seg_1 (
    .a(pas_perceron_v3_1_p2[4]), .b(pas_perceron_v3_1_p2[5]), .c(pas_perceron_v3_1_p2[6]),
    .d(pas_perceron_v3_1_p2[7]), .e(pas_perceron_v3_1_p2[0]), .f(pas_perceron_v3_1_p2[1]),
    .g(pas_perceron_v3_1_p2[2]), .dp(pas_perceron_v3_1_p2[3]));
  Seven_Seg seven_seg_2 (
    .a(pas_perceron_v3_1_p4[4]), .b(pas_perceron_v3_1_p4[5]), .c(pas_perceron_v3_1_p4[6]),
    .d(pas_perceron_v3_1_p4[7]), .e(pas_perceron_v3_1_p4[0]), .f(pas_perceron_v3_1_p4[1]),
    .g(pas_perceron_v3_1_p4[2]), .dp(pas_perceron_v3_1_p4[3]));
  Seven_Seg seven_seg_3 (
    .a(pas_perceron_v3_2_p2[4]), .b(pas_perceron_v3_2_p2[5]), .c(pas_perceron_v3_2_p2[6]),
    .d(pas_perceron_v3_2_p2[7]), .e(pas_perceron_v3_2_p2[0]), .f(pas_perceron_v3_2_p2[1]),
    .g(pas_perceron_v3_2_p2[2]), .dp(pas_perceron_v3_2_p2[3]));
  Seven_Seg seven_seg_4 (
    .a(pas_perceron_v3_2_p4[4]), .b(pas_perceron_v3_2_p4[5]), .c(pas_perceron_v3_2_p4[6]),
    .d(pas_perceron_v3_2_p4[7]), .e(pas_perceron_v3_2_p4[0]), .f(pas_perceron_v3_2_p4[1]),
    .g(pas_perceron_v3_2_p4[2]), .dp(pas_perceron_v3_2_p4[3]));
  Seven_Seg seven_seg_5 (
    .a(pas_perceron_v3_1_p1[8]), .b(pas_perceron_v3_1_p1[9]), .c(pas_perceron_v3_1_p1[10]),
    .d(pas_perceron_v3_1_p1[11]), .e(pas_perceron_v3_1_p1[12]), .f(pas_perceron_v3_1_p1[13]),
    .g(pas_perceron_v3_1_p1[14]), .dp(pas_perceron_v3_1_p1[15]));
  Seven_Seg seven_seg_6 (
    .a(pas_perceron_v3_1_p3[8]), .b(pas_perceron_v3_1_p3[9]), .c(pas_perceron_v3_1_p3[10]),
    .d(pas_perceron_v3_1_p3[11]), .e(pas_perceron_v3_1_p3[12]), .f(pas_perceron_v3_1_p3[13]),
    .g(pas_perceron_v3_1_p3[14]), .dp(pas_perceron_v3_1_p3[15]));
  Seven_Seg seven_seg_7 (
    .a(pas_perceron_v3_2_p1[8]), .b(pas_perceron_v3_2_p1[9]), .c(pas_perceron_v3_2_p1[10]),
    .d(pas_perceron_v3_2_p1[11]), .e(pas_perceron_v3_2_p1[12]), .f(pas_perceron_v3_2_p1[13]),
    .g(pas_perceron_v3_2_p1[14]), .dp(pas_perceron_v3_2_p1[15]));
  Seven_Seg seven_seg_8 (
    .a(pas_perceron_v3_2_p3[8]), .b(pas_perceron_v3_2_p3[9]), .c(pas_perceron_v3_2_p3[10]),
    .d(pas_perceron_v3_2_p3[11]), .e(pas_perceron_v3_2_p3[12]), .f(pas_perceron_v3_2_p3[13]),
    .g(pas_perceron_v3_2_p3[14]), .dp(pas_perceron_v3_2_p3[15]));
  Seven_Seg seven_seg_9 (
    .a(pas_perceron_v3_1_p1[4]), .b(pas_perceron_v3_1_p1[5]), .c(pas_perceron_v3_1_p1[6]),
    .d(pas_perceron_v3_1_p1[7]), .e(pas_perceron_v3_1_p1_2[0]), .f(pas_perceron_v3_1_p1_2[1]),
    .g(pas_perceron_v3_1_p1_2[2]), .dp(pas_perceron_v3_1_p1_2[3]));
  Seven_Seg seven_seg_10 (
    .a(pas_perceron_v3_1_p3[4]), .b(pas_perceron_v3_1_p3[5]), .c(pas_perceron_v3_1_p3[6]),
    .d(pas_perceron_v3_1_p3[7]), .e(pas_perceron_v3_1_p3_2[0]), .f(pas_perceron_v3_1_p3_2[1]),
    .g(pas_perceron_v3_1_p3_2[2]), .dp(pas_perceron_v3_1_p3_2[3]));
  Seven_Seg seven_seg_11 (
    .a(pas_perceron_v3_2_p1[4]), .b(pas_perceron_v3_2_p1[5]), .c(pas_perceron_v3_2_p1[6]),
    .d(pas_perceron_v3_2_p1[7]), .e(pas_perceron_v3_2_p1_2[0]), .f(pas_perceron_v3_2_p1_2[1]),
    .g(pas_perceron_v3_2_p1_2[2]), .dp(pas_perceron_v3_2_p1_2[3]));
  Seven_Seg seven_seg_12 (
    .a(pas_perceron_v3_2_p3[4]), .b(pas_perceron_v3_2_p3[5]), .c(pas_perceron_v3_2_p3[6]),
    .d(pas_perceron_v3_2_p3[7]), .e(pas_perceron_v3_2_p3_2[0]), .f(pas_perceron_v3_2_p3_2[1]),
    .g(pas_perceron_v3_2_p3_2[2]), .dp(pas_perceron_v3_2_p3_2[3]));
  Seven_Seg seven_seg_13 (
    .a(pas_perceron_v3_1_p1[0]), .b(pas_perceron_v3_1_p1[1]), .c(pas_perceron_v3_1_p1[2]),
    .d(pas_perceron_v3_1_p1[3]), .e(pas_perceron_v3_1_p1_3[0]), .f(pas_perceron_v3_1_p1_3[1]),
    .g(pas_perceron_v3_1_p1_3[2]), .dp(pas_perceron_v3_1_p1_3[3]));
  Seven_Seg seven_seg_14 (
    .a(pas_perceron_v3_1_p3[0]), .b(pas_perceron_v3_1_p3[1]), .c(pas_perceron_v3_1_p3[2]),
    .d(pas_perceron_v3_1_p3[3]), .e(pas_perceron_v3_1_p3_3[0]), .f(pas_perceron_v3_1_p3_3[1]),
    .g(pas_perceron_v3_1_p3_3[2]), .dp(pas_perceron_v3_1_p3_3[3]));
  Seven_Seg seven_seg_15 (
    .a(pas_perceron_v3_2_p1[0]), .b(pas_perceron_v3_2_p1[1]), .c(pas_perceron_v3_2_p1[2]),
    .d(pas_perceron_v3_2_p1[3]), .e(pas_perceron_v3_2_p1_3[0]), .f(pas_perceron_v3_2_p1_3[1]),
    .g(pas_perceron_v3_2_p1_3[2]), .dp(pas_perceron_v3_2_p1_3[3]));
  Seven_Seg seven_seg_16 (
    .a(pas_perceron_v3_2_p3[0]), .b(pas_perceron_v3_2_p3[1]), .c(pas_perceron_v3_2_p3[2]),
    .d(pas_perceron_v3_2_p3[3]), .e(pas_perceron_v3_2_p3_3[0]), .f(pas_perceron_v3_2_p3_3[1]),
    .g(pas_perceron_v3_2_p3_3[2]), .dp(pas_perceron_v3_2_p3_3[3]));

  assign out_17 = {in_7, in_5, in_3, in_1};
  assign out_18 = {in_8, in_6, in_4, in_2};
  assign out_19 = {in_12, in_11, in_10, in_9};
  assign out_20 = {in_16, in_15, in_14, in_13};
  assign out_37 = {in_27, in_25, in_23, in_21};
  assign out_38 = {in_28, in_26, in_24, in_22};
  assign out_39 = {in_32, in_31, in_30, in_29};
  assign out_40 = {in_36, in_35, in_34, in_33};
  assign out_57 = {W_16, W_12, W_8, W_4};
  assign out_58 = {W_15, W_11, W_7, W_3};
  assign out_59 = {W_14, W_10, W_6, W_2};
  assign out_60 = {W_13, W_9, W_5, W_1};

  // Notes on the sheet:
  //   WEIGHTS_A
  //   INPUT_A1
  //   INPUT_A2
  //   N_1
  //   N_2
endmodule
