// Digital circuit PAS-Perceron-V1.dig as structural Verilog
module PAS_Perceron_V1 (
  input  in_1,
  input  in_2,
  input  in_3,
  input  in_4,
  input  in_5,
  input  in_6,
  input  in_7,
  input  in_8,
  input  in_9,
  input  in_10,
  input  in_11,
  input  in_12,
  input  in_13,
  input  in_14,
  input  in_15,
  input  in_16,
  input  [4:0] W_1,
  input  [4:0] W_5,
  input  [4:0] W_9,
  input  [4:0] W_13,
  input  [4:0] W_2,
  input  [4:0] W_6,
  input  [4:0] W_10,
  input  [4:0] W_14,
  input  [4:0] W_3,
  input  [4:0] W_7,
  input  [4:0] W_11,
  input  [4:0] W_15,
  input  [4:0] W_4,
  input  [4:0] W_8,
  input  [4:0] W_12,
  input  [4:0] W_16,
  input  [4:0] in_36,
  input  [9:0] THRESHOLD,
  output [15:0] out_17,
  output out_18,
  output out_19,
  output [4:0] out_37,
  output [3:0] out_39,
  output [3:0] out_40,
  output [3:0] out_41,
  output [3:0] out_42,
  output [19:0] out_43,
  output [19:0] out_44,
  output [19:0] out_45,
  output [19:0] out_46,
  output [9:0] out_47,
  output [9:0] out_48,
  output [9:0] out_49,
  output [9:0] out_50,
  output [9:0] out_51,
  output [9:0] out_52,
  output [9:0] out_53,
  output [9:0] out_54,
  output [9:0] out_55,
  output [9:0] out_56,
  output [9:0] out_57,
  output [9:0] out_58,
  output [9:0] out_59,
  output [9:0] out_60,
  output [9:0] out_61,
  output [9:0] out_62
);

  wire add_1_c_o, add_2_c_o, add_3_c_o, add_4_c_o, add_5_c_o, add_6_c_o, add_7_c_o, add_8_c_o, add_9_c_o,
       add_10_c_o, add_11_c_o, add_12_c_o, add_13_c_o, add_14_c_o, add_15_c_o, comparator_1_eq,
       comparator_1_gt, comparator_1_lt, driver_1_out, pulldown_1_out, pulldown_2_out, pullup_1_out;
  wire [9:0] add_1_s, add_2_s, add_3_s, add_4_s, add_5_s, add_6_s, add_7_s, add_8_s, add_9_s, add_10_s,
       add_11_s, add_12_s, add_13_s, add_14_s, add_15_s;

  LED led_1 (.in(driver_1_out));
  LED led_2 (.in(driver_1_out));
  LED led_3 (.in(driver_1_out));
  LED led_4 (.in(comparator_1_eq));
  LED led_5 (.in(driver_1_out));
  // RotEncoder rotencoder_1: pin names not known; wires that end beside it: 1'b0, out_18, out_19
  Mul #(.Bits(5), .Signed("true")) mul_1 (.a({4'b0000, in_1}), .b(W_1), .mul(out_47));
  Mul #(.Bits(5)) mul_2 (.a({4'b0000, in_3}), .b(W_5), .mul(out_48));
  Mul #(.Bits(5)) mul_3 (.a({4'b0000, in_5}), .b(W_9), .mul(out_49));
  Mul #(.Bits(5)) mul_4 (.a({4'b0000, in_7}), .b(W_13), .mul(out_50));
  Mul #(.Bits(5)) mul_5 (.a({4'b0000, in_2}), .b(W_2), .mul(out_51));
  Mul #(.Bits(5)) mul_6 (.a({4'b0000, in_4}), .b(W_6), .mul(out_52));
  Mul #(.Bits(5)) mul_7 (.a({4'b0000, in_6}), .b(W_10), .mul(out_53));
  Mul #(.Bits(5)) mul_8 (.a({4'b0000, in_8}), .b(W_14), .mul(out_54));
  Mul #(.Bits(5)) mul_9 (.a({4'b0000, in_9}), .b(W_3), .mul(out_55));
  Mul #(.Bits(5)) mul_10 (.a({4'b0000, in_10}), .b(W_7), .mul(out_56));
  Mul #(.Bits(5)) mul_11 (.a({4'b0000, in_11}), .b(W_11), .mul(out_57));
  Mul #(.Bits(5)) mul_12 (.a({4'b0000, in_12}), .b(W_15), .mul(out_58));
  Mul #(.Bits(5)) mul_13 (.a({4'b0000, in_13}), .b(W_4), .mul(out_59));
  Mul #(.Bits(5)) mul_14 (.a({4'b0000, in_14}), .b(W_8), .mul(out_60));
  Mul #(.Bits(5)) mul_15 (.a({4'b0000, in_15}), .b(W_12), .mul(out_61));
  Mul #(.Bits(5)) mul_16 (.a({4'b0000, in_16}), .b(W_16), .mul(out_62));
  Add #(.Bits(10)) add_1 (.a(out_47), .b(out_48), .c_i(1'b0), .s(add_1_s), .c_o(add_1_c_o));
  Add #(.Bits(10)) add_2 (.a(add_1_s), .b(out_49), .c_i(1'b0), .s(add_2_s), .c_o(add_2_c_o));
  Add #(.Bits(10)) add_3 (.a(add_2_s), .b(out_50), .c_i(1'b0), .s(add_3_s), .c_o(add_3_c_o));
  Add #(.Bits(10)) add_4 (.a(add_3_s), .b(out_51), .c_i(1'b0), .s(add_4_s), .c_o(add_4_c_o));
  Add #(.Bits(10)) add_5 (.a(add_4_s), .b(out_52), .c_i(1'b0), .s(add_5_s), .c_o(add_5_c_o));
  Add #(.Bits(10)) add_6 (.a(add_5_s), .b(out_53), .c_i(1'b0), .s(add_6_s), .c_o(add_6_c_o));
  Add #(.Bits(10)) add_7 (.a(add_6_s), .b(out_54), .c_i(1'b0), .s(add_7_s), .c_o(add_7_c_o));
  Add #(.Bits(10)) add_8 (.a(add_7_s), .b(out_55), .c_i(1'b0), .s(add_8_s), .c_o(add_8_c_o));
  Add #(.Bits(10)) add_9 (.a(add_8_s), .b(out_56), .c_i(1'b0), .s(add_9_s), .c_o(add_9_c_o));
  Add #(.Bits(10)) add_10 (.a(add_9_s), .b(out_57), .c_i(1'b0), .s(add_10_s), .c_o(add_10_c_o));
  Add #(.Bits(10)) add_11 (.a(add_10_s), .b(out_58), .c_i(1'b0), .s(add_11_s), .c_o(add_11_c_o));
  Add #(.Bits(10)) add_12 (.a(add_11_s), .b(out_59), .c_i(1'b0), .s(add_12_s), .c_o(add_12_c_o));
  Add #(.Bits(10)) add_13 (.a(add_12_s), .b(out_60), .c_i(1'b0), .s(add_13_s), .c_o(add_13_c_o));
  Add #(.Bits(10)) add_14 (.a(add_13_s), .b(out_61), .c_i(1'b0), .s(add_14_s), .c_o(add_14_c_o));
  Add #(.Bits(10)) add_15 (.a(add_14_s), .b(out_62), .c_i(1'b0), .s(add_15_s), .c_o(add_15_c_o));
  Comparator #(.Bits(10)) comparator_1 (
    .a(add_15_s), .b(THRESHOLD), .gt(comparator_1_gt), .eq(comparator_1_eq), .lt(comparator_1_lt));
  PullDown pulldown_1 (.out(pulldown_1_out));
  PullUp pullup_1 (.out(pullup_1_out));
  assign driver_1_out = comparator_1_gt ? pullup_1_out : 1'bz;  // Driver driver_1
  assign driver_1_out = comparator_1_lt ? pulldown_1_out : 1'bz;  // Driver driver_2
  assign driver_1_out = comparator_1_eq ? pulldown_2_out : 1'bz;  // Driver driver_3
  PullDown pulldown_2 (.out(pulldown_2_out));
  LED led_6 (.in(comparator_1_eq));
  LED led_7 (.in(driver_1_out));

  assign out_17 = {in_16, in_15, in_14, in_13, in_12, in_11, in_10, in_9, in_8, in_6, in_4, in_2, in_7, in_5, in_3, in_1};
  assign out_37 = in_36;
  assign out_39 = {in_7, in_5, in_3, in_1};
  assign out_40 = {in_8, in_6, in_4, in_2};
  assign out_41 = {in_12, in_11, in_10, in_9};
  assign out_42 = {in_16, in_15, in_14, in_13};
  assign out_43 = {W_16, W_12, W_8, W_4};
  assign out_44 = {W_15, W_11, W_7, W_3};
  assign out_45 = {W_14, W_10, W_6, W_2};
  assign out_46 = {W_13, W_9, W_5, W_1};

  // Notes on the sheet:
  //   SUM|STEP
  //   F:R -> {0,1}
  //   A>B = 1
  //   A<B = 0
endmodule
