// Digital circuit PAS-1B-Perceron-V1.dig as structural Verilog
module PAS_1B_Perceron_V1 (
  input  in_1,
  input  in_2,
  input  [4:0] in_3,
  input  [4:0] in_4,
  output [9:0] out_5
);

  wire add_1_c_o;
  wire [4:0] driver_1_out, driver_2_out;
  wire [9:0] mul_1_mul, mul_2_mul;

  assign driver_1_out = in_1 ? 5'b00001 : 5'bz;  // Driver driver_1
  assign driver_1_out = ~in_1 ? {5{1'b1}} : 5'bz;  // DriverInvSel driverinvsel_1
  assign driver_2_out = in_2 ? 5'b00001 : 5'bz;  // Driver driver_2
  assign driver_2_out = ~in_2 ? {5{1'b1}} : 5'bz;  // DriverInvSel driverinvsel_2
  Mul #(.Signed("true"), .Bits(5)) mul_1 (.a(driver_1_out), .b(in_3), .mul(mul_1_mul));
  Mul #(.Signed("true"), .Bits(5)) mul_2 (.a(driver_2_out), .b(in_4), .mul(mul_2_mul));
  Add #(.Bits(10)) add_1 (.a(mul_1_mul), .b(mul_2_mul), .c_i(1'b0), .s(out_5), .c_o(add_1_c_o));

  // Notes on the sheet:
  //   SUM | STEP
endmodule
