// Digital circuit 27SEG.dig as structural Verilog
module _27SEG (
  input  [9:0] IN,
  input  [23:0] OUT_IN,
  output [9:0] ADDR,
  output SEL,
  output [23:0] OUT_MAIN,
  output [7:0] OUT_EXT
);

  wire comparator_1_eq, comparator_1_gt, comparator_1_lt;

  Comparator #(.Bits(10)) comparator_1 (
    .a(IN), .b(10'h1ff), .gt(comparator_1_gt), .eq(comparator_1_eq), .lt(comparator_1_lt));
  and and_1 (OUT_EXT[2], comparator_1_gt, 1'b1);
  // Pins of 1 and 8 bits meet at {{5{1'b0}}, OUT_EXT[2], 2'b00}
  // Pins of 1 and 24 bits meet at {OUT_IN[7:4], OUT_IN[15:12], OUT_IN[23:16], OUT_IN[11:8], OUT_IN[3:0]}

  assign ADDR = IN;
  assign {OUT_EXT[7:3], OUT_EXT[1:0]} = {7{1'b0}};
  assign OUT_MAIN = {OUT_IN[7:4], OUT_IN[15:12], OUT_IN[23:16], OUT_IN[11:8], OUT_IN[3:0]};
  assign SEL = 1'b1;
endmodule
