// Digital circuit NEURON.dig as structural Verilog
module NEURON (
  input  X_0,
  input  X_1,
  input  [4:0] W_0,
  input  [4:0] W_1,
  output [9:0] Y_0,
  output [9:0] Y_1
);

  wire [4:0] driver_1_out, driver_2_out;

  assign driver_1_out = X_0 ? 5'b00001 : 5'bz;  // Driver driver_1
  assign driver_1_out = ~X_0 ? {5{1'b1}} : 5'bz;  // DriverInvSel driverinvsel_1
  assign driver_2_out = X_1 ? 5'b00001 : 5'bz;  // Driver driver_2
  assign driver_2_out = ~X_1 ? {5{1'b1}} : 5'bz;  // DriverInvSel driverinvsel_2
  Mul #(.Signed("true"), .Bits(5)) mul_1 (.a(driver_1_out), .b(W_0), .mul(Y_0));
  Mul #(.Signed("true"), .Bits(5)) mul_2 (.a(driver_2_out), .b(W_1), .mul(Y_1));
endmodule
