// Digital circuit main.dig as structural Verilog
module main (
  input  X_0,
  input  X_1,
  input  [4:0] W_0,
  input  [4:0] W_1,
  input  [4:0] W_2,
  input  [4:0] W_3,
  input  [4:0] W_4,
  input  [4:0] W_5,
  input  [9:0] B_0,
  input  [9:0] B_1,
  input  [9:0] B_2,
  input  N_0,
  input  N_1,
  input  N_2,
  input  N_3,
  input  N_4,
  input  N_5,
  input  N_6,
  input  N_7,
  input  N_8,
  input  N_9,
  input  in_25,
  input  in_26,
  input  in_27,
  input  in_28,
  input  in_29,
  input  in_30,
  input  in_31,
  input  in_32,
  input  in_33,
  input  in_34,
  input  in_35,
  input  in_36,
  input  in_37,
  input  in_38,
  input  in_39,
  input  in_40,
  input  in_41,
  input  in_42,
  input  in_43,
  input  in_44,
  input  in_45,
  input  in_46,
  input  in_47,
  input  in_48,
  input  in_49,
  input  E_0,
  input  E_1,
  input  E_2,
  input  E_3,
  input  E_4,
  input  E_5,
  input  E_6,
  input  E_7,
  input  X_2,
  input  [4:0] W_6,
  input  X_3,
  input  [4:0] W_7,
  input  X_4,
  input  [4:0] W_8,
  input  X_5,
  input  [4:0] W_9,
  input  X_6,
  input  [4:0] W_10,
  input  X_7,
  input  [4:0] W_11,
  input  X_8,
  input  [4:0] W_12,
  input  X_9,
  input  [4:0] W_13,
  output [9:0] out_9,
  output [9:0] out_10,
  output [9:0] out_13,
  output [9:0] Y_0,
  output [9:0] Y_1,
  output [9:0] Y_2,
  output [9:0] Y_3,
  output [9:0] Y_4,
  output [9:0] Y_5,
  output [9:0] Y_6,
  output [9:0] Y_7
);

  wire _27seg_1_p4, _27seg_2_p4, _27seg_3_p4, _27seg_4_p4, _27seg_5_p4, _27seg_6_p4, add_1_c_o, add_2_c_o,
       add_3_c_o, config_1_p4, config_2_p4, config_3_p4;
  wire [4:0] driver_1_out, driver_2_out, driver_3_out, driver_4_out, driver_5_out, driver_6_out,
       driver_7_out, driver_8_out;
  wire [7:0] _27seg_1_p6, _27seg_2_p6, _27seg_3_p6, _27seg_4_p6, _27seg_5_p6, _27seg_6_p6;
  wire [9:0] _27seg_1_p3, _27seg_2_p3, _27seg_3_p3, _27seg_4_p3, _27seg_5_p3, _27seg_6_p3, neuron_1_y_0,
       neuron_1_y_1, neuron_2_y_0, neuron_2_y_1, neuron_3_y_0, neuron_3_y_1;
  wire [23:0] _27seg_1_p5, _27seg_2_p5, _27seg_3_p5, _27seg_4_p5, _27seg_5_p5, _27seg_6_p5, rom_1_out,
       rom_2_out, rom_3_out, rom_4_out, rom_5_out, rom_6_out;

  assign driver_1_out = X_2 ? 5'b00001 : 5'bz;  // Driver driver_1
  assign driver_1_out = ~X_2 ? {5{1'b1}} : 5'bz;  // DriverInvSel driverinvsel_1
  assign driver_2_out = X_3 ? 5'b00001 : 5'bz;  // Driver driver_2
  assign driver_2_out = ~X_3 ? {5{1'b1}} : 5'bz;  // DriverInvSel driverinvsel_2
  assign driver_3_out = X_4 ? 5'b00001 : 5'bz;  // Driver driver_3
  assign driver_3_out = ~X_4 ? {5{1'b1}} : 5'bz;  // DriverInvSel driverinvsel_3
  assign driver_4_out = X_5 ? 5'b00001 : 5'bz;  // Driver driver_4
  assign driver_4_out = ~X_5 ? {5{1'b1}} : 5'bz;  // DriverInvSel driverinvsel_4
  assign driver_5_out = X_6 ? 5'b00001 : 5'bz;  // Driver driver_5
  assign driver_5_out = ~X_6 ? {5{1'b1}} : 5'bz;  // DriverInvSel driverinvsel_5
  assign driver_6_out = X_7 ? 5'b00001 : 5'bz;  // Driver driver_6
  assign driver_6_out = ~X_7 ? {5{1'b1}} : 5'bz;  // DriverInvSel driverinvsel_6
  assign driver_7_out = X_8 ? 5'b00001 : 5'bz;  // Driver driver_7
  assign driver_7_out = ~X_8 ? {5{1'b1}} : 5'bz;  // DriverInvSel driverinvsel_7
  assign driver_8_out = X_9 ? 5'b00001 : 5'bz;  // Driver driver_8
  assign driver_8_out = ~X_9 ? {5{1'b1}} : 5'bz;  // DriverInvSel driverinvsel_8
  Mul #(.Signed("true"), .Bits(5)) mul_1 (.a(driver_1_out), .b(W_6), .mul(Y_0));
  Mul #(.Signed("true"), .Bits(5)) mul_2 (.a(driver_2_out), .b(W_7), .mul(Y_1));
  Mul #(.Signed("true"), .Bits(5)) mul_3 (.a(driver_3_out), .b(W_8), .mul(Y_2));
  Mul #(.Signed("true"), .Bits(5)) mul_4 (.a(driver_4_out), .b(W_9), .mul(Y_3));
  Mul #(.Signed("true"), .Bits(5)) mul_5 (.a(driver_5_out), .b(W_10), .mul(Y_4));
  Mul #(.Signed("true"), .Bits(5)) mul_6 (.a(driver_6_out), .b(W_11), .mul(Y_5));
  Mul #(.Signed("true"), .Bits(5)) mul_7 (.a(driver_7_out), .b(W_12), .mul(Y_6));
  Mul #(.Signed("true"), .Bits(5)) mul_8 (.a(driver_8_out), .b(W_13), .mul(Y_7));
  NEURON neuron_1 (.X_0(X_0), .X_1(X_1), .W_0(W_0), .W_1(W_1), .Y_0(neuron_1_y_0), .Y_1(neuron_1_y_1));
  NEURON neuron_2 (.X_0(X_0), .X_1(X_1), .W_0(W_2), .W_1(W_3), .Y_0(neuron_2_y_0), .Y_1(neuron_2_y_1));
  Add #(.Bits(10)) add_1 (.a(neuron_1_y_0), .b(neuron_1_y_1), .c_i(1'b0), .s(out_9), .c_o(add_1_c_o));
  Add #(.Bits(10)) add_2 (.a(neuron_2_y_0), .b(neuron_2_y_1), .c_i(1'b0), .s(out_10), .c_o(add_2_c_o));
  // CONFIG config_1: pin names not known; wires that end beside it: add_1_c_o, out_9, B_0, config_1_p4
  // CONFIG config_2: pin names not known; wires that end beside it: add_2_c_o, out_10, B_1, config_2_p4
  ROM rom_1 (.A_IN(_27seg_1_p3), .SEL(_27seg_1_p4), .OUT(rom_1_out));
  // _27SEG _27seg_1: pin names not known; wires that end beside it: B_0, rom_1_out, _27seg_1_p3, _27seg_1_p4, _27seg_1_p5, _27seg_1_p6
  ROM rom_2 (.A_IN(_27seg_2_p3), .SEL(_27seg_2_p4), .OUT(rom_2_out));
  // _27SEG _27seg_2: pin names not known; wires that end beside it: out_9, rom_2_out, _27seg_2_p3, _27seg_2_p4, _27seg_2_p5, _27seg_2_p6
  ROM rom_3 (.A_IN(_27seg_3_p3), .SEL(_27seg_3_p4), .OUT(rom_3_out));
  // _27SEG _27seg_3: pin names not known; wires that end beside it: B_1, rom_3_out, _27seg_3_p3, _27seg_3_p4, _27seg_3_p5, _27seg_3_p6
  ROM rom_4 (.A_IN(_27seg_4_p3), .SEL(_27seg_4_p4), .OUT(rom_4_out));
  // _27SEG _27seg_4: pin names not known; wires that end beside it: out_10, rom_4_out, _27seg_4_p3, _27seg_4_p4, _27seg_4_p5, _27seg_4_p6
  NEURON neuron_3 (.X_0(config_1_p4), .X_1(config_2_p4), .W_0(W_4), .W_1(W_5), .Y_0(neuron_3_y_0), .Y_1(neuron_3_y_1));
  Add #(.Bits(10)) add_3 (.a(neuron_3_y_0), .b(neuron_3_y_1), .c_i(1'b0), .s(out_13), .c_o(add_3_c_o));
  Seven_Seg seven_seg_1 (
    .a(_27seg_1_p6[4]), .b(_27seg_1_p6[5]), .c(_27seg_1_p6[6]), .d(_27seg_1_p6[7]), .e(_27seg_1_p6[0]),
    .f(_27seg_1_p6[1]), .g(_27seg_1_p6[2]), .dp(_27seg_1_p6[3]));
  Seven_Seg seven_seg_2 (
    .a(_27seg_2_p6[4]), .b(_27seg_2_p6[5]), .c(_27seg_2_p6[6]), .d(_27seg_2_p6[7]), .e(_27seg_2_p6[0]),
    .f(_27seg_2_p6[1]), .g(_27seg_2_p6[2]), .dp(_27seg_2_p6[3]));
  Seven_Seg seven_seg_3 (
    .a(_27seg_3_p6[4]), .b(_27seg_3_p6[5]), .c(_27seg_3_p6[6]), .d(_27seg_3_p6[7]), .e(_27seg_3_p6[0]),
    .f(_27seg_3_p6[1]), .g(_27seg_3_p6[2]), .dp(_27seg_3_p6[3]));
  Seven_Seg seven_seg_4 (
    .a(_27seg_4_p6[4]), .b(_27seg_4_p6[5]), .c(_27seg_4_p6[6]), .d(_27seg_4_p6[7]), .e(_27seg_4_p6[0]),
    .f(_27seg_4_p6[1]), .g(_27seg_4_p6[2]), .dp(_27seg_4_p6[3]));
  Seven_Seg seven_seg_5 (
    .a(_27seg_1_p5[8]), .b(_27seg_1_p5[9]), .c(_27seg_1_p5[10]), .d(_27seg_1_p5[11]), .e(_27seg_1_p5[12]),
    .f(_27seg_1_p5[13]), .g(_27seg_1_p5[14]), .dp(_27seg_1_p5[15]));
  Seven_Seg seven_seg_6 (
    .a(_27seg_2_p5[8]), .b(_27seg_2_p5[9]), .c(_27seg_2_p5[10]), .d(_27seg_2_p5[11]), .e(_27seg_2_p5[12]),
    .f(_27seg_2_p5[13]), .g(_27seg_2_p5[14]), .dp(_27seg_2_p5[15]));
  Seven_Seg seven_seg_7 (
    .a(_27seg_3_p5[8]), .b(_27seg_3_p5[9]), .c(_27seg_3_p5[10]), .d(_27seg_3_p5[11]), .e(_27seg_3_p5[12]),
    .f(_27seg_3_p5[13]), .g(_27seg_3_p5[14]), .dp(_27seg_3_p5[15]));
  Seven_Seg seven_seg_8 (
    .a(_27seg_4_p5[8]), .b(_27seg_4_p5[9]), .c(_27seg_4_p5[10]), .d(_27seg_4_p5[11]), .e(_27seg_4_p5[12]),
    .f(_27seg_4_p5[13]), .g(_27seg_4_p5[14]), .dp(_27seg_4_p5[15]));
  // CONFIG config_3: pin names not known; wires that end beside it: add_3_c_o, out_13, B_2, config_3_p4
  Seven_Seg seven_seg_9 (
    .a(_27seg_1_p5[4]), .b(_27seg_1_p5[5]), .c(_27seg_1_p5[6]), .d(_27seg_1_p5[7]), .e(_27seg_1_p5[16]),
    .f(_27seg_1_p5[17]), .g(_27seg_1_p5[18]), .dp(_27seg_1_p5[19]));
  Seven_Seg seven_seg_10 (
    .a(_27seg_2_p5[4]), .b(_27seg_2_p5[5]), .c(_27seg_2_p5[6]), .d(_27seg_2_p5[7]), .e(_27seg_2_p5[16]),
    .f(_27seg_2_p5[17]), .g(_27seg_2_p5[18]), .dp(_27seg_2_p5[19]));
  Seven_Seg seven_seg_11 (
    .a(_27seg_3_p5[4]), .b(_27seg_3_p5[5]), .c(_27seg_3_p5[6]), .d(_27seg_3_p5[7]), .e(_27seg_3_p5[16]),
    .f(_27seg_3_p5[17]), .g(_27seg_3_p5[18]), .dp(_27seg_3_p5[19]));
  Seven_Seg seven_seg_12 (
    .a(_27seg_4_p5[4]), .b(_27seg_4_p5[5]), .c(_27seg_4_p5[6]), .d(_27seg_4_p5[7]), .e(_27seg_4_p5[16]),
    .f(_27seg_4_p5[17]), .g(_27seg_4_p5[18]), .dp(_27seg_4_p5[19]));
  Seven_Seg seven_seg_13 (
    .a(_27seg_1_p5[0]), .b(_27seg_1_p5[1]), .c(_27seg_1_p5[2]), .d(_27seg_1_p5[3]), .e(_27seg_1_p5[20]),
    .f(_27seg_1_p5[21]), .g(_27seg_1_p5[22]), .dp(_27seg_1_p5[23]));
  Seven_Seg seven_seg_14 (
    .a(_27seg_2_p5[0]), .b(_27seg_2_p5[1]), .c(_27seg_2_p5[2]), .d(_27seg_2_p5[3]), .e(_27seg_2_p5[20]),
    .f(_27seg_2_p5[21]), .g(_27seg_2_p5[22]), .dp(_27seg_2_p5[23]));
  Seven_Seg seven_seg_15 (
    .a(_27seg_3_p5[0]), .b(_27seg_3_p5[1]), .c(_27seg_3_p5[2]), .d(_27seg_3_p5[3]), .e(_27seg_3_p5[20]),
    .f(_27seg_3_p5[21]), .g(_27seg_3_p5[22]), .dp(_27seg_3_p5[23]));
  Seven_Seg seven_seg_16 (
    .a(_27seg_4_p5[0]), .b(_27seg_4_p5[1]), .c(_27seg_4_p5[2]), .d(_27seg_4_p5[3]), .e(_27seg_4_p5[20]),
    .f(_27seg_4_p5[21]), .g(_27seg_4_p5[22]), .dp(_27seg_4_p5[23]));
  LED led_1 (.in(config_3_p4));
  LED led_2 (.in(config_3_p4));
  LED led_3 (.in(config_3_p4));
  LED led_4 (.in(config_3_p4));
  ROM rom_5 (.A_IN(_27seg_5_p3), .SEL(_27seg_5_p4), .OUT(rom_5_out));
  // _27SEG _27seg_5: pin names not known; wires that end beside it: B_2, rom_5_out, _27seg_5_p3, _27seg_5_p4, _27seg_5_p5, _27seg_5_p6
  ROM rom_6 (.A_IN(_27seg_6_p3), .SEL(_27seg_6_p4), .OUT(rom_6_out));
  // _27SEG _27seg_6: pin names not known; wires that end beside it: out_13, rom_6_out, _27seg_6_p3, _27seg_6_p4, _27seg_6_p5, _27seg_6_p6
  Seven_Seg seven_seg_17 (
    .a(_27seg_5_p6[4]), .b(_27seg_5_p6[5]), .c(_27seg_5_p6[6]), .d(_27seg_5_p6[7]), .e(_27seg_5_p6[0]),
    .f(_27seg_5_p6[1]), .g(_27seg_5_p6[2]), .dp(_27seg_5_p6[3]));
  Seven_Seg seven_seg_18 (
    .a(_27seg_6_p6[4]), .b(_27seg_6_p6[5]), .c(_27seg_6_p6[6]), .d(_27seg_6_p6[7]), .e(_27seg_6_p6[0]),
    .f(_27seg_6_p6[1]), .g(_27seg_6_p6[2]), .dp(_27seg_6_p6[3]));
  Seven_Seg seven_seg_19 (
    .a(_27seg_5_p5[8]), .b(_27seg_5_p5[9]), .c(_27seg_5_p5[10]), .d(_27seg_5_p5[11]), .e(_27seg_5_p5[12]),
    .f(_27seg_5_p5[13]), .g(_27seg_5_p5[14]), .dp(_27seg_5_p5[15]));
  Seven_Seg seven_seg_20 (
    .a(_27seg_6_p5[8]), .b(_27seg_6_p5[9]), .c(_27seg_6_p5[10]), .d(_27seg_6_p5[11]), .e(_27seg_6_p5[12]),
    .f(_27seg_6_p5[13]), .g(_27seg_6_p5[14]), .dp(_27seg_6_p5[15]));
  Seven_Seg seven_seg_21 (
    .a(_27seg_5_p5[4]), .b(_27seg_5_p5[5]), .c(_27seg_5_p5[6]), .d(_27seg_5_p5[7]), .e(_27seg_5_p5[16]),
    .f(_27seg_5_p5[17]), .g(_27seg_5_p5[18]), .dp(_27seg_5_p5[19]));
  Seven_Seg seven_seg_22 (
    .a(_27seg_6_p5[4]), .b(_27seg_6_p5[5]), .c(_27seg_6_p5[6]), .d(_27seg_6_p5[7]), .e(_27seg_6_p5[16]),
    .f(_27seg_6_p5[17]), .g(_27seg_6_p5[18]), .dp(_27seg_6_p5[19]));
  Seven_Seg seven_seg_23 (
    .a(_27seg_5_p5[0]), .b(_27seg_5_p5[1]), .c(_27seg_5_p5[2]), .d(_27seg_5_p5[3]), .e(_27seg_5_p5[20]),
    .f(_27seg_5_p5[21]), .g(_27seg_5_p5[22]), .dp(_27seg_5_p5[23]));
  Seven_Seg seven_seg_24 (
    .a(_27seg_6_p5[0]), .b(_27seg_6_p5[1]), .c(_27seg_6_p5[2]), .d(_27seg_6_p5[3]), .e(_27seg_6_p5[20]),
    .f(_27seg_6_p5[21]), .g(_27seg_6_p5[22]), .dp(_27seg_6_p5[23]));

  // Other names for the same wires on the sheet: D_0 = in_25; D_1 = in_26; D_2 = in_27; D_3 = in_28; D_4 = in_29;
  //   D_5 = in_30; D_6 = in_31; D_7 = in_32; D_8 = in_33; D_9 = in_34; D_10 = in_35; D_11 = in_36; D_12 = in_37;
  //   D_13 = in_38; D_14 = in_39; D_15 = in_40; D_16 = in_41; D_17 = in_42; D_18 = in_43; D_19 = in_44; D_20 = in_45;
  //   D_21 = in_46; D_22 = in_47; D_23 = in_48; D_24 = in_49

  // Notes on the sheet:
  //   THRESHOLD
  //   N_0
  //   OUTPUT
  //   N_1
  //   N_2
endmodule
