// Digital circuit main09.dig as structural Verilog
module main09 (
  input  in_1,
  input  in_2,
  input  in_3,
  input  in_4,
  input  in_5,
  input  in_6,
  input  in_7,
  input  in_8,
  input  in_9,
  input  in_10,
  input  in_11,
  input  in_12,
  input  in_13,
  input  in_14,
  input  in_15,
  input  in_16,
  input  in_17,
  input  in_18,
  input  in_19,
  input  in_20,
  input  in_21,
  input  in_22,
  input  in_23,
  input  in_24,
  input  in_25,
  input  [4:0] in_31,
  input  [4:0] in_32,
  input  [4:0] in_33,
  input  [4:0] in_34,
  input  [4:0] in_35,
  input  [4:0] in_36,
  input  [4:0] in_37,
  input  [4:0] in_38,
  input  [4:0] in_39,
  input  [4:0] in_40,
  input  [4:0] in_41,
  input  [4:0] in_42,
  input  [4:0] in_43,
  input  [4:0] in_44,
  input  [4:0] in_45,
  input  [9:0] in_56,
  input  [9:0] in_57,
  input  [9:0] in_58,
  input  [4:0] in_68,
  input  [4:0] in_69,
  input  [4:0] in_70,
  input  [4:0] in_71,
  input  [4:0] in_72,
  input  [4:0] in_73,
  input  [4:0] in_74,
  input  [4:0] in_75,
  input  [4:0] in_76,
  input  [9:0] in_77,
  input  [9:0] in_78,
  input  [9:0] in_79,
  output [9:0] Y_0,
  output [9:0] Y_1,
  output [9:0] Y_2,
  output [9:0] Y_3,
  output [9:0] Y_4,
  output [9:0] Y_5,
  output [9:0] Y_6,
  output [9:0] Y_7,
  output [9:0] Y_8,
  output [9:0] Y_9,
  output [9:0] Y_10,
  output [9:0] Y_11,
  output [9:0] Y_12,
  output [9:0] Y_13,
  output [9:0] Y_14,
  output [9:0] Y_15,
  output [9:0] Y_16,
  output [9:0] Y_17,
  output [9:0] Y_18,
  output [9:0] Y_19,
  output [9:0] Y_20,
  output [9:0] Y_21,
  output [9:0] Y_22,
  output [9:0] Y_23
);

  wire add_1_c_o, add_2_c_o, add_3_c_o, add_4_c_o, add_5_c_o, add_6_c_o, add_7_c_o, add_8_c_o, add_9_c_o,
       add_10_c_o, add_11_c_o, add_12_c_o, add_13_c_o, add_14_c_o, add_15_c_o, add_16_c_o, add_17_c_o,
       add_18_c_o, mainconfig_1_out, mainconfig_2_out, mainconfig_3_out, O_0, O_1, O_2;
  wire [4:0] driver_1_out, driver_2_out, driver_3_out, driver_4_out, driver_5_out, driver_6_out,
       driver_7_out, driver_8_out, driver_9_out, driver_10_out, driver_11_out, driver_12_out, driver_13_out,
       driver_14_out, driver_15_out, driver_16_out, driver_17_out, driver_18_out, driver_19_out,
       driver_20_out, driver_21_out, driver_22_out, driver_23_out, driver_24_out;
  wire [9:0] add_1_s, add_2_s, add_3_s, add_4_s, add_5_s, add_6_s, add_7_s, add_8_s, add_9_s, add_10_s,
       add_11_s, add_12_s, add_13_s, add_14_s, add_15_s, add_16_s, add_17_s, add_18_s;

  LED led_1 (.in(O_0));
  LED led_2 (.in(O_1));
  LED led_3 (.in(O_2));
  assign driver_1_out = in_1 ? 5'b00001 : 5'bz;  // Driver driver_1
  assign driver_1_out = ~in_1 ? {5{1'b1}} : 5'bz;  // DriverInvSel driverinvsel_1
  assign driver_2_out = in_2 ? 5'b00001 : 5'bz;  // Driver driver_2
  assign driver_2_out = ~in_2 ? {5{1'b1}} : 5'bz;  // DriverInvSel driverinvsel_2
  assign driver_3_out = in_3 ? 5'b00001 : 5'bz;  // Driver driver_3
  assign driver_3_out = ~in_3 ? {5{1'b1}} : 5'bz;  // DriverInvSel driverinvsel_3
  assign driver_4_out = in_4 ? 5'b00001 : 5'bz;  // Driver driver_4
  assign driver_4_out = ~in_4 ? {5{1'b1}} : 5'bz;  // DriverInvSel driverinvsel_4
  assign driver_5_out = in_5 ? 5'b00001 : 5'bz;  // Driver driver_5
  assign driver_5_out = ~in_5 ? {5{1'b1}} : 5'bz;  // DriverInvSel driverinvsel_5
  assign driver_6_out = in_1 ? 5'b00001 : 5'bz;  // Driver driver_6
  assign driver_6_out = ~in_1 ? {5{1'b1}} : 5'bz;  // DriverInvSel driverinvsel_6
  assign driver_7_out = in_2 ? 5'b00001 : 5'bz;  // Driver driver_7
  assign driver_7_out = ~in_2 ? {5{1'b1}} : 5'bz;  // DriverInvSel driverinvsel_7
  assign driver_8_out = in_3 ? 5'b00001 : 5'bz;  // Driver driver_8
  assign driver_8_out = ~in_3 ? {5{1'b1}} : 5'bz;  // DriverInvSel driverinvsel_8
  assign driver_9_out = in_4 ? 5'b00001 : 5'bz;  // Driver driver_9
  assign driver_9_out = ~in_4 ? {5{1'b1}} : 5'bz;  // DriverInvSel driverinvsel_9
  assign driver_10_out = in_5 ? 5'b00001 : 5'bz;  // Driver driver_10
  assign driver_10_out = ~in_5 ? {5{1'b1}} : 5'bz;  // DriverInvSel driverinvsel_10
  assign driver_11_out = in_1 ? 5'b00001 : 5'bz;  // Driver driver_11
  assign driver_11_out = ~in_1 ? {5{1'b1}} : 5'bz;  // DriverInvSel driverinvsel_11
  assign driver_12_out = in_2 ? 5'b00001 : 5'bz;  // Driver driver_12
  assign driver_12_out = ~in_2 ? {5{1'b1}} : 5'bz;  // DriverInvSel driverinvsel_12
  assign driver_13_out = in_3 ? 5'b00001 : 5'bz;  // Driver driver_13
  assign driver_13_out = ~in_3 ? {5{1'b1}} : 5'bz;  // DriverInvSel driverinvsel_13
  assign driver_14_out = in_4 ? 5'b00001 : 5'bz;  // Driver driver_14
  assign driver_14_out = ~in_4 ? {5{1'b1}} : 5'bz;  // DriverInvSel driverinvsel_14
  assign driver_15_out = in_5 ? 5'b00001 : 5'bz;  // Driver driver_15
  assign driver_15_out = ~in_5 ? {5{1'b1}} : 5'bz;  // DriverInvSel driverinvsel_15
  Mul #(.Signed("true"), .Bits(5)) mul_1 (.a(driver_1_out), .b(in_31), .mul(Y_0));
  Mul #(.Signed("true"), .Bits(5)) mul_2 (.a(driver_2_out), .b(in_32), .mul(Y_1));
  Mul #(.Signed("true"), .Bits(5)) mul_3 (.a(driver_3_out), .b(in_33), .mul(Y_2));
  Mul #(.Signed("true"), .Bits(5)) mul_4 (.a(driver_4_out), .b(in_34), .mul(Y_3));
  Mul #(.Signed("true"), .Bits(5)) mul_5 (.a(driver_5_out), .b(in_35), .mul(Y_4));
  Mul #(.Signed("true"), .Bits(5)) mul_6 (.a(driver_6_out), .b(in_36), .mul(Y_5));
  Mul #(.Signed("true"), .Bits(5)) mul_7 (.a(driver_7_out), .b(in_37), .mul(Y_6));
  Mul #(.Signed("true"), .Bits(5)) mul_8 (.a(driver_8_out), .b(in_38), .mul(Y_7));
  Mul #(.Signed("true"), .Bits(5)) mul_9 (.a(driver_9_out), .b(in_39), .mul(Y_8));
  Mul #(.Signed("true"), .Bits(5)) mul_10 (.a(driver_10_out), .b(in_40), .mul(Y_9));
  Mul #(.Signed("true"), .Bits(5)) mul_11 (.a(driver_11_out), .b(in_41), .mul(Y_10));
  Mul #(.Signed("true"), .Bits(5)) mul_12 (.a(driver_12_out), .b(in_42), .mul(Y_11));
  Mul #(.Signed("true"), .Bits(5)) mul_13 (.a(driver_13_out), .b(in_43), .mul(Y_12));
  Mul #(.Signed("true"), .Bits(5)) mul_14 (.a(driver_14_out), .b(in_44), .mul(Y_13));
  Mul #(.Signed("true"), .Bits(5)) mul_15 (.a(driver_15_out), .b(in_45), .mul(Y_14));
  Add #(.Bits(10)) add_1 (.a(Y_0), .b(Y_1), .c_i(1'b0), .s(add_1_s), .c_o(add_1_c_o));
  Add #(.Bits(10)) add_2 (.a(Y_2), .b(Y_3), .c_i(1'b0), .s(add_2_s), .c_o(add_2_c_o));
  Add #(.Bits(10)) add_3 (.a(Y_5), .b(Y_6), .c_i(1'b0), .s(add_3_s), .c_o(add_3_c_o));
  Add #(.Bits(10)) add_4 (.a(Y_7), .b(Y_8), .c_i(1'b0), .s(add_4_s), .c_o(add_4_c_o));
  Add #(.Bits(10)) add_5 (.a(Y_10), .b(Y_11), .c_i(1'b0), .s(add_5_s), .c_o(add_5_c_o));
  Add #(.Bits(10)) add_6 (.a(Y_12), .b(Y_13), .c_i(1'b0), .s(add_6_s), .c_o(add_6_c_o));
  Add #(.Bits(10)) add_7 (.a(add_1_s), .b(add_2_s), .c_i(1'b0), .s(add_7_s), .c_o(add_7_c_o));
  Add #(.Bits(10)) add_8 (.a(add_3_s), .b(add_4_s), .c_i(1'b0), .s(add_8_s), .c_o(add_8_c_o));
  Add #(.Bits(10)) add_9 (.a(add_5_s), .b(add_6_s), .c_i(1'b0), .s(add_9_s), .c_o(add_9_c_o));
  Add #(.Bits(10)) add_10 (.a(add_7_s), .b(Y_4), .c_i(1'b0), .s(add_10_s), .c_o(add_10_c_o));
  Add #(.Bits(10)) add_11 (.a(add_8_s), .b(Y_9), .c_i(1'b0), .s(add_11_s), .c_o(add_11_c_o));
  Add #(.Bits(10)) add_12 (.a(add_9_s), .b(Y_14), .c_i(1'b0), .s(add_12_s), .c_o(add_12_c_o));
  mainCONFIG mainconfig_1 (.C_0(add_10_s), .C_1(in_58), .OUT(mainconfig_1_out));
  mainCONFIG mainconfig_2 (.C_0(add_11_s), .C_1(in_57), .OUT(mainconfig_2_out));
  mainCONFIG mainconfig_3 (.C_0(add_12_s), .C_1(in_56), .OUT(mainconfig_3_out));
  assign driver_16_out = mainconfig_1_out ? 5'b00001 : 5'bz;  // Driver driver_16
  assign driver_16_out = ~mainconfig_1_out ? {5{1'b1}} : 5'bz;  // DriverInvSel driverinvsel_16
  assign driver_17_out = mainconfig_2_out ? 5'b00001 : 5'bz;  // Driver driver_17
  assign driver_17_out = ~mainconfig_2_out ? {5{1'b1}} : 5'bz;  // DriverInvSel driverinvsel_17
  assign driver_18_out = mainconfig_3_out ? 5'b00001 : 5'bz;  // Driver driver_18
  assign driver_18_out = ~mainconfig_3_out ? {5{1'b1}} : 5'bz;  // DriverInvSel driverinvsel_18
  assign driver_19_out = mainconfig_1_out ? 5'b00001 : 5'bz;  // Driver driver_19
  assign driver_19_out = ~mainconfig_1_out ? {5{1'b1}} : 5'bz;  // DriverInvSel driverinvsel_19
  assign driver_20_out = mainconfig_2_out ? 5'b00001 : 5'bz;  // Driver driver_20
  assign driver_20_out = ~mainconfig_2_out ? {5{1'b1}} : 5'bz;  // DriverInvSel driverinvsel_20
  assign driver_21_out = mainconfig_3_out ? 5'b00001 : 5'bz;  // Driver driver_21
  assign driver_21_out = ~mainconfig_3_out ? {5{1'b1}} : 5'bz;  // DriverInvSel driverinvsel_21
  assign driver_22_out = mainconfig_1_out ? 5'b00001 : 5'bz;  // Driver driver_22
  assign driver_22_out = ~mainconfig_1_out ? {5{1'b1}} : 5'bz;  // DriverInvSel driverinvsel_22
  assign driver_23_out = mainconfig_2_out ? 5'b00001 : 5'bz;  // Driver driver_23
  assign driver_23_out = ~mainconfig_2_out ? {5{1'b1}} : 5'bz;  // DriverInvSel driverinvsel_23
  assign driver_24_out = mainconfig_3_out ? 5'b00001 : 5'bz;  // Driver driver_24
  assign driver_24_out = ~mainconfig_3_out ? {5{1'b1}} : 5'bz;  // DriverInvSel driverinvsel_24
  Mul #(.Signed("true"), .Bits(5)) mul_16 (.a(driver_16_out), .b(in_68), .mul(Y_15));
  Mul #(.Signed("true"), .Bits(5)) mul_17 (.a(driver_17_out), .b(in_69), .mul(Y_16));
  Mul #(.Signed("true"), .Bits(5)) mul_18 (.a(driver_18_out), .b(in_70), .mul(Y_17));
  Mul #(.Signed("true"), .Bits(5)) mul_19 (.a(driver_19_out), .b(in_71), .mul(Y_18));
  Mul #(.Signed("true"), .Bits(5)) mul_20 (.a(driver_20_out), .b(in_72), .mul(Y_19));
  Mul #(.Signed("true"), .Bits(5)) mul_21 (.a(driver_21_out), .b(in_73), .mul(Y_20));
  Mul #(.Signed("true"), .Bits(5)) mul_22 (.a(driver_22_out), .b(in_74), .mul(Y_21));
  Mul #(.Signed("true"), .Bits(5)) mul_23 (.a(driver_23_out), .b(in_75), .mul(Y_22));
  Mul #(.Signed("true"), .Bits(5)) mul_24 (.a(driver_24_out), .b(in_76), .mul(Y_23));
  Add #(.Bits(10)) add_13 (.a(Y_15), .b(Y_16), .c_i(1'b0), .s(add_13_s), .c_o(add_13_c_o));
  Add #(.Bits(10)) add_14 (.a(Y_18), .b(Y_19), .c_i(1'b0), .s(add_14_s), .c_o(add_14_c_o));
  Add #(.Bits(10)) add_15 (.a(Y_21), .b(Y_22), .c_i(1'b0), .s(add_15_s), .c_o(add_15_c_o));
  Add #(.Bits(10)) add_16 (.a(add_13_s), .b(Y_17), .c_i(1'b0), .s(add_16_s), .c_o(add_16_c_o));
  Add #(.Bits(10)) add_17 (.a(add_14_s), .b(Y_20), .c_i(1'b0), .s(add_17_s), .c_o(add_17_c_o));
  Add #(.Bits(10)) add_18 (.a(add_15_s), .b(Y_23), .c_i(1'b0), .s(add_18_s), .c_o(add_18_c_o));
  mainCONFIG mainconfig_4 (.C_0(add_16_s), .C_1(in_77), .OUT(O_0));
  mainCONFIG mainconfig_5 (.C_0(add_17_s), .C_1(in_78), .OUT(O_1));
  mainCONFIG mainconfig_6 (.C_0(add_18_s), .C_1(in_79), .OUT(O_2));
  LED led_4 (.in(O_0));
  LED led_5 (.in(O_1));
  LED led_6 (.in(O_2));

  // Other names for the same wires on the sheet: D_0 = in_1; D_1 = in_2; D_2 = in_3; D_3 = in_4; D_4 = in_5;
  //   D_5 = in_6; D_6 = in_7; D_7 = in_8; D_8 = in_9; D_9 = in_10; D_10 = in_11; D_11 = in_12; D_12 = in_13;
  //   D_13 = in_14; D_14 = in_15; D_15 = in_16; D_16 = in_17; D_17 = in_18; D_18 = in_19; D_19 = in_20; D_20 = in_21;
  //   D_21 = in_22; D_22 = in_23; D_23 = in_24; D_24 = in_25

  // Notes on the sheet:
  //   INPUT
  //   WH_100(0)
  //   WH_010(0)
  //   WH_001(0)
  //   BH_(0)
  //   IN
  //   H_0
  //   WH_100(1)
  //   WH_010(1)
  //   WH_001(1)
  //   BH_(1)
  //   11000
  //   00100
  //   00011
  //   OUT
endmodule
