// Digital circuit mainCONFIG.dig as structural Verilog
module mainCONFIG (
  input  [9:0] C_0,
  input  [9:0] C_1,
  output OUT
);

  wire comparator_1_eq, comparator_1_gt, comparator_1_lt, delay_1_out, delay_2_out, delay_3_out, delay_4_out,
       delay_5_out, delay_6_out, driver_1_out, driver_3_out, driver_4_out, pulldown_1_out, pullup_1_out,
       pullup_2_out;

  Comparator #(.Signed("true"), .Bits(10)) comparator_1 (
    .a(C_0), .b(C_1), .gt(comparator_1_gt), .eq(comparator_1_eq), .lt(comparator_1_lt));
  PullUp pullup_1 (.out(pullup_1_out));
  assign driver_1_out = comparator_1_gt ? pullup_1_out : 1'bz;  // Driver driver_1
  assign driver_1_out = comparator_1_eq ? pullup_1_out : 1'bz;  // Driver driver_2
  PullDown pulldown_1 (.out(pulldown_1_out));
  PullUp pullup_2 (.out(pullup_2_out));
  PullDown pulldown_2 (.out(driver_1_out));
  assign driver_3_out = driver_1_out ? pullup_2_out : 1'bz;  // Driver driver_3
  assign driver_4_out = comparator_1_lt ? pulldown_1_out : 1'bz;  // Driver driver_4
  PullDown pulldown_3 (.out(driver_3_out));
  Delay #(.delayTime(20)) delay_1 (.in(driver_3_out), .out(delay_1_out));
  Delay #(.delayTime(20)) delay_2 (.in(driver_4_out), .out(delay_2_out));
  PullDown pulldown_4 (.out(driver_4_out));
  Delay #(.delayTime(20)) delay_3 (.in(delay_1_out), .out(delay_3_out));
  Delay #(.delayTime(20)) delay_4 (.in(delay_3_out), .out(delay_4_out));
  Delay #(.delayTime(20)) delay_5 (.in(delay_2_out), .out(delay_5_out));
  Delay #(.delayTime(20)) delay_6 (.in(delay_5_out), .out(delay_6_out));
  PullDown pulldown_5 (.out(OUT));
  assign OUT = delay_4_out ? delay_4_out : 1'bz;  // Driver driver_5
  assign OUT = delay_6_out ? delay_6_out : 1'bz;  // Driver driver_6
endmodule
