// Digital circuit PAS-Perceron-V3.dig as structural Verilog
module PAS_Perceron_V3 (
  input  [9:0] THRESH,
  input  [15:0] X,
  input  [39:0] W_1,
  input  [39:0] W_2,
  output [9:0] OUTPUT,
  output [23:0] OUT_VAL,
  output [7:0] OUT_EXT,
  output [23:0] THR_VAL,
  output [7:0] THR_EXT,
  output plus
);

  wire add_1_c_o, add_2_c_o, add_3_c_o, add_4_c_o, add_5_c_o, add_6_c_o, add_7_c_o, add_8_c_o, add_9_c_o,
       add_10_c_o, add_11_c_o, add_12_c_o, add_13_c_o, add_14_c_o, add_15_c_o, comparator_1_eq,
       comparator_1_gt, comparator_1_lt, delay_4_out, delay_5_out, delay_6_out, delay_7_out, delay_8_out,
       delay_9_out, driver_17_out, driver_19_out, driver_20_out, one_1_p4, one_2_p4, pulldown_2_out,
       pullup_1_out, pullup_2_out;
  wire [4:0] driver_1_out, driver_2_out, driver_3_out, driver_4_out, driver_5_out, driver_6_out,
       driver_7_out, driver_8_out, driver_9_out, driver_10_out, driver_11_out, driver_12_out, driver_13_out,
       driver_14_out, driver_15_out, driver_16_out;
  wire [9:0] add_1_s, add_2_s, add_3_s, add_4_s, add_5_s, add_6_s, add_7_s, add_8_s, add_9_s, add_10_s,
       add_11_s, add_12_s, add_13_s, add_14_s, delay_1_out, delay_2_out, delay_3_out, mul_1_mul, mul_2_mul,
       mul_3_mul, mul_4_mul, mul_5_mul, mul_6_mul, mul_7_mul, mul_8_mul, mul_9_mul, mul_10_mul, mul_11_mul,
       mul_12_mul, mul_13_mul, mul_14_mul, mul_15_mul, mul_16_mul, one_1_p3, one_2_p3;
  wire [23:0] rom_1_d, rom_2_d;

  ROM #(.AddrBits(10), .Bits(24)) rom_1 (.A(one_1_p3), .sel(one_1_p4), .D(rom_1_d));
  // one one_1: pin names not known; wires that end beside it: OUTPUT, rom_1_d, one_1_p3, one_1_p4, OUT_VAL, OUT_EXT
  ROM #(.AddrBits(10), .Bits(24)) rom_2 (.A(one_2_p3), .sel(one_2_p4), .D(rom_2_d));
  // one one_2: pin names not known; wires that end beside it: THRESH, rom_2_d, one_2_p3, one_2_p4, THR_VAL, THR_EXT
  assign driver_1_out = X[0] ? 5'b00001 : 5'bz;  // Driver driver_1
  assign driver_1_out = ~X[0] ? {5{1'b1}} : 5'bz;  // DriverInvSel driverinvsel_1
  assign driver_2_out = X[1] ? 5'b00001 : 5'bz;  // Driver driver_2
  assign driver_2_out = ~X[1] ? {5{1'b1}} : 5'bz;  // DriverInvSel driverinvsel_2
  assign driver_3_out = X[2] ? 5'b00001 : 5'bz;  // Driver driver_3
  assign driver_3_out = ~X[2] ? {5{1'b1}} : 5'bz;  // DriverInvSel driverinvsel_3
  assign driver_4_out = X[3] ? 5'b00001 : 5'bz;  // Driver driver_4
  assign driver_4_out = ~X[3] ? {5{1'b1}} : 5'bz;  // DriverInvSel driverinvsel_4
  assign driver_5_out = X[4] ? 5'b00001 : 5'bz;  // Driver driver_5
  assign driver_5_out = ~X[4] ? {5{1'b1}} : 5'bz;  // DriverInvSel driverinvsel_5
  assign driver_6_out = X[5] ? 5'b00001 : 5'bz;  // Driver driver_6
  assign driver_6_out = ~X[5] ? {5{1'b1}} : 5'bz;  // DriverInvSel driverinvsel_6
  assign driver_7_out = X[6] ? 5'b00001 : 5'bz;  // Driver driver_7
  assign driver_7_out = ~X[6] ? {5{1'b1}} : 5'bz;  // DriverInvSel driverinvsel_7
  assign driver_8_out = X[7] ? 5'b00001 : 5'bz;  // Driver driver_8
  assign driver_8_out = ~X[7] ? {5{1'b1}} : 5'bz;  // DriverInvSel driverinvsel_8
  assign driver_9_out = X[8] ? 5'b00001 : 5'bz;  // Driver driver_9
  assign driver_9_out = ~X[8] ? {5{1'b1}} : 5'bz;  // DriverInvSel driverinvsel_9
  assign driver_10_out = X[9] ? 5'b00001 : 5'bz;  // Driver driver_10
  assign driver_10_out = ~X[9] ? {5{1'b1}} : 5'bz;  // DriverInvSel driverinvsel_10
  assign driver_11_out = X[10] ? 5'b00001 : 5'bz;  // Driver driver_11
  assign driver_11_out = ~X[10] ? {5{1'b1}} : 5'bz;  // DriverInvSel driverinvsel_11
  assign driver_12_out = X[11] ? 5'b00001 : 5'bz;  // Driver driver_12
  assign driver_12_out = ~X[11] ? {5{1'b1}} : 5'bz;  // DriverInvSel driverinvsel_12
  assign driver_13_out = X[12] ? 5'b00001 : 5'bz;  // Driver driver_13
  assign driver_13_out = ~X[12] ? {5{1'b1}} : 5'bz;  // DriverInvSel driverinvsel_13
  assign driver_14_out = X[13] ? 5'b00001 : 5'bz;  // Driver driver_14
  assign driver_14_out = ~X[13] ? {5{1'b1}} : 5'bz;  // DriverInvSel driverinvsel_14
  assign driver_15_out = X[14] ? 5'b00001 : 5'bz;  // Driver driver_15
  assign driver_15_out = ~X[14] ? {5{1'b1}} : 5'bz;  // DriverInvSel driverinvsel_15
  assign driver_16_out = X[15] ? 5'b00001 : 5'bz;  // Driver driver_16
  assign driver_16_out = ~X[15] ? {5{1'b1}} : 5'bz;  // DriverInvSel driverinvsel_16
  Mul #(.Signed("true"), .Bits(5)) mul_1 (.a(driver_1_out), .b(W_1[4:0]), .mul(mul_1_mul));
  Mul #(.Signed("true"), .Bits(5)) mul_2 (.a(driver_2_out), .b(W_1[9:5]), .mul(mul_2_mul));
  Mul #(.Signed("true"), .Bits(5)) mul_3 (.a(driver_3_out), .b(W_1[14:10]), .mul(mul_3_mul));
  Mul #(.Signed("true"), .Bits(5)) mul_4 (.a(driver_4_out), .b(W_1[19:15]), .mul(mul_4_mul));
  Mul #(.Signed("true"), .Bits(5)) mul_5 (.a(driver_5_out), .b(W_1[24:20]), .mul(mul_5_mul));
  Mul #(.Signed("true"), .Bits(5)) mul_6 (.a(driver_6_out), .b(W_1[29:25]), .mul(mul_6_mul));
  Mul #(.Signed("true"), .Bits(5)) mul_7 (.a(driver_7_out), .b(W_1[34:30]), .mul(mul_7_mul));
  Mul #(.Signed("true"), .Bits(5)) mul_8 (.a(driver_8_out), .b(W_1[39:35]), .mul(mul_8_mul));
  Mul #(.Signed("true"), .Bits(5)) mul_9 (.a(driver_9_out), .b(W_2[4:0]), .mul(mul_9_mul));
  Mul #(.Signed("true"), .Bits(5)) mul_10 (.a(driver_10_out), .b(W_2[9:5]), .mul(mul_10_mul));
  Mul #(.Signed("true"), .Bits(5)) mul_11 (.a(driver_11_out), .b(W_2[14:10]), .mul(mul_11_mul));
  Mul #(.Signed("true"), .Bits(5)) mul_12 (.a(driver_12_out), .b(W_2[19:15]), .mul(mul_12_mul));
  Mul #(.Signed("true"), .Bits(5)) mul_13 (.a(driver_13_out), .b(W_2[24:20]), .mul(mul_13_mul));
  Mul #(.Signed("true"), .Bits(5)) mul_14 (.a(driver_14_out), .b(W_2[29:25]), .mul(mul_14_mul));
  Mul #(.Signed("true"), .Bits(5)) mul_15 (.a(driver_15_out), .b(W_2[34:30]), .mul(mul_15_mul));
  Mul #(.Signed("true"), .Bits(5)) mul_16 (.a(driver_16_out), .b(W_2[39:35]), .mul(mul_16_mul));
  Add #(.Bits(10)) add_1 (.a(mul_1_mul), .b(mul_2_mul), .c_i(1'b0), .s(add_1_s), .c_o(add_1_c_o));
  Add #(.Bits(10)) add_2 (.a(mul_3_mul), .b(mul_4_mul), .c_i(1'b0), .s(add_2_s), .c_o(add_2_c_o));
  Add #(.Bits(10)) add_3 (.a(mul_5_mul), .b(mul_6_mul), .c_i(1'b0), .s(add_3_s), .c_o(add_3_c_o));
  Add #(.Bits(10)) add_4 (.a(mul_7_mul), .b(mul_8_mul), .c_i(1'b0), .s(add_4_s), .c_o(add_4_c_o));
  Add #(.Bits(10)) add_5 (.a(mul_9_mul), .b(mul_10_mul), .c_i(1'b0), .s(add_5_s), .c_o(add_5_c_o));
  Add #(.Bits(10)) add_6 (.a(mul_11_mul), .b(mul_12_mul), .c_i(1'b0), .s(add_6_s), .c_o(add_6_c_o));
  Add #(.Bits(10)) add_7 (.a(mul_13_mul), .b(mul_14_mul), .c_i(1'b0), .s(add_7_s), .c_o(add_7_c_o));
  Add #(.Bits(10)) add_8 (.a(mul_15_mul), .b(mul_16_mul), .c_i(1'b0), .s(add_8_s), .c_o(add_8_c_o));
  Add #(.Bits(10)) add_9 (.a(add_1_s), .b(add_2_s), .c_i(1'b0), .s(add_9_s), .c_o(add_9_c_o));
  Add #(.Bits(10)) add_10 (.a(add_3_s), .b(add_4_s), .c_i(1'b0), .s(add_10_s), .c_o(add_10_c_o));
  Add #(.Bits(10)) add_11 (.a(add_5_s), .b(add_6_s), .c_i(1'b0), .s(add_11_s), .c_o(add_11_c_o));
  Add #(.Bits(10)) add_12 (.a(add_7_s), .b(add_8_s), .c_i(1'b0), .s(add_12_s), .c_o(add_12_c_o));
  Add #(.Bits(10)) add_13 (.a(add_9_s), .b(add_10_s), .c_i(1'b0), .s(add_13_s), .c_o(add_13_c_o));
  Add #(.Bits(10)) add_14 (.a(add_11_s), .b(add_12_s), .c_i(1'b0), .s(add_14_s), .c_o(add_14_c_o));
  Add #(.Bits(10)) add_15 (.a(add_13_s), .b(add_14_s), .c_i(1'b0), .s(OUTPUT), .c_o(add_15_c_o));
  Delay #(.Bits(10), .delayTime(20)) delay_1 (.in(OUTPUT), .out(delay_1_out));
  Delay #(.Bits(10), .delayTime(20)) delay_2 (.in(delay_1_out), .out(delay_2_out));
  Delay #(.Bits(10), .delayTime(20)) delay_3 (.in(delay_2_out), .out(delay_3_out));
  Comparator #(.Signed("true"), .Bits(10)) comparator_1 (
    .a(delay_3_out), .b(THRESH), .gt(comparator_1_gt), .eq(comparator_1_eq), .lt(comparator_1_lt));
  PullUp pullup_1 (.out(pullup_1_out));
  assign driver_17_out = comparator_1_gt ? pullup_1_out : 1'bz;  // Driver driver_17
  assign driver_17_out = comparator_1_eq ? pullup_1_out : 1'bz;  // Driver driver_18
  PullUp pullup_2 (.out(pullup_2_out));
  PullDown pulldown_1 (.out(driver_17_out));
  assign driver_19_out = driver_17_out ? pullup_2_out : 1'bz;  // Driver driver_19
  assign driver_20_out = comparator_1_lt ? pulldown_2_out : 1'bz;  // Driver driver_20
  PullDown pulldown_2 (.out(pulldown_2_out));
  PullDown pulldown_3 (.out(driver_19_out));
  Delay #(.delayTime(20)) delay_4 (.in(driver_19_out), .out(delay_4_out));
  Delay #(.delayTime(20)) delay_5 (.in(driver_20_out), .out(delay_5_out));
  PullDown pulldown_4 (.out(driver_20_out));
  Delay #(.delayTime(20)) delay_6 (.in(delay_4_out), .out(delay_6_out));
  Delay #(.delayTime(20)) delay_7 (.in(delay_5_out), .out(delay_7_out));
  Delay #(.delayTime(20)) delay_8 (.in(delay_6_out), .out(delay_8_out));
  Delay #(.delayTime(20)) delay_9 (.in(delay_7_out), .out(delay_9_out));
  assign plus = delay_8_out ? delay_8_out : 1'bz;  // Driver driver_21
  assign plus = delay_9_out ? delay_9_out : 1'bz;  // Driver driver_22
  PullDown pulldown_5 (.out(plus));

  // Notes on the sheet:
  //   J_L =0
  //   J_R =0
  //   T_L =1
  //   T_R =1
  //   contents of rom_1 (hex, n*v repeats v):
  //   3f3f3f,3f3f06,3f3f5b,3f3f4f,3f3f66,3f3f6d,3f3f7d,3f3f07,3f3f7f
  //   ,3f3f6f,3f063f,3f0606,3f065b,3f064f,3f0666,3f066d,3f067d,3f0607
  //   ,3f067f,3f066f,3f5b3f,3f5b06,3f5b5b,3f5b4f,3f5b66,3f5b6d,3f5b7d
  //   ,3f5b07,3f5b7f,3f5b6f,3f4f3f,3f4f06,3f4f5b,3f4f4f,3f4f66,3f4f6d
  //   ,3f4f7d,3f4f07,3f4f7f,3f4f6f,3f663f,3f6606,3f665b,3f664f,3f6666
  //   ,3f666d,3f667d,3f6607,3f667f,3f666f,3f6d3f,3f6d06,3f6d5b,3f6d4f
  //   ,3f6d66,3f6d6d,3f6d7d,3f6d07,3f6d7f,3f6d6f,3f7d3f,3f7d06,3f7d5b
  //   ,3f7d4f,3f7d66,3f7d6d,3f7d7d,3f7d07,3f7d7f,3f7d6f,3f073f,3f0706
  //   ,3f075b,3f074f,3f0766,3f076d,3f077d,3f0707,3f077f,3f076f,3f7f3f
  //   ,3f7f06,3f7f5b,3f7f4f,3f7f66,3f7f6d,3f7f7d,3f7f07,3f7f7f,3f7f6f
  //   ,3f6f3f,3f6f06,3f6f5b,3f6f4f,3f6f66,3f6f6d,3f6f7d,3f6f07,3f6f7f
  //   ,3f6f6f,63f3f,63f06,63f5b,63f4f,63f66,63f6d,63f7d,63f07,63f7f
  //   ,63f6f,6063f,60606,6065b,6064f,60666,6066d,6067d,60607,6067f,6066f
  //   ,65b3f,65b06,65b5b,65b4f,65b66,65b6d,65b7d,65b07,65b7f,65b6f,64f3f
  //   ,64f06,64f5b,64f4f,64f66,64f6d,64f7d,64f07,64f7f,64f6f,6663f,66606
  //   ,6665b,6664f,66666,6666d,6667d,66607,6667f,6666f,66d3f,66d06,66d5b
  //   ,66d4f,66d66,66d6d,66d7d,66d07,66d7f,66d6f,67d3f,67d06,67d5b,67d4f
  //   ,67d66,67d6d,67d7d,67d07,67d7f,67d6f,6073f,60706,6075b,6074f,60766
  //   ,6076d,6077d,60707,6077f,6076f,67f3f,67f06,67f5b,67f4f,67f66,67f6d
  //   ,67f7d,67f07,67f7f,67f6f,66f3f,66f06,66f5b,66f4f,66f66,66f6d,66f7d
  //   ,66f07,66f7f,66f6f,5b3f3f,5b3f06,5b3f5b,5b3f4f,5b3f66,5b3f6d,5b3f7d
  //   ,5b3f07,5b3f7f,5b3f6f,5b063f,5b0606,5b065b,5b064f,5b0666,5b066d
  //   ,5b067d,5b0607,5b067f,5b066f,5b5b3f,5b5b06,5b5b5b,5b5b4f,5b5b66
  //   ,5b5b6d,5b5b7d,5b5b07,5b5b7f,5b5b6f,5b4f3f,5b4f06,5b4f5b,5b4f4f
  //   ,5b4f66,5b4f6d,5b4f7d,5b4f07,5b4f7f,5b4f6f,5b663f,5b6606,5b665b
  //   ,5b664f,5b6666,5b666d,5b667d,5b6607,5b667f,5b666f,5b6d3f,5b6d06
  //   ,5b6d5b,5b6d4f,5b6d66,5b6d6d,5b6d7d,5b6d07,5b6d7f,5b6d6f,5b7d3f
  //   ,5b7d06,5b7d5b,5b7d4f,5b7d66,5b7d6d,5b7d7d,5b7d07,5b7d7f,5b7d6f
  //   ,5b073f,5b0706,5b075b,5b074f,5b0766,5b076d,5b077d,5b0707,5b077f
  //   ,5b076f,5b7f3f,5b7f06,5b7f5b,5b7f4f,5b7f66,5b7f6d,5b7f7d,5b7f07
  //   ,5b7f7f,5b7f6f,5b6f3f,5b6f06,5b6f5b,5b6f4f,5b6f66,5b6f6d,5b6f7d
  //   ,5b6f07,5b6f7f,5b6f6f,4f3f3f,4f3f06,4f3f5b,4f3f4f,4f3f66,4f3f6d
  //   ,4f3f7d,4f3f07,4f3f7f,4f3f6f,4f063f,4f0606,4f065b,4f064f,4f0666
  //   ,4f066d,4f067d,4f0607,4f067f,4f066f,4f5b3f,4f5b06,4f5b5b,4f5b4f
  //   ,4f5b66,4f5b6d,4f5b7d,4f5b07,4f5b7f,4f5b6f,4f4f3f,4f4f06,4f4f5b
  //   ,4f4f4f,4f4f66,4f4f6d,4f4f7d,4f4f07,4f4f7f,4f4f6f,4f663f,4f6606
  //   ,4f665b,4f664f,4f6666,4f666d,4f667d,4f6607,4f667f,4f666f,4f6d3f
  //   ,4f6d06,4f6d5b,4f6d4f,4f6d66,4f6d6d,4f6d7d,4f6d07,4f6d7f,4f6d6f
  //   ,4f7d3f,4f7d06,4f7d5b,4f7d4f,4f7d66,4f7d6d,4f7d7d,4f7d07,4f7d7f
  //   ,4f7d6f,4f073f,4f0706,4f075b,4f074f,4f0766,4f076d,4f077d,4f0707
  //   ,4f077f,4f076f,4f7f3f,4f7f06,4f7f5b,4f7f4f,4f7f66,4f7f6d,4f7f7d
  //   ,4f7f07,4f7f7f,4f7f6f,4f6f3f,4f6f06,4f6f5b,4f6f4f,4f6f66,4f6f6d
  //   ,4f6f7d,4f6f07,4f6f7f,4f6f6f,663f3f,663f06,663f5b,663f4f,663f66
  //   ,663f6d,663f7d,663f07,663f7f,663f6f,66063f,660606,66065b,66064f
  //   ,660666,66066d,66067d,660607,66067f,66066f,665b3f,665b06,665b5b
  //   ,665b4f,665b66,665b6d,665b7d,665b07,665b7f,665b6f,664f3f,664f06
  //   ,664f5b,664f4f,664f66,664f6d,664f7d,664f07,664f7f,664f6f,66663f
  //   ,666606,66665b,66664f,666666,66666d,66667d,666607,66667f,66666f
  //   ,666d3f,666d06,666d5b,666d4f,666d66,666d6d,666d7d,666d07,666d7f
  //   ,666d6f,667d3f,667d06,667d5b,667d4f,667d66,667d6d,667d7d,667d07
  //   ,667d7f,667d6f,66073f,660706,66075b,66074f,660766,66076d,66077d
  //   ,660707,66077f,66076f,667f3f,667f06,667f5b,667f4f,667f66,667f6d
  //   ,667f7d,667f07,667f7f,667f6f,666f3f,666f06,666f5b,666f4f,666f66
  //   ,666f6d,666f7d,666f07,666f7f,666f6f,6d3f3f,6d3f06,6d3f5b,6d3f4f
  //   ,6d3f66,6d3f6d,6d3f7d,6d3f07,6d3f7f,6d3f6f,6d063f,6d0606,6d065b
  //   ,6d0606,6d063f,6d3f6f,6d3f7f,6d3f07,6d3f7d,6d3f6d,6d3f66,6d3f4f
  //   ,6d3f5b,6d3f06,6d3f3f,666f6f,666f7f,666f07,666f7d,666f6d,666f66
  //   ,666f4f,666f5b,666f06,666f3f,667f6f,667f7f,667f07,667f7d,667f6d
  //   ,667f66,667f4f,667f5b,667f06,667f3f,66076f,66077f,660707,66077d
  //   ,66076d,660766,66074f,66075b,660706,66073f,667d6f,667d7f,667d07
  //   ,667d7d,667d6d,667d66,667d4f,667d5b,667d06,667d3f,666d6f,666d7f
  //   ,666d07,666d7d,666d6d,666d66,666d4f,666d5b,666d06,666d3f,66666f
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  //   contents of rom_2 (hex, n*v repeats v):
  //   3f3f3f,3f3f06,3f3f5b,3f3f4f,3f3f66,3f3f6d,3f3f7d,3f3f07,3f3f7f
  //   ,3f3f6f,3f063f,3f0606,3f065b,3f064f,3f0666,3f066d,3f067d,3f0607
  //   ,3f067f,3f066f,3f5b3f,3f5b06,3f5b5b,3f5b4f,3f5b66,3f5b6d,3f5b7d
  //   ,3f5b07,3f5b7f,3f5b6f,3f4f3f,3f4f06,3f4f5b,3f4f4f,3f4f66,3f4f6d
  //   ,3f4f7d,3f4f07,3f4f7f,3f4f6f,3f663f,3f6606,3f665b,3f664f,3f6666
  //   ,3f666d,3f667d,3f6607,3f667f,3f666f,3f6d3f,3f6d06,3f6d5b,3f6d4f
  //   ,3f6d66,3f6d6d,3f6d7d,3f6d07,3f6d7f,3f6d6f,3f7d3f,3f7d06,3f7d5b
  //   ,3f7d4f,3f7d66,3f7d6d,3f7d7d,3f7d07,3f7d7f,3f7d6f,3f073f,3f0706
  //   ,3f075b,3f074f,3f0766,3f076d,3f077d,3f0707,3f077f,3f076f,3f7f3f
  //   ,3f7f06,3f7f5b,3f7f4f,3f7f66,3f7f6d,3f7f7d,3f7f07,3f7f7f,3f7f6f
  //   ,3f6f3f,3f6f06,3f6f5b,3f6f4f,3f6f66,3f6f6d,3f6f7d,3f6f07,3f6f7f
  //   ,3f6f6f,63f3f,63f06,63f5b,63f4f,63f66,63f6d,63f7d,63f07,63f7f
  //   ,63f6f,6063f,60606,6065b,6064f,60666,6066d,6067d,60607,6067f,6066f
  //   ,65b3f,65b06,65b5b,65b4f,65b66,65b6d,65b7d,65b07,65b7f,65b6f,64f3f
  //   ,64f06,64f5b,64f4f,64f66,64f6d,64f7d,64f07,64f7f,64f6f,6663f,66606
  //   ,6665b,6664f,66666,6666d,6667d,66607,6667f,6666f,66d3f,66d06,66d5b
  //   ,66d4f,66d66,66d6d,66d7d,66d07,66d7f,66d6f,67d3f,67d06,67d5b,67d4f
  //   ,67d66,67d6d,67d7d,67d07,67d7f,67d6f,6073f,60706,6075b,6074f,60766
  //   ,6076d,6077d,60707,6077f,6076f,67f3f,67f06,67f5b,67f4f,67f66,67f6d
  //   ,67f7d,67f07,67f7f,67f6f,66f3f,66f06,66f5b,66f4f,66f66,66f6d,66f7d
  //   ,66f07,66f7f,66f6f,5b3f3f,5b3f06,5b3f5b,5b3f4f,5b3f66,5b3f6d,5b3f7d
  //   ,5b3f07,5b3f7f,5b3f6f,5b063f,5b0606,5b065b,5b064f,5b0666,5b066d
  //   ,5b067d,5b0607,5b067f,5b066f,5b5b3f,5b5b06,5b5b5b,5b5b4f,5b5b66
  //   ,5b5b6d,5b5b7d,5b5b07,5b5b7f,5b5b6f,5b4f3f,5b4f06,5b4f5b,5b4f4f
  //   ,5b4f66,5b4f6d,5b4f7d,5b4f07,5b4f7f,5b4f6f,5b663f,5b6606,5b665b
  //   ,5b664f,5b6666,5b666d,5b667d,5b6607,5b667f,5b666f,5b6d3f,5b6d06
  //   ,5b6d5b,5b6d4f,5b6d66,5b6d6d,5b6d7d,5b6d07,5b6d7f,5b6d6f,5b7d3f
  //   ,5b7d06,5b7d5b,5b7d4f,5b7d66,5b7d6d,5b7d7d,5b7d07,5b7d7f,5b7d6f
  //   ,5b073f,5b0706,5b075b,5b074f,5b0766,5b076d,5b077d,5b0707,5b077f
  //   ,5b076f,5b7f3f,5b7f06,5b7f5b,5b7f4f,5b7f66,5b7f6d,5b7f7d,5b7f07
  //   ,5b7f7f,5b7f6f,5b6f3f,5b6f06,5b6f5b,5b6f4f,5b6f66,5b6f6d,5b6f7d
  //   ,5b6f07,5b6f7f,5b6f6f,4f3f3f,4f3f06,4f3f5b,4f3f4f,4f3f66,4f3f6d
  //   ,4f3f7d,4f3f07,4f3f7f,4f3f6f,4f063f,4f0606,4f065b,4f064f,4f0666
  //   ,4f066d,4f067d,4f0607,4f067f,4f066f,4f5b3f,4f5b06,4f5b5b,4f5b4f
  //   ,4f5b66,4f5b6d,4f5b7d,4f5b07,4f5b7f,4f5b6f,4f4f3f,4f4f06,4f4f5b
  //   ,4f4f4f,4f4f66,4f4f6d,4f4f7d,4f4f07,4f4f7f,4f4f6f,4f663f,4f6606
  //   ,4f665b,4f664f,4f6666,4f666d,4f667d,4f6607,4f667f,4f666f,4f6d3f
  //   ,4f6d06,4f6d5b,4f6d4f,4f6d66,4f6d6d,4f6d7d,4f6d07,4f6d7f,4f6d6f
  //   ,4f7d3f,4f7d06,4f7d5b,4f7d4f,4f7d66,4f7d6d,4f7d7d,4f7d07,4f7d7f
  //   ,4f7d6f,4f073f,4f0706,4f075b,4f074f,4f0766,4f076d,4f077d,4f0707
  //   ,4f077f,4f076f,4f7f3f,4f7f06,4f7f5b,4f7f4f,4f7f66,4f7f6d,4f7f7d
  //   ,4f7f07,4f7f7f,4f7f6f,4f6f3f,4f6f06,4f6f5b,4f6f4f,4f6f66,4f6f6d
  //   ,4f6f7d,4f6f07,4f6f7f,4f6f6f,663f3f,663f06,663f5b,663f4f,663f66
  //   ,663f6d,663f7d,663f07,663f7f,663f6f,66063f,660606,66065b,66064f
  //   ,660666,66066d,66067d,660607,66067f,66066f,665b3f,665b06,665b5b
  //   ,665b4f,665b66,665b6d,665b7d,665b07,665b7f,665b6f,664f3f,664f06
  //   ,664f5b,664f4f,664f66,664f6d,664f7d,664f07,664f7f,664f6f,66663f
  //   ,666606,66665b,66664f,666666,66666d,66667d,666607,66667f,66666f
  //   ,666d3f,666d06,666d5b,666d4f,666d66,666d6d,666d7d,666d07,666d7f
  //   ,666d6f,667d3f,667d06,667d5b,667d4f,667d66,667d6d,667d7d,667d07
  //   ,667d7f,667d6f,66073f,660706,66075b,66074f,660766,66076d,66077d
  //   ,660707,66077f,66076f,667f3f,667f06,667f5b,667f4f,667f66,667f6d
  //   ,667f7d,667f07,667f7f,667f6f,666f3f,666f06,666f5b,666f4f,666f66
  //   ,666f6d,666f7d,666f07,666f7f,666f6f,6d3f3f,6d3f06,6d3f5b,6d3f4f
  //   ,6d3f66,6d3f6d,6d3f7d,6d3f07,6d3f7f,6d3f6f,6d063f,6d0606,6d065b
  //   ,6d0606,6d063f,6d3f6f,6d3f7f,6d3f07,6d3f7d,6d3f6d,6d3f66,6d3f4f
  //   ,6d3f5b,6d3f06,6d3f3f,666f6f,666f7f,666f07,666f7d,666f6d,666f66
  //   ,666f4f,666f5b,666f06,666f3f,667f6f,667f7f,667f07,667f7d,667f6d
  //   ,667f66,667f4f,667f5b,667f06,667f3f,66076f,66077f,660707,66077d
  //   ,66076d,660766,66074f,66075b,660706,66073f,667d6f,667d7f,667d07
  //   ,667d7d,667d6d,667d66,667d4f,667d5b,667d06,667d3f,666d6f,666d7f
  //   ,666d07,666d7d,666d6d,666d66,666d4f,666d5b,666d06,666d3f,66666f
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  //   SUM | STEP
  //   CONFIG
endmodule
