// Digital circuit mainmain.dig as structural Verilog
module mainmain (
  input  [4:0] W_1,
  input  [4:0] W_5,
  input  [4:0] W_9,
  input  [4:0] W_13,
  input  [4:0] W_2,
  input  [4:0] W_6,
  input  [4:0] W_10,
  input  [4:0] W_14,
  input  [4:0] W_3,
  input  [4:0] W_7,
  input  [4:0] W_11,
  input  [4:0] W_15,
  input  [4:0] W_4,
  input  [4:0] W_8,
  input  [4:0] W_12,
  input  [4:0] W_16,
  input  in_21,
  input  in_22,
  input  in_23,
  input  in_24,
  input  in_25,
  input  in_26,
  input  in_27,
  input  in_28,
  input  in_29,
  input  in_30,
  input  in_31,
  input  in_32,
  input  in_33,
  input  in_34,
  input  in_35,
  input  in_36,
  input  [9:0] THRESHOLD,
  output [19:0] out_17,
  output [19:0] out_18,
  output [19:0] out_19,
  output [19:0] out_20,
  output [3:0] out_37,
  output [3:0] out_38,
  output [3:0] out_39,
  output [3:0] out_40,
  output [9:0] THRESHOLD_2,
  output [9:0] OUT
);

  wire pas_perceron_v3_1_plus;
  wire [3:0] pas_perceron_v3_1_out_val_2, pas_perceron_v3_1_thr_val_2;
  wire [7:0] pas_perceron_v3_1_out_ext, pas_perceron_v3_1_thr_ext;
  wire [19:0] pas_perceron_v3_1_out_val, pas_perceron_v3_1_thr_val;

  PAS_Perceron_V3 pas_perceron_v3_1 (
    .THRESH(THRESHOLD),
    .X({in_36, in_35, in_34, in_33, in_32, in_31, in_30, in_29, in_28, in_26, in_24, in_22, in_27, in_25, in_23, in_21}),
    .W_1({W_14, W_10, W_6, W_2, W_13, W_9, W_5, W_1}), .W_2({W_16, W_12, W_8, W_4, W_15, W_11, W_7, W_3}),
    .OUTPUT(OUT), .OUT_VAL({pas_perceron_v3_1_out_val_2, pas_perceron_v3_1_out_val}),
    .OUT_EXT(pas_perceron_v3_1_out_ext), .THR_VAL({pas_perceron_v3_1_thr_val_2, pas_perceron_v3_1_thr_val}),
    .THR_EXT(pas_perceron_v3_1_thr_ext), .plus(pas_perceron_v3_1_plus));
  LED led_1 (.in(pas_perceron_v3_1_plus));
  LED led_2 (.in(pas_perceron_v3_1_plus));
  LED led_3 (.in(pas_perceron_v3_1_plus));
  LED led_4 (.in(pas_perceron_v3_1_plus));
  Seven_Seg seven_seg_1 (
    .a(pas_perceron_v3_1_out_ext[4]), .b(pas_perceron_v3_1_out_ext[5]), .c(pas_perceron_v3_1_out_ext[6]),
    .d(pas_perceron_v3_1_out_ext[7]), .e(pas_perceron_v3_1_out_ext[0]), .f(pas_perceron_v3_1_out_ext[1]),
    .g(pas_perceron_v3_1_out_ext[2]), .dp(pas_perceron_v3_1_out_ext[3]));
  Seven_Seg seven_seg_2 (
    .a(pas_perceron_v3_1_thr_ext[4]), .b(pas_perceron_v3_1_thr_ext[5]), .c(pas_perceron_v3_1_thr_ext[6]),
    .d(pas_perceron_v3_1_thr_ext[7]), .e(pas_perceron_v3_1_thr_ext[0]), .f(pas_perceron_v3_1_thr_ext[1]),
    .g(pas_perceron_v3_1_thr_ext[2]), .dp(pas_perceron_v3_1_thr_ext[3]));
  Seven_Seg seven_seg_3 (
    .a(pas_perceron_v3_1_out_val[8]), .b(pas_perceron_v3_1_out_val[9]), .c(pas_perceron_v3_1_out_val[10]),
    .d(pas_perceron_v3_1_out_val[11]), .e(pas_perceron_v3_1_out_val[12]), .f(pas_perceron_v3_1_out_val[13]),
    .g(pas_perceron_v3_1_out_val[14]), .dp(pas_perceron_v3_1_out_val[15]));
  Seven_Seg seven_seg_4 (
    .a(pas_perceron_v3_1_thr_val[8]), .b(pas_perceron_v3_1_thr_val[9]), .c(pas_perceron_v3_1_thr_val[10]),
    .d(pas_perceron_v3_1_thr_val[11]), .e(pas_perceron_v3_1_thr_val[12]), .f(pas_perceron_v3_1_thr_val[13]),
    .g(pas_perceron_v3_1_thr_val[14]), .dp(pas_perceron_v3_1_thr_val[15]));
  Seven_Seg seven_seg_5 (
    .a(pas_perceron_v3_1_out_val[4]), .b(pas_perceron_v3_1_out_val[5]), .c(pas_perceron_v3_1_out_val[6]),
    .d(pas_perceron_v3_1_out_val[7]), .e(pas_perceron_v3_1_out_val[16]), .f(pas_perceron_v3_1_out_val[17]),
    .g(pas_perceron_v3_1_out_val[18]), .dp(pas_perceron_v3_1_out_val[19]));
  Seven_Seg seven_seg_6 (
    .a(pas_perceron_v3_1_thr_val[4]), .b(pas_perceron_v3_1_thr_val[5]), .c(pas_perceron_v3_1_thr_val[6]),
    .d(pas_perceron_v3_1_thr_val[7]), .e(pas_perceron_v3_1_thr_val[16]), .f(pas_perceron_v3_1_thr_val[17]),
    .g(pas_perceron_v3_1_thr_val[18]), .dp(pas_perceron_v3_1_thr_val[19]));
  Seven_Seg seven_seg_7 (
    .a(pas_perceron_v3_1_out_val[0]), .b(pas_perceron_v3_1_out_val[1]), .c(pas_perceron_v3_1_out_val[2]),
    .d(pas_perceron_v3_1_out_val[3]), .e(pas_perceron_v3_1_out_val_2[0]), .f(pas_perceron_v3_1_out_val_2[1]),
    .g(pas_perceron_v3_1_out_val_2[2]), .dp(pas_perceron_v3_1_out_val_2[3]));
  Seven_Seg seven_seg_8 (
    .a(pas_perceron_v3_1_thr_val[0]), .b(pas_perceron_v3_1_thr_val[1]), .c(pas_perceron_v3_1_thr_val[2]),
    .d(pas_perceron_v3_1_thr_val[3]), .e(pas_perceron_v3_1_thr_val_2[0]), .f(pas_perceron_v3_1_thr_val_2[1]),
    .g(pas_perceron_v3_1_thr_val_2[2]), .dp(pas_perceron_v3_1_thr_val_2[3]));

  assign out_17 = {W_16, W_12, W_8, W_4};
  assign out_18 = {W_15, W_11, W_7, W_3};
  assign out_19 = {W_14, W_10, W_6, W_2};
  assign out_20 = {W_13, W_9, W_5, W_1};
  assign out_37 = {in_27, in_25, in_23, in_21};
  assign out_38 = {in_28, in_26, in_24, in_22};
  assign out_39 = {in_32, in_31, in_30, in_29};
  assign out_40 = {in_36, in_35, in_34, in_33};
  assign THRESHOLD_2 = THRESHOLD;

  // Notes on the sheet:
  //   WEIGHTS
  //   INPUTS
  //   OUTPUT
endmodule
